// Logisim project 4bitLA.circ as structural Verilog
module Computer (
  input  [3:0] in_1,
  input  [3:0] in_2,
  input  [3:0] in_3,
  input  ON,
  input  MANUAL
);

  wire ACC_led_0, ACC_led_1, ACC_led_2, ACC_led_3, ACC_ledr, ACC_ledrst, ACC_ledw, ACC_out_0, ACC_out_1,
       ACC_out_2, ACC_out_3, acc_r, acc_w, alu_1_ledcin, alu_1_ledop, alu_1_sum_0, alu_1_sum_1, alu_1_sum_2,
       alu_1_sum_3, bin_display_1_led0, bin_display_1_led1, bin_display_1_led2, bin_display_1_led3, cin, clk,
       CLOCK_out, controlunit_1_led0, controlunit_1_led1, controlunit_1_led2, controlunit_1_led3,
       controlunit_1_led4, controlunit_1_led5, controlunit_1_led6, controlunit_1_led7, controlunit_1_led8,
       controlunit_1_led9, controlunit_1_led10, controlunit_1_led11, controlunit_1_led12,
       controlunit_1_led13, controlunit_1_led14, controlunit_1_led15, controlunit_1_led16,
       controlunit_1_ledclk, controlunit_1_ledclkr, controlunit_1_ledclkw, controlunit_1_ledhalt,
       controlunit_1_ledinstr0, controlunit_1_ledinstr1, controlunit_1_ledinstr2, controlunit_1_ledinstr3,
       controlunit_1_ledrst, controlunit_1_ledstep1, controlunit_1_ledstep2, controlunit_1_ledstep3,
       controlunit_1_ledstep4, controlunit_1_ledstep5, controlunit_1_ledstep6, controlunit_1_ledstep7,
       controlunit_1_ledzero, DATA_led_0__0, DATA_led_0__1, DATA_led_0__2, DATA_led_0__3, DATA_led_1__0,
       DATA_led_1__1, DATA_led_1__2, DATA_led_1__3, DATA_led_2__0, DATA_led_2__1, DATA_led_2__2,
       DATA_led_2__3, DATA_led_3__0, DATA_led_3__1, DATA_led_3__2, DATA_led_3__3, DATA_led_4__0,
       DATA_led_4__1, DATA_led_4__2, DATA_led_4__3, DATA_led_5__0, DATA_led_5__1, DATA_led_5__2,
       DATA_led_5__3, DATA_led_6__0, DATA_led_6__1, DATA_led_6__2, DATA_led_6__3, DATA_led_7__0,
       DATA_led_7__1, DATA_led_7__2, DATA_led_7__3, DATA_led_8__0, DATA_led_8__1, DATA_led_8__2,
       DATA_led_8__3, DATA_led_9__0, DATA_led_9__1, DATA_led_9__2, DATA_led_9__3, DATA_led_a__0,
       DATA_led_a__1, DATA_led_a__2, DATA_led_a__3, DATA_led_b__0, DATA_led_b__1, DATA_led_b__2,
       DATA_led_b__3, DATA_led_c__0, DATA_led_c__1, DATA_led_c__2, DATA_led_c__3, DATA_led_d__0,
       DATA_led_d__1, DATA_led_d__2, DATA_led_d__3, DATA_led_e__0, DATA_led_e__1, DATA_led_e__2,
       DATA_led_e__3, DATA_led_f__0, DATA_led_f__1, DATA_led_f__2, DATA_led_f__3, DATA_ledaddr_0,
       DATA_ledaddr_0_2, DATA_ledaddr_1, DATA_ledaddr_1_2, DATA_ledr, DATA_ledrst, DATA_ledsel,
       DATA_ledsel_0, DATA_ledsel_1, DATA_ledsel_2, DATA_ledsel_3, DATA_ledsel_4, DATA_ledsel_5,
       DATA_ledsel_6, DATA_ledsel_7, DATA_ledsel_8, DATA_ledsel_9, DATA_ledsel_a, DATA_ledsel_b,
       DATA_ledsel_c, DATA_ledsel_d, DATA_ledsel_e, DATA_ledsel_f, DATA_ledw, drom_r, hex_display_1_hex0,
       hex_display_1_hex1, hex_display_1_hex2, hex_display_1_hex3, hex_display_1_led0, hex_display_1_led1,
       hex_display_1_led2, hex_display_1_led3, hex_display_2_hex0, hex_display_2_hex1, hex_display_2_hex2,
       hex_display_2_hex3, hex_display_2_led0, hex_display_2_led1, hex_display_2_led2, hex_display_2_led3,
       hex_display_3_hex0, hex_display_3_hex1, hex_display_3_hex2, hex_display_3_hex3, hex_display_3_led0,
       hex_display_3_led1, hex_display_3_led2, hex_display_3_led3, hex_display_4_hex0, hex_display_4_hex1,
       hex_display_4_hex2, hex_display_4_hex3, hex_display_4_led0, hex_display_4_led1, hex_display_4_led2,
       hex_display_4_led3, hex_display_5_hex0, hex_display_5_hex1, hex_display_5_hex2, hex_display_5_hex3,
       hex_display_5_led0, hex_display_5_led1, hex_display_5_led2, hex_display_5_led3, hex_display_6_hex0,
       hex_display_6_hex1, hex_display_6_hex2, hex_display_6_hex3, hex_display_6_led0, hex_display_6_led1,
       hex_display_6_led2, hex_display_6_led3, INSTR_led_0__0, INSTR_led_0__1, INSTR_led_0__2,
       INSTR_led_0__3, INSTR_led_1__0, INSTR_led_1__1, INSTR_led_1__2, INSTR_led_1__3, INSTR_led_2__0,
       INSTR_led_2__1, INSTR_led_2__2, INSTR_led_2__3, INSTR_led_3__0, INSTR_led_3__1, INSTR_led_3__2,
       INSTR_led_3__3, INSTR_led_4__0, INSTR_led_4__1, INSTR_led_4__2, INSTR_led_4__3, INSTR_led_5__0,
       INSTR_led_5__1, INSTR_led_5__2, INSTR_led_5__3, INSTR_led_6__0, INSTR_led_6__1, INSTR_led_6__2,
       INSTR_led_6__3, INSTR_led_7__0, INSTR_led_7__1, INSTR_led_7__2, INSTR_led_7__3, INSTR_led_8__0,
       INSTR_led_8__1, INSTR_led_8__2, INSTR_led_8__3, INSTR_led_9__0, INSTR_led_9__1, INSTR_led_9__2,
       INSTR_led_9__3, INSTR_led_a__0, INSTR_led_a__1, INSTR_led_a__2, INSTR_led_a__3, INSTR_led_b__0,
       INSTR_led_b__1, INSTR_led_b__2, INSTR_led_b__3, INSTR_led_c__0, INSTR_led_c__1, INSTR_led_c__2,
       INSTR_led_c__3, INSTR_led_d__0, INSTR_led_d__1, INSTR_led_d__2, INSTR_led_d__3, INSTR_led_e__0,
       INSTR_led_e__1, INSTR_led_e__2, INSTR_led_e__3, INSTR_led_f__0, INSTR_led_f__1, INSTR_led_f__2,
       INSTR_led_f__3, INSTR_ledaddr_0, INSTR_ledaddr_0_2, INSTR_ledaddr_1, INSTR_ledaddr_1_2, INSTR_ledr,
       INSTR_ledrst, INSTR_ledsel, INSTR_ledsel_0, INSTR_ledsel_1, INSTR_ledsel_2, INSTR_ledsel_3,
       INSTR_ledsel_4, INSTR_ledsel_5, INSTR_ledsel_6, INSTR_ledsel_7, INSTR_ledsel_8, INSTR_ledsel_9,
       INSTR_ledsel_a, INSTR_ledsel_b, INSTR_ledsel_c, INSTR_ledsel_d, INSTR_ledsel_e, INSTR_ledsel_f,
       INSTR_ledw, IR_led_0, IR_led_1, IR_led_2, IR_led_3, IR_ledr, IR_ledrst, IR_ledw, IR_out_0, IR_out_1,
       IR_out_2, IR_out_3, ir_w, irom_r, mar_w, mux2x4_1_ledsel, mux2x4_1_out0, mux2x4_1_out1, mux2x4_1_out2,
       mux2x4_1_out3, muxB, n7segdisplay_hex_adapter_1_a, n7segdisplay_hex_adapter_1_b,
       n7segdisplay_hex_adapter_1_c, n7segdisplay_hex_adapter_1_d, n7segdisplay_hex_adapter_1_dp,
       n7segdisplay_hex_adapter_1_e, n7segdisplay_hex_adapter_1_f, n7segdisplay_hex_adapter_1_g,
       n7segdisplay_hex_adapter_2_a, n7segdisplay_hex_adapter_2_b, n7segdisplay_hex_adapter_2_c,
       n7segdisplay_hex_adapter_2_d, n7segdisplay_hex_adapter_2_dp, n7segdisplay_hex_adapter_2_e,
       n7segdisplay_hex_adapter_2_f, n7segdisplay_hex_adapter_2_g, n7segdisplay_hex_adapter_3_a,
       n7segdisplay_hex_adapter_3_b, n7segdisplay_hex_adapter_3_c, n7segdisplay_hex_adapter_3_d,
       n7segdisplay_hex_adapter_3_dp, n7segdisplay_hex_adapter_3_e, n7segdisplay_hex_adapter_3_f,
       n7segdisplay_hex_adapter_3_g, n7segdisplay_hex_adapter_4_a, n7segdisplay_hex_adapter_4_b,
       n7segdisplay_hex_adapter_4_c, n7segdisplay_hex_adapter_4_d, n7segdisplay_hex_adapter_4_dp,
       n7segdisplay_hex_adapter_4_e, n7segdisplay_hex_adapter_4_f, n7segdisplay_hex_adapter_4_g,
       n7segdisplay_hex_adapter_5_a, n7segdisplay_hex_adapter_5_b, n7segdisplay_hex_adapter_5_c,
       n7segdisplay_hex_adapter_5_d, n7segdisplay_hex_adapter_5_dp, n7segdisplay_hex_adapter_5_e,
       n7segdisplay_hex_adapter_5_f, n7segdisplay_hex_adapter_5_g, n7segdisplay_hex_adapter_6_a,
       n7segdisplay_hex_adapter_6_b, n7segdisplay_hex_adapter_6_c, n7segdisplay_hex_adapter_6_d,
       n7segdisplay_hex_adapter_6_dp, n7segdisplay_hex_adapter_6_e, n7segdisplay_hex_adapter_6_f,
       n7segdisplay_hex_adapter_6_g, nrom_rst, nrst, op, PC_led_0, PC_led_1, PC_led_2, PC_led_3, PC_ledr,
       PC_ledrst, PC_ledw, pc_r, pc_w, RAM_led_0__0, RAM_led_0__1, RAM_led_0__2, RAM_led_0__3, RAM_led_1__0,
       RAM_led_1__1, RAM_led_1__2, RAM_led_1__3, RAM_led_2__0, RAM_led_2__1, RAM_led_2__2, RAM_led_2__3,
       RAM_led_3__0, RAM_led_3__1, RAM_led_3__2, RAM_led_3__3, RAM_led_4__0, RAM_led_4__1, RAM_led_4__2,
       RAM_led_4__3, RAM_led_5__0, RAM_led_5__1, RAM_led_5__2, RAM_led_5__3, RAM_led_6__0, RAM_led_6__1,
       RAM_led_6__2, RAM_led_6__3, RAM_led_7__0, RAM_led_7__1, RAM_led_7__2, RAM_led_7__3, RAM_led_8__0,
       RAM_led_8__1, RAM_led_8__2, RAM_led_8__3, RAM_led_9__0, RAM_led_9__1, RAM_led_9__2, RAM_led_9__3,
       RAM_led_a__0, RAM_led_a__1, RAM_led_a__2, RAM_led_a__3, RAM_led_b__0, RAM_led_b__1, RAM_led_b__2,
       RAM_led_b__3, RAM_led_c__0, RAM_led_c__1, RAM_led_c__2, RAM_led_c__3, RAM_led_d__0, RAM_led_d__1,
       RAM_led_d__2, RAM_led_d__3, RAM_led_e__0, RAM_led_e__1, RAM_led_e__2, RAM_led_e__3, RAM_led_f__0,
       RAM_led_f__1, RAM_led_f__2, RAM_led_f__3, RAM_ledaddr_0, RAM_ledaddr_0_2, RAM_ledaddr_1,
       RAM_ledaddr_1_2, RAM_ledr, RAM_ledrst, RAM_ledsel, RAM_ledsel_0, RAM_ledsel_1, RAM_ledsel_2,
       RAM_ledsel_3, RAM_ledsel_4, RAM_ledsel_5, RAM_ledsel_6, RAM_ledsel_7, RAM_ledsel_8, RAM_ledsel_9,
       RAM_ledsel_a, RAM_ledsel_b, RAM_ledsel_c, RAM_ledsel_d, RAM_ledsel_e, RAM_ledsel_f, RAM_ledw,
       RAM_MAR_led_0, RAM_MAR_led_1, RAM_MAR_led_2, RAM_MAR_led_3, RAM_MAR_ledr, RAM_MAR_ledrst,
       RAM_MAR_ledw, RAM_MAR_out_0, RAM_MAR_out_1, RAM_MAR_out_2, RAM_MAR_out_3, RAM_out_0, RAM_out_1,
       RAM_out_2, RAM_out_3, ram_r, ram_w, res_r, res_w, RESET_out, RESET_ROM_out, RESULT_led_0,
       RESULT_led_1, RESULT_led_2, RESULT_led_3, RESULT_ledr, RESULT_ledrst, RESULT_ledw, resume, rmar_w,
       ROM_MAR_led_0, ROM_MAR_led_1, ROM_MAR_led_2, ROM_MAR_led_3, ROM_MAR_ledr, ROM_MAR_ledrst,
       ROM_MAR_ledw, ROM_MAR_out_0, ROM_MAR_out_1, ROM_MAR_out_2, ROM_MAR_out_3, rom_w, TEMP_led_0,
       TEMP_led_1, TEMP_led_2, TEMP_led_3, TEMP_ledr, TEMP_ledrst, TEMP_ledw, TEMP_out_0, TEMP_out_1,
       TEMP_out_2, TEMP_out_3, tmp_w, WRITE_ROM_out, zero4_1_zero, zeropass4_1_leden, zeropass4_1_out_0,
       zeropass4_1_out_1, zeropass4_1_out_2, zeropass4_1_out_3;

  Reg4 RAM_MAR (
    .LED_3(RAM_MAR_led_3), .OUT_3(RAM_MAR_out_3), .IN_3(RAM_out_3), .read(1'b1), .LEDr(RAM_MAR_ledr),
    .write(mar_w), .LEDw(RAM_MAR_ledw), .nrst(nrst), .LEDrst(RAM_MAR_ledrst), .LED_2(RAM_MAR_led_2),
    .OUT_2(RAM_MAR_out_2), .IN_2(RAM_out_2), .LED_1(RAM_MAR_led_1), .OUT_1(RAM_MAR_out_1), .IN_1(RAM_out_1),
    .LED_0(RAM_MAR_led_0), .OUT_0(RAM_MAR_out_0), .IN_0(RAM_out_0));
  Reg4 TEMP (
    .LED_3(TEMP_led_3), .OUT_3(TEMP_out_3), .IN_3(RAM_out_3), .read(1'b1), .LEDr(TEMP_ledr), .write(tmp_w),
    .LEDw(TEMP_ledw), .nrst(nrst), .LEDrst(TEMP_ledrst), .LED_2(TEMP_led_2), .OUT_2(TEMP_out_2),
    .IN_2(RAM_out_2), .LED_1(TEMP_led_1), .OUT_1(TEMP_out_1), .IN_1(RAM_out_1), .LED_0(TEMP_led_0),
    .OUT_0(TEMP_out_0), .IN_0(RAM_out_0));
  LED led_1 (.in(TEMP_ledw));
  LED led_2 (.in(TEMP_ledrst));
  LED led_3 (.in(TEMP_ledr));
  HEX_Display hex_display_1 (
    .BIN_0(RAM_MAR_led_0), .LED0(hex_display_1_led0), .BIN_1(RAM_MAR_led_1), .LED1(hex_display_1_led1),
    .BIN_2(RAM_MAR_led_2), .LED2(hex_display_1_led2), .BIN_3(RAM_MAR_led_3), .LED3(hex_display_1_led3),
    .HEX3(hex_display_1_hex3), .HEX2(hex_display_1_hex2), .HEX1(hex_display_1_hex1), .HEX0(hex_display_1_hex0));
  LED led_4 (.in(hex_display_1_led3));
  _7SegDisplay_HEX_Adapter u_7segdisplay_hex_adapter_1 (
    .IN_0(hex_display_1_hex0), .IN_1(hex_display_1_hex1), .IN_2(hex_display_1_hex2),
    .IN_3(hex_display_1_hex3), .a(n7segdisplay_hex_adapter_1_a), .b(n7segdisplay_hex_adapter_1_b),
    .c(n7segdisplay_hex_adapter_1_c), .d(n7segdisplay_hex_adapter_1_d), .e(n7segdisplay_hex_adapter_1_e),
    .f(n7segdisplay_hex_adapter_1_f), .g(n7segdisplay_hex_adapter_1_g), .dp(n7segdisplay_hex_adapter_1_dp));
  LED led_5 (.in(RAM_MAR_ledw));
  LED led_6 (.in(RAM_MAR_ledrst));
  LED led_7 (.in(RAM_MAR_ledr));
  SRAM_16x4bit RAM (
    .read(ram_r), .write(ram_w), .nrst(nrst), .LEDsel_0(RAM_ledsel_0), .LED_0__0(RAM_led_0__0),
    .LED_0__1(RAM_led_0__1), .LED_0__2(RAM_led_0__2), .LED_0__3(RAM_led_0__3), .LEDsel_1(RAM_ledsel_1),
    .LED_1__0(RAM_led_1__0), .LED_1__1(RAM_led_1__1), .LED_1__2(RAM_led_1__2), .LED_1__3(RAM_led_1__3),
    .LEDsel_2(RAM_ledsel_2), .LED_2__0(RAM_led_2__0), .LED_2__1(RAM_led_2__1), .LED_2__2(RAM_led_2__2),
    .LED_2__3(RAM_led_2__3), .LEDsel_3(RAM_ledsel_3), .LED_3__0(RAM_led_3__0), .LED_3__1(RAM_led_3__1),
    .LED_3__2(RAM_led_3__2), .LED_3__3(RAM_led_3__3), .LEDsel_4(RAM_ledsel_4), .LED_4__0(RAM_led_4__0),
    .LED_4__1(RAM_led_4__1), .LED_4__2(RAM_led_4__2), .LED_4__3(RAM_led_4__3), .LEDsel_5(RAM_ledsel_5),
    .LED_5__0(RAM_led_5__0), .LED_5__1(RAM_led_5__1), .LED_5__2(RAM_led_5__2), .LED_5__3(RAM_led_5__3),
    .LEDsel_6(RAM_ledsel_6), .LED_6__0(RAM_led_6__0), .LED_6__1(RAM_led_6__1), .LED_6__2(RAM_led_6__2),
    .LED_6__3(RAM_led_6__3), .LEDsel_7(RAM_ledsel_7), .LED_7__0(RAM_led_7__0), .LED_7__1(RAM_led_7__1),
    .LED_7__2(RAM_led_7__2), .LED_7__3(RAM_led_7__3), .LEDr(RAM_ledr), .LEDw(RAM_ledw), .LEDrst(RAM_ledrst),
    .ADDR_3(RAM_MAR_out_3), .ADDR_2(RAM_MAR_out_2), .ADDR_1(RAM_MAR_out_1), .ADDR_0(RAM_MAR_out_0),
    .select(1'b1), .IN_3(RAM_out_3), .IN_2(RAM_out_2), .IN_1(RAM_out_1), .IN_0(RAM_out_0),
    .LEDaddr_1_2(RAM_ledaddr_1_2), .LEDaddr_0_2(RAM_ledaddr_0_2), .LEDaddr_1(RAM_ledaddr_1),
    .LEDaddr_0(RAM_ledaddr_0), .LEDsel(RAM_ledsel), .OUT_3(RAM_out_3), .OUT_2(RAM_out_2), .OUT_1(RAM_out_1),
    .OUT_0(RAM_out_0), .LEDsel_8(RAM_ledsel_8), .LED_8__0(RAM_led_8__0), .LED_8__1(RAM_led_8__1),
    .LED_8__2(RAM_led_8__2), .LED_8__3(RAM_led_8__3), .LEDsel_9(RAM_ledsel_9), .LED_9__0(RAM_led_9__0),
    .LED_9__1(RAM_led_9__1), .LED_9__2(RAM_led_9__2), .LED_9__3(RAM_led_9__3), .LEDsel_A(RAM_ledsel_a),
    .LED_A__0(RAM_led_a__0), .LED_A__1(RAM_led_a__1), .LED_A__2(RAM_led_a__2), .LED_A__3(RAM_led_a__3),
    .LEDsel_B(RAM_ledsel_b), .LED_B__0(RAM_led_b__0), .LED_B__1(RAM_led_b__1), .LED_B__2(RAM_led_b__2),
    .LED_B__3(RAM_led_b__3), .LEDsel_C(RAM_ledsel_c), .LED_C__0(RAM_led_c__0), .LED_C__1(RAM_led_c__1),
    .LED_C__2(RAM_led_c__2), .LED_C__3(RAM_led_c__3), .LEDsel_D(RAM_ledsel_d), .LED_D__0(RAM_led_d__0),
    .LED_D__1(RAM_led_d__1), .LED_D__2(RAM_led_d__2), .LED_D__3(RAM_led_d__3), .LEDsel_E(RAM_ledsel_e),
    .LED_E__0(RAM_led_e__0), .LED_E__1(RAM_led_e__1), .LED_E__2(RAM_led_e__2), .LED_E__3(RAM_led_e__3),
    .LEDsel_F(RAM_ledsel_f), .LED_F__0(RAM_led_f__0), .LED_F__1(RAM_led_f__1), .LED_F__2(RAM_led_f__2),
    .LED_F__3(RAM_led_f__3));
  LED led_8 (.in(RAM_ledaddr_1_2));
  LED led_9 (.in(RAM_ledsel));
  LED led_10 (.in(RAM_ledw));
  LED led_11 (.in(RAM_ledrst));
  LED led_12 (.in(RAM_ledr));
  HEX_Display hex_display_2 (
    .BIN_0(TEMP_led_0), .LED0(hex_display_2_led0), .BIN_1(TEMP_led_1), .LED1(hex_display_2_led1),
    .BIN_2(TEMP_led_2), .LED2(hex_display_2_led2), .BIN_3(TEMP_led_3), .LED3(hex_display_2_led3),
    .HEX3(hex_display_2_hex3), .HEX2(hex_display_2_hex2), .HEX1(hex_display_2_hex1), .HEX0(hex_display_2_hex0));
  LED led_13 (.in(hex_display_2_led3));
  _7SegDisplay_HEX_Adapter u_7segdisplay_hex_adapter_2 (
    .IN_0(hex_display_2_hex0), .IN_1(hex_display_2_hex1), .IN_2(hex_display_2_hex2),
    .IN_3(hex_display_2_hex3), .a(n7segdisplay_hex_adapter_2_a), .b(n7segdisplay_hex_adapter_2_b),
    .c(n7segdisplay_hex_adapter_2_c), .d(n7segdisplay_hex_adapter_2_d), .e(n7segdisplay_hex_adapter_2_e),
    .f(n7segdisplay_hex_adapter_2_f), .g(n7segdisplay_hex_adapter_2_g), .dp(n7segdisplay_hex_adapter_2_dp));
  _7_Segment_Display u_7_segment_display_1 (
    .g(n7segdisplay_hex_adapter_2_g), .f(n7segdisplay_hex_adapter_2_f), .a(n7segdisplay_hex_adapter_2_a),
    .b(n7segdisplay_hex_adapter_2_b), .e(n7segdisplay_hex_adapter_2_e), .d(n7segdisplay_hex_adapter_2_d),
    .c(n7segdisplay_hex_adapter_2_c), .dp(n7segdisplay_hex_adapter_2_dp));
  LED led_14 (.in(hex_display_1_led0));
  LED led_15 (.in(hex_display_1_led1));
  LED led_16 (.in(hex_display_1_led2));
  _7_Segment_Display u_7_segment_display_2 (
    .g(n7segdisplay_hex_adapter_1_g), .f(n7segdisplay_hex_adapter_1_f), .a(n7segdisplay_hex_adapter_1_a),
    .b(n7segdisplay_hex_adapter_1_b), .e(n7segdisplay_hex_adapter_1_e), .d(n7segdisplay_hex_adapter_1_d),
    .c(n7segdisplay_hex_adapter_1_c), .dp(n7segdisplay_hex_adapter_1_dp));
  LED led_17 (.in(RAM_ledaddr_1));
  LED led_18 (.in(RAM_ledaddr_0_2));
  LED led_19 (.in(RAM_ledaddr_0));
  LED led_20 (.in(RAM_ledsel_0));
  LED led_21 (.in(RAM_ledsel_1));
  LED led_22 (.in(RAM_ledsel_2));
  LED led_23 (.in(RAM_ledsel_3));
  LED led_24 (.in(RAM_ledsel_4));
  LED led_25 (.in(RAM_ledsel_5));
  LED led_26 (.in(RAM_ledsel_6));
  LED led_27 (.in(RAM_ledsel_7));
  LED led_28 (.in(RAM_ledsel_8));
  LED led_29 (.in(RAM_ledsel_9));
  LED led_30 (.in(RAM_ledsel_a));
  LED led_31 (.in(RAM_ledsel_b));
  LED led_32 (.in(RAM_ledsel_c));
  LED led_33 (.in(RAM_ledsel_d));
  LED led_34 (.in(RAM_ledsel_e));
  LED led_35 (.in(RAM_ledsel_f));
  LED led_36 (.in(hex_display_2_led2));
  LED led_37 (.in(hex_display_2_led1));
  LED led_38 (.in(hex_display_2_led0));
  Reg4 RESULT (
    .LED_3(RESULT_led_3), .OUT_3(RAM_out_3), .IN_3(alu_1_sum_3), .read(res_r), .LEDr(RESULT_ledr),
    .write(res_w), .LEDw(RESULT_ledw), .nrst(nrst), .LEDrst(RESULT_ledrst), .LED_2(RESULT_led_2),
    .OUT_2(RAM_out_2), .IN_2(alu_1_sum_2), .LED_1(RESULT_led_1), .OUT_1(RAM_out_1), .IN_1(alu_1_sum_1),
    .LED_0(RESULT_led_0), .OUT_0(RAM_out_0), .IN_0(alu_1_sum_0));
  HEX_Display hex_display_3 (
    .BIN_0(RESULT_led_0), .LED0(hex_display_3_led0), .BIN_1(RESULT_led_1), .LED1(hex_display_3_led1),
    .BIN_2(RESULT_led_2), .LED2(hex_display_3_led2), .BIN_3(RESULT_led_3), .LED3(hex_display_3_led3),
    .HEX3(hex_display_3_hex3), .HEX2(hex_display_3_hex2), .HEX1(hex_display_3_hex1), .HEX0(hex_display_3_hex0));
  LED led_39 (.in(RESULT_ledw));
  LED led_40 (.in(RESULT_ledrst));
  LED led_41 (.in(RESULT_ledr));
  LED led_42 (.in(RAM_led_0__2));
  LED led_43 (.in(RAM_led_0__3));
  LED led_44 (.in(RAM_led_0__1));
  LED led_45 (.in(RAM_led_1__3));
  LED led_46 (.in(RAM_led_1__1));
  LED led_47 (.in(RAM_led_1__2));
  LED led_48 (.in(RAM_led_2__3));
  LED led_49 (.in(RAM_led_2__1));
  LED led_50 (.in(RAM_led_2__2));
  LED led_51 (.in(RAM_led_3__2));
  LED led_52 (.in(RAM_led_3__3));
  LED led_53 (.in(RAM_led_3__1));
  LED led_54 (.in(RAM_led_4__1));
  LED led_55 (.in(RAM_led_4__3));
  LED led_56 (.in(RAM_led_4__2));
  LED led_57 (.in(RAM_led_5__2));
  LED led_58 (.in(RAM_led_5__3));
  LED led_59 (.in(RAM_led_5__1));
  LED led_60 (.in(RAM_led_6__2));
  LED led_61 (.in(RAM_led_6__3));
  LED led_62 (.in(RAM_led_6__1));
  LED led_63 (.in(RAM_led_7__2));
  LED led_64 (.in(RAM_led_7__1));
  LED led_65 (.in(RAM_led_7__3));
  LED led_66 (.in(RAM_led_8__3));
  LED led_67 (.in(RAM_led_8__2));
  LED led_68 (.in(RAM_led_8__1));
  LED led_69 (.in(RAM_led_9__3));
  LED led_70 (.in(RAM_led_9__1));
  LED led_71 (.in(RAM_led_9__2));
  LED led_72 (.in(RAM_led_a__1));
  LED led_73 (.in(RAM_led_a__2));
  LED led_74 (.in(RAM_led_a__3));
  LED led_75 (.in(RAM_led_b__3));
  LED led_76 (.in(RAM_led_b__1));
  LED led_77 (.in(RAM_led_b__2));
  LED led_78 (.in(RAM_led_c__2));
  LED led_79 (.in(RAM_led_c__3));
  LED led_80 (.in(RAM_led_c__1));
  LED led_81 (.in(RAM_led_d__2));
  LED led_82 (.in(RAM_led_d__3));
  LED led_83 (.in(RAM_led_d__1));
  LED led_84 (.in(RAM_led_e__3));
  LED led_85 (.in(RAM_led_e__2));
  LED led_86 (.in(RAM_led_e__1));
  LED led_87 (.in(RAM_led_f__1));
  LED led_88 (.in(RAM_led_f__3));
  LED led_89 (.in(RAM_led_f__2));
  ALU_2 alu_1 (
    .a_0(TEMP_out_0), .a_1(TEMP_out_1), .a_2(TEMP_out_2), .a_3(TEMP_out_3), .b_0(zeropass4_1_out_0),
    .b_1(zeropass4_1_out_1), .b_2(zeropass4_1_out_2), .b_3(zeropass4_1_out_3), .op(op), .cin(cin),
    .sum_0(alu_1_sum_0), .sum_1(alu_1_sum_1), .sum_2(alu_1_sum_2), .sum_3(alu_1_sum_3),
    .LEDcin(alu_1_ledcin), .LEDop(alu_1_ledop));
  LED led_90 (.in(alu_1_ledcin));
  LED led_91 (.in(alu_1_ledop));
  LED led_92 (.in(hex_display_3_led3));
  LED led_93 (.in(hex_display_3_led2));
  LED led_94 (.in(hex_display_3_led1));
  _7SegDisplay_HEX_Adapter u_7segdisplay_hex_adapter_3 (
    .IN_0(hex_display_3_hex0), .IN_1(hex_display_3_hex1), .IN_2(hex_display_3_hex2),
    .IN_3(hex_display_3_hex3), .a(n7segdisplay_hex_adapter_3_a), .b(n7segdisplay_hex_adapter_3_b),
    .c(n7segdisplay_hex_adapter_3_c), .d(n7segdisplay_hex_adapter_3_d), .e(n7segdisplay_hex_adapter_3_e),
    .f(n7segdisplay_hex_adapter_3_f), .g(n7segdisplay_hex_adapter_3_g), .dp(n7segdisplay_hex_adapter_3_dp));
  _7_Segment_Display u_7_segment_display_3 (
    .g(n7segdisplay_hex_adapter_3_g), .f(n7segdisplay_hex_adapter_3_f), .a(n7segdisplay_hex_adapter_3_a),
    .b(n7segdisplay_hex_adapter_3_b), .e(n7segdisplay_hex_adapter_3_e), .d(n7segdisplay_hex_adapter_3_d),
    .c(n7segdisplay_hex_adapter_3_c), .dp(n7segdisplay_hex_adapter_3_dp));
  LED led_95 (.in(RAM_led_0__0));
  LED led_96 (.in(RAM_led_1__0));
  LED led_97 (.in(RAM_led_2__0));
  LED led_98 (.in(RAM_led_3__0));
  LED led_99 (.in(RAM_led_4__0));
  LED led_100 (.in(RAM_led_5__0));
  LED led_101 (.in(RAM_led_6__0));
  LED led_102 (.in(RAM_led_7__0));
  LED led_103 (.in(RAM_led_8__0));
  LED led_104 (.in(RAM_led_9__0));
  LED led_105 (.in(RAM_led_a__0));
  LED led_106 (.in(RAM_led_b__0));
  LED led_107 (.in(RAM_led_c__0));
  LED led_108 (.in(RAM_led_d__0));
  LED led_109 (.in(RAM_led_e__0));
  LED led_110 (.in(RAM_led_f__0));
  ZeroPass4 zeropass4_1 (
    .enable(muxB), .LEDen(zeropass4_1_leden), .IN_3(RAM_out_3), .IN_2(RAM_out_2), .IN_1(RAM_out_1),
    .IN_0(RAM_out_0), .OUT_3(zeropass4_1_out_3), .OUT_2(zeropass4_1_out_2), .OUT_1(zeropass4_1_out_1),
    .OUT_0(zeropass4_1_out_0));
  LED led_111 (.in(zeropass4_1_leden));
  LED led_112 (.in(hex_display_3_led0));
  SRAM_16x4bit INSTR (
    .read(irom_r), .write(rom_w), .nrst(nrom_rst), .LEDsel_0(INSTR_ledsel_0), .LED_0__0(INSTR_led_0__0),
    .LED_0__1(INSTR_led_0__1), .LED_0__2(INSTR_led_0__2), .LED_0__3(INSTR_led_0__3),
    .LEDsel_1(INSTR_ledsel_1), .LED_1__0(INSTR_led_1__0), .LED_1__1(INSTR_led_1__1),
    .LED_1__2(INSTR_led_1__2), .LED_1__3(INSTR_led_1__3), .LEDsel_2(INSTR_ledsel_2),
    .LED_2__0(INSTR_led_2__0), .LED_2__1(INSTR_led_2__1), .LED_2__2(INSTR_led_2__2),
    .LED_2__3(INSTR_led_2__3), .LEDsel_3(INSTR_ledsel_3), .LED_3__0(INSTR_led_3__0),
    .LED_3__1(INSTR_led_3__1), .LED_3__2(INSTR_led_3__2), .LED_3__3(INSTR_led_3__3),
    .LEDsel_4(INSTR_ledsel_4), .LED_4__0(INSTR_led_4__0), .LED_4__1(INSTR_led_4__1),
    .LED_4__2(INSTR_led_4__2), .LED_4__3(INSTR_led_4__3), .LEDsel_5(INSTR_ledsel_5),
    .LED_5__0(INSTR_led_5__0), .LED_5__1(INSTR_led_5__1), .LED_5__2(INSTR_led_5__2),
    .LED_5__3(INSTR_led_5__3), .LEDsel_6(INSTR_ledsel_6), .LED_6__0(INSTR_led_6__0),
    .LED_6__1(INSTR_led_6__1), .LED_6__2(INSTR_led_6__2), .LED_6__3(INSTR_led_6__3),
    .LEDsel_7(INSTR_ledsel_7), .LED_7__0(INSTR_led_7__0), .LED_7__1(INSTR_led_7__1),
    .LED_7__2(INSTR_led_7__2), .LED_7__3(INSTR_led_7__3), .LEDr(INSTR_ledr), .LEDw(INSTR_ledw),
    .LEDrst(INSTR_ledrst), .ADDR_3(mux2x4_1_out3), .ADDR_2(mux2x4_1_out2), .ADDR_1(mux2x4_1_out1),
    .ADDR_0(mux2x4_1_out0), .select(1'b1), .IN_3(in_2[3]), .IN_2(in_2[2]), .IN_1(in_2[1]), .IN_0(in_2[0]),
    .LEDaddr_1_2(INSTR_ledaddr_1_2), .LEDaddr_0_2(INSTR_ledaddr_0_2), .LEDaddr_1(INSTR_ledaddr_1),
    .LEDaddr_0(INSTR_ledaddr_0), .LEDsel(INSTR_ledsel), .OUT_3(RAM_out_3), .OUT_2(RAM_out_2),
    .OUT_1(RAM_out_1), .OUT_0(RAM_out_0), .LEDsel_8(INSTR_ledsel_8), .LED_8__0(INSTR_led_8__0),
    .LED_8__1(INSTR_led_8__1), .LED_8__2(INSTR_led_8__2), .LED_8__3(INSTR_led_8__3),
    .LEDsel_9(INSTR_ledsel_9), .LED_9__0(INSTR_led_9__0), .LED_9__1(INSTR_led_9__1),
    .LED_9__2(INSTR_led_9__2), .LED_9__3(INSTR_led_9__3), .LEDsel_A(INSTR_ledsel_a),
    .LED_A__0(INSTR_led_a__0), .LED_A__1(INSTR_led_a__1), .LED_A__2(INSTR_led_a__2),
    .LED_A__3(INSTR_led_a__3), .LEDsel_B(INSTR_ledsel_b), .LED_B__0(INSTR_led_b__0),
    .LED_B__1(INSTR_led_b__1), .LED_B__2(INSTR_led_b__2), .LED_B__3(INSTR_led_b__3),
    .LEDsel_C(INSTR_ledsel_c), .LED_C__0(INSTR_led_c__0), .LED_C__1(INSTR_led_c__1),
    .LED_C__2(INSTR_led_c__2), .LED_C__3(INSTR_led_c__3), .LEDsel_D(INSTR_ledsel_d),
    .LED_D__0(INSTR_led_d__0), .LED_D__1(INSTR_led_d__1), .LED_D__2(INSTR_led_d__2),
    .LED_D__3(INSTR_led_d__3), .LEDsel_E(INSTR_ledsel_e), .LED_E__0(INSTR_led_e__0),
    .LED_E__1(INSTR_led_e__1), .LED_E__2(INSTR_led_e__2), .LED_E__3(INSTR_led_e__3),
    .LEDsel_F(INSTR_ledsel_f), .LED_F__0(INSTR_led_f__0), .LED_F__1(INSTR_led_f__1),
    .LED_F__2(INSTR_led_f__2), .LED_F__3(INSTR_led_f__3));
  LED led_113 (.in(INSTR_ledaddr_1_2));
  LED led_114 (.in(INSTR_ledsel));
  LED led_115 (.in(INSTR_ledw));
  LED led_116 (.in(INSTR_ledrst));
  LED led_117 (.in(INSTR_ledr));
  Reg4 ACC (
    .LED_3(ACC_led_3), .OUT_3(ACC_out_3), .IN_3(RAM_out_3), .read(1'b1), .LEDr(ACC_ledr), .write(acc_w),
    .LEDw(ACC_ledw), .nrst(nrst), .LEDrst(ACC_ledrst), .LED_2(ACC_led_2), .OUT_2(ACC_out_2),
    .IN_2(RAM_out_2), .LED_1(ACC_led_1), .OUT_1(ACC_out_1), .IN_1(RAM_out_1), .LED_0(ACC_led_0),
    .OUT_0(ACC_out_0), .IN_0(RAM_out_0));
  LED led_118 (.in(ACC_ledw));
  LED led_119 (.in(ACC_ledrst));
  LED led_120 (.in(ACC_ledr));
  assign RAM_out_0 = acc_r ? ACC_out_0 : 1'bz;  // Controlled_Buffer controlled_buffer_1
  assign RAM_out_1 = acc_r ? ACC_out_1 : 1'bz;  // Controlled_Buffer controlled_buffer_2
  assign RAM_out_2 = acc_r ? ACC_out_2 : 1'bz;  // Controlled_Buffer controlled_buffer_3
  assign RAM_out_3 = acc_r ? ACC_out_3 : 1'bz;  // Controlled_Buffer controlled_buffer_4
  ControlUnit controlunit_1 (
    .zero(zero4_1_zero), .LEDzero(controlunit_1_ledzero), .LEDinstr0(controlunit_1_ledinstr0),
    .LEDinstr1(controlunit_1_ledinstr1), .LEDinstr2(controlunit_1_ledinstr2),
    .LEDinstr3(controlunit_1_ledinstr3), .clk(clk), .nrst(nrst), .LEDrst(controlunit_1_ledrst),
    .LEDhalt(controlunit_1_ledhalt), .resume(resume), .LEDclk(controlunit_1_ledclk), .INSTR_0(IR_out_0),
    .INSTR_1(IR_out_1), .INSTR_2(IR_out_2), .INSTR_3(IR_out_3), .LEDclkr(controlunit_1_ledclkr),
    .LEDclkw(controlunit_1_ledclkw), .LED16(controlunit_1_led16), .LED15(controlunit_1_led15),
    .LED14(controlunit_1_led14), .LED13(controlunit_1_led13), .LED12(controlunit_1_led12),
    .LED11(controlunit_1_led11), .LED10(controlunit_1_led10), .LED9(controlunit_1_led9),
    .LED8(controlunit_1_led8), .LED7(controlunit_1_led7), .LED6(controlunit_1_led6),
    .LED5(controlunit_1_led5), .LED4(controlunit_1_led4), .LED3(controlunit_1_led3),
    .LED2(controlunit_1_led2), .LED1(controlunit_1_led1), .LED0(controlunit_1_led0), .rom_mar_w(rmar_w),
    .irom_r(irom_r), .drom_r(drom_r), .pc_r(pc_r), .pc_w(pc_w), .ir_w(ir_w), .ram_mar_w(mar_w),
    .ram_r(ram_r), .ram_w(ram_w), .acc_r(acc_r), .acc_w(acc_w), .temp_w(tmp_w), .muxB(muxB), .aluop(op),
    .cin(cin), .res_r(res_r), .res_w(res_w), .LEDstep1(controlunit_1_ledstep1),
    .LEDstep2(controlunit_1_ledstep2), .LEDstep3(controlunit_1_ledstep3), .LEDstep4(controlunit_1_ledstep4),
    .LEDstep5(controlunit_1_ledstep5), .LEDstep6(controlunit_1_ledstep6), .LEDstep7(controlunit_1_ledstep7));
  LED led_121 (.in(controlunit_1_ledhalt));
  LED led_122 (.in(controlunit_1_ledclk));
  LED led_123 (.in(controlunit_1_ledrst));
  LED led_124 (.in(controlunit_1_led16));
  Reg4 ROM_MAR (
    .LED_3(ROM_MAR_led_3), .OUT_3(ROM_MAR_out_3), .IN_3(RAM_out_3), .read(1'b1), .LEDr(ROM_MAR_ledr),
    .write(rmar_w), .LEDw(ROM_MAR_ledw), .nrst(nrst), .LEDrst(ROM_MAR_ledrst), .LED_2(ROM_MAR_led_2),
    .OUT_2(ROM_MAR_out_2), .IN_2(RAM_out_2), .LED_1(ROM_MAR_led_1), .OUT_1(ROM_MAR_out_1), .IN_1(RAM_out_1),
    .LED_0(ROM_MAR_led_0), .OUT_0(ROM_MAR_out_0), .IN_0(RAM_out_0));
  LED led_125 (.in(INSTR_ledaddr_0));
  LED led_126 (.in(INSTR_ledaddr_1));
  LED led_127 (.in(INSTR_ledaddr_0_2));
  LED led_128 (.in(INSTR_ledsel_0));
  LED led_129 (.in(INSTR_ledsel_1));
  LED led_130 (.in(INSTR_ledsel_2));
  LED led_131 (.in(INSTR_ledsel_3));
  LED led_132 (.in(INSTR_ledsel_4));
  LED led_133 (.in(INSTR_ledsel_5));
  LED led_134 (.in(INSTR_ledsel_6));
  LED led_135 (.in(INSTR_ledsel_7));
  LED led_136 (.in(INSTR_ledsel_8));
  LED led_137 (.in(INSTR_ledsel_9));
  LED led_138 (.in(INSTR_ledsel_a));
  LED led_139 (.in(INSTR_ledsel_b));
  LED led_140 (.in(INSTR_ledsel_c));
  LED led_141 (.in(INSTR_ledsel_d));
  LED led_142 (.in(INSTR_ledsel_e));
  LED led_143 (.in(INSTR_ledsel_f));
  HEX_Display hex_display_4 (
    .BIN_0(ACC_led_0), .LED0(hex_display_4_led0), .BIN_1(ACC_led_1), .LED1(hex_display_4_led1),
    .BIN_2(ACC_led_2), .LED2(hex_display_4_led2), .BIN_3(ACC_led_3), .LED3(hex_display_4_led3),
    .HEX3(hex_display_4_hex3), .HEX2(hex_display_4_hex2), .HEX1(hex_display_4_hex1), .HEX0(hex_display_4_hex0));
  LED led_144 (.in(hex_display_4_led2));
  LED led_145 (.in(hex_display_4_led3));
  _7SegDisplay_HEX_Adapter u_7segdisplay_hex_adapter_4 (
    .IN_0(hex_display_4_hex0), .IN_1(hex_display_4_hex1), .IN_2(hex_display_4_hex2),
    .IN_3(hex_display_4_hex3), .a(n7segdisplay_hex_adapter_4_a), .b(n7segdisplay_hex_adapter_4_b),
    .c(n7segdisplay_hex_adapter_4_c), .d(n7segdisplay_hex_adapter_4_d), .e(n7segdisplay_hex_adapter_4_e),
    .f(n7segdisplay_hex_adapter_4_f), .g(n7segdisplay_hex_adapter_4_g), .dp(n7segdisplay_hex_adapter_4_dp));
  _7_Segment_Display u_7_segment_display_4 (
    .g(n7segdisplay_hex_adapter_4_g), .f(n7segdisplay_hex_adapter_4_f), .a(n7segdisplay_hex_adapter_4_a),
    .b(n7segdisplay_hex_adapter_4_b), .e(n7segdisplay_hex_adapter_4_e), .d(n7segdisplay_hex_adapter_4_d),
    .c(n7segdisplay_hex_adapter_4_c), .dp(n7segdisplay_hex_adapter_4_dp));
  Zero4 zero4_1 (._3(ACC_out_3), ._2(ACC_out_2), ._1(ACC_out_1), ._0(ACC_out_0), .zero(zero4_1_zero));
  LED led_146 (.in(controlunit_1_ledclkr));
  LED led_147 (.in(controlunit_1_ledclkw));
  LED led_148 (.in(controlunit_1_led15));
  HEX_Display hex_display_5 (
    .BIN_0(ROM_MAR_led_0), .LED0(hex_display_5_led0), .BIN_1(ROM_MAR_led_1), .LED1(hex_display_5_led1),
    .BIN_2(ROM_MAR_led_2), .LED2(hex_display_5_led2), .BIN_3(ROM_MAR_led_3), .LED3(hex_display_5_led3),
    .HEX3(hex_display_5_hex3), .HEX2(hex_display_5_hex2), .HEX1(hex_display_5_hex1), .HEX0(hex_display_5_hex0));
  LED led_149 (.in(ROM_MAR_ledw));
  LED led_150 (.in(ROM_MAR_ledrst));
  LED led_151 (.in(ROM_MAR_ledr));
  Mux2x4 mux2x4_1 (
    .sel(MANUAL), .a3(ROM_MAR_out_3), .b3(in_1[3]), .out3(mux2x4_1_out3), .a2(ROM_MAR_out_2), .b2(in_1[2]),
    .out2(mux2x4_1_out2), .a1(ROM_MAR_out_1), .b1(in_1[1]), .a0(ROM_MAR_out_0), .b0(in_1[0]),
    .out1(mux2x4_1_out1), .out0(mux2x4_1_out0), .LEDsel(mux2x4_1_ledsel));
  LED led_152 (.in(INSTR_led_0__2));
  LED led_153 (.in(INSTR_led_0__1));
  LED led_154 (.in(INSTR_led_0__3));
  LED led_155 (.in(INSTR_led_1__3));
  LED led_156 (.in(INSTR_led_1__1));
  LED led_157 (.in(INSTR_led_1__2));
  LED led_158 (.in(INSTR_led_2__3));
  LED led_159 (.in(INSTR_led_2__2));
  LED led_160 (.in(INSTR_led_2__1));
  LED led_161 (.in(INSTR_led_3__3));
  LED led_162 (.in(INSTR_led_3__1));
  LED led_163 (.in(INSTR_led_3__2));
  LED led_164 (.in(INSTR_led_4__1));
  LED led_165 (.in(INSTR_led_4__2));
  LED led_166 (.in(INSTR_led_4__3));
  LED led_167 (.in(INSTR_led_5__2));
  LED led_168 (.in(INSTR_led_5__1));
  LED led_169 (.in(INSTR_led_5__3));
  LED led_170 (.in(INSTR_led_6__1));
  LED led_171 (.in(INSTR_led_6__3));
  LED led_172 (.in(INSTR_led_6__2));
  LED led_173 (.in(INSTR_led_7__2));
  LED led_174 (.in(INSTR_led_7__1));
  LED led_175 (.in(INSTR_led_7__3));
  LED led_176 (.in(INSTR_led_8__2));
  LED led_177 (.in(INSTR_led_8__1));
  LED led_178 (.in(INSTR_led_8__3));
  LED led_179 (.in(INSTR_led_9__1));
  LED led_180 (.in(INSTR_led_9__2));
  LED led_181 (.in(INSTR_led_9__3));
  LED led_182 (.in(INSTR_led_a__3));
  LED led_183 (.in(INSTR_led_a__2));
  LED led_184 (.in(INSTR_led_a__1));
  LED led_185 (.in(INSTR_led_b__1));
  LED led_186 (.in(INSTR_led_b__2));
  LED led_187 (.in(INSTR_led_b__3));
  LED led_188 (.in(INSTR_led_c__3));
  LED led_189 (.in(INSTR_led_c__1));
  LED led_190 (.in(INSTR_led_c__2));
  LED led_191 (.in(INSTR_led_d__2));
  LED led_192 (.in(INSTR_led_d__1));
  LED led_193 (.in(INSTR_led_d__3));
  LED led_194 (.in(INSTR_led_e__3));
  LED led_195 (.in(INSTR_led_e__2));
  LED led_196 (.in(INSTR_led_e__1));
  LED led_197 (.in(INSTR_led_f__3));
  LED led_198 (.in(INSTR_led_f__1));
  LED led_199 (.in(INSTR_led_f__2));
  LED led_200 (.in(hex_display_4_led0));
  LED led_201 (.in(hex_display_4_led1));
  LED led_202 (.in(controlunit_1_led13));
  LED led_203 (.in(controlunit_1_led14));
  LED led_204 (.in(hex_display_5_led2));
  LED led_205 (.in(hex_display_5_led3));
  LED led_206 (.in(hex_display_5_led1));
  LED led_207 (.in(hex_display_5_led0));
  _7SegDisplay_HEX_Adapter u_7segdisplay_hex_adapter_5 (
    .IN_0(hex_display_5_hex0), .IN_1(hex_display_5_hex1), .IN_2(hex_display_5_hex2),
    .IN_3(hex_display_5_hex3), .a(n7segdisplay_hex_adapter_5_a), .b(n7segdisplay_hex_adapter_5_b),
    .c(n7segdisplay_hex_adapter_5_c), .d(n7segdisplay_hex_adapter_5_d), .e(n7segdisplay_hex_adapter_5_e),
    .f(n7segdisplay_hex_adapter_5_f), .g(n7segdisplay_hex_adapter_5_g), .dp(n7segdisplay_hex_adapter_5_dp));
  _7_Segment_Display u_7_segment_display_5 (
    .g(n7segdisplay_hex_adapter_5_g), .f(n7segdisplay_hex_adapter_5_f), .a(n7segdisplay_hex_adapter_5_a),
    .b(n7segdisplay_hex_adapter_5_b), .e(n7segdisplay_hex_adapter_5_e), .d(n7segdisplay_hex_adapter_5_d),
    .c(n7segdisplay_hex_adapter_5_c), .dp(n7segdisplay_hex_adapter_5_dp));
  LED led_208 (.in(mux2x4_1_ledsel));
  LED led_209 (.in(INSTR_led_0__0));
  LED led_210 (.in(INSTR_led_1__0));
  LED led_211 (.in(INSTR_led_2__0));
  LED led_212 (.in(INSTR_led_3__0));
  LED led_213 (.in(INSTR_led_4__0));
  LED led_214 (.in(INSTR_led_5__0));
  LED led_215 (.in(INSTR_led_6__0));
  LED led_216 (.in(INSTR_led_7__0));
  LED led_217 (.in(INSTR_led_8__0));
  LED led_218 (.in(INSTR_led_9__0));
  LED led_219 (.in(INSTR_led_a__0));
  LED led_220 (.in(INSTR_led_b__0));
  LED led_221 (.in(INSTR_led_c__0));
  LED led_222 (.in(INSTR_led_d__0));
  LED led_223 (.in(INSTR_led_e__0));
  LED led_224 (.in(INSTR_led_f__0));
  LED led_225 (.in(controlunit_1_led12));
  SRAM_16x4bit DATA (
    .read(drom_r), .write(rom_w), .nrst(nrom_rst), .LEDsel_0(DATA_ledsel_0), .LED_0__0(DATA_led_0__0),
    .LED_0__1(DATA_led_0__1), .LED_0__2(DATA_led_0__2), .LED_0__3(DATA_led_0__3), .LEDsel_1(DATA_ledsel_1),
    .LED_1__0(DATA_led_1__0), .LED_1__1(DATA_led_1__1), .LED_1__2(DATA_led_1__2), .LED_1__3(DATA_led_1__3),
    .LEDsel_2(DATA_ledsel_2), .LED_2__0(DATA_led_2__0), .LED_2__1(DATA_led_2__1), .LED_2__2(DATA_led_2__2),
    .LED_2__3(DATA_led_2__3), .LEDsel_3(DATA_ledsel_3), .LED_3__0(DATA_led_3__0), .LED_3__1(DATA_led_3__1),
    .LED_3__2(DATA_led_3__2), .LED_3__3(DATA_led_3__3), .LEDsel_4(DATA_ledsel_4), .LED_4__0(DATA_led_4__0),
    .LED_4__1(DATA_led_4__1), .LED_4__2(DATA_led_4__2), .LED_4__3(DATA_led_4__3), .LEDsel_5(DATA_ledsel_5),
    .LED_5__0(DATA_led_5__0), .LED_5__1(DATA_led_5__1), .LED_5__2(DATA_led_5__2), .LED_5__3(DATA_led_5__3),
    .LEDsel_6(DATA_ledsel_6), .LED_6__0(DATA_led_6__0), .LED_6__1(DATA_led_6__1), .LED_6__2(DATA_led_6__2),
    .LED_6__3(DATA_led_6__3), .LEDsel_7(DATA_ledsel_7), .LED_7__0(DATA_led_7__0), .LED_7__1(DATA_led_7__1),
    .LED_7__2(DATA_led_7__2), .LED_7__3(DATA_led_7__3), .LEDr(DATA_ledr), .LEDw(DATA_ledw),
    .LEDrst(DATA_ledrst), .ADDR_3(mux2x4_1_out3), .ADDR_2(mux2x4_1_out2), .ADDR_1(mux2x4_1_out1),
    .ADDR_0(mux2x4_1_out0), .select(1'b1), .IN_3(in_3[3]), .IN_2(in_3[2]), .IN_1(in_3[1]), .IN_0(in_3[0]),
    .LEDaddr_1_2(DATA_ledaddr_1_2), .LEDaddr_0_2(DATA_ledaddr_0_2), .LEDaddr_1(DATA_ledaddr_1),
    .LEDaddr_0(DATA_ledaddr_0), .LEDsel(DATA_ledsel), .OUT_3(RAM_out_3), .OUT_2(RAM_out_2),
    .OUT_1(RAM_out_1), .OUT_0(RAM_out_0), .LEDsel_8(DATA_ledsel_8), .LED_8__0(DATA_led_8__0),
    .LED_8__1(DATA_led_8__1), .LED_8__2(DATA_led_8__2), .LED_8__3(DATA_led_8__3), .LEDsel_9(DATA_ledsel_9),
    .LED_9__0(DATA_led_9__0), .LED_9__1(DATA_led_9__1), .LED_9__2(DATA_led_9__2), .LED_9__3(DATA_led_9__3),
    .LEDsel_A(DATA_ledsel_a), .LED_A__0(DATA_led_a__0), .LED_A__1(DATA_led_a__1), .LED_A__2(DATA_led_a__2),
    .LED_A__3(DATA_led_a__3), .LEDsel_B(DATA_ledsel_b), .LED_B__0(DATA_led_b__0), .LED_B__1(DATA_led_b__1),
    .LED_B__2(DATA_led_b__2), .LED_B__3(DATA_led_b__3), .LEDsel_C(DATA_ledsel_c), .LED_C__0(DATA_led_c__0),
    .LED_C__1(DATA_led_c__1), .LED_C__2(DATA_led_c__2), .LED_C__3(DATA_led_c__3), .LEDsel_D(DATA_ledsel_d),
    .LED_D__0(DATA_led_d__0), .LED_D__1(DATA_led_d__1), .LED_D__2(DATA_led_d__2), .LED_D__3(DATA_led_d__3),
    .LEDsel_E(DATA_ledsel_e), .LED_E__0(DATA_led_e__0), .LED_E__1(DATA_led_e__1), .LED_E__2(DATA_led_e__2),
    .LED_E__3(DATA_led_e__3), .LEDsel_F(DATA_ledsel_f), .LED_F__0(DATA_led_f__0), .LED_F__1(DATA_led_f__1),
    .LED_F__2(DATA_led_f__2), .LED_F__3(DATA_led_f__3));
  Reg4 IR (
    .LED_3(IR_led_3), .OUT_3(IR_out_3), .IN_3(RAM_out_3), .read(1'b1), .LEDr(IR_ledr), .write(ir_w),
    .LEDw(IR_ledw), .nrst(nrst), .LEDrst(IR_ledrst), .LED_2(IR_led_2), .OUT_2(IR_out_2), .IN_2(RAM_out_2),
    .LED_1(IR_led_1), .OUT_1(IR_out_1), .IN_1(RAM_out_1), .LED_0(IR_led_0), .OUT_0(IR_out_0), .IN_0(RAM_out_0));
  LED led_226 (.in(controlunit_1_led11));
  LED led_227 (.in(controlunit_1_led10));
  LED led_228 (.in(DATA_ledaddr_1_2));
  LED led_229 (.in(DATA_ledaddr_0_2));
  LED led_230 (.in(DATA_ledaddr_1));
  LED led_231 (.in(DATA_ledsel_0));
  LED led_232 (.in(DATA_ledsel));
  LED led_233 (.in(DATA_ledsel_1));
  LED led_234 (.in(DATA_ledw));
  LED led_235 (.in(DATA_ledsel_2));
  LED led_236 (.in(DATA_ledrst));
  LED led_237 (.in(DATA_ledr));
  LED led_238 (.in(DATA_ledsel_3));
  LED led_239 (.in(DATA_ledsel_4));
  LED led_240 (.in(DATA_ledsel_5));
  LED led_241 (.in(DATA_ledsel_6));
  LED led_242 (.in(DATA_ledsel_7));
  LED led_243 (.in(DATA_ledsel_8));
  LED led_244 (.in(DATA_ledsel_9));
  LED led_245 (.in(DATA_ledsel_a));
  LED led_246 (.in(DATA_ledsel_b));
  LED led_247 (.in(DATA_ledsel_c));
  LED led_248 (.in(DATA_ledsel_d));
  LED led_249 (.in(DATA_ledsel_e));
  LED led_250 (.in(DATA_ledsel_f));
  BIN_Display bin_display_1 (
    .IN_0(IR_led_0), .IN_1(IR_led_1), .IN_2(IR_led_2), .IN_3(IR_led_3), .LED0(bin_display_1_led0),
    .LED1(bin_display_1_led1), .LED2(bin_display_1_led2), .LED3(bin_display_1_led3));
  LED led_251 (.in(IR_ledw));
  LED led_252 (.in(IR_ledrst));
  LED led_253 (.in(IR_ledr));
  LED led_254 (.in(controlunit_1_ledzero));
  LED led_255 (.in(controlunit_1_ledstep1));
  LED led_256 (.in(controlunit_1_ledstep3));
  LED led_257 (.in(controlunit_1_ledstep2));
  LED led_258 (.in(controlunit_1_led9));
  LED led_259 (.in(controlunit_1_led8));
  LED led_260 (.in(DATA_ledaddr_0));
  LED led_261 (.in(DATA_led_0__3));
  LED led_262 (.in(DATA_led_1__3));
  LED led_263 (.in(DATA_led_2__3));
  LED led_264 (.in(DATA_led_3__3));
  LED led_265 (.in(DATA_led_4__3));
  LED led_266 (.in(DATA_led_5__3));
  LED led_267 (.in(DATA_led_6__3));
  LED led_268 (.in(DATA_led_7__3));
  LED led_269 (.in(DATA_led_8__3));
  LED led_270 (.in(DATA_led_9__3));
  LED led_271 (.in(DATA_led_a__3));
  LED led_272 (.in(DATA_led_b__3));
  LED led_273 (.in(DATA_led_c__3));
  LED led_274 (.in(DATA_led_d__3));
  LED led_275 (.in(DATA_led_e__3));
  LED led_276 (.in(DATA_led_f__3));
  LED led_277 (.in(bin_display_1_led0));
  LED led_278 (.in(bin_display_1_led3));
  LED led_279 (.in(bin_display_1_led1));
  LED led_280 (.in(bin_display_1_led2));
  LED led_281 (.in(controlunit_1_ledinstr0));
  LED led_282 (.in(controlunit_1_ledinstr1));
  LED led_283 (.in(controlunit_1_ledinstr2));
  LED led_284 (.in(controlunit_1_ledinstr3));
  LED led_285 (.in(controlunit_1_ledstep5));
  LED led_286 (.in(controlunit_1_ledstep6));
  LED led_287 (.in(controlunit_1_ledstep7));
  LED led_288 (.in(controlunit_1_ledstep4));
  LED led_289 (.in(controlunit_1_led7));
  LED led_290 (.in(DATA_led_0__2));
  LED led_291 (.in(DATA_led_0__1));
  LED led_292 (.in(DATA_led_0__0));
  LED led_293 (.in(DATA_led_1__0));
  LED led_294 (.in(DATA_led_1__1));
  LED led_295 (.in(DATA_led_1__2));
  LED led_296 (.in(DATA_led_2__1));
  LED led_297 (.in(DATA_led_2__0));
  LED led_298 (.in(DATA_led_2__2));
  LED led_299 (.in(DATA_led_3__0));
  LED led_300 (.in(DATA_led_3__1));
  LED led_301 (.in(DATA_led_3__2));
  LED led_302 (.in(DATA_led_4__1));
  LED led_303 (.in(DATA_led_4__0));
  LED led_304 (.in(DATA_led_4__2));
  LED led_305 (.in(DATA_led_5__1));
  LED led_306 (.in(DATA_led_5__0));
  LED led_307 (.in(DATA_led_5__2));
  LED led_308 (.in(DATA_led_6__1));
  LED led_309 (.in(DATA_led_6__2));
  LED led_310 (.in(DATA_led_6__0));
  LED led_311 (.in(DATA_led_7__1));
  LED led_312 (.in(DATA_led_7__0));
  LED led_313 (.in(DATA_led_7__2));
  LED led_314 (.in(DATA_led_8__2));
  LED led_315 (.in(DATA_led_8__0));
  LED led_316 (.in(DATA_led_8__1));
  LED led_317 (.in(DATA_led_9__1));
  LED led_318 (.in(DATA_led_9__2));
  LED led_319 (.in(DATA_led_9__0));
  LED led_320 (.in(DATA_led_a__1));
  LED led_321 (.in(DATA_led_a__2));
  LED led_322 (.in(DATA_led_a__0));
  LED led_323 (.in(DATA_led_b__1));
  LED led_324 (.in(DATA_led_b__0));
  LED led_325 (.in(DATA_led_b__2));
  LED led_326 (.in(DATA_led_c__2));
  LED led_327 (.in(DATA_led_c__1));
  LED led_328 (.in(DATA_led_c__0));
  LED led_329 (.in(DATA_led_d__1));
  LED led_330 (.in(DATA_led_d__0));
  LED led_331 (.in(DATA_led_d__2));
  LED led_332 (.in(DATA_led_e__0));
  LED led_333 (.in(DATA_led_e__2));
  LED led_334 (.in(DATA_led_e__1));
  LED led_335 (.in(DATA_led_f__1));
  LED led_336 (.in(DATA_led_f__0));
  LED led_337 (.in(DATA_led_f__2));
  LED led_338 (.in(controlunit_1_led6));
  LED led_339 (.in(controlunit_1_led5));
  LED led_340 (.in(controlunit_1_led4));
  Reg4 PC (
    .LED_3(PC_led_3), .OUT_3(RAM_out_3), .IN_3(RAM_out_3), .read(pc_r), .LEDr(PC_ledr), .write(pc_w),
    .LEDw(PC_ledw), .nrst(nrst), .LEDrst(PC_ledrst), .LED_2(PC_led_2), .OUT_2(RAM_out_2), .IN_2(RAM_out_2),
    .LED_1(PC_led_1), .OUT_1(RAM_out_1), .IN_1(RAM_out_1), .LED_0(PC_led_0), .OUT_0(RAM_out_0),
    .IN_0(RAM_out_0));
  LED led_341 (.in(PC_ledw));
  LED led_342 (.in(PC_ledrst));
  LED led_343 (.in(PC_ledr));
  LED led_344 (.in(controlunit_1_led3));
  LED led_345 (.in(controlunit_1_led2));
  HEX_Display hex_display_6 (
    .BIN_0(PC_led_0), .LED0(hex_display_6_led0), .BIN_1(PC_led_1), .LED1(hex_display_6_led1),
    .BIN_2(PC_led_2), .LED2(hex_display_6_led2), .BIN_3(PC_led_3), .LED3(hex_display_6_led3),
    .HEX3(hex_display_6_hex3), .HEX2(hex_display_6_hex2), .HEX1(hex_display_6_hex1), .HEX0(hex_display_6_hex0));
  LED led_346 (.in(hex_display_6_led2));
  LED led_347 (.in(hex_display_6_led3));
  LED led_348 (.in(hex_display_6_led1));
  _7SegDisplay_HEX_Adapter u_7segdisplay_hex_adapter_6 (
    .IN_0(hex_display_6_hex0), .IN_1(hex_display_6_hex1), .IN_2(hex_display_6_hex2),
    .IN_3(hex_display_6_hex3), .a(n7segdisplay_hex_adapter_6_a), .b(n7segdisplay_hex_adapter_6_b),
    .c(n7segdisplay_hex_adapter_6_c), .d(n7segdisplay_hex_adapter_6_d), .e(n7segdisplay_hex_adapter_6_e),
    .f(n7segdisplay_hex_adapter_6_f), .g(n7segdisplay_hex_adapter_6_g), .dp(n7segdisplay_hex_adapter_6_dp));
  _7_Segment_Display u_7_segment_display_6 (
    .g(n7segdisplay_hex_adapter_6_g), .f(n7segdisplay_hex_adapter_6_f), .a(n7segdisplay_hex_adapter_6_a),
    .b(n7segdisplay_hex_adapter_6_b), .e(n7segdisplay_hex_adapter_6_e), .d(n7segdisplay_hex_adapter_6_d),
    .c(n7segdisplay_hex_adapter_6_c), .dp(n7segdisplay_hex_adapter_6_dp));
  LED led_349 (.in(controlunit_1_led1));
  LED led_350 (.in(controlunit_1_led0));
  LED led_351 (.in(hex_display_6_led0));
  Clock_part CLOCK (.out(CLOCK_out));
  Button WRITE_ROM (.out(WRITE_ROM_out));
  Button RESET_ROM (.out(RESET_ROM_out));
  Button RESET (.out(RESET_out));
  Button u_RESUME (.out(resume));
  and and_1 (clk, CLOCK_out, ~MANUAL);  // AND_Gate
  and and_2 (rom_w, MANUAL, WRITE_ROM_out);
  and and_3 (nrom_rst, ~RESET_ROM_out, ON);  // AND_Gate
  and and_4 (nrst, ~RESET_out, ON);  // AND_Gate

  // Other names for the same wires on the sheet: muxROM = MANUAL; romADDR[3:0] = in_1; romDATA[3:0] = in_3;
  //   romINSTR[3:0] = in_2

  // Notes on the sheet:
  //   0000 imm  -  add  imm   -  ACC = ACC +  imm
  //   0001 imm  -  add [imm]  -  ACC = ACC + [imm]
  //   0010 imm  -  sub  imm   -  ACC = ACC -  imm
  //   0011 imm  -  sub [imm]  -  ACC = ACC - [imm]
  //   0100 imm  -  mov  imm   -  ACC =  imm
  //   0101 imm  -  ld  [imm]  -  ACC = [imm]
  //   011x imm  -  str [imm]  -  [imm] = ACC
  //   1000 imm  -  bz   imm   -  if ACC == 0: PC =  imm
  //   1001 imm  -  bz  [imm]  -  if ACC == 0: PC = [imm]
  //   1100 imm  -  bnz  imm   -  if ACC != 0: PC =  imm
  //   1101 imm  -  bnz [imm]  -  if ACC != 0: PC = [imm]
  //   1100 imm  -  jmp  imm   -  PC =  imm
  //   1101 imm  -  jmp [imm]  -  PC = [imm]
  //   111x imm  -  halt       -  ignore clock
endmodule

module ControlUnit (
  input  INSTR_0,
  input  INSTR_1,
  input  INSTR_2,
  input  INSTR_3,
  input  zero,
  input  resume,
  input  clk,
  input  nrst,
  output LEDinstr0,
  output LEDinstr1,
  output LEDinstr2,
  output LEDinstr3,
  output LEDzero,
  output LEDstep1,
  output LEDstep2,
  output LEDstep3,
  output LEDclk,
  output LEDstep4,
  output LEDstep5,
  output LEDstep6,
  output LEDstep7,
  output LEDhalt,
  output LEDclkr,
  output LEDclkw,
  output LEDrst,
  output LED16,
  output LED15,
  output LED14,
  output LED13,
  output LED12,
  output LED11,
  output LED10,
  output LED9,
  output LED8,
  output LED7,
  output LED6,
  output LED5,
  output LED4,
  output LED3,
  output LED2,
  output LED1,
  output LED0,
  output rom_mar_w,
  output irom_r,
  output drom_r,
  output pc_r,
  output pc_w,
  output ir_w,
  output ram_mar_w,
  output ram_r,
  output ram_w,
  output acc_r,
  output acc_w,
  output temp_w,
  output muxB,
  output aluop,
  output cin,
  output res_r,
  output res_w
);

  wire and_1_out, and_2_out, and_3_out, and_6_out, and_9_out, and_11_out, and_12_out, and_13_out, and_16_out,
       and_18_out, and_19_out, and_21_out, and_23_out, and_24_out, and_26_out, and_27_out, and_29_out,
       and_30_out, and_32_out, and_33_out, and_35_out, and_36_out, and_38_out, and_39_out,
       clocklogic_1_clk_out, nor_1_out, or_1_out, or_2_out, or_3_out, or_4_out, or_5_out, or_6_out, or_7_out;

  ClockLogic clocklogic_1 (
    .clk(clk), .halt(and_3_out), .resume(resume), .nrst(nrst), .clk_out(clocklogic_1_clk_out),
    .halt_out(LEDhalt));
  Stepper7 stepper7_1 (
    .clk(LEDclk), .nrst(nrst), .step1(LEDstep1), .step2(cin), .step3(LEDstep3), .step4(LEDstep4),
    .step5(LEDstep5), .step6(LEDstep6), .step7(LEDstep7));
  Clock clock_1 (.clk(clocklogic_1_clk_out), .nrst(nrst), .clk_r(LEDclkr), .clk_w(LEDclkw), .clk_out(LEDclk));
  and and_1 (and_1_out, INSTR_3, INSTR_2, INSTR_1);
  and and_2 (and_2_out, LEDstep7, and_1_out);
  and and_3 (and_3_out, and_2_out, nor_1_out);
  nor nor_1 (nor_1_out, LEDclkw, LEDclkr);
  and and_4 (LED16, LEDclkw, LEDstep1);
  and and_5 (irom_r, LEDclkr, cin);
  and and_6 (and_6_out, LEDstep6, ~INSTR_0);  // AND_Gate
  or or_1 (or_1_out, LEDstep4, and_6_out);
  and and_7 (drom_r, LEDclkr, or_1_out);
  and and_8 (LED13, LEDclkr, LEDstep1);
  and and_9 (and_9_out, INSTR_3, ~INSTR_2, ~INSTR_1, zero);  // AND_Gate
  and and_10 (LED12, LEDclkw, or_3_out);
  and and_11 (and_11_out, INSTR_3, ~INSTR_2, INSTR_1, ~zero);  // AND_Gate
  or or_2 (or_2_out, and_9_out, and_11_out, and_13_out);
  and and_12 (and_12_out, LEDstep6, or_2_out);
  or or_3 (or_3_out, LEDstep3, and_12_out);
  and and_13 (and_13_out, INSTR_3, INSTR_2, ~INSTR_1);  // AND_Gate
  and and_14 (ir_w, LEDclkw, cin);
  and and_15 (LED10, LEDclkw, LEDstep4);
  and and_16 (and_16_out, LEDstep6, INSTR_0);
  and and_17 (LED9, LEDclkr, and_16_out);
  and and_18 (and_18_out, ~INSTR_3, INSTR_2, INSTR_1);  // AND_Gate
  and and_19 (and_19_out, LEDstep5, and_18_out);
  and and_20 (LED8, LEDclkw, and_19_out);
  and and_21 (and_21_out, LEDstep5, ~INSTR_3);  // AND_Gate
  and and_22 (acc_r, LEDclkr, and_21_out);
  and and_23 (and_23_out, ~INSTR_3, ~INSTR_2);  // AND_Gate
  and and_24 (and_24_out, LEDstep7, and_23_out);
  or or_4 (or_4_out, and_24_out, and_27_out);
  and and_25 (acc_w, LEDclkw, or_4_out);
  and and_26 (and_26_out, ~INSTR_3, INSTR_2, ~INSTR_1);  // AND_Gate
  and and_27 (and_27_out, LEDstep6, and_26_out);
  or or_5 (or_5_out, LEDstep1, and_30_out);
  and and_28 (LED5, LEDclkw, or_5_out);
  and and_29 (and_29_out, ~INSTR_3, ~INSTR_2);  // AND_Gate
  and and_30 (and_30_out, LEDstep5, and_29_out);
  and and_31 (LED4, LEDclkr, and_33_out);
  and and_32 (and_32_out, ~INSTR_3, ~INSTR_2);  // AND_Gate
  and and_33 (and_33_out, LEDstep6, and_32_out);
  and and_34 (aluop, LEDstep6, INSTR_1);
  and and_35 (and_35_out, ~INSTR_3, ~INSTR_2);  // AND_Gate
  and and_36 (and_36_out, LEDstep7, and_35_out);
  or or_6 (or_6_out, LEDstep3, and_36_out);
  and and_37 (LED1, LEDclkr, or_6_out);
  and and_38 (and_38_out, ~INSTR_3, ~INSTR_2);  // AND_Gate
  and and_39 (and_39_out, LEDstep6, and_38_out);
  or or_7 (or_7_out, cin, and_39_out);
  and and_40 (LED0, LEDclkw, or_7_out);

  assign LED2 = cin;
  assign LED3 = aluop;
  assign LED6 = acc_w;
  assign LED7 = acc_r;
  assign LED11 = ir_w;
  assign LED14 = drom_r;
  assign LED15 = irom_r;
  assign LEDinstr0 = INSTR_0;
  assign LEDinstr1 = INSTR_1;
  assign LEDinstr2 = INSTR_2;
  assign LEDinstr3 = INSTR_3;
  assign LEDrst = nrst;
  assign LEDstep2 = cin;
  assign LEDzero = zero;
  assign muxB = LED4;
  assign pc_r = LED13;
  assign pc_w = LED12;
  assign ram_mar_w = LED10;
  assign ram_r = LED9;
  assign ram_w = LED8;
  assign res_r = LED1;
  assign res_w = LED0;
  assign rom_mar_w = LED16;
  assign temp_w = LED5;
endmodule

module ClockLogic (
  input  clk,
  input  halt,
  input  resume,
  input  nrst,
  output clk_out,
  output halt_out
);

  wire and_1_out, and_2_out, and_3_out, and_4_out, d_flipflop_1_nq, d_flipflop_2_nq, d_flipflop_3_nq,
       d_flipflop_3_q;

  D_FlipFlop d_flipflop_1 (.clk(resume), .D(1'b1), .nrst(and_1_out), .nQ(d_flipflop_1_nq));  // open: Q
  and and_1 (and_1_out, nrst, d_flipflop_1_nq);
  D_FlipFlop d_flipflop_2 (.clk(halt), .D(1'b1), .nrst(and_2_out), .Q(halt_out), .nQ(d_flipflop_2_nq));
  and and_2 (and_2_out, d_flipflop_1_nq, nrst);
  and and_3 (and_3_out, d_flipflop_3_nq, ~clk);  // AND_Gate
  D_FlipFlop d_flipflop_3 (.clk(and_3_out), .D(1'b1), .nrst(and_4_out), .Q(d_flipflop_3_q), .nQ(d_flipflop_3_nq));
  and and_4 (and_4_out, d_flipflop_1_nq, nrst);
  and and_5 (clk_out, clk, d_flipflop_2_nq, d_flipflop_3_q);
endmodule

module Clock (
  input  clk,
  input  nrst,
  output clk_r,
  output clk_w,
  output clk_out
);

  wire and_1_out, and_2_out, or_1_out, or_2_out, reset_logic_nq, reset_logic_q, state_nq;

  and and_1 (and_1_out, clk, reset_logic_nq);
  _8bitLA_D_FlipFlop reset_logic (.clk(and_1_out), .D(1'b1), .nrst(nrst), .Q(reset_logic_q), .nQ(reset_logic_nq));
  and and_2 (and_2_out, clk, reset_logic_q);
  _8bitLA_D_FlipFlop state (.clk(and_2_out), .D(state_nq), .nrst(nrst), .Q(clk_out), .nQ(state_nq));
  or or_1 (or_1_out, and_2_out, clk_out);
  buf buffer_1 (clk_r, or_1_out);
  not not_1 (clk_w, or_2_out);
  or or_2 (or_2_out, state_nq, and_2_out);
endmodule

module Stepper7 (
  input  clk,
  input  nrst,
  output step1,
  output step2,
  output step3,
  output step4,
  output step5,
  output step6,
  output step7
);

  wire d_latch_1_q, d_latch_2_q, d_latch_3_nq, d_latch_3_q, d_latch_4_q, d_latch_5_nq, d_latch_5_q,
       d_latch_6_q, d_latch_7_nq, d_latch_7_q, d_latch_8_q, d_latch_9_nq, d_latch_9_q, d_latch_10_q,
       d_latch_11_nq, d_latch_11_q, d_latch_12_nq, d_latch_12_q, d_latch_13_q, d_latch_14_q, d_latch_15_nq,
       d_latch_15_q, not_1_out, not_2_out, or_1_out, or_2_out;

  not not_1 (not_1_out, clk);
  or or_1 (or_1_out, d_latch_15_q, not_1_out);
  or or_2 (or_2_out, clk, d_latch_15_q);
  not not_2 (not_2_out, d_latch_15_q);
  _8bitLA_D_Latch d_latch_1 (.D(not_2_out), .write(or_2_out), .nrst(nrst), .Q(d_latch_1_q));  // open: nQ
  _8bitLA_D_Latch d_latch_2 (.D(d_latch_1_q), .write(or_1_out), .nrst(nrst), .Q(d_latch_2_q));  // open: nQ
  _8bitLA_D_Latch d_latch_3 (.D(d_latch_2_q), .write(or_2_out), .nrst(nrst), .Q(d_latch_3_q), .nQ(d_latch_3_nq));
  and and_1 (step1, d_latch_1_q, d_latch_3_nq);
  _8bitLA_D_Latch d_latch_4 (.D(d_latch_3_q), .write(or_1_out), .nrst(nrst), .Q(d_latch_4_q));  // open: nQ
  _8bitLA_D_Latch d_latch_5 (.D(d_latch_4_q), .write(or_2_out), .nrst(nrst), .Q(d_latch_5_q), .nQ(d_latch_5_nq));
  and and_2 (step2, d_latch_3_q, d_latch_5_nq);
  _8bitLA_D_Latch d_latch_6 (.D(d_latch_5_q), .write(or_1_out), .nrst(nrst), .Q(d_latch_6_q));  // open: nQ
  and and_3 (step3, d_latch_5_q, d_latch_7_nq);
  _8bitLA_D_Latch d_latch_7 (.D(d_latch_6_q), .write(or_2_out), .nrst(nrst), .Q(d_latch_7_q), .nQ(d_latch_7_nq));
  _8bitLA_D_Latch d_latch_8 (.D(d_latch_7_q), .write(or_1_out), .nrst(nrst), .Q(d_latch_8_q));  // open: nQ
  and and_4 (step4, d_latch_7_q, d_latch_9_nq);
  _8bitLA_D_Latch d_latch_9 (.D(d_latch_8_q), .write(or_2_out), .nrst(nrst), .Q(d_latch_9_q), .nQ(d_latch_9_nq));
  _8bitLA_D_Latch d_latch_10 (.D(d_latch_9_q), .write(or_1_out), .nrst(nrst), .Q(d_latch_10_q));  // open: nQ
  and and_5 (step5, d_latch_9_q, d_latch_11_nq);
  _8bitLA_D_Latch d_latch_11 (.D(d_latch_10_q), .write(or_2_out), .nrst(nrst), .Q(d_latch_11_q), .nQ(d_latch_11_nq));
  _8bitLA_D_Latch d_latch_12 (.D(d_latch_13_q), .write(or_2_out), .nrst(nrst), .Q(d_latch_12_q), .nQ(d_latch_12_nq));
  _8bitLA_D_Latch d_latch_13 (.D(d_latch_11_q), .write(or_1_out), .nrst(nrst), .Q(d_latch_13_q));  // open: nQ
  and and_6 (step6, d_latch_11_q, d_latch_12_nq);
  _8bitLA_D_Latch d_latch_14 (.D(d_latch_12_q), .write(or_1_out), .nrst(nrst), .Q(d_latch_14_q));  // open: nQ
  _8bitLA_D_Latch d_latch_15 (.D(d_latch_14_q), .write(or_2_out), .nrst(nrst), .Q(d_latch_15_q), .nQ(d_latch_15_nq));
  and and_7 (step7, d_latch_12_q, d_latch_15_nq);
endmodule

module FullAdder (
  input  a,
  input  b,
  input  cin,
  output sum,
  output cout
);

  wire and_1_out, and_2_out, xor_1_out;

  xor xor_1 (xor_1_out, a, b);
  and and_1 (and_1_out, xor_1_out, cin);
  and and_2 (and_2_out, a, b);
  xor xor_2 (sum, xor_1_out, cin);
  or or_1 (cout, and_1_out, and_2_out);
endmodule

module Add4 (
  input  a3,
  input  b3,
  input  a2,
  input  b2,
  input  a1,
  input  b1,
  input  a0,
  input  b0,
  input  cin,
  output cout,
  output sum_3,
  output sum_2,
  output sum_1,
  output sum_0
);

  wire fulladder_2_cout, fulladder_3_cout, fulladder_4_cout;

  FullAdder fulladder_1 (.a(a3), .b(b3), .cin(fulladder_2_cout), .sum(sum_3), .cout(cout));
  FullAdder fulladder_2 (.a(a2), .b(b2), .cin(fulladder_3_cout), .sum(sum_2), .cout(fulladder_2_cout));
  FullAdder fulladder_3 (.a(a1), .b(b1), .cin(fulladder_4_cout), .sum(sum_1), .cout(fulladder_3_cout));
  FullAdder fulladder_4 (.a(a0), .b(b0), .cin(cin), .sum(sum_0), .cout(fulladder_4_cout));
endmodule

module Inc4 (
  input  cin,
  input  in0,
  input  in1,
  input  in2,
  input  in3,
  output out0,
  output out1,
  output out2,
  output cout,
  output out3
);

  wire and_1_out, and_2_out, and_3_out;

  and and_1 (and_1_out, in0, cin);
  xor xor_1 (out0, in0, cin);
  and and_2 (and_2_out, in1, and_1_out);
  xor xor_2 (out1, in1, and_1_out);
  and and_3 (and_3_out, in2, and_2_out);
  xor xor_3 (out2, in2, and_2_out);
  and and_4 (cout, in3, and_3_out);
  xor xor_4 (out3, in3, and_3_out);
endmodule

module Inverter4 (
  input  in_3,
  input  in_2,
  input  in_1,
  input  in_0,
  input  inv,
  output out_3,
  output out_2,
  output out_1,
  output out_0
);

  xor xor_1 (out_3, inv, in_3);
  xor xor_2 (out_2, inv, in_2);
  xor xor_3 (out_1, inv, in_1);
  xor xor_4 (out_0, inv, in_0);
endmodule

module Zero4 (
  input  _3,
  input  _2,
  input  _1,
  input  _0,
  output zero
);

  wire or_1_out, or_2_out;

  or or_1 (or_1_out, _3, _2);
  or or_2 (or_2_out, _1, _0);
  nor nor_1 (zero, or_2_out, or_1_out);
endmodule

module ALU_2 (
  input  a_0,
  input  b_0,
  input  a_1,
  input  b_1,
  input  a_2,
  input  b_2,
  input  a_3,
  input  b_3,
  input  op,
  input  cin,
  output LEDop,
  output LEDcin,
  output sum_0,
  output sum_1,
  output sum_2,
  output sum_3
);

  wire inverter4_1_out_0, inverter4_1_out_1, inverter4_1_out_2, inverter4_1_out_3, xor_1_out;

  Add4 add4_1 (
    .cin(xor_1_out), .a3(a_3), .b3(inverter4_1_out_3), .a2(a_2), .b2(inverter4_1_out_2), .a1(a_1),
    .b1(inverter4_1_out_1), .a0(a_0), .b0(inverter4_1_out_0), .sum_3(sum_3), .sum_2(sum_2), .sum_1(sum_1),
    .sum_0(sum_0));  // open: cout
  Inverter4 inverter4_1 (
    .inv(op), .in_3(b_3), .in_2(b_2), .in_1(b_1), .in_0(b_0), .out_3(inverter4_1_out_3),
    .out_2(inverter4_1_out_2), .out_1(inverter4_1_out_1), .out_0(inverter4_1_out_0));
  xor xor_1 (xor_1_out, op, cin);

  assign LEDcin = cin;
  assign LEDop = op;
endmodule

module SR_Latch (
  input  set,
  input  reset,
  output Q,
  output nQ
);

  wire or_1_out, or_2_out;

  or or_1 (or_1_out, set, Q);
  not not_1 (Q, or_2_out);
  not not_2 (nQ, or_1_out);
  or or_2 (or_2_out, nQ, reset);
endmodule

module D_Latch (
  input  D,
  input  write,
  input  nrst,
  output Q,
  output nQ
);

  wire and_1_out, and_2_out, not_1_out, not_2_out, or_1_out;

  not not_1 (not_1_out, D);
  not not_2 (not_2_out, nrst);
  and and_1 (and_1_out, D, write);
  and and_2 (and_2_out, write, not_1_out);
  SR_Latch sr_latch_1 (.set(and_1_out), .Q(Q), .nQ(nQ), .reset(or_1_out));
  or or_1 (or_1_out, and_2_out, not_2_out);
endmodule

module D_FlipFlop (
  input  clk,
  input  D,
  input  nrst,
  output Q,
  output nQ
);

  wire d_latch_1_q, not_1_out, not_2_out;

  not not_1 (not_1_out, clk);
  D_Latch d_latch_1 (.D(D), .write(not_1_out), .nrst(nrst), .Q(d_latch_1_q));  // open: nQ
  not not_2 (not_2_out, not_1_out);
  D_Latch d_latch_2 (.D(d_latch_1_q), .write(not_2_out), .nrst(nrst), .Q(Q), .nQ(nQ));
endmodule

module Reg1 (
  input  IN,
  input  read,
  input  write,
  input  nrst,
  output LED,
  output OUT,
  output LEDr,
  output LEDw,
  output LEDrst
);

  D_Latch d_latch_1 (.D(IN), .write(write), .nrst(nrst), .Q(LED));  // open: nQ
  assign OUT = read ? LED : 1'bz;  // Controlled_Buffer controlled_buffer_1

  assign LEDr = read;
  assign LEDrst = nrst;
  assign LEDw = write;
endmodule

module Reg4 (
  input  IN_3,
  input  IN_2,
  input  IN_1,
  input  IN_0,
  input  read,
  input  write,
  input  nrst,
  output LED_3,
  output LED_2,
  output LED_1,
  output LED_0,
  output OUT_3,
  output OUT_2,
  output OUT_1,
  output OUT_0,
  output LEDr,
  output LEDw,
  output LEDrst
);

  D_Latch d_latch_1 (.D(IN_3), .write(write), .nrst(nrst), .Q(LED_3));  // open: nQ
  assign OUT_3 = read ? LED_3 : 1'bz;  // Controlled_Buffer controlled_buffer_1
  D_Latch d_latch_2 (.D(IN_2), .write(write), .nrst(nrst), .Q(LED_2));  // open: nQ
  assign OUT_2 = read ? LED_2 : 1'bz;  // Controlled_Buffer controlled_buffer_2
  D_Latch d_latch_3 (.D(IN_1), .write(write), .nrst(nrst), .Q(LED_1));  // open: nQ
  assign OUT_1 = read ? LED_1 : 1'bz;  // Controlled_Buffer controlled_buffer_3
  D_Latch d_latch_4 (.D(IN_0), .write(write), .nrst(nrst), .Q(LED_0));  // open: nQ
  assign OUT_0 = read ? LED_0 : 1'bz;  // Controlled_Buffer controlled_buffer_4

  assign LEDr = read;
  assign LEDrst = nrst;
  assign LEDw = write;
endmodule

module ZeroPass4 (
  input  IN_3,
  input  IN_2,
  input  IN_1,
  input  IN_0,
  input  enable,
  output LEDen,
  output OUT_3,
  output OUT_2,
  output OUT_1,
  output OUT_0
);

  and and_1 (OUT_3, enable, IN_3);
  and and_2 (OUT_2, enable, IN_2);
  and and_3 (OUT_1, enable, IN_1);
  and and_4 (OUT_0, enable, IN_0);

  assign LEDen = enable;
endmodule

module SRAM_Cell (
  input  IN,
  input  select,
  input  read,
  input  write,
  input  nrst,
  output LED,
  output OUT,
  output LEDsel,
  output LEDr,
  output LEDw,
  output LEDrst
);

  wire and_1_out, and_2_out;

  and and_1 (and_1_out, select, write);
  D_Latch d_latch_1 (.D(IN), .write(and_1_out), .nrst(nrst), .Q(LED));  // open: nQ
  assign OUT = and_2_out ? LED : 1'bz;  // Controlled_Buffer controlled_buffer_1
  and and_2 (and_2_out, select, read);

  assign LEDr = read;
  assign LEDrst = nrst;
  assign LEDsel = select;
  assign LEDw = write;
endmodule

module SRAM_4x4bit (
  input  ADDR_1,
  input  ADDR_0,
  input  select,
  input  IN_3,
  input  IN_2,
  input  IN_1,
  input  IN_0,
  input  read,
  input  write,
  input  nrst,
  output LEDsel_0,
  output LED_0__0,
  output LED_0__1,
  output LED_0__2,
  output LED_0__3,
  output LEDsel_1,
  output LED_1__0,
  output LED_1__1,
  output LED_1__2,
  output LED_1__3,
  output LEDsel_2,
  output LED_2__0,
  output LED_2__1,
  output LED_2__2,
  output LED_2__3,
  output LEDsel_3,
  output LED_3__0,
  output LED_3__1,
  output LED_3__2,
  output LED_3__3,
  output LEDsel,
  output LEDaddr_0,
  output LEDaddr_1,
  output LEDr,
  output LEDw,
  output LEDrst,
  output OUT_3,
  output OUT_2,
  output OUT_1,
  output OUT_0
);

  wire not_1_out, not_2_out;

  not not_1 (not_1_out, ADDR_1);
  not not_2 (not_2_out, ADDR_0);
  and and_1 (LEDsel_0, not_2_out, not_1_out, select);
  and and_2 (LEDsel_1, ADDR_0, not_1_out, select);
  and and_3 (LEDsel_2, not_2_out, ADDR_1, select);
  and and_4 (LEDsel_3, ADDR_0, ADDR_1, select);
  SRAM_Cell sram_cell_1 (
    .IN(IN_3), .select(LEDsel_0), .read(read), .write(write), .nrst(nrst), .LED(LED_0__3), .OUT(OUT_3));  // open: LEDsel, LEDr, LEDw, LEDrst
  SRAM_Cell sram_cell_2 (
    .IN(IN_3), .select(LEDsel_1), .read(read), .write(write), .nrst(nrst), .LED(LED_1__3), .OUT(OUT_3));  // open: LEDsel, LEDr, LEDw, LEDrst
  SRAM_Cell sram_cell_3 (
    .IN(IN_3), .select(LEDsel_2), .read(read), .write(write), .nrst(nrst), .LED(LED_2__3), .OUT(OUT_3));  // open: LEDsel, LEDr, LEDw, LEDrst
  SRAM_Cell sram_cell_4 (
    .IN(IN_3), .select(LEDsel_3), .read(read), .write(write), .nrst(nrst), .LED(LED_3__3), .OUT(OUT_3));  // open: LEDsel, LEDr, LEDw, LEDrst
  SRAM_Cell sram_cell_5 (
    .IN(IN_2), .select(LEDsel_0), .read(read), .write(write), .nrst(nrst), .LED(LED_0__2), .OUT(OUT_2));  // open: LEDsel, LEDr, LEDw, LEDrst
  SRAM_Cell sram_cell_6 (
    .IN(IN_2), .select(LEDsel_1), .read(read), .write(write), .nrst(nrst), .LED(LED_1__2), .OUT(OUT_2));  // open: LEDsel, LEDr, LEDw, LEDrst
  SRAM_Cell sram_cell_7 (
    .IN(IN_2), .select(LEDsel_2), .read(read), .write(write), .nrst(nrst), .LED(LED_2__2), .OUT(OUT_2));  // open: LEDsel, LEDr, LEDw, LEDrst
  SRAM_Cell sram_cell_8 (
    .IN(IN_2), .select(LEDsel_3), .read(read), .write(write), .nrst(nrst), .LED(LED_3__2), .OUT(OUT_2));  // open: LEDsel, LEDr, LEDw, LEDrst
  SRAM_Cell sram_cell_9 (
    .IN(IN_1), .select(LEDsel_0), .read(read), .write(write), .nrst(nrst), .LED(LED_0__1), .OUT(OUT_1));  // open: LEDsel, LEDr, LEDw, LEDrst
  SRAM_Cell sram_cell_10 (
    .IN(IN_1), .select(LEDsel_1), .read(read), .write(write), .nrst(nrst), .LED(LED_1__1), .OUT(OUT_1));  // open: LEDsel, LEDr, LEDw, LEDrst
  SRAM_Cell sram_cell_11 (
    .IN(IN_1), .select(LEDsel_2), .read(read), .write(write), .nrst(nrst), .LED(LED_2__1), .OUT(OUT_1));  // open: LEDsel, LEDr, LEDw, LEDrst
  SRAM_Cell sram_cell_12 (
    .IN(IN_1), .select(LEDsel_3), .read(read), .write(write), .nrst(nrst), .LED(LED_3__1), .OUT(OUT_1));  // open: LEDsel, LEDr, LEDw, LEDrst
  SRAM_Cell sram_cell_13 (
    .IN(IN_0), .select(LEDsel_0), .read(read), .write(write), .nrst(nrst), .LED(LED_0__0), .OUT(OUT_0));  // open: LEDsel, LEDr, LEDw, LEDrst
  SRAM_Cell sram_cell_14 (
    .IN(IN_0), .select(LEDsel_1), .read(read), .write(write), .nrst(nrst), .LED(LED_1__0), .OUT(OUT_0));  // open: LEDsel, LEDr, LEDw, LEDrst
  SRAM_Cell sram_cell_15 (
    .IN(IN_0), .select(LEDsel_2), .read(read), .write(write), .nrst(nrst), .LED(LED_2__0), .OUT(OUT_0));  // open: LEDsel, LEDr, LEDw, LEDrst
  SRAM_Cell sram_cell_16 (
    .IN(IN_0), .select(LEDsel_3), .read(read), .write(write), .nrst(nrst), .LED(LED_3__0), .OUT(OUT_0));  // open: LEDsel, LEDr, LEDw, LEDrst

  assign LEDaddr_0 = ADDR_0;
  assign LEDaddr_1 = ADDR_1;
  assign LEDr = read;
  assign LEDrst = nrst;
  assign LEDsel = select;
  assign LEDw = write;

  // Other names for the same wires on the sheet: _00 = LED_0__0; _01 = LED_0__1; _02 = LED_0__2; _03 = LED_0__3;
  //   _10 = LED_1__0; _11 = LED_1__1; _12 = LED_1__2; _13 = LED_1__3; _20 = LED_2__0; _21 = LED_2__1; _22 = LED_2__2;
  //   _23 = LED_2__3; _30 = LED_3__0; _31 = LED_3__1; _32 = LED_3__2; _33 = LED_3__3
endmodule

module SRAM_16x4bit (
  input  ADDR_3,
  input  ADDR_2,
  input  ADDR_1,
  input  ADDR_0,
  input  select,
  input  IN_3,
  input  IN_2,
  input  IN_1,
  input  IN_0,
  input  read,
  input  write,
  input  nrst,
  output LEDsel_0,
  output LED_0__0,
  output LED_0__1,
  output LED_0__2,
  output LED_0__3,
  output LEDsel_1,
  output LED_1__0,
  output LED_1__1,
  output LED_1__2,
  output LED_1__3,
  output LEDsel_2,
  output LED_2__0,
  output LED_2__1,
  output LED_2__2,
  output LED_2__3,
  output LEDsel_3,
  output LED_3__0,
  output LED_3__1,
  output LED_3__2,
  output LED_3__3,
  output LEDsel_4,
  output LED_4__0,
  output LED_4__1,
  output LED_4__2,
  output LED_4__3,
  output LEDsel_5,
  output LED_5__0,
  output LED_5__1,
  output LED_5__2,
  output LED_5__3,
  output LEDsel_6,
  output LED_6__0,
  output LED_6__1,
  output LED_6__2,
  output LED_6__3,
  output LEDsel_7,
  output LED_7__0,
  output LED_7__1,
  output LED_7__2,
  output LED_7__3,
  output LEDsel_8,
  output LED_8__0,
  output LED_8__1,
  output LED_8__2,
  output LED_8__3,
  output LEDsel_9,
  output LED_9__0,
  output LED_9__1,
  output LED_9__2,
  output LED_9__3,
  output LEDsel_A,
  output LED_A__0,
  output LED_A__1,
  output LED_A__2,
  output LED_A__3,
  output LEDsel_B,
  output LED_B__0,
  output LED_B__1,
  output LED_B__2,
  output LED_B__3,
  output LEDsel_C,
  output LED_C__0,
  output LED_C__1,
  output LED_C__2,
  output LED_C__3,
  output LEDsel_D,
  output LED_D__0,
  output LED_D__1,
  output LED_D__2,
  output LED_D__3,
  output LEDsel_E,
  output LED_E__0,
  output LED_E__1,
  output LED_E__2,
  output LED_E__3,
  output LEDsel_F,
  output LED_F__0,
  output LED_F__1,
  output LED_F__2,
  output LEDsel,
  output LED_F__3,
  output LEDaddr_0,
  output LEDaddr_1,
  output LEDaddr_0_2,
  output LEDaddr_1_2,
  output LEDr,
  output LEDw,
  output LEDrst,
  output OUT_3,
  output OUT_2,
  output OUT_1,
  output OUT_0
);

  wire not_1_out, not_2_out, not_3_out, not_4_out;

  not not_1 (not_1_out, ADDR_2);
  not not_2 (not_2_out, ADDR_3);
  not not_3 (not_3_out, ADDR_1);
  not not_4 (not_4_out, ADDR_0);
  and and_1 (LEDsel_0, select, not_4_out, not_3_out, not_1_out, not_2_out);
  and and_2 (LEDsel_1, select, ADDR_0, not_3_out, not_1_out, not_2_out);
  and and_3 (LEDsel_2, select, not_4_out, ADDR_1, not_1_out, not_2_out);
  and and_4 (LEDsel_3, select, ADDR_0, ADDR_1, not_1_out, not_2_out);
  and and_5 (LEDsel_4, select, not_4_out, not_3_out, ADDR_2, not_2_out);
  and and_6 (LEDsel_5, select, ADDR_0, not_3_out, ADDR_2, not_2_out);
  and and_7 (LEDsel_6, select, not_4_out, ADDR_1, ADDR_2, not_2_out);
  and and_8 (LEDsel_7, select, ADDR_0, ADDR_1, ADDR_2, not_2_out);
  and and_9 (LEDsel_8, select, not_4_out, not_3_out, not_1_out, ADDR_3);
  and and_10 (LEDsel_9, select, ADDR_0, not_3_out, not_1_out, ADDR_3);
  and and_11 (LEDsel_A, select, not_4_out, ADDR_1, not_1_out, ADDR_3);
  and and_12 (LEDsel_B, select, ADDR_0, ADDR_1, not_1_out, ADDR_3);
  and and_13 (LEDsel_C, select, not_4_out, not_3_out, ADDR_2, ADDR_3);
  and and_14 (LEDsel_D, select, ADDR_0, not_3_out, ADDR_2, ADDR_3);
  and and_15 (LEDsel_E, select, not_4_out, ADDR_1, ADDR_2, ADDR_3);
  and and_16 (LEDsel_F, select, ADDR_0, ADDR_1, ADDR_2, ADDR_3);
  SRAM_Cell sram_cell_1 (
    .IN(IN_3), .select(LEDsel_0), .read(read), .write(write), .nrst(nrst), .LED(LED_0__3), .OUT(OUT_3));  // open: LEDsel, LEDr, LEDw, LEDrst
  SRAM_Cell sram_cell_2 (
    .IN(IN_3), .select(LEDsel_1), .read(read), .write(write), .nrst(nrst), .LED(LED_1__3), .OUT(OUT_3));  // open: LEDsel, LEDr, LEDw, LEDrst
  SRAM_Cell sram_cell_3 (
    .IN(IN_3), .select(LEDsel_2), .read(read), .write(write), .nrst(nrst), .LED(LED_2__3), .OUT(OUT_3));  // open: LEDsel, LEDr, LEDw, LEDrst
  SRAM_Cell sram_cell_4 (
    .IN(IN_3), .select(LEDsel_3), .read(read), .write(write), .nrst(nrst), .LED(LED_3__3), .OUT(OUT_3));  // open: LEDsel, LEDr, LEDw, LEDrst
  SRAM_Cell sram_cell_5 (
    .IN(IN_3), .select(LEDsel_4), .read(read), .write(write), .nrst(nrst), .LED(LED_4__3), .OUT(OUT_3));  // open: LEDsel, LEDr, LEDw, LEDrst
  SRAM_Cell sram_cell_6 (
    .IN(IN_3), .select(LEDsel_5), .read(read), .write(write), .nrst(nrst), .LED(LED_5__3), .OUT(OUT_3));  // open: LEDsel, LEDr, LEDw, LEDrst
  SRAM_Cell sram_cell_7 (
    .IN(IN_3), .select(LEDsel_6), .read(read), .write(write), .nrst(nrst), .LED(LED_6__3), .OUT(OUT_3));  // open: LEDsel, LEDr, LEDw, LEDrst
  SRAM_Cell sram_cell_8 (
    .IN(IN_3), .select(LEDsel_7), .read(read), .write(write), .nrst(nrst), .LED(LED_7__3), .OUT(OUT_3));  // open: LEDsel, LEDr, LEDw, LEDrst
  SRAM_Cell sram_cell_9 (
    .IN(IN_3), .select(LEDsel_8), .read(read), .write(write), .nrst(nrst), .LED(LED_8__3), .OUT(OUT_3));  // open: LEDsel, LEDr, LEDw, LEDrst
  SRAM_Cell sram_cell_10 (
    .IN(IN_3), .select(LEDsel_9), .read(read), .write(write), .nrst(nrst), .LED(LED_9__3), .OUT(OUT_3));  // open: LEDsel, LEDr, LEDw, LEDrst
  SRAM_Cell sram_cell_11 (
    .IN(IN_3), .select(LEDsel_A), .read(read), .write(write), .nrst(nrst), .LED(LED_A__3), .OUT(OUT_3));  // open: LEDsel, LEDr, LEDw, LEDrst
  SRAM_Cell sram_cell_12 (
    .IN(IN_3), .select(LEDsel_B), .read(read), .write(write), .nrst(nrst), .LED(LED_B__3), .OUT(OUT_3));  // open: LEDsel, LEDr, LEDw, LEDrst
  SRAM_Cell sram_cell_13 (
    .IN(IN_3), .select(LEDsel_C), .read(read), .write(write), .nrst(nrst), .LED(LED_C__3), .OUT(OUT_3));  // open: LEDsel, LEDr, LEDw, LEDrst
  SRAM_Cell sram_cell_14 (
    .IN(IN_3), .select(LEDsel_D), .read(read), .write(write), .nrst(nrst), .LED(LED_D__3), .OUT(OUT_3));  // open: LEDsel, LEDr, LEDw, LEDrst
  SRAM_Cell sram_cell_15 (
    .IN(IN_3), .select(LEDsel_E), .read(read), .write(write), .nrst(nrst), .LED(LED_E__3), .OUT(OUT_3));  // open: LEDsel, LEDr, LEDw, LEDrst
  SRAM_Cell sram_cell_16 (
    .IN(IN_3), .select(LEDsel_F), .read(read), .write(write), .nrst(nrst), .LED(LED_F__3), .OUT(OUT_3));  // open: LEDsel, LEDr, LEDw, LEDrst
  SRAM_Cell sram_cell_17 (
    .IN(IN_2), .select(LEDsel_0), .read(read), .write(write), .nrst(nrst), .LED(LED_0__2), .OUT(OUT_2));  // open: LEDsel, LEDr, LEDw, LEDrst
  SRAM_Cell sram_cell_18 (
    .IN(IN_2), .select(LEDsel_1), .read(read), .write(write), .nrst(nrst), .LED(LED_1__2), .OUT(OUT_2));  // open: LEDsel, LEDr, LEDw, LEDrst
  SRAM_Cell sram_cell_19 (
    .IN(IN_2), .select(LEDsel_2), .read(read), .write(write), .nrst(nrst), .LED(LED_2__2), .OUT(OUT_2));  // open: LEDsel, LEDr, LEDw, LEDrst
  SRAM_Cell sram_cell_20 (
    .IN(IN_2), .select(LEDsel_3), .read(read), .write(write), .nrst(nrst), .LED(LED_3__2), .OUT(OUT_2));  // open: LEDsel, LEDr, LEDw, LEDrst
  SRAM_Cell sram_cell_21 (
    .IN(IN_2), .select(LEDsel_4), .read(read), .write(write), .nrst(nrst), .LED(LED_4__2), .OUT(OUT_2));  // open: LEDsel, LEDr, LEDw, LEDrst
  SRAM_Cell sram_cell_22 (
    .IN(IN_2), .select(LEDsel_5), .read(read), .write(write), .nrst(nrst), .LED(LED_5__2), .OUT(OUT_2));  // open: LEDsel, LEDr, LEDw, LEDrst
  SRAM_Cell sram_cell_23 (
    .IN(IN_2), .select(LEDsel_6), .read(read), .write(write), .nrst(nrst), .LED(LED_6__2), .OUT(OUT_2));  // open: LEDsel, LEDr, LEDw, LEDrst
  SRAM_Cell sram_cell_24 (
    .IN(IN_2), .select(LEDsel_7), .read(read), .write(write), .nrst(nrst), .LED(LED_7__2), .OUT(OUT_2));  // open: LEDsel, LEDr, LEDw, LEDrst
  SRAM_Cell sram_cell_25 (
    .IN(IN_2), .select(LEDsel_8), .read(read), .write(write), .nrst(nrst), .LED(LED_8__2), .OUT(OUT_2));  // open: LEDsel, LEDr, LEDw, LEDrst
  SRAM_Cell sram_cell_26 (
    .IN(IN_2), .select(LEDsel_9), .read(read), .write(write), .nrst(nrst), .LED(LED_9__2), .OUT(OUT_2));  // open: LEDsel, LEDr, LEDw, LEDrst
  SRAM_Cell sram_cell_27 (
    .IN(IN_2), .select(LEDsel_A), .read(read), .write(write), .nrst(nrst), .LED(LED_A__2), .OUT(OUT_2));  // open: LEDsel, LEDr, LEDw, LEDrst
  SRAM_Cell sram_cell_28 (
    .IN(IN_2), .select(LEDsel_B), .read(read), .write(write), .nrst(nrst), .LED(LED_B__2), .OUT(OUT_2));  // open: LEDsel, LEDr, LEDw, LEDrst
  SRAM_Cell sram_cell_29 (
    .IN(IN_2), .select(LEDsel_C), .read(read), .write(write), .nrst(nrst), .LED(LED_C__2), .OUT(OUT_2));  // open: LEDsel, LEDr, LEDw, LEDrst
  SRAM_Cell sram_cell_30 (
    .IN(IN_2), .select(LEDsel_D), .read(read), .write(write), .nrst(nrst), .LED(LED_D__2), .OUT(OUT_2));  // open: LEDsel, LEDr, LEDw, LEDrst
  SRAM_Cell sram_cell_31 (
    .IN(IN_2), .select(LEDsel_E), .read(read), .write(write), .nrst(nrst), .LED(LED_E__2), .OUT(OUT_2));  // open: LEDsel, LEDr, LEDw, LEDrst
  SRAM_Cell sram_cell_32 (
    .IN(IN_2), .select(LEDsel_F), .read(read), .write(write), .nrst(nrst), .LED(LED_F__2), .OUT(OUT_2));  // open: LEDsel, LEDr, LEDw, LEDrst
  SRAM_Cell sram_cell_33 (
    .IN(IN_1), .select(LEDsel_0), .read(read), .write(write), .nrst(nrst), .LED(LED_0__1), .OUT(OUT_1));  // open: LEDsel, LEDr, LEDw, LEDrst
  SRAM_Cell sram_cell_34 (
    .IN(IN_1), .select(LEDsel_1), .read(read), .write(write), .nrst(nrst), .LED(LED_1__1), .OUT(OUT_1));  // open: LEDsel, LEDr, LEDw, LEDrst
  SRAM_Cell sram_cell_35 (
    .IN(IN_1), .select(LEDsel_2), .read(read), .write(write), .nrst(nrst), .LED(LED_2__1), .OUT(OUT_1));  // open: LEDsel, LEDr, LEDw, LEDrst
  SRAM_Cell sram_cell_36 (
    .IN(IN_1), .select(LEDsel_3), .read(read), .write(write), .nrst(nrst), .LED(LED_3__1), .OUT(OUT_1));  // open: LEDsel, LEDr, LEDw, LEDrst
  SRAM_Cell sram_cell_37 (
    .IN(IN_1), .select(LEDsel_4), .read(read), .write(write), .nrst(nrst), .LED(LED_4__1), .OUT(OUT_1));  // open: LEDsel, LEDr, LEDw, LEDrst
  SRAM_Cell sram_cell_38 (
    .IN(IN_1), .select(LEDsel_5), .read(read), .write(write), .nrst(nrst), .LED(LED_5__1), .OUT(OUT_1));  // open: LEDsel, LEDr, LEDw, LEDrst
  SRAM_Cell sram_cell_39 (
    .IN(IN_1), .select(LEDsel_6), .read(read), .write(write), .nrst(nrst), .LED(LED_6__1), .OUT(OUT_1));  // open: LEDsel, LEDr, LEDw, LEDrst
  SRAM_Cell sram_cell_40 (
    .IN(IN_1), .select(LEDsel_7), .read(read), .write(write), .nrst(nrst), .LED(LED_7__1), .OUT(OUT_1));  // open: LEDsel, LEDr, LEDw, LEDrst
  SRAM_Cell sram_cell_41 (
    .IN(IN_1), .select(LEDsel_8), .read(read), .write(write), .nrst(nrst), .LED(LED_8__1), .OUT(OUT_1));  // open: LEDsel, LEDr, LEDw, LEDrst
  SRAM_Cell sram_cell_42 (
    .IN(IN_1), .select(LEDsel_9), .read(read), .write(write), .nrst(nrst), .LED(LED_9__1), .OUT(OUT_1));  // open: LEDsel, LEDr, LEDw, LEDrst
  SRAM_Cell sram_cell_43 (
    .IN(IN_1), .select(LEDsel_A), .read(read), .write(write), .nrst(nrst), .LED(LED_A__1), .OUT(OUT_1));  // open: LEDsel, LEDr, LEDw, LEDrst
  SRAM_Cell sram_cell_44 (
    .IN(IN_1), .select(LEDsel_B), .read(read), .write(write), .nrst(nrst), .LED(LED_B__1), .OUT(OUT_1));  // open: LEDsel, LEDr, LEDw, LEDrst
  SRAM_Cell sram_cell_45 (
    .IN(IN_1), .select(LEDsel_C), .read(read), .write(write), .nrst(nrst), .LED(LED_C__1), .OUT(OUT_1));  // open: LEDsel, LEDr, LEDw, LEDrst
  SRAM_Cell sram_cell_46 (
    .IN(IN_1), .select(LEDsel_D), .read(read), .write(write), .nrst(nrst), .LED(LED_D__1), .OUT(OUT_1));  // open: LEDsel, LEDr, LEDw, LEDrst
  SRAM_Cell sram_cell_47 (
    .IN(IN_1), .select(LEDsel_E), .read(read), .write(write), .nrst(nrst), .LED(LED_E__1), .OUT(OUT_1));  // open: LEDsel, LEDr, LEDw, LEDrst
  SRAM_Cell sram_cell_48 (
    .IN(IN_1), .select(LEDsel_F), .read(read), .write(write), .nrst(nrst), .LED(LED_F__1), .OUT(OUT_1));  // open: LEDsel, LEDr, LEDw, LEDrst
  SRAM_Cell sram_cell_49 (
    .IN(IN_0), .select(LEDsel_0), .read(read), .write(write), .nrst(nrst), .LED(LED_0__0), .OUT(OUT_0));  // open: LEDsel, LEDr, LEDw, LEDrst
  SRAM_Cell sram_cell_50 (
    .IN(IN_0), .select(LEDsel_1), .read(read), .write(write), .nrst(nrst), .LED(LED_1__0), .OUT(OUT_0));  // open: LEDsel, LEDr, LEDw, LEDrst
  SRAM_Cell sram_cell_51 (
    .IN(IN_0), .select(LEDsel_2), .read(read), .write(write), .nrst(nrst), .LED(LED_2__0), .OUT(OUT_0));  // open: LEDsel, LEDr, LEDw, LEDrst
  SRAM_Cell sram_cell_52 (
    .IN(IN_0), .select(LEDsel_3), .read(read), .write(write), .nrst(nrst), .LED(LED_3__0), .OUT(OUT_0));  // open: LEDsel, LEDr, LEDw, LEDrst
  SRAM_Cell sram_cell_53 (
    .IN(IN_0), .select(LEDsel_4), .read(read), .write(write), .nrst(nrst), .LED(LED_4__0), .OUT(OUT_0));  // open: LEDsel, LEDr, LEDw, LEDrst
  SRAM_Cell sram_cell_54 (
    .IN(IN_0), .select(LEDsel_5), .read(read), .write(write), .nrst(nrst), .LED(LED_5__0), .OUT(OUT_0));  // open: LEDsel, LEDr, LEDw, LEDrst
  SRAM_Cell sram_cell_55 (
    .IN(IN_0), .select(LEDsel_6), .read(read), .write(write), .nrst(nrst), .LED(LED_6__0), .OUT(OUT_0));  // open: LEDsel, LEDr, LEDw, LEDrst
  SRAM_Cell sram_cell_56 (
    .IN(IN_0), .select(LEDsel_7), .read(read), .write(write), .nrst(nrst), .LED(LED_7__0), .OUT(OUT_0));  // open: LEDsel, LEDr, LEDw, LEDrst
  SRAM_Cell sram_cell_57 (
    .IN(IN_0), .select(LEDsel_8), .read(read), .write(write), .nrst(nrst), .LED(LED_8__0), .OUT(OUT_0));  // open: LEDsel, LEDr, LEDw, LEDrst
  SRAM_Cell sram_cell_58 (
    .IN(IN_0), .select(LEDsel_9), .read(read), .write(write), .nrst(nrst), .LED(LED_9__0), .OUT(OUT_0));  // open: LEDsel, LEDr, LEDw, LEDrst
  SRAM_Cell sram_cell_59 (
    .IN(IN_0), .select(LEDsel_A), .read(read), .write(write), .nrst(nrst), .LED(LED_A__0), .OUT(OUT_0));  // open: LEDsel, LEDr, LEDw, LEDrst
  SRAM_Cell sram_cell_60 (
    .IN(IN_0), .select(LEDsel_B), .read(read), .write(write), .nrst(nrst), .LED(LED_B__0), .OUT(OUT_0));  // open: LEDsel, LEDr, LEDw, LEDrst
  SRAM_Cell sram_cell_61 (
    .IN(IN_0), .select(LEDsel_C), .read(read), .write(write), .nrst(nrst), .LED(LED_C__0), .OUT(OUT_0));  // open: LEDsel, LEDr, LEDw, LEDrst
  SRAM_Cell sram_cell_62 (
    .IN(IN_0), .select(LEDsel_D), .read(read), .write(write), .nrst(nrst), .LED(LED_D__0), .OUT(OUT_0));  // open: LEDsel, LEDr, LEDw, LEDrst
  SRAM_Cell sram_cell_63 (
    .IN(IN_0), .select(LEDsel_E), .read(read), .write(write), .nrst(nrst), .LED(LED_E__0), .OUT(OUT_0));  // open: LEDsel, LEDr, LEDw, LEDrst
  SRAM_Cell sram_cell_64 (
    .IN(IN_0), .select(LEDsel_F), .read(read), .write(write), .nrst(nrst), .LED(LED_F__0), .OUT(OUT_0));  // open: LEDsel, LEDr, LEDw, LEDrst

  assign LEDaddr_0 = ADDR_0;
  assign LEDaddr_0_2 = ADDR_2;
  assign LEDaddr_1 = ADDR_1;
  assign LEDaddr_1_2 = ADDR_3;
  assign LEDr = read;
  assign LEDrst = nrst;
  assign LEDsel = select;
  assign LEDw = write;

  // Other names for the same wires on the sheet: _00 = LED_0__0; _01 = LED_0__1; _02 = LED_0__2; _03 = LED_0__3;
  //   _10 = LED_1__0; _11 = LED_1__1; _12 = LED_1__2; _13 = LED_1__3; _20 = LED_2__0; _21 = LED_2__1; _22 = LED_2__2;
  //   _23 = LED_2__3; _30 = LED_3__0; _31 = LED_3__1; _32 = LED_3__2; _33 = LED_3__3; _40 = LED_4__0; _41 = LED_4__1;
  //   _42 = LED_4__2; _43 = LED_4__3; _50 = LED_5__0; _51 = LED_5__1; _52 = LED_5__2; _53 = LED_5__3; _60 = LED_6__0;
  //   _61 = LED_6__1; _62 = LED_6__2; _63 = LED_6__3; _70 = LED_7__0; _71 = LED_7__1; _72 = LED_7__2; _73 = LED_7__3;
  //   _80 = LED_8__0; _81 = LED_8__1; _82 = LED_8__2; _83 = LED_8__3; _90 = LED_9__0; _91 = LED_9__1; _92 = LED_9__2;
  //   _93 = LED_9__3; A0 = LED_A__0; A1 = LED_A__1; A2 = LED_A__2; A3 = LED_A__3; B0 = LED_B__0; B1 = LED_B__1;
  //   B2 = LED_B__2; B3 = LED_B__3; C0 = LED_C__0; C1 = LED_C__1; C2 = LED_C__2; C3 = LED_C__3; D0 = LED_D__0;
  //   D1 = LED_D__1; D2 = LED_D__2; D3 = LED_D__3; E0 = LED_E__0; E1 = LED_E__1; E2 = LED_E__2; E3 = LED_E__3;
  //   F0 = LED_F__0; F1 = LED_F__1; F2 = LED_F__2; F3 = LED_F__3
endmodule

module Delayer (
  input  in,
  output out
);

  wire not_1_out, not_2_out, not_3_out, not_4_out, not_5_out, not_6_out, not_7_out;

  not not_1 (not_1_out, in);
  not not_2 (not_2_out, not_1_out);
  not not_3 (not_3_out, not_4_out);
  not not_4 (not_4_out, not_2_out);
  not not_5 (not_5_out, not_3_out);
  not not_6 (not_6_out, not_5_out);
  not not_7 (not_7_out, not_6_out);
  not not_8 (out, not_7_out);
endmodule

module Decoder2x4 (
  input  sel0,
  input  sel1,
  output _00,
  output _01,
  output _10,
  output _11
);

  wire not_1_out, not_2_out;

  not not_1 (not_1_out, sel0);
  not not_2 (not_2_out, sel1);
  and and_1 (_00, not_2_out, not_1_out);
  and and_2 (_01, not_2_out, sel0);
  and and_3 (_11, sel1, sel0);
  and and_4 (_10, sel1, not_1_out);
endmodule

module Mux2x4 (
  input  a3,
  input  b3,
  input  a2,
  input  b2,
  input  a1,
  input  b1,
  input  a0,
  input  b0,
  input  sel,
  output LEDsel,
  output out3,
  output out2,
  output out1,
  output out0
);

  Multiplexer #(.enable("false")) multiplexer_1 (.in0(a3), .in1(b3), .out(out3), .sel(sel));
  Multiplexer #(.enable("false")) multiplexer_2 (.in0(a1), .in1(b1), .out(out1), .sel(sel));
  Multiplexer #(.enable("false")) multiplexer_3 (.in0(a2), .in1(b2), .out(out2), .sel(sel));
  Multiplexer #(.enable("false")) multiplexer_4 (.in0(a0), .in1(b0), .out(out0), .sel(sel));

  assign LEDsel = sel;
endmodule

module BinToBCD___Add3 (
  input  IN_0,
  input  IN_1,
  input  IN_2,
  input  IN_3,
  output OUT_3,
  output OUT_2,
  output OUT_1,
  output OUT_0
);

  wire and_1_out, and_2_out, and_3_out, and_4_out, and_5_out, and_6_out, and_7_out, and_8_out, and_9_out,
       and_10_out, not_1_out, not_2_out, not_3_out, not_4_out;

  not not_1 (not_1_out, IN_0);
  not not_2 (not_2_out, IN_1);
  not not_3 (not_3_out, IN_2);
  not not_4 (not_4_out, IN_3);
  and and_1 (and_1_out, IN_2, IN_0);
  and and_2 (and_2_out, IN_2, IN_1);
  or or_1 (OUT_3, IN_3, and_2_out, and_1_out);
  and and_3 (and_3_out, IN_3, IN_0);
  or or_2 (OUT_2, and_3_out, and_4_out);
  and and_4 (and_4_out, IN_2, not_2_out, not_1_out);
  and and_5 (and_5_out, IN_3, not_1_out);
  and and_6 (and_6_out, not_3_out, IN_1);
  and and_7 (and_7_out, IN_1, IN_0);
  or or_3 (OUT_1, and_5_out, and_6_out, and_7_out);
  and and_8 (and_8_out, IN_3, not_1_out);
  and and_9 (and_9_out, IN_2, IN_1, not_1_out);
  and and_10 (and_10_out, not_4_out, not_3_out, IN_0);
  or or_4 (OUT_0, and_8_out, and_9_out, and_10_out);
endmodule

module BinToBCD4 (
  input  BIN_0,
  input  BIN_1,
  input  BIN_2,
  input  BIN_3,
  output BCD1_0,
  output BCD1_1,
  output BCD1_2,
  output BCD1_3,
  output BCD10_0,
  output BCD10_1,
  output BCD10_2,
  output BCD10_3
);

  BinToBCD___Add3 bintobcd_add3_1 (
    .IN_3(1'b0), .IN_2(BIN_3), .IN_1(BIN_2), .IN_0(BIN_1), .OUT_3(BCD10_0), .OUT_2(BCD1_3), .OUT_1(BCD1_2),
    .OUT_0(BCD1_1));

  assign BCD1_0 = BIN_0;
  assign BCD10_1 = 1'b0;
  assign BCD10_2 = 1'b0;
  assign BCD10_3 = 1'b0;
endmodule

module _7SegDisplay_BCD_Adapter (
  input  BCD_0,
  input  BCD_1,
  input  BCD_2,
  input  BCD_3,
  output a,
  output b,
  output c,
  output d,
  output e,
  output f,
  output g,
  output dp
);

  wire decoder_1_out0, decoder_1_out1, decoder_1_out2, decoder_1_out3, decoder_1_out4, decoder_1_out5,
       decoder_1_out6, decoder_1_out7, decoder_1_out8, decoder_1_out9;

  Decoder #(.select(4), .enable("false")) decoder_1 (
    .out0(decoder_1_out0), .out1(decoder_1_out1), .out2(decoder_1_out2), .out3(decoder_1_out3),
    .out4(decoder_1_out4), .out5(decoder_1_out5), .out6(decoder_1_out6), .out7(decoder_1_out7),
    .out8(decoder_1_out8), .out9(decoder_1_out9), .sel({BCD_3, BCD_2, BCD_1, BCD_0}));  // open: out10, out11, out12, out13, out14, out15
  or or_1 (a, decoder_1_out9, decoder_1_out8, decoder_1_out7, decoder_1_out6, decoder_1_out5, 1'b0, decoder_1_out3, decoder_1_out2, 1'b0, decoder_1_out0);
  or or_2 (b, decoder_1_out9, decoder_1_out8, decoder_1_out7, 1'b0, 1'b0, decoder_1_out4, decoder_1_out3, decoder_1_out2, decoder_1_out1, decoder_1_out0);
  or or_3 (c, decoder_1_out9, decoder_1_out8, decoder_1_out7, decoder_1_out6, decoder_1_out5, decoder_1_out4, decoder_1_out3, 1'b0, decoder_1_out1, decoder_1_out0);
  or or_4 (d, decoder_1_out9, decoder_1_out8, 1'b0, decoder_1_out6, decoder_1_out5, 1'b0, decoder_1_out3, decoder_1_out2, 1'b0, decoder_1_out0);
  or or_5 (e, 1'b0, decoder_1_out8, 1'b0, decoder_1_out6, 1'b0, 1'b0, 1'b0, decoder_1_out2, 1'b0, decoder_1_out0);
  or or_6 (f, decoder_1_out9, decoder_1_out8, 1'b0, decoder_1_out6, decoder_1_out5, decoder_1_out4, 1'b0, 1'b0, 1'b0, decoder_1_out0);
  or or_7 (g, decoder_1_out9, decoder_1_out8, 1'b0, decoder_1_out6, decoder_1_out5, decoder_1_out4, decoder_1_out3, decoder_1_out2, 1'b0, 1'b0);
  or or_8 (dp, 1'b0, 1'b0, 1'b0, 1'b0, 1'b0, 1'b0, 1'b0, 1'b0, 1'b0, 1'b0);
endmodule

module _7SegDisplay_HEX_Adapter (
  input  IN_0,
  input  IN_1,
  input  IN_2,
  input  IN_3,
  output a,
  output b,
  output c,
  output d,
  output e,
  output f,
  output g,
  output dp
);

  wire decoder_1_out0, decoder_1_out1, decoder_1_out2, decoder_1_out3, decoder_1_out4, decoder_1_out5,
       decoder_1_out6, decoder_1_out7, decoder_1_out8, decoder_1_out9, decoder_1_out10, decoder_1_out11,
       decoder_1_out12, decoder_1_out13, decoder_1_out14, decoder_1_out15;

  Decoder #(.select(4), .enable("false")) decoder_1 (
    .out0(decoder_1_out0), .out1(decoder_1_out1), .out2(decoder_1_out2), .out3(decoder_1_out3),
    .out4(decoder_1_out4), .out5(decoder_1_out5), .out6(decoder_1_out6), .out7(decoder_1_out7),
    .out8(decoder_1_out8), .out9(decoder_1_out9), .out10(decoder_1_out10), .out11(decoder_1_out11),
    .out12(decoder_1_out12), .out13(decoder_1_out13), .out14(decoder_1_out14), .out15(decoder_1_out15),
    .sel({IN_3, IN_2, IN_1, IN_0}));
  or or_1 (a, decoder_1_out15, decoder_1_out14, 1'b0, decoder_1_out12, 1'b0, decoder_1_out10, decoder_1_out9, decoder_1_out8, decoder_1_out7, decoder_1_out6, decoder_1_out5, 1'b0, decoder_1_out3, decoder_1_out2, 1'b0, decoder_1_out0);
  or or_2 (b, 1'b0, 1'b0, decoder_1_out13, 1'b0, 1'b0, decoder_1_out10, decoder_1_out9, decoder_1_out8, decoder_1_out7, 1'b0, 1'b0, decoder_1_out4, decoder_1_out3, decoder_1_out2, decoder_1_out1, decoder_1_out0);
  or or_3 (c, 1'b0, 1'b0, decoder_1_out13, 1'b0, decoder_1_out11, decoder_1_out10, decoder_1_out9, decoder_1_out8, decoder_1_out7, decoder_1_out6, decoder_1_out5, decoder_1_out4, decoder_1_out3, 1'b0, decoder_1_out1, decoder_1_out0);
  or or_4 (d, 1'b0, decoder_1_out14, decoder_1_out13, decoder_1_out12, decoder_1_out11, 1'b0, decoder_1_out9, decoder_1_out8, 1'b0, decoder_1_out6, decoder_1_out5, 1'b0, decoder_1_out3, decoder_1_out2, 1'b0, decoder_1_out0);
  or or_5 (e, decoder_1_out15, decoder_1_out14, decoder_1_out13, decoder_1_out12, decoder_1_out11, decoder_1_out10, 1'b0, decoder_1_out8, 1'b0, decoder_1_out6, 1'b0, 1'b0, 1'b0, decoder_1_out2, 1'b0, decoder_1_out0);
  or or_6 (f, decoder_1_out15, decoder_1_out14, 1'b0, decoder_1_out12, decoder_1_out11, decoder_1_out10, decoder_1_out9, decoder_1_out8, 1'b0, decoder_1_out6, decoder_1_out5, decoder_1_out4, 1'b0, 1'b0, 1'b0, decoder_1_out0);
  or or_7 (g, decoder_1_out15, decoder_1_out14, decoder_1_out13, 1'b0, decoder_1_out11, decoder_1_out10, decoder_1_out9, decoder_1_out8, 1'b0, decoder_1_out6, decoder_1_out5, decoder_1_out4, decoder_1_out3, decoder_1_out2, 1'b0, 1'b0);
  or or_8 (dp, 1'b0, 1'b0, 1'b0, 1'b0, 1'b0, 1'b0, 1'b0, 1'b0, 1'b0, 1'b0, 1'b0, 1'b0, 1'b0, 1'b0, 1'b0, 1'b0);
endmodule

module DEC_Diplay (
  input  BIN_0,
  input  BIN_1,
  input  BIN_2,
  input  BIN_3,
  output LED0,
  output LED1,
  output LED2,
  output LED3,
  output BCD1_0,
  output BCD1_1,
  output BCD1_2,
  output BCD1_3,
  output BCD10_0,
  output BCD10_1,
  output BCD10_2,
  output BCD10_3
);

  BinToBCD4 bintobcd4_1 (
    .BIN_0(BIN_0), .BIN_1(BIN_1), .BIN_2(BIN_2), .BIN_3(BIN_3), .BCD1_0(BCD1_0), .BCD1_1(BCD1_1),
    .BCD1_2(BCD1_2), .BCD1_3(BCD1_3), .BCD10_0(BCD10_0), .BCD10_1(BCD10_1), .BCD10_2(BCD10_2),
    .BCD10_3(BCD10_3));

  assign LED0 = BIN_0;
  assign LED1 = BIN_1;
  assign LED2 = BIN_2;
  assign LED3 = BIN_3;
endmodule

module BIN_Display (
  input  IN_0,
  input  IN_1,
  input  IN_2,
  input  IN_3,
  output LED0,
  output LED1,
  output LED2,
  output LED3
);


  assign LED0 = IN_0;
  assign LED1 = IN_1;
  assign LED2 = IN_2;
  assign LED3 = IN_3;
endmodule

module HEX_Display (
  input  BIN_0,
  input  BIN_1,
  input  BIN_2,
  input  BIN_3,
  output LED0,
  output LED1,
  output LED2,
  output LED3,
  output HEX3,
  output HEX2,
  output HEX1,
  output HEX0
);


  assign HEX0 = BIN_0;
  assign HEX1 = BIN_1;
  assign HEX2 = BIN_2;
  assign HEX3 = BIN_3;
  assign LED0 = BIN_0;
  assign LED1 = BIN_1;
  assign LED2 = BIN_2;
  assign LED3 = BIN_3;
endmodule
