// Logisim project 8bitLA.circ as structural Verilog
module Computer (
  input  in_1,
  input  in_2
);

  wire alu_1_ledcin, alu_1_ledop, alu_1_ledz, alu_1_sum_0, alu_1_sum_1, alu_1_sum_2, alu_1_sum_3,
       alu_1_sum_4, alu_1_sum_5, alu_1_sum_6, alu_1_sum_7, alu_1_zero, b_en, B_led0, B_led1, B_led2, B_led3,
       B_led4, B_led5, B_led6, B_led7, B_leden, B_out_0, B_out_1, B_out_2, B_out_3, B_out_4, B_out_5,
       B_out_6, B_out_7, bcd_display_1_a, bcd_display_1_b, bcd_display_1_c, bcd_display_1_d,
       bcd_display_1_dp, bcd_display_1_e, bcd_display_1_f, bcd_display_1_g, bcd_display_2_a, bcd_display_2_b,
       bcd_display_2_c, bcd_display_2_d, bcd_display_2_dp, bcd_display_2_e, bcd_display_2_f, bcd_display_2_g,
       bcd_display_3_a, bcd_display_3_b, bcd_display_3_c, bcd_display_3_d, bcd_display_3_dp, bcd_display_3_e,
       bcd_display_3_f, bcd_display_3_g, bcd_display_4_a, bcd_display_4_b, bcd_display_4_c, bcd_display_4_d,
       bcd_display_4_dp, bcd_display_4_e, bcd_display_4_f, bcd_display_4_g, bcd_display_5_a, bcd_display_5_b,
       bcd_display_5_c, bcd_display_5_d, bcd_display_5_dp, bcd_display_5_e, bcd_display_5_f, bcd_display_5_g,
       bcd_display_6_a, bcd_display_6_b, bcd_display_6_c, bcd_display_6_d, bcd_display_6_dp, bcd_display_6_e,
       bcd_display_6_f, bcd_display_6_g, bcd_display_7_a, bcd_display_7_b, bcd_display_7_c, bcd_display_7_d,
       bcd_display_7_dp, bcd_display_7_e, bcd_display_7_f, bcd_display_7_g, bcd_display_8_a, bcd_display_8_b,
       bcd_display_8_c, bcd_display_8_d, bcd_display_8_dp, bcd_display_8_e, bcd_display_8_f, bcd_display_8_g,
       bcd_display_9_a, bcd_display_9_b, bcd_display_9_c, bcd_display_9_d, bcd_display_9_dp, bcd_display_9_e,
       bcd_display_9_f, bcd_display_9_g, bcd_display_10_a, bcd_display_10_b, bcd_display_10_c,
       bcd_display_10_d, bcd_display_10_dp, bcd_display_10_e, bcd_display_10_f, bcd_display_10_g,
       bcd_display_11_a, bcd_display_11_b, bcd_display_11_c, bcd_display_11_d, bcd_display_11_dp,
       bcd_display_11_e, bcd_display_11_f, bcd_display_11_g, bcd_display_12_a, bcd_display_12_b,
       bcd_display_12_c, bcd_display_12_d, bcd_display_12_dp, bcd_display_12_e, bcd_display_12_f,
       bcd_display_12_g, bcd_display_13_a, bcd_display_13_b, bcd_display_13_c, bcd_display_13_d,
       bcd_display_13_dp, bcd_display_13_e, bcd_display_13_f, bcd_display_13_g, bcd_display_14_a,
       bcd_display_14_b, bcd_display_14_c, bcd_display_14_d, bcd_display_14_dp, bcd_display_14_e,
       bcd_display_14_f, bcd_display_14_g, bcd_display_15_a, bcd_display_15_b, bcd_display_15_c,
       bcd_display_15_d, bcd_display_15_dp, bcd_display_15_e, bcd_display_15_f, bcd_display_15_g,
       bcd_display_16_a, bcd_display_16_b, bcd_display_16_c, bcd_display_16_d, bcd_display_16_dp,
       bcd_display_16_e, bcd_display_16_f, bcd_display_16_g, bcd_display_17_a, bcd_display_17_b,
       bcd_display_17_c, bcd_display_17_d, bcd_display_17_dp, bcd_display_17_e, bcd_display_17_f,
       bcd_display_17_g, bcd_display_18_a, bcd_display_18_b, bcd_display_18_c, bcd_display_18_d,
       bcd_display_18_dp, bcd_display_18_e, bcd_display_18_f, bcd_display_18_g, bcd_display_19_a,
       bcd_display_19_b, bcd_display_19_c, bcd_display_19_d, bcd_display_19_dp, bcd_display_19_e,
       bcd_display_19_f, bcd_display_19_g, bcd_display_20_a, bcd_display_20_b, bcd_display_20_c,
       bcd_display_20_d, bcd_display_20_dp, bcd_display_20_e, bcd_display_20_f, bcd_display_20_g,
       bcd_display_21_a, bcd_display_21_b, bcd_display_21_c, bcd_display_21_d, bcd_display_21_dp,
       bcd_display_21_e, bcd_display_21_f, bcd_display_21_g, bin_display_1_led0, bin_display_1_led1,
       bin_display_1_led2, bin_display_1_led3, bin_display_1_led4, bin_display_1_led5, bin_display_1_led6,
       bin_display_1_led7, cin, clk, controlunit_1_ledclk, controlunit_1_ledclkr, controlunit_1_ledclkw,
       controlunit_1_ledhalt, controlunit_1_ledrst, controlunit_1_ledstep1, controlunit_1_ledstep2,
       controlunit_1_ledstep3, controlunit_1_ledstep4, controlunit_1_ledstep5, controlunit_1_ledstep6,
       dec_diplay_1_bcd1_0, dec_diplay_1_bcd1_1, dec_diplay_1_bcd1_2, dec_diplay_1_bcd1_3,
       dec_diplay_1_bcd10_0, dec_diplay_1_bcd10_1, dec_diplay_1_bcd10_2, dec_diplay_1_bcd10_3,
       dec_diplay_1_bcd100_0, dec_diplay_1_bcd100_1, dec_diplay_1_bcd100_2, dec_diplay_1_bcd100_3,
       dec_diplay_1_led0, dec_diplay_1_led1, dec_diplay_1_led2, dec_diplay_1_led3, dec_diplay_1_led4,
       dec_diplay_1_led5, dec_diplay_1_led6, dec_diplay_1_led7, dec_diplay_2_bcd1_0, dec_diplay_2_bcd1_1,
       dec_diplay_2_bcd1_2, dec_diplay_2_bcd1_3, dec_diplay_2_bcd10_0, dec_diplay_2_bcd10_1,
       dec_diplay_2_bcd10_2, dec_diplay_2_bcd10_3, dec_diplay_2_bcd100_0, dec_diplay_2_bcd100_1,
       dec_diplay_2_bcd100_2, dec_diplay_2_bcd100_3, dec_diplay_2_led0, dec_diplay_2_led1, dec_diplay_2_led2,
       dec_diplay_2_led3, dec_diplay_2_led4, dec_diplay_2_led5, dec_diplay_2_led6, dec_diplay_2_led7,
       dec_diplay_3_bcd1_0, dec_diplay_3_bcd1_1, dec_diplay_3_bcd1_2, dec_diplay_3_bcd1_3,
       dec_diplay_3_bcd10_0, dec_diplay_3_bcd10_1, dec_diplay_3_bcd10_2, dec_diplay_3_bcd10_3,
       dec_diplay_3_bcd100_0, dec_diplay_3_bcd100_1, dec_diplay_3_bcd100_2, dec_diplay_3_bcd100_3,
       dec_diplay_3_led0, dec_diplay_3_led1, dec_diplay_3_led2, dec_diplay_3_led3, dec_diplay_3_led4,
       dec_diplay_3_led5, dec_diplay_3_led6, dec_diplay_3_led7, dec_diplay_4_bcd1_0, dec_diplay_4_bcd1_1,
       dec_diplay_4_bcd1_2, dec_diplay_4_bcd1_3, dec_diplay_4_bcd10_0, dec_diplay_4_bcd10_1,
       dec_diplay_4_bcd10_2, dec_diplay_4_bcd10_3, dec_diplay_4_bcd100_0, dec_diplay_4_bcd100_1,
       dec_diplay_4_bcd100_2, dec_diplay_4_bcd100_3, dec_diplay_4_led0, dec_diplay_4_led1, dec_diplay_4_led2,
       dec_diplay_4_led3, dec_diplay_4_led4, dec_diplay_4_led5, dec_diplay_4_led6, dec_diplay_4_led7,
       dec_diplay_5_bcd1_0, dec_diplay_5_bcd1_1, dec_diplay_5_bcd1_2, dec_diplay_5_bcd1_3,
       dec_diplay_5_bcd10_0, dec_diplay_5_bcd10_1, dec_diplay_5_bcd10_2, dec_diplay_5_bcd10_3,
       dec_diplay_5_bcd100_0, dec_diplay_5_bcd100_1, dec_diplay_5_bcd100_2, dec_diplay_5_bcd100_3,
       dec_diplay_5_led0, dec_diplay_5_led1, dec_diplay_5_led2, dec_diplay_5_led3, dec_diplay_5_led4,
       dec_diplay_5_led5, dec_diplay_5_led6, dec_diplay_5_led7, dec_diplay_6_bcd1_0, dec_diplay_6_bcd1_1,
       dec_diplay_6_bcd1_2, dec_diplay_6_bcd1_3, dec_diplay_6_bcd10_0, dec_diplay_6_bcd10_1,
       dec_diplay_6_bcd10_2, dec_diplay_6_bcd10_3, dec_diplay_6_bcd100_0, dec_diplay_6_bcd100_1,
       dec_diplay_6_bcd100_2, dec_diplay_6_bcd100_3, dec_diplay_6_led0, dec_diplay_6_led1, dec_diplay_6_led2,
       dec_diplay_6_led3, dec_diplay_6_led4, dec_diplay_6_led5, dec_diplay_6_led6, dec_diplay_6_led7,
       dec_diplay_7_bcd1_0, dec_diplay_7_bcd1_1, dec_diplay_7_bcd1_2, dec_diplay_7_bcd1_3,
       dec_diplay_7_bcd10_0, dec_diplay_7_bcd10_1, dec_diplay_7_bcd10_2, dec_diplay_7_bcd10_3,
       dec_diplay_7_bcd100_0, dec_diplay_7_bcd100_1, dec_diplay_7_bcd100_2, dec_diplay_7_bcd100_3,
       dec_diplay_7_led0, dec_diplay_7_led1, dec_diplay_7_led2, dec_diplay_7_led3, dec_diplay_7_led4,
       dec_diplay_7_led5, dec_diplay_7_led6, dec_diplay_7_led7, fr_w, hex_display_1_led0, hex_display_1_led1,
       hex_display_1_led2, hex_display_1_led3, hex_display_1_led4, hex_display_1_led5, hex_display_1_led6,
       hex_display_1_led7, hex_display_2_led0, hex_display_2_led1, hex_display_2_led2, hex_display_2_led3,
       hex_display_2_led4, hex_display_2_led5, hex_display_2_led6, hex_display_2_led7, IR_led0, IR_led1,
       IR_led2, IR_led3, IR_led4, IR_led5, IR_led6, IR_led7, IR_ledr, IR_ledrst, IR_ledw, IR_out_0, IR_out_1,
       IR_out_2, IR_out_3, IR_out_4, IR_out_5, IR_out_6, IR_out_7, ir_w, MAR_led0, MAR_led1, MAR_led2,
       MAR_led3, MAR_led4, MAR_led5, MAR_led6, MAR_led7, MAR_ledr, MAR_ledrst, MAR_ledw, MAR_out_0,
       MAR_out_1, MAR_out_2, MAR_out_3, MAR_out_4, MAR_out_5, MAR_out_6, MAR_out_7, mar_w, mem_r, mem_w,
       memory_1_clk_out, memory_1_en_out, memory_1_ld_out, memory_1_ledr, memory_1_ledrst, memory_1_ledw,
       memory_1_rst_out, memory_1_str_out, op, PC_led0, PC_led1, PC_led2, PC_led3, PC_led4, PC_led5, PC_led6,
       PC_led7, PC_ledr, PC_ledrst, PC_ledw, pc_r, pc_w, R0_led0, R0_led1, R0_led2, R0_led3, R0_led4,
       R0_led5, R0_led6, R0_led7, R0_ledr, R0_ledrst, R0_ledw, R0_out_0, R0_out_1, R0_out_2, R0_out_3,
       R0_out_4, R0_out_5, R0_out_6, R0_out_7, r0_r, r0_w, R1_led0, R1_led1, R1_led2, R1_led3, R1_led4,
       R1_led5, R1_led6, R1_led7, R1_ledr, R1_ledrst, R1_ledw, r1_r, r1_w, R2_led0, R2_led1, R2_led2,
       R2_led3, R2_led4, R2_led5, R2_led6, R2_led7, R2_ledr, R2_ledrst, R2_ledw, r2_r, r2_w, R3_led0,
       R3_led1, R3_led2, R3_led3, R3_led4, R3_led5, R3_led6, R3_led7, R3_ledr, R3_ledrst, R3_ledw, r3_r,
       r3_w, RA_led0, RA_led1, RA_led2, RA_led3, RA_led4, RA_led5, RA_led6, RA_led7, RA_ledr, RA_ledrst,
       RA_ledw, RA_out_0, RA_out_1, RA_out_2, RA_out_3, RA_out_4, RA_out_5, RA_out_6, RA_out_7, ra_w,
       RD_led0, RD_led1, RD_led2, RD_led3, RD_led4, RD_led5, RD_led6, RD_led7, RD_ledr, RD_ledrst, RD_ledw,
       rd_r, rd_w, resume, Z_led, Z_ledr, Z_ledrst, Z_ledw, Z_out;
  wire [3:0] hex_display_1_lsn, hex_display_1_msn, hex_display_2_lsn, hex_display_2_msn;
  wire [7:0] memory_1_addr_out, memory_1_data_out, ram_1_data;
  wire [23:15] \µINSTR ;

  DEC_Diplay dec_diplay_1 (
    .BIN_0(R0_led0), .BIN_1(R0_led1), .BIN_2(R0_led2), .BIN_3(R0_led3), .BIN_4(R0_led4), .BIN_5(R0_led5),
    .BIN_6(R0_led6), .BIN_7(R0_led7), .BCD1_0(dec_diplay_1_bcd1_0), .BCD1_1(dec_diplay_1_bcd1_1),
    .BCD1_2(dec_diplay_1_bcd1_2), .BCD1_3(dec_diplay_1_bcd1_3), .BCD10_0(dec_diplay_1_bcd10_0),
    .BCD10_1(dec_diplay_1_bcd10_1), .BCD10_2(dec_diplay_1_bcd10_2), .BCD10_3(dec_diplay_1_bcd10_3),
    .BCD100_0(dec_diplay_1_bcd100_0), .BCD100_1(dec_diplay_1_bcd100_1), .BCD100_2(dec_diplay_1_bcd100_2),
    .BCD100_3(dec_diplay_1_bcd100_3), .LED0(dec_diplay_1_led0), .LED1(dec_diplay_1_led1),
    .LED2(dec_diplay_1_led2), .LED3(dec_diplay_1_led3), .LED4(dec_diplay_1_led4), .LED5(dec_diplay_1_led5),
    .LED6(dec_diplay_1_led6), .LED7(dec_diplay_1_led7));
  LED led_1 (.in(dec_diplay_1_led7));
  LED led_2 (.in(R0_ledw));
  BCD_Display bcd_display_1 (
    .BCD_0(dec_diplay_1_bcd100_0), .BCD_1(dec_diplay_1_bcd100_1), .BCD_2(dec_diplay_1_bcd100_2),
    .BCD_3(dec_diplay_1_bcd100_3), .a(bcd_display_1_a), .b(bcd_display_1_b), .c(bcd_display_1_c),
    .d(bcd_display_1_d), .e(bcd_display_1_e), .f(bcd_display_1_f), .g(bcd_display_1_g), .dp(bcd_display_1_dp));
  _7_Segment_Display u_7_segment_display_1 (
    .g(bcd_display_1_g), .f(bcd_display_1_f), .a(bcd_display_1_a), .b(bcd_display_1_b), .e(bcd_display_1_e),
    .d(bcd_display_1_d), .c(bcd_display_1_c), .dp(bcd_display_1_dp));
  LED led_3 (.in(R0_ledrst));
  LED led_4 (.in(R0_ledr));
  DEC_Diplay dec_diplay_2 (
    .BIN_0(RA_led0), .BIN_1(RA_led1), .BIN_2(RA_led2), .BIN_3(RA_led3), .BIN_4(RA_led4), .BIN_5(RA_led5),
    .BIN_6(RA_led6), .BIN_7(RA_led7), .BCD1_0(dec_diplay_2_bcd1_0), .BCD1_1(dec_diplay_2_bcd1_1),
    .BCD1_2(dec_diplay_2_bcd1_2), .BCD1_3(dec_diplay_2_bcd1_3), .BCD10_0(dec_diplay_2_bcd10_0),
    .BCD10_1(dec_diplay_2_bcd10_1), .BCD10_2(dec_diplay_2_bcd10_2), .BCD10_3(dec_diplay_2_bcd10_3),
    .BCD100_0(dec_diplay_2_bcd100_0), .BCD100_1(dec_diplay_2_bcd100_1), .BCD100_2(dec_diplay_2_bcd100_2),
    .BCD100_3(dec_diplay_2_bcd100_3), .LED0(dec_diplay_2_led0), .LED1(dec_diplay_2_led1),
    .LED2(dec_diplay_2_led2), .LED3(dec_diplay_2_led3), .LED4(dec_diplay_2_led4), .LED5(dec_diplay_2_led5),
    .LED6(dec_diplay_2_led6), .LED7(dec_diplay_2_led7));
  LED led_5 (.in(dec_diplay_2_led7));
  LED led_6 (.in(RA_ledw));
  BCD_Display bcd_display_2 (
    .BCD_0(dec_diplay_2_bcd100_0), .BCD_1(dec_diplay_2_bcd100_1), .BCD_2(dec_diplay_2_bcd100_2),
    .BCD_3(dec_diplay_2_bcd100_3), .a(bcd_display_2_a), .b(bcd_display_2_b), .c(bcd_display_2_c),
    .d(bcd_display_2_d), .e(bcd_display_2_e), .f(bcd_display_2_f), .g(bcd_display_2_g), .dp(bcd_display_2_dp));
  _7_Segment_Display u_7_segment_display_2 (
    .g(bcd_display_2_g), .f(bcd_display_2_f), .a(bcd_display_2_a), .b(bcd_display_2_b), .e(bcd_display_2_e),
    .d(bcd_display_2_d), .c(bcd_display_2_c), .dp(bcd_display_2_dp));
  LED led_7 (.in(RA_ledrst));
  LED led_8 (.in(RA_ledr));
  LED led_9 (.in(dec_diplay_1_led3));
  LED led_10 (.in(dec_diplay_1_led4));
  LED led_11 (.in(dec_diplay_1_led6));
  LED led_12 (.in(dec_diplay_1_led5));
  BCD_Display bcd_display_3 (
    .BCD_0(dec_diplay_1_bcd10_0), .BCD_1(dec_diplay_1_bcd10_1), .BCD_2(dec_diplay_1_bcd10_2),
    .BCD_3(dec_diplay_1_bcd10_3), .a(bcd_display_3_a), .b(bcd_display_3_b), .c(bcd_display_3_c),
    .d(bcd_display_3_d), .e(bcd_display_3_e), .f(bcd_display_3_f), .g(bcd_display_3_g), .dp(bcd_display_3_dp));
  _7_Segment_Display u_7_segment_display_3 (
    .g(bcd_display_3_g), .f(bcd_display_3_f), .a(bcd_display_3_a), .b(bcd_display_3_b), .e(bcd_display_3_e),
    .d(bcd_display_3_d), .c(bcd_display_3_c), .dp(bcd_display_3_dp));
  Reg8 R0 (
    .read(r0_r), .write(r0_w), .nrst(in_1), .IN_7(R0_out_7), .IN_6(R0_out_6), .IN_5(R0_out_5),
    .IN_4(R0_out_4), .IN_3(R0_out_3), .IN_2(R0_out_2), .IN_1(R0_out_1), .IN_0(R0_out_0), .OUT_7(R0_out_7),
    .OUT_6(R0_out_6), .OUT_5(R0_out_5), .OUT_4(R0_out_4), .OUT_3(R0_out_3), .OUT_2(R0_out_2),
    .OUT_1(R0_out_1), .OUT_0(R0_out_0), .LEDr(R0_ledr), .LEDw(R0_ledw), .LEDrst(R0_ledrst), .LED0(R0_led0),
    .LED1(R0_led1), .LED2(R0_led2), .LED3(R0_led3), .LED4(R0_led4), .LED5(R0_led5), .LED6(R0_led6),
    .LED7(R0_led7));
  LED led_13 (.in(dec_diplay_2_led5));
  LED led_14 (.in(dec_diplay_2_led3));
  LED led_15 (.in(dec_diplay_2_led6));
  LED led_16 (.in(dec_diplay_2_led4));
  BCD_Display bcd_display_4 (
    .BCD_0(dec_diplay_2_bcd10_0), .BCD_1(dec_diplay_2_bcd10_1), .BCD_2(dec_diplay_2_bcd10_2),
    .BCD_3(dec_diplay_2_bcd10_3), .a(bcd_display_4_a), .b(bcd_display_4_b), .c(bcd_display_4_c),
    .d(bcd_display_4_d), .e(bcd_display_4_e), .f(bcd_display_4_f), .g(bcd_display_4_g), .dp(bcd_display_4_dp));
  _7_Segment_Display u_7_segment_display_4 (
    .g(bcd_display_4_g), .f(bcd_display_4_f), .a(bcd_display_4_a), .b(bcd_display_4_b), .e(bcd_display_4_e),
    .d(bcd_display_4_d), .c(bcd_display_4_c), .dp(bcd_display_4_dp));
  Reg8 RA (
    .read(1'b1), .write(ra_w), .nrst(in_1), .IN_7(R0_out_7), .IN_6(R0_out_6), .IN_5(R0_out_5),
    .IN_4(R0_out_4), .IN_3(R0_out_3), .IN_2(R0_out_2), .IN_1(R0_out_1), .IN_0(R0_out_0), .OUT_7(RA_out_7),
    .OUT_6(RA_out_6), .OUT_5(RA_out_5), .OUT_4(RA_out_4), .OUT_3(RA_out_3), .OUT_2(RA_out_2),
    .OUT_1(RA_out_1), .OUT_0(RA_out_0), .LEDr(RA_ledr), .LEDw(RA_ledw), .LEDrst(RA_ledrst), .LED0(RA_led0),
    .LED1(RA_led1), .LED2(RA_led2), .LED3(RA_led3), .LED4(RA_led4), .LED5(RA_led5), .LED6(RA_led6),
    .LED7(RA_led7));
  LED led_17 (.in(dec_diplay_1_led1));
  LED led_18 (.in(dec_diplay_1_led0));
  LED led_19 (.in(dec_diplay_1_led2));
  BCD_Display bcd_display_5 (
    .BCD_0(dec_diplay_1_bcd1_0), .BCD_1(dec_diplay_1_bcd1_1), .BCD_2(dec_diplay_1_bcd1_2),
    .BCD_3(dec_diplay_1_bcd1_3), .a(bcd_display_5_a), .b(bcd_display_5_b), .c(bcd_display_5_c),
    .d(bcd_display_5_d), .e(bcd_display_5_e), .f(bcd_display_5_f), .g(bcd_display_5_g), .dp(bcd_display_5_dp));
  _7_Segment_Display u_7_segment_display_5 (
    .g(bcd_display_5_g), .f(bcd_display_5_f), .a(bcd_display_5_a), .b(bcd_display_5_b), .e(bcd_display_5_e),
    .d(bcd_display_5_d), .c(bcd_display_5_c), .dp(bcd_display_5_dp));
  LED led_20 (.in(dec_diplay_2_led1));
  LED led_21 (.in(dec_diplay_2_led0));
  LED led_22 (.in(dec_diplay_2_led2));
  BCD_Display bcd_display_6 (
    .BCD_0(dec_diplay_2_bcd1_0), .BCD_1(dec_diplay_2_bcd1_1), .BCD_2(dec_diplay_2_bcd1_2),
    .BCD_3(dec_diplay_2_bcd1_3), .a(bcd_display_6_a), .b(bcd_display_6_b), .c(bcd_display_6_c),
    .d(bcd_display_6_d), .e(bcd_display_6_e), .f(bcd_display_6_f), .g(bcd_display_6_g), .dp(bcd_display_6_dp));
  _7_Segment_Display u_7_segment_display_6 (
    .g(bcd_display_6_g), .f(bcd_display_6_f), .a(bcd_display_6_a), .b(bcd_display_6_b), .e(bcd_display_6_e),
    .d(bcd_display_6_d), .c(bcd_display_6_c), .dp(bcd_display_6_dp));
  DEC_Diplay dec_diplay_3 (
    .BIN_0(RD_led0), .BIN_1(RD_led1), .BIN_2(RD_led2), .BIN_3(RD_led3), .BIN_4(RD_led4), .BIN_5(RD_led5),
    .BIN_6(RD_led6), .BIN_7(RD_led7), .BCD1_0(dec_diplay_3_bcd1_0), .BCD1_1(dec_diplay_3_bcd1_1),
    .BCD1_2(dec_diplay_3_bcd1_2), .BCD1_3(dec_diplay_3_bcd1_3), .BCD10_0(dec_diplay_3_bcd10_0),
    .BCD10_1(dec_diplay_3_bcd10_1), .BCD10_2(dec_diplay_3_bcd10_2), .BCD10_3(dec_diplay_3_bcd10_3),
    .BCD100_0(dec_diplay_3_bcd100_0), .BCD100_1(dec_diplay_3_bcd100_1), .BCD100_2(dec_diplay_3_bcd100_2),
    .BCD100_3(dec_diplay_3_bcd100_3), .LED0(dec_diplay_3_led0), .LED1(dec_diplay_3_led1),
    .LED2(dec_diplay_3_led2), .LED3(dec_diplay_3_led3), .LED4(dec_diplay_3_led4), .LED5(dec_diplay_3_led5),
    .LED6(dec_diplay_3_led6), .LED7(dec_diplay_3_led7));
  LED led_23 (.in(dec_diplay_3_led7));
  LED led_24 (.in(RD_ledw));
  BCD_Display bcd_display_7 (
    .BCD_0(dec_diplay_3_bcd100_0), .BCD_1(dec_diplay_3_bcd100_1), .BCD_2(dec_diplay_3_bcd100_2),
    .BCD_3(dec_diplay_3_bcd100_3), .a(bcd_display_7_a), .b(bcd_display_7_b), .c(bcd_display_7_c),
    .d(bcd_display_7_d), .e(bcd_display_7_e), .f(bcd_display_7_f), .g(bcd_display_7_g), .dp(bcd_display_7_dp));
  LED led_25 (.in(RD_ledrst));
  LED led_26 (.in(RD_ledr));
  ALU_2 alu_1 (
    .a_0(RA_out_0), .a_1(RA_out_1), .a_2(RA_out_2), .a_3(RA_out_3), .a_4(RA_out_4), .a_5(RA_out_5),
    .a_6(RA_out_6), .a_7(RA_out_7), .zero(alu_1_zero), .b_0(B_out_0), .b_1(B_out_1), .b_2(B_out_2),
    .b_3(B_out_3), .b_4(B_out_4), .b_5(B_out_5), .b_6(B_out_6), .b_7(B_out_7), .op(op), .cin(cin),
    .sum_0(alu_1_sum_0), .sum_1(alu_1_sum_1), .sum_2(alu_1_sum_2), .sum_3(alu_1_sum_3), .sum_4(alu_1_sum_4),
    .sum_5(alu_1_sum_5), .sum_6(alu_1_sum_6), .sum_7(alu_1_sum_7), .LEDcin(alu_1_ledcin),
    .LEDop(alu_1_ledop), .LEDz(alu_1_ledz));
  LED led_27 (.in(alu_1_ledop));
  LED led_28 (.in(dec_diplay_3_led6));
  LED led_29 (.in(dec_diplay_3_led5));
  LED led_30 (.in(dec_diplay_3_led4));
  BCD_Display bcd_display_8 (
    .BCD_0(dec_diplay_3_bcd10_0), .BCD_1(dec_diplay_3_bcd10_1), .BCD_2(dec_diplay_3_bcd10_2),
    .BCD_3(dec_diplay_3_bcd10_3), .a(bcd_display_8_a), .b(bcd_display_8_b), .c(bcd_display_8_c),
    .d(bcd_display_8_d), .e(bcd_display_8_e), .f(bcd_display_8_f), .g(bcd_display_8_g), .dp(bcd_display_8_dp));
  _7_Segment_Display u_7_segment_display_7 (
    .g(bcd_display_7_g), .f(bcd_display_7_f), .a(bcd_display_7_a), .b(bcd_display_7_b), .e(bcd_display_7_e),
    .d(bcd_display_7_d), .c(bcd_display_7_c), .dp(bcd_display_7_dp));
  _7_Segment_Display u_7_segment_display_8 (
    .g(bcd_display_8_g), .f(bcd_display_8_f), .a(bcd_display_8_a), .b(bcd_display_8_b), .e(bcd_display_8_e),
    .d(bcd_display_8_d), .c(bcd_display_8_c), .dp(bcd_display_8_dp));
  Reg8 RD (
    .read(rd_r), .write(rd_w), .nrst(in_1), .IN_7(alu_1_sum_7), .IN_6(alu_1_sum_6), .IN_5(alu_1_sum_5),
    .IN_4(alu_1_sum_4), .IN_3(alu_1_sum_3), .IN_2(alu_1_sum_2), .IN_1(alu_1_sum_1), .IN_0(alu_1_sum_0),
    .OUT_7(R0_out_7), .OUT_6(R0_out_6), .OUT_5(R0_out_5), .OUT_4(R0_out_4), .OUT_3(R0_out_3),
    .OUT_2(R0_out_2), .OUT_1(R0_out_1), .OUT_0(R0_out_0), .LEDr(RD_ledr), .LEDw(RD_ledw), .LEDrst(RD_ledrst),
    .LED0(RD_led0), .LED1(RD_led1), .LED2(RD_led2), .LED3(RD_led3), .LED4(RD_led4), .LED5(RD_led5),
    .LED6(RD_led6), .LED7(RD_led7));
  DEC_Diplay dec_diplay_4 (
    .BIN_0(R1_led0), .BIN_1(R1_led1), .BIN_2(R1_led2), .BIN_3(R1_led3), .BIN_4(R1_led4), .BIN_5(R1_led5),
    .BIN_6(R1_led6), .BIN_7(R1_led7), .BCD1_0(dec_diplay_4_bcd1_0), .BCD1_1(dec_diplay_4_bcd1_1),
    .BCD1_2(dec_diplay_4_bcd1_2), .BCD1_3(dec_diplay_4_bcd1_3), .BCD10_0(dec_diplay_4_bcd10_0),
    .BCD10_1(dec_diplay_4_bcd10_1), .BCD10_2(dec_diplay_4_bcd10_2), .BCD10_3(dec_diplay_4_bcd10_3),
    .BCD100_0(dec_diplay_4_bcd100_0), .BCD100_1(dec_diplay_4_bcd100_1), .BCD100_2(dec_diplay_4_bcd100_2),
    .BCD100_3(dec_diplay_4_bcd100_3), .LED0(dec_diplay_4_led0), .LED1(dec_diplay_4_led1),
    .LED2(dec_diplay_4_led2), .LED3(dec_diplay_4_led3), .LED4(dec_diplay_4_led4), .LED5(dec_diplay_4_led5),
    .LED6(dec_diplay_4_led6), .LED7(dec_diplay_4_led7));
  LED led_31 (.in(R1_ledw));
  LED led_32 (.in(R1_ledrst));
  LED led_33 (.in(R1_ledr));
  DEC_Diplay dec_diplay_5 (
    .BIN_0(B_led0), .BIN_1(B_led1), .BIN_2(B_led2), .BIN_3(B_led3), .BIN_4(B_led4), .BIN_5(B_led5),
    .BIN_6(B_led6), .BIN_7(B_led7), .BCD1_0(dec_diplay_5_bcd1_0), .BCD1_1(dec_diplay_5_bcd1_1),
    .BCD1_2(dec_diplay_5_bcd1_2), .BCD1_3(dec_diplay_5_bcd1_3), .BCD10_0(dec_diplay_5_bcd10_0),
    .BCD10_1(dec_diplay_5_bcd10_1), .BCD10_2(dec_diplay_5_bcd10_2), .BCD10_3(dec_diplay_5_bcd10_3),
    .BCD100_0(dec_diplay_5_bcd100_0), .BCD100_1(dec_diplay_5_bcd100_1), .BCD100_2(dec_diplay_5_bcd100_2),
    .BCD100_3(dec_diplay_5_bcd100_3), .LED0(dec_diplay_5_led0), .LED1(dec_diplay_5_led1),
    .LED2(dec_diplay_5_led2), .LED3(dec_diplay_5_led3), .LED4(dec_diplay_5_led4), .LED5(dec_diplay_5_led5),
    .LED6(dec_diplay_5_led6), .LED7(dec_diplay_5_led7));
  LED led_34 (.in(B_leden));
  LED led_35 (.in(alu_1_ledcin));
  LED led_36 (.in(dec_diplay_3_led0));
  LED led_37 (.in(dec_diplay_3_led2));
  LED led_38 (.in(dec_diplay_3_led1));
  LED led_39 (.in(dec_diplay_3_led3));
  BCD_Display bcd_display_9 (
    .BCD_0(dec_diplay_3_bcd1_0), .BCD_1(dec_diplay_3_bcd1_1), .BCD_2(dec_diplay_3_bcd1_2),
    .BCD_3(dec_diplay_3_bcd1_3), .a(bcd_display_9_a), .b(bcd_display_9_b), .c(bcd_display_9_c),
    .d(bcd_display_9_d), .e(bcd_display_9_e), .f(bcd_display_9_f), .g(bcd_display_9_g), .dp(bcd_display_9_dp));
  _7_Segment_Display u_7_segment_display_9 (
    .g(bcd_display_9_g), .f(bcd_display_9_f), .a(bcd_display_9_a), .b(bcd_display_9_b), .e(bcd_display_9_e),
    .d(bcd_display_9_d), .c(bcd_display_9_c), .dp(bcd_display_9_dp));
  LED led_40 (.in(dec_diplay_4_led6));
  LED led_41 (.in(dec_diplay_4_led4));
  LED led_42 (.in(dec_diplay_4_led5));
  LED led_43 (.in(dec_diplay_4_led7));
  BCD_Display bcd_display_10 (
    .BCD_0(dec_diplay_4_bcd10_0), .BCD_1(dec_diplay_4_bcd10_1), .BCD_2(dec_diplay_4_bcd10_2),
    .BCD_3(dec_diplay_4_bcd10_3), .a(bcd_display_10_a), .b(bcd_display_10_b), .c(bcd_display_10_c),
    .d(bcd_display_10_d), .e(bcd_display_10_e), .f(bcd_display_10_f), .g(bcd_display_10_g),
    .dp(bcd_display_10_dp));
  BCD_Display bcd_display_11 (
    .BCD_0(dec_diplay_4_bcd100_0), .BCD_1(dec_diplay_4_bcd100_1), .BCD_2(dec_diplay_4_bcd100_2),
    .BCD_3(dec_diplay_4_bcd100_3), .a(bcd_display_11_a), .b(bcd_display_11_b), .c(bcd_display_11_c),
    .d(bcd_display_11_d), .e(bcd_display_11_e), .f(bcd_display_11_f), .g(bcd_display_11_g),
    .dp(bcd_display_11_dp));
  _7_Segment_Display u_7_segment_display_10 (
    .g(bcd_display_10_g), .f(bcd_display_10_f), .a(bcd_display_10_a), .b(bcd_display_10_b),
    .e(bcd_display_10_e), .d(bcd_display_10_d), .c(bcd_display_10_c), .dp(bcd_display_10_dp));
  _7_Segment_Display u_7_segment_display_11 (
    .g(bcd_display_11_g), .f(bcd_display_11_f), .a(bcd_display_11_a), .b(bcd_display_11_b),
    .e(bcd_display_11_e), .d(bcd_display_11_d), .c(bcd_display_11_c), .dp(bcd_display_11_dp));
  Reg8 R1 (
    .read(r1_r), .write(r1_w), .nrst(in_1), .IN_7(R0_out_7), .IN_6(R0_out_6), .IN_5(R0_out_5),
    .IN_4(R0_out_4), .IN_3(R0_out_3), .IN_2(R0_out_2), .IN_1(R0_out_1), .IN_0(R0_out_0), .OUT_7(R0_out_7),
    .OUT_6(R0_out_6), .OUT_5(R0_out_5), .OUT_4(R0_out_4), .OUT_3(R0_out_3), .OUT_2(R0_out_2),
    .OUT_1(R0_out_1), .OUT_0(R0_out_0), .LEDr(R1_ledr), .LEDw(R1_ledw), .LEDrst(R1_ledrst), .LED0(R1_led0),
    .LED1(R1_led1), .LED2(R1_led2), .LED3(R1_led3), .LED4(R1_led4), .LED5(R1_led5), .LED6(R1_led6),
    .LED7(R1_led7));
  LED led_44 (.in(dec_diplay_5_led5));
  LED led_45 (.in(dec_diplay_5_led6));
  LED led_46 (.in(dec_diplay_5_led4));
  LED led_47 (.in(dec_diplay_5_led7));
  BCD_Display bcd_display_12 (
    .BCD_0(dec_diplay_5_bcd10_0), .BCD_1(dec_diplay_5_bcd10_1), .BCD_2(dec_diplay_5_bcd10_2),
    .BCD_3(dec_diplay_5_bcd10_3), .a(bcd_display_12_a), .b(bcd_display_12_b), .c(bcd_display_12_c),
    .d(bcd_display_12_d), .e(bcd_display_12_e), .f(bcd_display_12_f), .g(bcd_display_12_g),
    .dp(bcd_display_12_dp));
  BCD_Display bcd_display_13 (
    .BCD_0(dec_diplay_5_bcd100_0), .BCD_1(dec_diplay_5_bcd100_1), .BCD_2(dec_diplay_5_bcd100_2),
    .BCD_3(dec_diplay_5_bcd100_3), .a(bcd_display_13_a), .b(bcd_display_13_b), .c(bcd_display_13_c),
    .d(bcd_display_13_d), .e(bcd_display_13_e), .f(bcd_display_13_f), .g(bcd_display_13_g),
    .dp(bcd_display_13_dp));
  _7_Segment_Display u_7_segment_display_12 (
    .g(bcd_display_12_g), .f(bcd_display_12_f), .a(bcd_display_12_a), .b(bcd_display_12_b),
    .e(bcd_display_12_e), .d(bcd_display_12_d), .c(bcd_display_12_c), .dp(bcd_display_12_dp));
  _7_Segment_Display u_7_segment_display_13 (
    .g(bcd_display_13_g), .f(bcd_display_13_f), .a(bcd_display_13_a), .b(bcd_display_13_b),
    .e(bcd_display_13_e), .d(bcd_display_13_d), .c(bcd_display_13_c), .dp(bcd_display_13_dp));
  ZeroPass8 B (
    .enable(b_en), .LEDen(B_leden), .LED7(B_led7), .LED6(B_led6), .LED5(B_led5), .LED4(B_led4),
    .LED3(B_led3), .LED2(B_led2), .LED1(B_led1), .LED0(B_led0), .IN_7(R0_out_7), .IN_6(R0_out_6),
    .IN_5(R0_out_5), .IN_4(R0_out_4), .IN_3(R0_out_3), .IN_2(R0_out_2), .IN_1(R0_out_1), .IN_0(R0_out_0),
    .OUT_7(B_out_7), .OUT_6(B_out_6), .OUT_5(B_out_5), .OUT_4(B_out_4), .OUT_3(B_out_3), .OUT_2(B_out_2),
    .OUT_1(B_out_1), .OUT_0(B_out_0));
  LED led_48 (.in(alu_1_ledz));
  LED led_49 (.in(dec_diplay_4_led1));
  LED led_50 (.in(dec_diplay_4_led0));
  LED led_51 (.in(dec_diplay_4_led2));
  LED led_52 (.in(dec_diplay_4_led3));
  BCD_Display bcd_display_14 (
    .BCD_0(dec_diplay_4_bcd1_0), .BCD_1(dec_diplay_4_bcd1_1), .BCD_2(dec_diplay_4_bcd1_2),
    .BCD_3(dec_diplay_4_bcd1_3), .a(bcd_display_14_a), .b(bcd_display_14_b), .c(bcd_display_14_c),
    .d(bcd_display_14_d), .e(bcd_display_14_e), .f(bcd_display_14_f), .g(bcd_display_14_g),
    .dp(bcd_display_14_dp));
  _7_Segment_Display u_7_segment_display_14 (
    .g(bcd_display_14_g), .f(bcd_display_14_f), .a(bcd_display_14_a), .b(bcd_display_14_b),
    .e(bcd_display_14_e), .d(bcd_display_14_d), .c(bcd_display_14_c), .dp(bcd_display_14_dp));
  LED led_53 (.in(dec_diplay_5_led2));
  LED led_54 (.in(dec_diplay_5_led1));
  LED led_55 (.in(dec_diplay_5_led3));
  LED led_56 (.in(dec_diplay_5_led0));
  BCD_Display bcd_display_15 (
    .BCD_0(dec_diplay_5_bcd1_0), .BCD_1(dec_diplay_5_bcd1_1), .BCD_2(dec_diplay_5_bcd1_2),
    .BCD_3(dec_diplay_5_bcd1_3), .a(bcd_display_15_a), .b(bcd_display_15_b), .c(bcd_display_15_c),
    .d(bcd_display_15_d), .e(bcd_display_15_e), .f(bcd_display_15_f), .g(bcd_display_15_g),
    .dp(bcd_display_15_dp));
  _7_Segment_Display u_7_segment_display_15 (
    .g(bcd_display_15_g), .f(bcd_display_15_f), .a(bcd_display_15_a), .b(bcd_display_15_b),
    .e(bcd_display_15_e), .d(bcd_display_15_d), .c(bcd_display_15_c), .dp(bcd_display_15_dp));
  LED led_57 (.in(Z_ledw));
  Reg1 Z (
    .IN(alu_1_zero), .read(1'b1), .write(fr_w), .nrst(in_1), .LED(Z_led), .OUT(Z_out), .LEDr(Z_ledr),
    .LEDw(Z_ledw), .LEDrst(Z_ledrst));
  LED led_58 (.in(Z_ledrst));
  LED led_59 (.in(Z_led));
  LED led_60 (.in(Z_ledr));
  Clock_part clock_1 (.out(clk));
  LED led_61 (.in(R2_ledw));
  LED led_62 (.in(R2_ledrst));
  LED led_63 (.in(R2_ledr));
  LED led_64 (.in(IR_ledw));
  LED led_65 (.in(IR_ledrst));
  LED led_66 (.in(IR_ledr));
  ControlUnit controlunit_1 (
    .INSTR_0(IR_out_0), .INSTR_1(IR_out_1), .INSTR_2(IR_out_2), .INSTR_3(IR_out_3), .INSTR_4(IR_out_4),
    .INSTR_5(IR_out_5), .INSTR_6(IR_out_6), .INSTR_7(IR_out_7), .FLAG_z(Z_out),
    .\µINSTR ({\µINSTR [23], mem_r, mem_w, mar_w, \µINSTR [19], ir_w, pc_r, pc_w, \µINSTR [15], fr_w, op, cin, rd_r, rd_w, ra_w, b_en, r3_r, r3_w, r2_r, r2_w, r1_r, r1_w, r0_r, r0_w}),
    .clk(clk), .nrst(in_1), .LEDclk(controlunit_1_ledclk), .LEDrst(controlunit_1_ledrst),
    .LEDclkw(controlunit_1_ledclkw), .LEDclkr(controlunit_1_ledclkr), .LEDstep1(controlunit_1_ledstep1),
    .LEDstep2(controlunit_1_ledstep2), .LEDstep3(controlunit_1_ledstep3), .LEDstep4(controlunit_1_ledstep4),
    .LEDstep5(controlunit_1_ledstep5), .LEDstep6(controlunit_1_ledstep6), .LEDhalt(controlunit_1_ledhalt),
    .resume(resume));
  LED led_67 (.in(controlunit_1_ledclk));
  LED led_68 (.in(controlunit_1_ledrst));
  Button button_1 (.out(resume));
  DEC_Diplay dec_diplay_6 (
    .BIN_0(R2_led0), .BIN_1(R2_led1), .BIN_2(R2_led2), .BIN_3(R2_led3), .BIN_4(R2_led4), .BIN_5(R2_led5),
    .BIN_6(R2_led6), .BIN_7(R2_led7), .BCD1_0(dec_diplay_6_bcd1_0), .BCD1_1(dec_diplay_6_bcd1_1),
    .BCD1_2(dec_diplay_6_bcd1_2), .BCD1_3(dec_diplay_6_bcd1_3), .BCD10_0(dec_diplay_6_bcd10_0),
    .BCD10_1(dec_diplay_6_bcd10_1), .BCD10_2(dec_diplay_6_bcd10_2), .BCD10_3(dec_diplay_6_bcd10_3),
    .BCD100_0(dec_diplay_6_bcd100_0), .BCD100_1(dec_diplay_6_bcd100_1), .BCD100_2(dec_diplay_6_bcd100_2),
    .BCD100_3(dec_diplay_6_bcd100_3), .LED0(dec_diplay_6_led0), .LED1(dec_diplay_6_led1),
    .LED2(dec_diplay_6_led2), .LED3(dec_diplay_6_led3), .LED4(dec_diplay_6_led4), .LED5(dec_diplay_6_led5),
    .LED6(dec_diplay_6_led6), .LED7(dec_diplay_6_led7));
  LED led_69 (.in(dec_diplay_6_led7));
  LED led_70 (.in(dec_diplay_6_led5));
  LED led_71 (.in(dec_diplay_6_led6));
  BCD_Display bcd_display_16 (
    .BCD_0(dec_diplay_6_bcd100_0), .BCD_1(dec_diplay_6_bcd100_1), .BCD_2(dec_diplay_6_bcd100_2),
    .BCD_3(dec_diplay_6_bcd100_3), .a(bcd_display_16_a), .b(bcd_display_16_b), .c(bcd_display_16_c),
    .d(bcd_display_16_d), .e(bcd_display_16_e), .f(bcd_display_16_f), .g(bcd_display_16_g),
    .dp(bcd_display_16_dp));
  BCD_Display bcd_display_17 (
    .BCD_0(dec_diplay_6_bcd10_0), .BCD_1(dec_diplay_6_bcd10_1), .BCD_2(dec_diplay_6_bcd10_2),
    .BCD_3(dec_diplay_6_bcd10_3), .a(bcd_display_17_a), .b(bcd_display_17_b), .c(bcd_display_17_c),
    .d(bcd_display_17_d), .e(bcd_display_17_e), .f(bcd_display_17_f), .g(bcd_display_17_g),
    .dp(bcd_display_17_dp));
  _7_Segment_Display u_7_segment_display_16 (
    .g(bcd_display_16_g), .f(bcd_display_16_f), .a(bcd_display_16_a), .b(bcd_display_16_b),
    .e(bcd_display_16_e), .d(bcd_display_16_d), .c(bcd_display_16_c), .dp(bcd_display_16_dp));
  BIN_Display bin_display_1 (
    .IN_0(IR_led0), .IN_1(IR_led1), .IN_2(IR_led2), .IN_3(IR_led3), .IN_4(IR_led4), .IN_5(IR_led5),
    .IN_6(IR_led6), .IN_7(IR_led7), .LED0(bin_display_1_led0), .LED1(bin_display_1_led1),
    .LED2(bin_display_1_led2), .LED3(bin_display_1_led3), .LED4(bin_display_1_led4),
    .LED5(bin_display_1_led5), .LED6(bin_display_1_led6), .LED7(bin_display_1_led7));
  LED led_72 (.in(bin_display_1_led7));
  LED led_73 (.in(bin_display_1_led6));
  LED led_74 (.in(bin_display_1_led5));
  LED led_75 (.in(controlunit_1_ledhalt));
  LED led_76 (.in(controlunit_1_ledclkr));
  LED led_77 (.in(controlunit_1_ledclkw));
  LED led_78 (.in(dec_diplay_6_led1));
  LED led_79 (.in(dec_diplay_6_led3));
  LED led_80 (.in(dec_diplay_6_led2));
  LED led_81 (.in(dec_diplay_6_led4));
  BCD_Display bcd_display_18 (
    .BCD_0(dec_diplay_6_bcd1_0), .BCD_1(dec_diplay_6_bcd1_1), .BCD_2(dec_diplay_6_bcd1_2),
    .BCD_3(dec_diplay_6_bcd1_3), .a(bcd_display_18_a), .b(bcd_display_18_b), .c(bcd_display_18_c),
    .d(bcd_display_18_d), .e(bcd_display_18_e), .f(bcd_display_18_f), .g(bcd_display_18_g),
    .dp(bcd_display_18_dp));
  _7_Segment_Display u_7_segment_display_17 (
    .g(bcd_display_17_g), .f(bcd_display_17_f), .a(bcd_display_17_a), .b(bcd_display_17_b),
    .e(bcd_display_17_e), .d(bcd_display_17_d), .c(bcd_display_17_c), .dp(bcd_display_17_dp));
  _7_Segment_Display u_7_segment_display_18 (
    .g(bcd_display_18_g), .f(bcd_display_18_f), .a(bcd_display_18_a), .b(bcd_display_18_b),
    .e(bcd_display_18_e), .d(bcd_display_18_d), .c(bcd_display_18_c), .dp(bcd_display_18_dp));
  Reg8 R2 (
    .read(r2_r), .write(r2_w), .nrst(in_1), .IN_7(R0_out_7), .IN_6(R0_out_6), .IN_5(R0_out_5),
    .IN_4(R0_out_4), .IN_3(R0_out_3), .IN_2(R0_out_2), .IN_1(R0_out_1), .IN_0(R0_out_0), .OUT_7(R0_out_7),
    .OUT_6(R0_out_6), .OUT_5(R0_out_5), .OUT_4(R0_out_4), .OUT_3(R0_out_3), .OUT_2(R0_out_2),
    .OUT_1(R0_out_1), .OUT_0(R0_out_0), .LEDr(R2_ledr), .LEDw(R2_ledw), .LEDrst(R2_ledrst), .LED0(R2_led0),
    .LED1(R2_led1), .LED2(R2_led2), .LED3(R2_led3), .LED4(R2_led4), .LED5(R2_led5), .LED6(R2_led6),
    .LED7(R2_led7));
  LED led_82 (.in(bin_display_1_led2));
  LED led_83 (.in(bin_display_1_led1));
  LED led_84 (.in(bin_display_1_led4));
  LED led_85 (.in(bin_display_1_led3));
  Reg8 IR (
    .read(1'b1), .write(ir_w), .nrst(in_1), .IN_7(R0_out_7), .IN_6(R0_out_6), .IN_5(R0_out_5),
    .IN_4(R0_out_4), .IN_3(R0_out_3), .IN_2(R0_out_2), .IN_1(R0_out_1), .IN_0(R0_out_0), .OUT_7(IR_out_7),
    .OUT_6(IR_out_6), .OUT_5(IR_out_5), .OUT_4(IR_out_4), .OUT_3(IR_out_3), .OUT_2(IR_out_2),
    .OUT_1(IR_out_1), .OUT_0(IR_out_0), .LEDr(IR_ledr), .LEDw(IR_ledw), .LEDrst(IR_ledrst), .LED0(IR_led0),
    .LED1(IR_led1), .LED2(IR_led2), .LED3(IR_led3), .LED4(IR_led4), .LED5(IR_led5), .LED6(IR_led6),
    .LED7(IR_led7));
  LED led_86 (.in(controlunit_1_ledstep2));
  LED led_87 (.in(controlunit_1_ledstep3));
  LED led_88 (.in(controlunit_1_ledstep1));
  LED led_89 (.in(dec_diplay_6_led0));
  LED led_90 (.in(bin_display_1_led0));
  LED led_91 (.in(controlunit_1_ledstep5));
  LED led_92 (.in(controlunit_1_ledstep6));
  LED led_93 (.in(controlunit_1_ledstep4));
  LED led_94 (.in(R3_ledw));
  LED led_95 (.in(R3_ledrst));
  LED led_96 (.in(R3_ledr));
  LED led_97 (.in(PC_ledw));
  LED led_98 (.in(PC_ledrst));
  LED led_99 (.in(PC_ledr));
  DEC_Diplay dec_diplay_7 (
    .BIN_0(R3_led0), .BIN_1(R3_led1), .BIN_2(R3_led2), .BIN_3(R3_led3), .BIN_4(R3_led4), .BIN_5(R3_led5),
    .BIN_6(R3_led6), .BIN_7(R3_led7), .BCD1_0(dec_diplay_7_bcd1_0), .BCD1_1(dec_diplay_7_bcd1_1),
    .BCD1_2(dec_diplay_7_bcd1_2), .BCD1_3(dec_diplay_7_bcd1_3), .BCD10_0(dec_diplay_7_bcd10_0),
    .BCD10_1(dec_diplay_7_bcd10_1), .BCD10_2(dec_diplay_7_bcd10_2), .BCD10_3(dec_diplay_7_bcd10_3),
    .BCD100_0(dec_diplay_7_bcd100_0), .BCD100_1(dec_diplay_7_bcd100_1), .BCD100_2(dec_diplay_7_bcd100_2),
    .BCD100_3(dec_diplay_7_bcd100_3), .LED0(dec_diplay_7_led0), .LED1(dec_diplay_7_led1),
    .LED2(dec_diplay_7_led2), .LED3(dec_diplay_7_led3), .LED4(dec_diplay_7_led4), .LED5(dec_diplay_7_led5),
    .LED6(dec_diplay_7_led6), .LED7(dec_diplay_7_led7));
  LED led_100 (.in(dec_diplay_7_led7));
  LED led_101 (.in(dec_diplay_7_led6));
  BCD_Display bcd_display_19 (
    .BCD_0(dec_diplay_7_bcd100_0), .BCD_1(dec_diplay_7_bcd100_1), .BCD_2(dec_diplay_7_bcd100_2),
    .BCD_3(dec_diplay_7_bcd100_3), .a(bcd_display_19_a), .b(bcd_display_19_b), .c(bcd_display_19_c),
    .d(bcd_display_19_d), .e(bcd_display_19_e), .f(bcd_display_19_f), .g(bcd_display_19_g),
    .dp(bcd_display_19_dp));
  _7_Segment_Display u_7_segment_display_19 (
    .g(bcd_display_19_g), .f(bcd_display_19_f), .a(bcd_display_19_a), .b(bcd_display_19_b),
    .e(bcd_display_19_e), .d(bcd_display_19_d), .c(bcd_display_19_c), .dp(bcd_display_19_dp));
  HEX_Display hex_display_1 (
    .BIN_0(PC_led0), .LED0(hex_display_1_led0), .BIN_1(PC_led1), .LED1(hex_display_1_led1), .BIN_2(PC_led2),
    .LED2(hex_display_1_led2), .BIN_3(PC_led3), .LED3(hex_display_1_led3), .BIN_4(PC_led4),
    .LED4(hex_display_1_led4), .BIN_5(PC_led5), .LED5(hex_display_1_led5), .BIN_6(PC_led6),
    .LED6(hex_display_1_led6), .BIN_7(PC_led7), .LED7(hex_display_1_led7), .MSN(hex_display_1_msn),
    .LSN(hex_display_1_lsn));
  LED led_102 (.in(hex_display_1_led7));
  LED led_103 (.in(hex_display_1_led6));
  LED led_104 (.in(dec_diplay_7_led2));
  LED led_105 (.in(dec_diplay_7_led3));
  LED led_106 (.in(dec_diplay_7_led5));
  LED led_107 (.in(dec_diplay_7_led4));
  BCD_Display bcd_display_20 (
    .BCD_0(dec_diplay_7_bcd10_0), .BCD_1(dec_diplay_7_bcd10_1), .BCD_2(dec_diplay_7_bcd10_2),
    .BCD_3(dec_diplay_7_bcd10_3), .a(bcd_display_20_a), .b(bcd_display_20_b), .c(bcd_display_20_c),
    .d(bcd_display_20_d), .e(bcd_display_20_e), .f(bcd_display_20_f), .g(bcd_display_20_g),
    .dp(bcd_display_20_dp));
  BCD_Display bcd_display_21 (
    .BCD_0(dec_diplay_7_bcd1_0), .BCD_1(dec_diplay_7_bcd1_1), .BCD_2(dec_diplay_7_bcd1_2),
    .BCD_3(dec_diplay_7_bcd1_3), .a(bcd_display_21_a), .b(bcd_display_21_b), .c(bcd_display_21_c),
    .d(bcd_display_21_d), .e(bcd_display_21_e), .f(bcd_display_21_f), .g(bcd_display_21_g),
    .dp(bcd_display_21_dp));
  _7_Segment_Display u_7_segment_display_20 (
    .g(bcd_display_21_g), .f(bcd_display_21_f), .a(bcd_display_21_a), .b(bcd_display_21_b),
    .e(bcd_display_21_e), .d(bcd_display_21_d), .c(bcd_display_21_c), .dp(bcd_display_21_dp));
  _7_Segment_Display u_7_segment_display_21 (
    .g(bcd_display_20_g), .f(bcd_display_20_f), .a(bcd_display_20_a), .b(bcd_display_20_b),
    .e(bcd_display_20_e), .d(bcd_display_20_d), .c(bcd_display_20_c), .dp(bcd_display_20_dp));
  Reg8 R3 (
    .read(r3_r), .write(r3_w), .nrst(in_1), .IN_7(R0_out_7), .IN_6(R0_out_6), .IN_5(R0_out_5),
    .IN_4(R0_out_4), .IN_3(R0_out_3), .IN_2(R0_out_2), .IN_1(R0_out_1), .IN_0(R0_out_0), .OUT_7(R0_out_7),
    .OUT_6(R0_out_6), .OUT_5(R0_out_5), .OUT_4(R0_out_4), .OUT_3(R0_out_3), .OUT_2(R0_out_2),
    .OUT_1(R0_out_1), .OUT_0(R0_out_0), .LEDr(R3_ledr), .LEDw(R3_ledw), .LEDrst(R3_ledrst), .LED0(R3_led0),
    .LED1(R3_led1), .LED2(R3_led2), .LED3(R3_led3), .LED4(R3_led4), .LED5(R3_led5), .LED6(R3_led6),
    .LED7(R3_led7));
  LED led_108 (.in(hex_display_1_led3));
  LED led_109 (.in(hex_display_1_led4));
  LED led_110 (.in(hex_display_1_led2));
  LED led_111 (.in(hex_display_1_led5));
  Reg8 PC (
    .read(pc_r), .write(pc_w), .nrst(in_1), .IN_7(R0_out_7), .IN_6(R0_out_6), .IN_5(R0_out_5),
    .IN_4(R0_out_4), .IN_3(R0_out_3), .IN_2(R0_out_2), .IN_1(R0_out_1), .IN_0(R0_out_0), .OUT_7(R0_out_7),
    .OUT_6(R0_out_6), .OUT_5(R0_out_5), .OUT_4(R0_out_4), .OUT_3(R0_out_3), .OUT_2(R0_out_2),
    .OUT_1(R0_out_1), .OUT_0(R0_out_0), .LEDr(PC_ledr), .LEDw(PC_ledw), .LEDrst(PC_ledrst), .LED0(PC_led0),
    .LED1(PC_led1), .LED2(PC_led2), .LED3(PC_led3), .LED4(PC_led4), .LED5(PC_led5), .LED6(PC_led6),
    .LED7(PC_led7));
  Hex_Digit_Display hex_digit_display_1 (.value(hex_display_1_msn));  // open: dp
  Hex_Digit_Display hex_digit_display_2 (.value(hex_display_1_lsn));  // open: dp
  LED led_112 (.in(dec_diplay_7_led1));
  LED led_113 (.in(dec_diplay_7_led0));
  LED led_114 (.in(hex_display_1_led1));
  LED led_115 (.in(hex_display_1_led0));
  HEX_Display hex_display_2 (
    .BIN_0(MAR_led0), .LED0(hex_display_2_led0), .BIN_1(MAR_led1), .LED1(hex_display_2_led1),
    .BIN_2(MAR_led2), .LED2(hex_display_2_led2), .BIN_3(MAR_led3), .LED3(hex_display_2_led3),
    .BIN_4(MAR_led4), .LED4(hex_display_2_led4), .BIN_5(MAR_led5), .LED5(hex_display_2_led5),
    .BIN_6(MAR_led6), .LED6(hex_display_2_led6), .BIN_7(MAR_led7), .LED7(hex_display_2_led7),
    .MSN(hex_display_2_msn), .LSN(hex_display_2_lsn));
  LED led_116 (.in(MAR_ledw));
  LED led_117 (.in(MAR_ledrst));
  LED led_118 (.in(MAR_ledr));
  Memory_2 memory_1 (
    .ADDR_0(MAR_out_0), .ADDR_1(MAR_out_1), .ADDR_2(MAR_out_2), .ADDR_3(MAR_out_3), .ADDR_4(MAR_out_4),
    .ADDR_5(MAR_out_5), .ADDR_6(MAR_out_6), .ADDR_7(MAR_out_7), .IN_0(R0_out_0), .IN_1(R0_out_1),
    .IN_2(R0_out_2), .IN_3(R0_out_3), .IN_4(R0_out_4), .IN_5(R0_out_5), .IN_6(R0_out_6), .IN_7(R0_out_7),
    .OUT_0(R0_out_0), .OUT_1(R0_out_1), .OUT_2(R0_out_2), .OUT_3(R0_out_3), .OUT_4(R0_out_4),
    .OUT_5(R0_out_5), .OUT_6(R0_out_6), .OUT_7(R0_out_7), .rst(in_2), .write(mem_w), .read(mem_r),
    .LEDr(memory_1_ledr), .LEDw(memory_1_ledw), .LEDrst(memory_1_ledrst), .ADDR_OUT(memory_1_addr_out),
    .str_out(memory_1_str_out), .ld_out(memory_1_ld_out), .clk_out(memory_1_clk_out),
    .rst_out(memory_1_rst_out), .en_out(memory_1_en_out), .DATA_OUT(memory_1_data_out), .DATA_IN(ram_1_data));
  LED led_119 (.in(memory_1_ledw));
  LED led_120 (.in(memory_1_ledrst));
  LED led_121 (.in(memory_1_ledr));
  LED led_122 (.in(hex_display_2_led5));
  LED led_123 (.in(hex_display_2_led7));
  LED led_124 (.in(hex_display_2_led4));
  LED led_125 (.in(hex_display_2_led6));
  Reg8 MAR (
    .read(1'b1), .write(mar_w), .nrst(in_1), .IN_7(R0_out_7), .IN_6(R0_out_6), .IN_5(R0_out_5),
    .IN_4(R0_out_4), .IN_3(R0_out_3), .IN_2(R0_out_2), .IN_1(R0_out_1), .IN_0(R0_out_0), .OUT_7(MAR_out_7),
    .OUT_6(MAR_out_6), .OUT_5(MAR_out_5), .OUT_4(MAR_out_4), .OUT_3(MAR_out_3), .OUT_2(MAR_out_2),
    .OUT_1(MAR_out_1), .OUT_0(MAR_out_0), .LEDr(MAR_ledr), .LEDw(MAR_ledw), .LEDrst(MAR_ledrst),
    .LED0(MAR_led0), .LED1(MAR_led1), .LED2(MAR_led2), .LED3(MAR_led3), .LED4(MAR_led4), .LED5(MAR_led5),
    .LED6(MAR_led6), .LED7(MAR_led7));
  Hex_Digit_Display hex_digit_display_3 (.value(hex_display_2_msn));  // open: dp
  LED led_126 (.in(hex_display_2_led2));
  LED led_127 (.in(hex_display_2_led3));
  LED led_128 (.in(hex_display_2_led1));
  LED led_129 (.in(hex_display_2_led0));
  Hex_Digit_Display hex_digit_display_4 (.value(hex_display_2_lsn));  // open: dp
  RAM #(.bus("separate")) ram_1 (
    .addr(memory_1_addr_out), .din(memory_1_data_out), .data(ram_1_data), .str(memory_1_str_out),
    .sel(memory_1_en_out), .clk(memory_1_clk_out), .ld(memory_1_ld_out), .clr(memory_1_rst_out));

  // Other names for the same wires on the sheet: mem_rst = in_2; nrst = in_1;
  //   µINSTR (some bits) = {mem_r, mem_w, mar_w, ir_w, pc_r, pc_w, fr_w, op, cin, rd_r, rd_w, ra_w, b_en, r3_r, r3_w, r2_r, r2_w, r1_r, r1_w, r0_r, r0_w}

  // Notes on the sheet:
  //   0000 ra rb  |  mov  ra, rb    |  ra = rb
  //   0001 ra xx  |  data ra, imm8  |  ra = ram[pc++]
  //   0010 ra rb  |  ldr  ra, [rb]  |  ra = ram[rb]
  //   0011 ra rb  |  str  ra, [rb]  |  ram[rb] = ra
  //   0101 00 00  |  br   imm8      |  if true: pc = ram[pc+1]
  //   0101 00 01  |  bz   imm8      |  if z==1: pc = ram[pc+1]
  //   0101 00 10  |  bnz  imm8      |  if z==0: pc = ram[pc+1]
  //   0110 xx xx  |  halt           |  stop computer
  //   1000 ra rb  |  add  ra, rb    |  ra = ra + rb;  (z)
  //   1001 ra rb  |  sub  ra, rb    |  ra = ra - rb;  (z)
endmodule

module ControlUnit (
  input  resume,
  input  clk,
  input  nrst,
  input  INSTR_0,
  input  INSTR_1,
  input  FLAG_z,
  input  INSTR_2,
  input  INSTR_3,
  input  INSTR_4,
  input  INSTR_5,
  input  INSTR_6,
  input  INSTR_7,
  output LEDhalt,
  output [23:0] \µINSTR ,
  output LEDclkr,
  output LEDclkw,
  output LEDstep1,
  output LEDstep4,
  output LEDclk,
  output LEDstep2,
  output LEDstep5,
  output LEDstep3,
  output LEDstep6,
  output LEDrst
);

  wire add_step4_2, add_step5_2, add_step6_2, and_1_out, and_3_out, and_4_out, and_5_out, and_6_out,
       and_7_out, and_8_out, and_9_out, and_10_out, and_11_out, and_12_out, and_13_out, and_14_out,
       and_15_out, br_step4_2, br_step5_2, br_step6_2, clock_1_clk_out, d_flipflop_1_nq, d_flipflop_2_nq,
       data_step4_2, data_step5_2, data_step6_2, decoder2x4_1__00, decoder2x4_1__01, decoder2x4_1__10,
       decoder2x4_1__11, decoder2x4_2__00, decoder2x4_2__01, decoder2x4_2__10, decoder2x4_2__11,
       decoder2x4_3__00, decoder2x4_3__01, decoder2x4_3__10, decoder2x4_3__11, decoder_1_out0,
       decoder_1_out1, decoder_1_out2, decoder_1_out3, decoder_1_out4, decoder_1_out5, decoder_1_out6,
       decoder_1_out7, decoder_1_out8, decoder_1_out9, decoder_1_out10, decoder_1_out11, decoder_1_out12,
       decoder_1_out13, decoder_1_out14, decoder_1_out15, halt, halt_step4_2, halt_step5_2, halt_step6_2,
       ldr_step4_2, ldr_step5_2, ldr_step6_2, mov_step4_2, mov_step5_2, mov_step6_2, or_1_out, or_5_out,
       or_6_out, or_7_out, or_8_out, or_9_out, or_10_out, or_11_out, or_12_out, or_13_out, or_14_out,
       or_15_out, or_16_out, or_17_out, ra_r, ra_w, rb_r, stepper6_1_step1, stepper6_1_step2,
       stepper6_1_step3, stepper6_1_step4, stepper6_1_step5, stepper6_1_step6, str_step4_2, str_step5_2,
       str_step6_2, sub_step4_2, sub_step5_2, sub_step6_2;

  D_FlipFlop d_flipflop_1 (.clk(resume), .D(1'b1), .nrst(and_1_out), .nQ(d_flipflop_1_nq));  // open: Q
  and and_1 (and_1_out, nrst, d_flipflop_1_nq);
  and and_2 (LEDclk, d_flipflop_2_nq, clk);
  D_FlipFlop d_flipflop_2 (.clk(halt), .D(d_flipflop_2_nq), .nrst(and_3_out), .Q(LEDhalt), .nQ(d_flipflop_2_nq));
  and and_3 (and_3_out, d_flipflop_1_nq, nrst);
  Clock clock_1 (.clk_r(LEDclkr), .clk(LEDclk), .clk_w(LEDclkw), .nrst(nrst), .clk_out(clock_1_clk_out));
  Decoder #(.select(4), .enable("false")) decoder_1 (
    .out0(decoder_1_out0), .out1(decoder_1_out1), .out2(decoder_1_out2), .out3(decoder_1_out3),
    .out4(decoder_1_out4), .out5(decoder_1_out5), .out6(decoder_1_out6), .out7(decoder_1_out7),
    .out8(decoder_1_out8), .out9(decoder_1_out9), .out10(decoder_1_out10), .out11(decoder_1_out11),
    .out12(decoder_1_out12), .out13(decoder_1_out13), .out14(decoder_1_out14), .out15(decoder_1_out15),
    .sel({INSTR_7, INSTR_6, INSTR_5, INSTR_4}));
  Stepper6 stepper6_1 (
    .clk(clock_1_clk_out), .nrst(nrst), .LED1(LEDstep1), .LED2(LEDstep2), .LED3(LEDstep3), .LED4(LEDstep4),
    .LED5(LEDstep5), .LED6(LEDstep6), .step1(stepper6_1_step1), .step2(stepper6_1_step2),
    .step3(stepper6_1_step3), .step4(stepper6_1_step4), .step5(stepper6_1_step5), .step6(stepper6_1_step6));  // open: LEDrst, LEDclk
  StepSelect data (
    .enable(decoder_1_out1), .step4(stepper6_1_step4), .step5(stepper6_1_step5), .step6(stepper6_1_step6),
    .step4_2(data_step4_2), .step5_2(data_step5_2), .step6_2(data_step6_2));
  StepSelect mov (
    .enable(decoder_1_out0), .step4(stepper6_1_step4), .step5(stepper6_1_step5), .step6(stepper6_1_step6),
    .step4_2(mov_step4_2), .step5_2(mov_step5_2), .step6_2(mov_step6_2));
  StepSelect ldr (
    .enable(decoder_1_out2), .step4(stepper6_1_step4), .step5(stepper6_1_step5), .step6(stepper6_1_step6),
    .step4_2(ldr_step4_2), .step5_2(ldr_step5_2), .step6_2(ldr_step6_2));
  StepSelect str (
    .enable(decoder_1_out3), .step4(stepper6_1_step4), .step5(stepper6_1_step5), .step6(stepper6_1_step6),
    .step4_2(str_step4_2), .step5_2(str_step5_2), .step6_2(str_step6_2));
  and and_4 (and_4_out, 1'b1, ~INSTR_1, ~INSTR_0);  // AND_Gate
  StepSelect br (
    .enable(decoder_1_out5), .step4(stepper6_1_step4), .step5(stepper6_1_step5), .step6(stepper6_1_step6),
    .step4_2(br_step4_2), .step5_2(br_step5_2), .step6_2(br_step6_2));
  StepSelect stepselect_1 (
    .enable(decoder_1_out4), .step4(stepper6_1_step4), .step5(stepper6_1_step5), .step6(stepper6_1_step6));  // open: step4_2, step5_2, step6_2
  and and_5 (and_5_out, FLAG_z, ~INSTR_1, INSTR_0);  // AND_Gate
  and and_6 (and_6_out, ~FLAG_z, INSTR_1, ~INSTR_0);  // AND_Gate
  or or_1 (or_1_out, and_4_out, and_5_out, and_6_out);
  StepSelect u_halt (
    .enable(decoder_1_out6), .step4(stepper6_1_step4), .step5(stepper6_1_step5), .step6(stepper6_1_step6),
    .step4_2(halt_step4_2), .step5_2(halt_step5_2), .step6_2(halt_step6_2));
  and and_7 (and_7_out, br_step6_2, or_1_out);
  StepSelect stepselect_2 (
    .enable(decoder_1_out7), .step4(stepper6_1_step4), .step5(stepper6_1_step5), .step6(stepper6_1_step6));  // open: step4_2, step5_2, step6_2
  StepSelect sub (
    .enable(decoder_1_out9), .step4(stepper6_1_step4), .step5(stepper6_1_step5), .step6(stepper6_1_step6),
    .step4_2(sub_step4_2), .step5_2(sub_step5_2), .step6_2(sub_step6_2));
  StepSelect add (
    .enable(decoder_1_out8), .step4(stepper6_1_step4), .step5(stepper6_1_step5), .step6(stepper6_1_step6),
    .step4_2(add_step4_2), .step5_2(add_step5_2), .step6_2(add_step6_2));
  StepSelect stepselect_3 (
    .enable(decoder_1_out10), .step4(stepper6_1_step4), .step5(stepper6_1_step5), .step6(stepper6_1_step6));  // open: step4_2, step5_2, step6_2
  StepSelect stepselect_4 (
    .enable(decoder_1_out11), .step4(stepper6_1_step4), .step5(stepper6_1_step5), .step6(stepper6_1_step6));  // open: step4_2, step5_2, step6_2
  StepSelect stepselect_5 (
    .enable(decoder_1_out12), .step4(stepper6_1_step4), .step5(stepper6_1_step5), .step6(stepper6_1_step6));  // open: step4_2, step5_2, step6_2
  StepSelect stepselect_6 (
    .enable(decoder_1_out13), .step4(stepper6_1_step4), .step5(stepper6_1_step5), .step6(stepper6_1_step6));  // open: step4_2, step5_2, step6_2
  StepSelect stepselect_7 (
    .enable(decoder_1_out14), .step4(stepper6_1_step4), .step5(stepper6_1_step5), .step6(stepper6_1_step6));  // open: step4_2, step5_2, step6_2
  StepSelect stepselect_8 (
    .enable(decoder_1_out15), .step4(stepper6_1_step4), .step5(stepper6_1_step5), .step6(stepper6_1_step6));  // open: step4_2, step5_2, step6_2
  Decoder2x4 decoder2x4_1 (
    .sel0(INSTR_0), .sel1(INSTR_1), ._00(decoder2x4_1__00), ._01(decoder2x4_1__01), ._10(decoder2x4_1__10),
    ._11(decoder2x4_1__11));
  Decoder2x4 decoder2x4_2 (
    .sel0(INSTR_2), .sel1(INSTR_3), ._00(decoder2x4_2__00), ._01(decoder2x4_2__01), ._10(decoder2x4_2__10),
    ._11(decoder2x4_2__11));
  Decoder2x4 decoder2x4_3 (
    .sel0(INSTR_2), .sel1(INSTR_3), ._00(decoder2x4_3__00), ._01(decoder2x4_3__01), ._10(decoder2x4_3__10),
    ._11(decoder2x4_3__11));
  or or_2 (rb_r, sub_step5_2, add_step5_2, str_step4_2, ldr_step4_2, mov_step4_2);
  or or_3 (ra_r, sub_step4_2, add_step4_2, str_step5_2);
  or or_4 (ra_w, sub_step6_2, add_step6_2, ldr_step5_2, data_step6_2, mov_step6_2);
  or or_5 (or_5_out, sub_step4_2, add_step4_2, br_step4_2, data_step4_2, mov_step4_2, stepper6_1_step1);
  or or_6 (or_6_out, sub_step5_2, add_step5_2);
  buf or_7 (or_7_out, sub_step5_2);  // OR_Gate
  or or_8 (or_8_out, br_step4_2, data_step4_2, stepper6_1_step1);
  or or_9 (or_9_out, sub_step6_2, add_step6_2, br_step5_2, data_step5_2, mov_step6_2, stepper6_1_step2);
  or or_10 (or_10_out, sub_step5_2, add_step5_2, br_step4_2, data_step4_2, mov_step5_2, stepper6_1_step1);
  or or_11 (or_11_out, sub_step5_2, add_step5_2);
  or or_12 (or_12_out, br_step4_2, data_step4_2, stepper6_1_step1);
  or or_13 (or_13_out, and_7_out, br_step5_2, data_step5_2, stepper6_1_step2);
  buf or_14 (or_14_out, stepper6_1_step3);  // OR_Gate
  or or_15 (or_15_out, br_step4_2, str_step4_2, ldr_step4_2, data_step4_2, stepper6_1_step1);
  or or_16 (or_16_out, and_7_out, ldr_step5_2, data_step6_2, stepper6_1_step3);
  buf or_17 (or_17_out, str_step5_2);  // OR_Gate
  and and_8 (and_8_out, LEDclkr, decoder2x4_1__00, rb_r);
  and and_9 (and_9_out, LEDclkr, decoder2x4_1__01, rb_r);
  and and_10 (and_10_out, LEDclkr, decoder2x4_1__10, rb_r);
  and and_11 (and_11_out, LEDclkr, decoder2x4_1__11, rb_r);
  and and_12 (and_12_out, LEDclkr, decoder2x4_2__00, ra_r);
  and and_13 (and_13_out, LEDclkr, decoder2x4_2__01, ra_r);
  and and_14 (and_14_out, LEDclkr, decoder2x4_2__10, ra_r);
  and and_15 (and_15_out, LEDclkr, decoder2x4_2__11, ra_r);
  and and_16 (\µINSTR [0], LEDclkw, decoder2x4_3__00, ra_w);
  and and_17 (\µINSTR [2], LEDclkw, decoder2x4_3__01, ra_w);
  and and_18 (\µINSTR [4], LEDclkw, decoder2x4_3__10, ra_w);
  and and_19 (\µINSTR [6], LEDclkw, decoder2x4_3__11, ra_w);
  and and_20 (\µINSTR [9], LEDclkw, or_5_out);
  and and_21 (\µINSTR [8], LEDclkw, or_6_out);
  and and_22 (\µINSTR [13], LEDclkr, or_7_out);
  and and_23 (\µINSTR [12], LEDclkr, or_8_out);
  and and_24 (\µINSTR [11], LEDclkr, or_9_out);
  and and_25 (\µINSTR [10], LEDclkw, or_10_out);
  and and_26 (\µINSTR [14], LEDclkw, or_11_out);
  and and_27 (\µINSTR [17], LEDclkr, or_12_out);
  and and_28 (\µINSTR [16], LEDclkw, or_13_out);
  and and_29 (\µINSTR [18], LEDclkw, or_14_out);
  and and_30 (\µINSTR [20], LEDclkw, or_15_out);
  and and_31 (\µINSTR [22], LEDclkr, or_16_out);
  and and_32 (\µINSTR [21], LEDclkw, or_17_out);
  and and_33 (halt, ~LEDclkw, ~LEDclkr, halt_step6_2);  // AND_Gate
  or or_18 (\µINSTR [1], and_8_out, and_12_out);
  or or_19 (\µINSTR [3], and_9_out, and_13_out);
  or or_20 (\µINSTR [5], and_10_out, and_14_out);
  or or_21 (\µINSTR [7], and_11_out, and_15_out);

  assign LEDrst = nrst;
  assign {\µINSTR [23], \µINSTR [19], \µINSTR [15]} = 3'b000;

  // Other names for the same wires on the sheet: _1 = LEDstep1; _2 = LEDstep2; _3 = LEDstep3; _4 = LEDstep4;
  //   _5 = LEDstep5; _6 = LEDstep6; r0_w = \µINSTR [0]; r0_r = \µINSTR [1]; r1_w = \µINSTR [2]; r1_r = \µINSTR [3];
  //   r2_w = \µINSTR [4]; r2_r = \µINSTR [5]; r3_w = \µINSTR [6]; r3_r = \µINSTR [7]; b_en = \µINSTR [8];
  //   a_w = \µINSTR [9]; d_w = \µINSTR [10]; d_r = \µINSTR [11]; cin = \µINSTR [12]; op = \µINSTR [13];
  //   fr_w = \µINSTR [14]; pc_w = \µINSTR [16]; pc_r = \µINSTR [17]; ir_w = \µINSTR [18]; mar_w = \µINSTR [20];
  //   mem_w = \µINSTR [21]; mem_r = \µINSTR [22]

  // Notes on the sheet:
  //   r
endmodule

module Clock (
  input  clk,
  input  nrst,
  output clk_r,
  output clk_w,
  output clk_out
);

  wire and_1_out, and_2_out, or_1_out, or_2_out, reset_logic_nq, reset_logic_q, state_nq;

  and and_1 (and_1_out, clk, reset_logic_nq);
  D_FlipFlop reset_logic (.clk(and_1_out), .D(1'b1), .nrst(nrst), .Q(reset_logic_q), .nQ(reset_logic_nq));
  and and_2 (and_2_out, clk, reset_logic_q);
  D_FlipFlop state (.clk(and_2_out), .D(state_nq), .nrst(nrst), .Q(clk_out), .nQ(state_nq));
  or or_1 (or_1_out, and_2_out, clk_out);
  buf buffer_1 (clk_r, or_1_out);
  or or_2 (or_2_out, state_nq, and_2_out);
  not not_1 (clk_w, or_2_out);
endmodule

module Stepper6 (
  input  clk,
  input  nrst,
  output LEDclk,
  output LEDrst,
  output LED1,
  output LED2,
  output LED3,
  output LED4,
  output LED5,
  output LED6,
  output step1,
  output step2,
  output step3,
  output step4,
  output step5,
  output step6
);

  wire d_latch_1_q, d_latch_2_q, d_latch_3_nq, d_latch_3_q, d_latch_4_q, d_latch_5_nq, d_latch_5_q,
       d_latch_6_q, d_latch_7_nq, d_latch_7_q, d_latch_8_q, d_latch_9_nq, d_latch_9_q, d_latch_10_q,
       d_latch_11_nq, d_latch_11_q, d_latch_12_q, d_latch_13_nq, d_latch_13_q, not_1_out, not_2_out,
       or_1_out, or_2_out;

  not not_1 (not_1_out, clk);
  or or_1 (or_1_out, d_latch_13_q, not_1_out);
  or or_2 (or_2_out, clk, d_latch_13_q);
  not not_2 (not_2_out, d_latch_13_q);
  D_Latch d_latch_1 (.D(not_2_out), .write(or_2_out), .nrst(nrst), .Q(d_latch_1_q));  // open: nQ
  D_Latch d_latch_2 (.D(d_latch_1_q), .write(or_1_out), .nrst(nrst), .Q(d_latch_2_q));  // open: nQ
  D_Latch d_latch_3 (.D(d_latch_2_q), .write(or_2_out), .nrst(nrst), .Q(d_latch_3_q), .nQ(d_latch_3_nq));
  and and_1 (LED1, d_latch_1_q, d_latch_3_nq);
  D_Latch d_latch_4 (.D(d_latch_3_q), .write(or_1_out), .nrst(nrst), .Q(d_latch_4_q));  // open: nQ
  D_Latch d_latch_5 (.D(d_latch_4_q), .write(or_2_out), .nrst(nrst), .Q(d_latch_5_q), .nQ(d_latch_5_nq));
  and and_2 (LED2, d_latch_3_q, d_latch_5_nq);
  D_Latch d_latch_6 (.D(d_latch_5_q), .write(or_1_out), .nrst(nrst), .Q(d_latch_6_q));  // open: nQ
  D_Latch d_latch_7 (.D(d_latch_6_q), .write(or_2_out), .nrst(nrst), .Q(d_latch_7_q), .nQ(d_latch_7_nq));
  and and_3 (LED3, d_latch_5_q, d_latch_7_nq);
  D_Latch d_latch_8 (.D(d_latch_7_q), .write(or_1_out), .nrst(nrst), .Q(d_latch_8_q));  // open: nQ
  and and_4 (LED4, d_latch_7_q, d_latch_9_nq);
  D_Latch d_latch_9 (.D(d_latch_8_q), .write(or_2_out), .nrst(nrst), .Q(d_latch_9_q), .nQ(d_latch_9_nq));
  D_Latch d_latch_10 (.D(d_latch_9_q), .write(or_1_out), .nrst(nrst), .Q(d_latch_10_q));  // open: nQ
  and and_5 (LED5, d_latch_9_q, d_latch_11_nq);
  D_Latch d_latch_11 (.D(d_latch_10_q), .write(or_2_out), .nrst(nrst), .Q(d_latch_11_q), .nQ(d_latch_11_nq));
  D_Latch d_latch_12 (.D(d_latch_11_q), .write(or_1_out), .nrst(nrst), .Q(d_latch_12_q));  // open: nQ
  and and_6 (LED6, d_latch_11_q, d_latch_13_nq);
  D_Latch d_latch_13 (.D(d_latch_12_q), .write(or_2_out), .nrst(nrst), .Q(d_latch_13_q), .nQ(d_latch_13_nq));

  assign LEDclk = clk;
  assign LEDrst = nrst;
  assign step1 = LED1;
  assign step2 = LED2;
  assign step3 = LED3;
  assign step4 = LED4;
  assign step5 = LED5;
  assign step6 = LED6;
endmodule

module Decoder2x4 (
  input  sel0,
  input  sel1,
  output _00,
  output _01,
  output _10,
  output _11
);

  wire not_1_out, not_2_out;

  not not_1 (not_1_out, sel0);
  not not_2 (not_2_out, sel1);
  and and_1 (_00, not_2_out, not_1_out);
  and and_2 (_01, not_2_out, sel0);
  and and_3 (_10, sel1, not_1_out);
  and and_4 (_11, sel1, sel0);
endmodule

module StepSelect (
  input  step4,
  input  step5,
  input  step6,
  input  enable,
  output step4_2,
  output step5_2,
  output step6_2
);

  and and_1 (step4_2, enable, step4);
  and and_2 (step5_2, enable, step5);
  and and_3 (step6_2, enable, step6);
endmodule

module FullAdder (
  input  a,
  input  b,
  input  cin,
  output sum,
  output cout
);

  wire and_1_out, and_2_out, xor_1_out;

  xor xor_1 (xor_1_out, a, b);
  and and_1 (and_1_out, xor_1_out, cin);
  and and_2 (and_2_out, a, b);
  xor xor_2 (sum, xor_1_out, cin);
  or or_1 (cout, and_1_out, and_2_out);
endmodule

module Add8 (
  input  a7,
  input  b7,
  input  a6,
  input  b6,
  input  a5,
  input  b5,
  input  a4,
  input  b4,
  input  a3,
  input  b3,
  input  a2,
  input  b2,
  input  a1,
  input  b1,
  input  a0,
  input  b0,
  input  cin,
  output cout,
  output sum_7,
  output sum_6,
  output sum_5,
  output sum_4,
  output sum_3,
  output sum_2,
  output sum_1,
  output sum_0
);

  wire fulladder_2_cout, fulladder_3_cout, fulladder_4_cout, fulladder_5_cout, fulladder_6_cout,
       fulladder_7_cout, fulladder_8_cout;

  FullAdder fulladder_1 (.a(a7), .b(b7), .cin(fulladder_2_cout), .sum(sum_7), .cout(cout));
  FullAdder fulladder_2 (.a(a6), .b(b6), .cin(fulladder_3_cout), .sum(sum_6), .cout(fulladder_2_cout));
  FullAdder fulladder_3 (.a(a5), .b(b5), .cin(fulladder_4_cout), .sum(sum_5), .cout(fulladder_3_cout));
  FullAdder fulladder_4 (.a(a4), .b(b4), .cin(fulladder_5_cout), .sum(sum_4), .cout(fulladder_4_cout));
  FullAdder fulladder_5 (.a(a3), .b(b3), .cin(fulladder_7_cout), .sum(sum_3), .cout(fulladder_5_cout));
  FullAdder fulladder_6 (.a(a1), .b(b1), .cin(fulladder_8_cout), .sum(sum_1), .cout(fulladder_6_cout));
  FullAdder fulladder_7 (.a(a2), .b(b2), .cin(fulladder_6_cout), .sum(sum_2), .cout(fulladder_7_cout));
  FullAdder fulladder_8 (.a(a0), .b(b0), .cin(cin), .sum(sum_0), .cout(fulladder_8_cout));
endmodule

module Inverter8 (
  input  in_7,
  input  in_6,
  input  in_5,
  input  in_4,
  input  in_3,
  input  in_2,
  input  in_1,
  input  in_0,
  input  inv,
  output out_7,
  output out_6,
  output out_5,
  output out_4,
  output out_3,
  output out_2,
  output out_1,
  output out_0
);

  xor xor_1 (out_7, inv, in_7);
  xor xor_2 (out_5, inv, in_5);
  xor xor_3 (out_6, inv, in_6);
  xor xor_4 (out_4, inv, in_4);
  xor xor_5 (out_2, inv, in_2);
  xor xor_6 (out_3, inv, in_3);
  xor xor_7 (out_1, inv, in_1);
  xor xor_8 (out_0, inv, in_0);
endmodule

module Zero8 (
  input  _7,
  input  _6,
  input  _5,
  input  _4,
  input  _3,
  input  _2,
  input  _1,
  input  _0,
  output zero
);

  wire or_1_out, or_2_out, or_3_out, or_4_out;

  nor nor_1 (zero, or_2_out, or_1_out, or_3_out, or_4_out);
  or or_1 (or_1_out, _5, _4);
  or or_2 (or_2_out, _7, _6);
  or or_3 (or_3_out, _3, _2);
  or or_4 (or_4_out, _1, _0);
endmodule

module ALU_2 (
  input  a_0,
  input  b_0,
  input  a_1,
  input  b_1,
  input  a_2,
  input  b_2,
  input  a_3,
  input  b_3,
  input  a_4,
  input  b_4,
  input  a_5,
  input  b_5,
  input  a_6,
  input  b_6,
  input  a_7,
  input  b_7,
  input  op,
  input  cin,
  output LEDop,
  output LEDcin,
  output sum_0,
  output sum_1,
  output sum_2,
  output sum_3,
  output sum_4,
  output sum_5,
  output sum_6,
  output sum_7,
  output LEDz,
  output zero
);

  wire inverter8_1_out_0, inverter8_1_out_1, inverter8_1_out_2, inverter8_1_out_3, inverter8_1_out_4,
       inverter8_1_out_5, inverter8_1_out_6, inverter8_1_out_7, xor_1_out;

  Inverter8 inverter8_1 (
    .inv(op), .in_7(b_7), .in_6(b_6), .in_5(b_5), .in_4(b_4), .in_3(b_3), .in_2(b_2), .in_1(b_1), .in_0(b_0),
    .out_7(inverter8_1_out_7), .out_6(inverter8_1_out_6), .out_5(inverter8_1_out_5),
    .out_4(inverter8_1_out_4), .out_3(inverter8_1_out_3), .out_2(inverter8_1_out_2),
    .out_1(inverter8_1_out_1), .out_0(inverter8_1_out_0));
  Add8 add8_1 (
    .cin(xor_1_out), .a7(a_7), .b7(inverter8_1_out_7), .a6(a_6), .b6(inverter8_1_out_6), .a5(a_5),
    .b5(inverter8_1_out_5), .a4(a_4), .b4(inverter8_1_out_4), .a3(a_3), .b3(inverter8_1_out_3), .a2(a_2),
    .b2(inverter8_1_out_2), .a1(a_1), .b1(inverter8_1_out_1), .a0(a_0), .b0(inverter8_1_out_0),
    .sum_7(sum_7), .sum_6(sum_6), .sum_5(sum_5), .sum_4(sum_4), .sum_3(sum_3), .sum_2(sum_2), .sum_1(sum_1),
    .sum_0(sum_0));  // open: cout
  Zero8 zero8_1 (
    .zero(LEDz), ._7(sum_7), ._6(sum_6), ._5(sum_5), ._4(sum_4), ._3(sum_3), ._2(sum_2), ._1(sum_1),
    ._0(sum_0));
  xor xor_1 (xor_1_out, op, cin);

  assign LEDcin = cin;
  assign LEDop = op;
  assign zero = LEDz;
endmodule

module SR_Latch (
  input  set,
  input  reset,
  output Q,
  output nQ
);

  wire or_1_out, or_2_out;

  or or_1 (or_1_out, set, Q);
  not not_1 (Q, or_2_out);
  not not_2 (nQ, or_1_out);
  or or_2 (or_2_out, nQ, reset);
endmodule

module D_Latch (
  input  D,
  input  write,
  input  nrst,
  output Q,
  output nQ
);

  wire and_1_out, and_2_out, not_1_out, not_2_out, or_1_out;

  not not_1 (not_1_out, D);
  not not_2 (not_2_out, nrst);
  and and_1 (and_1_out, D, write);
  and and_2 (and_2_out, write, not_1_out);
  SR_Latch sr_latch_1 (.set(and_1_out), .Q(Q), .nQ(nQ), .reset(or_1_out));
  or or_1 (or_1_out, and_2_out, not_2_out);
endmodule

module D_FlipFlop (
  input  clk,
  input  D,
  input  nrst,
  output Q,
  output nQ
);

  wire d_latch_1_q, not_1_out, not_2_out;

  not not_1 (not_1_out, clk);
  D_Latch d_latch_1 (.D(D), .write(not_1_out), .nrst(nrst), .Q(d_latch_1_q));  // open: nQ
  not not_2 (not_2_out, not_1_out);
  D_Latch d_latch_2 (.D(d_latch_1_q), .write(not_2_out), .nrst(nrst), .Q(Q), .nQ(nQ));
endmodule

module Reg1 (
  input  IN,
  input  read,
  input  write,
  input  nrst,
  output LED,
  output OUT,
  output LEDr,
  output LEDw,
  output LEDrst
);

  D_Latch d_latch_1 (.D(IN), .write(write), .nrst(nrst), .Q(LED));  // open: nQ
  assign OUT = read ? LED : 1'bz;  // Controlled_Buffer controlled_buffer_1

  assign LEDr = read;
  assign LEDrst = nrst;
  assign LEDw = write;
endmodule

module Reg8 (
  input  IN_7,
  input  IN_6,
  input  IN_5,
  input  IN_4,
  input  IN_3,
  input  IN_2,
  input  IN_1,
  input  IN_0,
  input  read,
  input  write,
  input  nrst,
  output OUT_7,
  output OUT_6,
  output OUT_5,
  output OUT_4,
  output OUT_3,
  output OUT_2,
  output OUT_1,
  output OUT_0,
  output LEDr,
  output LEDw,
  output LEDrst,
  output LED7,
  output LED6,
  output LED5,
  output LED4,
  output LED3,
  output LED2,
  output LED1,
  output LED0
);

  Reg1 reg1_1 (
    .IN(IN_7), .read(read), .write(write), .nrst(nrst), .LED(LED7), .OUT(OUT_7));  // open: LEDr, LEDw, LEDrst
  Reg1 reg1_2 (
    .IN(IN_6), .read(read), .write(write), .nrst(nrst), .LED(LED6), .OUT(OUT_6));  // open: LEDr, LEDw, LEDrst
  Reg1 reg1_3 (
    .IN(IN_5), .read(read), .write(write), .nrst(nrst), .LED(LED5), .OUT(OUT_5));  // open: LEDr, LEDw, LEDrst
  Reg1 reg1_4 (
    .IN(IN_4), .read(read), .write(write), .nrst(nrst), .LED(LED4), .OUT(OUT_4));  // open: LEDr, LEDw, LEDrst
  Reg1 reg1_5 (
    .IN(IN_3), .read(read), .write(write), .nrst(nrst), .LED(LED3), .OUT(OUT_3));  // open: LEDr, LEDw, LEDrst
  Reg1 reg1_6 (
    .IN(IN_2), .read(read), .write(write), .nrst(nrst), .LED(LED2), .OUT(OUT_2));  // open: LEDr, LEDw, LEDrst
  Reg1 reg1_7 (
    .IN(IN_1), .read(read), .write(write), .nrst(nrst), .LED(LED1), .OUT(OUT_1));  // open: LEDr, LEDw, LEDrst
  Reg1 reg1_8 (
    .IN(IN_0), .read(read), .write(write), .nrst(nrst), .LED(LED0), .OUT(OUT_0));  // open: LEDr, LEDw, LEDrst

  assign LEDr = read;
  assign LEDrst = nrst;
  assign LEDw = write;

  // Other names for the same wires on the sheet: _0 = LED0; _1 = LED1; _2 = LED2; _3 = LED3; _4 = LED4; _5 = LED5;
  //   _6 = LED6; _7 = LED7
endmodule

module ZeroPass8 (
  input  IN_7,
  input  IN_6,
  input  IN_5,
  input  IN_4,
  input  IN_3,
  input  IN_2,
  input  IN_1,
  input  IN_0,
  input  enable,
  output LEDen,
  output LED7,
  output LED6,
  output LED5,
  output LED4,
  output LED3,
  output LED2,
  output LED1,
  output LED0,
  output OUT_7,
  output OUT_6,
  output OUT_5,
  output OUT_4,
  output OUT_3,
  output OUT_2,
  output OUT_1,
  output OUT_0
);

  and and_1 (LED7, enable, IN_7);
  and and_2 (LED6, enable, IN_6);
  and and_3 (LED5, enable, IN_5);
  and and_4 (LED4, enable, IN_4);
  and and_5 (LED3, enable, IN_3);
  and and_6 (LED2, enable, IN_2);
  and and_7 (LED1, enable, IN_1);
  and and_8 (LED0, enable, IN_0);

  assign LEDen = enable;
  assign OUT_0 = LED0;
  assign OUT_1 = LED1;
  assign OUT_2 = LED2;
  assign OUT_3 = LED3;
  assign OUT_4 = LED4;
  assign OUT_5 = LED5;
  assign OUT_6 = LED6;
  assign OUT_7 = LED7;
endmodule

module SRAM_Cell (
  input  IN,
  input  select,
  input  read,
  input  write,
  input  nrst,
  output LED,
  output OUT,
  output LEDsel,
  output LEDr,
  output LEDw,
  output LEDrst
);

  wire and_1_out, and_2_out;

  and and_1 (and_1_out, select, write);
  D_Latch d_latch_1 (.D(IN), .write(and_1_out), .nrst(nrst), .Q(LED));  // open: nQ
  assign OUT = and_2_out ? LED : 1'bz;  // Controlled_Buffer controlled_buffer_1
  and and_2 (and_2_out, select, read);

  assign LEDr = read;
  assign LEDrst = nrst;
  assign LEDsel = select;
  assign LEDw = write;
endmodule

module SRAM_4B (
  input  ADDR_1,
  input  ADDR_0,
  input  select,
  input  IN_7,
  input  IN_6,
  input  IN_5,
  input  IN_4,
  input  IN_3,
  input  IN_2,
  input  IN_1,
  input  IN_0,
  input  read,
  input  write,
  input  nrst,
  output LEDsel_0,
  output LED_0__0,
  output LED_0__1,
  output LED_0__2,
  output LED_0__3,
  output LED_0__4,
  output LED_0__5,
  output LED_0__6,
  output LED_0__7,
  output LEDsel_1,
  output LED_1__0,
  output LED_1__1,
  output LED_1__2,
  output LED_1__3,
  output LED_1__4,
  output LED_1__5,
  output LED_1__6,
  output LED_1__7,
  output LEDsel_2,
  output LED_2__0,
  output LED_2__1,
  output LED_2__2,
  output LED_2__3,
  output LED_2__4,
  output LED_2__5,
  output LED_2__6,
  output LED_2__7,
  output LEDsel_3,
  output LED_3__0,
  output LED_3__1,
  output LED_3__2,
  output LED_3__3,
  output LEDsel,
  output LED_3__4,
  output LEDaddr_0,
  output LED_3__5,
  output LEDaddr_1,
  output LED_3__6,
  output LED_3__7,
  output LEDr,
  output LEDw,
  output LEDrst,
  output OUT_7,
  output OUT_6,
  output OUT_5,
  output OUT_4,
  output OUT_3,
  output OUT_2,
  output OUT_1,
  output OUT_0
);

  wire not_1_out, not_2_out;

  not not_1 (not_1_out, ADDR_1);
  not not_2 (not_2_out, ADDR_0);
  and and_1 (LEDsel_0, not_2_out, not_1_out, select);
  and and_2 (LEDsel_1, ADDR_0, not_1_out, select);
  and and_3 (LEDsel_2, not_2_out, ADDR_1, select);
  and and_4 (LEDsel_3, ADDR_0, ADDR_1, select);
  SRAM_Cell sram_cell_1 (
    .IN(IN_7), .select(LEDsel_0), .read(read), .write(write), .nrst(nrst), .LED(LED_0__7), .OUT(OUT_7));  // open: LEDsel, LEDr, LEDw, LEDrst
  SRAM_Cell sram_cell_2 (
    .IN(IN_7), .select(LEDsel_1), .read(read), .write(write), .nrst(nrst), .LED(LED_1__7), .OUT(OUT_7));  // open: LEDsel, LEDr, LEDw, LEDrst
  SRAM_Cell sram_cell_3 (
    .IN(IN_7), .select(LEDsel_2), .read(read), .write(write), .nrst(nrst), .LED(LED_2__7), .OUT(OUT_7));  // open: LEDsel, LEDr, LEDw, LEDrst
  SRAM_Cell sram_cell_4 (
    .IN(IN_7), .select(LEDsel_3), .read(read), .write(write), .nrst(nrst), .LED(LED_3__7), .OUT(OUT_7));  // open: LEDsel, LEDr, LEDw, LEDrst
  SRAM_Cell sram_cell_5 (
    .IN(IN_6), .select(LEDsel_0), .read(read), .write(write), .nrst(nrst), .LED(LED_0__6), .OUT(OUT_6));  // open: LEDsel, LEDr, LEDw, LEDrst
  SRAM_Cell sram_cell_6 (
    .IN(IN_6), .select(LEDsel_1), .read(read), .write(write), .nrst(nrst), .LED(LED_1__6), .OUT(OUT_6));  // open: LEDsel, LEDr, LEDw, LEDrst
  SRAM_Cell sram_cell_7 (
    .IN(IN_6), .select(LEDsel_2), .read(read), .write(write), .nrst(nrst), .LED(LED_2__6), .OUT(OUT_6));  // open: LEDsel, LEDr, LEDw, LEDrst
  SRAM_Cell sram_cell_8 (
    .IN(IN_6), .select(LEDsel_3), .read(read), .write(write), .nrst(nrst), .LED(LED_3__6), .OUT(OUT_6));  // open: LEDsel, LEDr, LEDw, LEDrst
  SRAM_Cell sram_cell_9 (
    .IN(IN_5), .select(LEDsel_0), .read(read), .write(write), .nrst(nrst), .LED(LED_0__5), .OUT(OUT_5));  // open: LEDsel, LEDr, LEDw, LEDrst
  SRAM_Cell sram_cell_10 (
    .IN(IN_5), .select(LEDsel_1), .read(read), .write(write), .nrst(nrst), .LED(LED_1__5), .OUT(OUT_5));  // open: LEDsel, LEDr, LEDw, LEDrst
  SRAM_Cell sram_cell_11 (
    .IN(IN_5), .select(LEDsel_2), .read(read), .write(write), .nrst(nrst), .LED(LED_2__5), .OUT(OUT_5));  // open: LEDsel, LEDr, LEDw, LEDrst
  SRAM_Cell sram_cell_12 (
    .IN(IN_5), .select(LEDsel_3), .read(read), .write(write), .nrst(nrst), .LED(LED_3__5), .OUT(OUT_5));  // open: LEDsel, LEDr, LEDw, LEDrst
  SRAM_Cell sram_cell_13 (
    .IN(IN_4), .select(LEDsel_0), .read(read), .write(write), .nrst(nrst), .LED(LED_0__4), .OUT(OUT_4));  // open: LEDsel, LEDr, LEDw, LEDrst
  SRAM_Cell sram_cell_14 (
    .IN(IN_4), .select(LEDsel_1), .read(read), .write(write), .nrst(nrst), .LED(LED_1__4), .OUT(OUT_4));  // open: LEDsel, LEDr, LEDw, LEDrst
  SRAM_Cell sram_cell_15 (
    .IN(IN_4), .select(LEDsel_2), .read(read), .write(write), .nrst(nrst), .LED(LED_2__4), .OUT(OUT_4));  // open: LEDsel, LEDr, LEDw, LEDrst
  SRAM_Cell sram_cell_16 (
    .IN(IN_4), .select(LEDsel_3), .read(read), .write(write), .nrst(nrst), .LED(LED_3__4), .OUT(OUT_4));  // open: LEDsel, LEDr, LEDw, LEDrst
  SRAM_Cell sram_cell_17 (
    .IN(IN_3), .select(LEDsel_0), .read(read), .write(write), .nrst(nrst), .LED(LED_0__3), .OUT(OUT_3));  // open: LEDsel, LEDr, LEDw, LEDrst
  SRAM_Cell sram_cell_18 (
    .IN(IN_3), .select(LEDsel_1), .read(read), .write(write), .nrst(nrst), .LED(LED_1__3), .OUT(OUT_3));  // open: LEDsel, LEDr, LEDw, LEDrst
  SRAM_Cell sram_cell_19 (
    .IN(IN_3), .select(LEDsel_2), .read(read), .write(write), .nrst(nrst), .LED(LED_2__3), .OUT(OUT_3));  // open: LEDsel, LEDr, LEDw, LEDrst
  SRAM_Cell sram_cell_20 (
    .IN(IN_3), .select(LEDsel_3), .read(read), .write(write), .nrst(nrst), .LED(LED_3__3), .OUT(OUT_3));  // open: LEDsel, LEDr, LEDw, LEDrst
  SRAM_Cell sram_cell_21 (
    .IN(IN_2), .select(LEDsel_0), .read(read), .write(write), .nrst(nrst), .LED(LED_0__2), .OUT(OUT_2));  // open: LEDsel, LEDr, LEDw, LEDrst
  SRAM_Cell sram_cell_22 (
    .IN(IN_2), .select(LEDsel_1), .read(read), .write(write), .nrst(nrst), .LED(LED_1__2), .OUT(OUT_2));  // open: LEDsel, LEDr, LEDw, LEDrst
  SRAM_Cell sram_cell_23 (
    .IN(IN_2), .select(LEDsel_2), .read(read), .write(write), .nrst(nrst), .LED(LED_2__2), .OUT(OUT_2));  // open: LEDsel, LEDr, LEDw, LEDrst
  SRAM_Cell sram_cell_24 (
    .IN(IN_2), .select(LEDsel_3), .read(read), .write(write), .nrst(nrst), .LED(LED_3__2), .OUT(OUT_2));  // open: LEDsel, LEDr, LEDw, LEDrst
  SRAM_Cell sram_cell_25 (
    .IN(IN_1), .select(LEDsel_0), .read(read), .write(write), .nrst(nrst), .LED(LED_0__1), .OUT(OUT_1));  // open: LEDsel, LEDr, LEDw, LEDrst
  SRAM_Cell sram_cell_26 (
    .IN(IN_1), .select(LEDsel_1), .read(read), .write(write), .nrst(nrst), .LED(LED_1__1), .OUT(OUT_1));  // open: LEDsel, LEDr, LEDw, LEDrst
  SRAM_Cell sram_cell_27 (
    .IN(IN_1), .select(LEDsel_2), .read(read), .write(write), .nrst(nrst), .LED(LED_2__1), .OUT(OUT_1));  // open: LEDsel, LEDr, LEDw, LEDrst
  SRAM_Cell sram_cell_28 (
    .IN(IN_1), .select(LEDsel_3), .read(read), .write(write), .nrst(nrst), .LED(LED_3__1), .OUT(OUT_1));  // open: LEDsel, LEDr, LEDw, LEDrst
  SRAM_Cell sram_cell_29 (
    .IN(IN_0), .select(LEDsel_0), .read(read), .write(write), .nrst(nrst), .LED(LED_0__0), .OUT(OUT_0));  // open: LEDsel, LEDr, LEDw, LEDrst
  SRAM_Cell sram_cell_30 (
    .IN(IN_0), .select(LEDsel_1), .read(read), .write(write), .nrst(nrst), .LED(LED_1__0), .OUT(OUT_0));  // open: LEDsel, LEDr, LEDw, LEDrst
  SRAM_Cell sram_cell_31 (
    .IN(IN_0), .select(LEDsel_2), .read(read), .write(write), .nrst(nrst), .LED(LED_2__0), .OUT(OUT_0));  // open: LEDsel, LEDr, LEDw, LEDrst
  SRAM_Cell sram_cell_32 (
    .IN(IN_0), .select(LEDsel_3), .read(read), .write(write), .nrst(nrst), .LED(LED_3__0), .OUT(OUT_0));  // open: LEDsel, LEDr, LEDw, LEDrst

  assign LEDaddr_0 = ADDR_0;
  assign LEDaddr_1 = ADDR_1;
  assign LEDr = read;
  assign LEDrst = nrst;
  assign LEDsel = select;
  assign LEDw = write;

  // Other names for the same wires on the sheet: _00 = LED_0__0; _01 = LED_0__1; _02 = LED_0__2; _03 = LED_0__3;
  //   _04 = LED_0__4; _05 = LED_0__5; _06 = LED_0__6; _07 = LED_0__7; _10 = LED_1__0; _11 = LED_1__1; _12 = LED_1__2;
  //   _13 = LED_1__3; _14 = LED_1__4; _15 = LED_1__5; _16 = LED_1__6; _17 = LED_1__7; _20 = LED_2__0; _21 = LED_2__1;
  //   _22 = LED_2__2; _23 = LED_2__3; _24 = LED_2__4; _25 = LED_2__5; _26 = LED_2__6; _27 = LED_2__7; _30 = LED_3__0;
  //   _31 = LED_3__1; _32 = LED_3__2; _33 = LED_3__3; _34 = LED_3__4; _35 = LED_3__5; _36 = LED_3__6; _37 = LED_3__7
endmodule

module Memory_2 (
  input  ADDR_0,
  input  IN_0,
  input  ADDR_1,
  input  IN_1,
  input  ADDR_2,
  input  IN_2,
  input  ADDR_3,
  input  IN_3,
  input  ADDR_4,
  input  IN_4,
  input  ADDR_5,
  input  IN_5,
  input  ADDR_6,
  input  IN_6,
  input  ADDR_7,
  input  IN_7,
  input  [7:0] DATA_IN,
  input  read,
  input  write,
  input  rst,
  output [7:0] ADDR_OUT,
  output [7:0] DATA_OUT,
  output en_out,
  output ld_out,
  output str_out,
  output OUT_0,
  output clk_out,
  output OUT_1,
  output rst_out,
  output OUT_2,
  output OUT_3,
  output OUT_4,
  output LEDr,
  output OUT_5,
  output LEDw,
  output OUT_6,
  output LEDrst,
  output OUT_7
);

  or or_1 (en_out, read, write);
  Delayer delayer_1 (.in(write), .out(clk_out));
  RAM #(.bus("separate")) ram_1 ();  // open: addr, din, data, str, sel, clk, ld, clr

  assign ADDR_OUT = {ADDR_7, ADDR_6, ADDR_5, ADDR_4, ADDR_3, ADDR_2, ADDR_1, ADDR_0};
  assign DATA_OUT = {IN_7, IN_6, IN_5, IN_4, IN_3, IN_2, IN_1, IN_0};
  assign ld_out = read;
  assign LEDr = read;
  assign LEDrst = rst;
  assign LEDw = write;
  assign OUT_0 = DATA_IN[0];
  assign OUT_1 = DATA_IN[1];
  assign OUT_2 = DATA_IN[2];
  assign OUT_3 = DATA_IN[3];
  assign OUT_4 = DATA_IN[4];
  assign OUT_5 = DATA_IN[5];
  assign OUT_6 = DATA_IN[6];
  assign OUT_7 = DATA_IN[7];
  assign rst_out = rst;
  assign str_out = write;
endmodule

module Delayer (
  input  in,
  output out
);

  wire not_1_out, not_2_out, not_3_out, not_4_out, not_5_out, not_6_out, not_7_out;

  not not_1 (not_1_out, in);
  not not_2 (not_2_out, not_1_out);
  not not_3 (not_3_out, not_2_out);
  not not_4 (not_4_out, not_5_out);
  not not_5 (not_5_out, not_3_out);
  not not_6 (not_6_out, not_4_out);
  not not_7 (not_7_out, not_6_out);
  not not_8 (out, not_7_out);
endmodule

module BinToBCD___Add3 (
  input  IN_0,
  input  IN_1,
  input  IN_2,
  input  IN_3,
  output OUT_3,
  output OUT_2,
  output OUT_1,
  output OUT_0
);

  wire and_1_out, and_2_out, and_3_out, and_4_out, and_5_out, and_6_out, and_7_out, and_8_out, and_9_out,
       and_10_out, not_1_out, not_2_out, not_3_out, not_4_out;

  not not_1 (not_1_out, IN_0);
  not not_2 (not_2_out, IN_1);
  not not_3 (not_3_out, IN_2);
  not not_4 (not_4_out, IN_3);
  and and_1 (and_1_out, IN_2, IN_0);
  and and_2 (and_2_out, IN_2, IN_1);
  or or_1 (OUT_3, IN_3, and_2_out, and_1_out);
  and and_3 (and_3_out, IN_3, IN_0);
  or or_2 (OUT_2, and_3_out, and_4_out);
  and and_4 (and_4_out, IN_2, not_2_out, not_1_out);
  and and_5 (and_5_out, IN_3, not_1_out);
  and and_6 (and_6_out, not_3_out, IN_1);
  and and_7 (and_7_out, IN_1, IN_0);
  or or_3 (OUT_1, and_5_out, and_6_out, and_7_out);
  and and_8 (and_8_out, IN_3, not_1_out);
  and and_9 (and_9_out, not_4_out, not_3_out, IN_0);
  and and_10 (and_10_out, IN_2, IN_1, not_1_out);
  or or_4 (OUT_0, and_8_out, and_10_out, and_9_out);
endmodule

module BinToBCD8 (
  input  BIN_0,
  input  BIN_1,
  input  BIN_2,
  input  BIN_3,
  input  BIN_4,
  input  BIN_5,
  input  BIN_6,
  input  BIN_7,
  output BCD1_0,
  output BCD1_1,
  output BCD1_2,
  output BCD1_3,
  output BCD10_0,
  output BCD10_1,
  output BCD10_2,
  output BCD10_3,
  output BCD100_0,
  output BCD100_1,
  output BCD100_2,
  output BCD100_3
);

  wire bintobcd_add3_1_out_0, bintobcd_add3_1_out_1, bintobcd_add3_1_out_2, bintobcd_add3_1_out_3,
       bintobcd_add3_2_out_0, bintobcd_add3_2_out_1, bintobcd_add3_2_out_2, bintobcd_add3_2_out_3,
       bintobcd_add3_3_out_0, bintobcd_add3_3_out_1, bintobcd_add3_3_out_2, bintobcd_add3_3_out_3,
       bintobcd_add3_4_out_0, bintobcd_add3_4_out_1, bintobcd_add3_4_out_2, bintobcd_add3_6_out_0,
       bintobcd_add3_6_out_1, bintobcd_add3_6_out_2, bintobcd_add3_6_out_3;

  BinToBCD___Add3 bintobcd_add3_1 (
    .IN_3(1'b0), .IN_2(BIN_7), .IN_1(BIN_6), .IN_0(BIN_5), .OUT_3(bintobcd_add3_1_out_3),
    .OUT_2(bintobcd_add3_1_out_2), .OUT_1(bintobcd_add3_1_out_1), .OUT_0(bintobcd_add3_1_out_0));
  BinToBCD___Add3 bintobcd_add3_2 (
    .IN_3(bintobcd_add3_1_out_2), .IN_2(bintobcd_add3_1_out_1), .IN_1(bintobcd_add3_1_out_0), .IN_0(BIN_4),
    .OUT_3(bintobcd_add3_2_out_3), .OUT_2(bintobcd_add3_2_out_2), .OUT_1(bintobcd_add3_2_out_1),
    .OUT_0(bintobcd_add3_2_out_0));
  BinToBCD___Add3 bintobcd_add3_3 (
    .IN_3(bintobcd_add3_2_out_2), .IN_2(bintobcd_add3_2_out_1), .IN_1(bintobcd_add3_2_out_0), .IN_0(BIN_3),
    .OUT_3(bintobcd_add3_3_out_3), .OUT_2(bintobcd_add3_3_out_2), .OUT_1(bintobcd_add3_3_out_1),
    .OUT_0(bintobcd_add3_3_out_0));
  BinToBCD___Add3 bintobcd_add3_4 (
    .IN_3(1'b0), .IN_2(bintobcd_add3_1_out_3), .IN_1(bintobcd_add3_2_out_3), .IN_0(bintobcd_add3_3_out_3),
    .OUT_3(BCD100_1), .OUT_2(bintobcd_add3_4_out_2), .OUT_1(bintobcd_add3_4_out_1),
    .OUT_0(bintobcd_add3_4_out_0));
  BinToBCD___Add3 bintobcd_add3_5 (
    .IN_3(bintobcd_add3_4_out_2), .IN_2(bintobcd_add3_4_out_1), .IN_1(bintobcd_add3_4_out_0),
    .IN_0(bintobcd_add3_6_out_3), .OUT_3(BCD100_0), .OUT_2(BCD10_3), .OUT_1(BCD10_2), .OUT_0(BCD10_1));
  BinToBCD___Add3 bintobcd_add3_6 (
    .IN_3(bintobcd_add3_3_out_2), .IN_2(bintobcd_add3_3_out_1), .IN_1(bintobcd_add3_3_out_0), .IN_0(BIN_2),
    .OUT_3(bintobcd_add3_6_out_3), .OUT_2(bintobcd_add3_6_out_2), .OUT_1(bintobcd_add3_6_out_1),
    .OUT_0(bintobcd_add3_6_out_0));
  BinToBCD___Add3 bintobcd_add3_7 (
    .IN_3(bintobcd_add3_6_out_2), .IN_2(bintobcd_add3_6_out_1), .IN_1(bintobcd_add3_6_out_0), .IN_0(BIN_1),
    .OUT_3(BCD10_0), .OUT_2(BCD1_3), .OUT_1(BCD1_2), .OUT_0(BCD1_1));

  assign BCD1_0 = BIN_0;
  assign BCD100_2 = 1'b0;
  assign BCD100_3 = 1'b0;
endmodule

module BCD_Display (
  input  BCD_0,
  input  BCD_1,
  input  BCD_2,
  input  BCD_3,
  output a,
  output b,
  output c,
  output d,
  output e,
  output f,
  output g,
  output dp
);

  wire decoder_1_out0, decoder_1_out1, decoder_1_out2, decoder_1_out3, decoder_1_out4, decoder_1_out5,
       decoder_1_out6, decoder_1_out7, decoder_1_out8, decoder_1_out9;

  Decoder #(.select(4), .enable("false")) decoder_1 (
    .out0(decoder_1_out0), .out1(decoder_1_out1), .out2(decoder_1_out2), .out3(decoder_1_out3),
    .out4(decoder_1_out4), .out5(decoder_1_out5), .out6(decoder_1_out6), .out7(decoder_1_out7),
    .out8(decoder_1_out8), .out9(decoder_1_out9), .sel({BCD_3, BCD_2, BCD_1, BCD_0}));  // open: out10, out11, out12, out13, out14, out15
  or or_1 (a, decoder_1_out9, decoder_1_out8, decoder_1_out7, decoder_1_out6, decoder_1_out5, 1'b0, decoder_1_out3, decoder_1_out2, 1'b0, decoder_1_out0);
  or or_2 (b, decoder_1_out9, decoder_1_out8, decoder_1_out7, 1'b0, 1'b0, decoder_1_out4, decoder_1_out3, decoder_1_out2, decoder_1_out1, decoder_1_out0);
  or or_3 (c, decoder_1_out9, decoder_1_out8, decoder_1_out7, decoder_1_out6, decoder_1_out5, decoder_1_out4, decoder_1_out3, 1'b0, decoder_1_out1, decoder_1_out0);
  or or_4 (d, decoder_1_out9, decoder_1_out8, 1'b0, decoder_1_out6, decoder_1_out5, 1'b0, decoder_1_out3, decoder_1_out2, 1'b0, decoder_1_out0);
  or or_5 (e, 1'b0, decoder_1_out8, 1'b0, decoder_1_out6, 1'b0, 1'b0, 1'b0, decoder_1_out2, 1'b0, decoder_1_out0);
  or or_6 (f, decoder_1_out9, decoder_1_out8, 1'b0, decoder_1_out6, decoder_1_out5, decoder_1_out4, 1'b0, 1'b0, 1'b0, decoder_1_out0);
  or or_7 (g, decoder_1_out9, decoder_1_out8, 1'b0, decoder_1_out6, decoder_1_out5, decoder_1_out4, decoder_1_out3, decoder_1_out2, 1'b0, 1'b0);
  or or_8 (dp, 1'b0, 1'b0, 1'b0, 1'b0, 1'b0, 1'b0, 1'b0, 1'b0, 1'b0, 1'b0);
endmodule

module DEC_Diplay (
  input  BIN_0,
  input  BIN_1,
  input  BIN_2,
  input  BIN_3,
  input  BIN_4,
  input  BIN_5,
  input  BIN_6,
  input  BIN_7,
  output LED0,
  output LED1,
  output LED2,
  output LED3,
  output LED4,
  output LED5,
  output LED6,
  output LED7,
  output BCD1_0,
  output BCD1_1,
  output BCD1_2,
  output BCD1_3,
  output BCD10_0,
  output BCD10_1,
  output BCD10_2,
  output BCD10_3,
  output BCD100_0,
  output BCD100_1,
  output BCD100_2,
  output BCD100_3
);

  BinToBCD8 bintobcd8_1 (
    .BIN_0(BIN_0), .BIN_1(BIN_1), .BIN_2(BIN_2), .BIN_3(BIN_3), .BIN_4(BIN_4), .BIN_5(BIN_5), .BIN_6(BIN_6),
    .BIN_7(BIN_7), .BCD1_0(BCD1_0), .BCD1_1(BCD1_1), .BCD1_2(BCD1_2), .BCD1_3(BCD1_3), .BCD10_0(BCD10_0),
    .BCD10_1(BCD10_1), .BCD10_2(BCD10_2), .BCD10_3(BCD10_3), .BCD100_0(BCD100_0), .BCD100_1(BCD100_1),
    .BCD100_2(BCD100_2), .BCD100_3(BCD100_3));

  assign LED0 = BIN_0;
  assign LED1 = BIN_1;
  assign LED2 = BIN_2;
  assign LED3 = BIN_3;
  assign LED4 = BIN_4;
  assign LED5 = BIN_5;
  assign LED6 = BIN_6;
  assign LED7 = BIN_7;
endmodule

module BIN_Display (
  input  IN_0,
  input  IN_1,
  input  IN_2,
  input  IN_3,
  input  IN_4,
  input  IN_5,
  input  IN_6,
  input  IN_7,
  output LED0,
  output LED1,
  output LED2,
  output LED3,
  output LED4,
  output LED5,
  output LED6,
  output LED7
);


  assign LED0 = IN_0;
  assign LED1 = IN_1;
  assign LED2 = IN_2;
  assign LED3 = IN_3;
  assign LED4 = IN_4;
  assign LED5 = IN_5;
  assign LED6 = IN_6;
  assign LED7 = IN_7;
endmodule

module HEX_Display (
  input  BIN_0,
  input  BIN_1,
  input  BIN_2,
  input  BIN_3,
  input  BIN_4,
  input  BIN_5,
  input  BIN_6,
  input  BIN_7,
  output LED0,
  output LED1,
  output LED2,
  output LED3,
  output LED4,
  output LED5,
  output LED6,
  output LED7,
  output [3:0] MSN,
  output [3:0] LSN
);


  assign LED0 = BIN_0;
  assign LED1 = BIN_1;
  assign LED2 = BIN_2;
  assign LED3 = BIN_3;
  assign LED4 = BIN_4;
  assign LED5 = BIN_5;
  assign LED6 = BIN_6;
  assign LED7 = BIN_7;
  assign LSN = {BIN_3, BIN_2, BIN_1, BIN_0};
  assign MSN = {BIN_7, BIN_6, BIN_5, BIN_4};
endmodule
