// Logisim project common.circ as structural Verilog
module FullAdder (
  input  a,
  input  b,
  input  cin,
  output sum,
  output cout
);

  wire and_1_out, and_2_out, xor_1_out;

  xor xor_1 (xor_1_out, a, b);
  and and_1 (and_1_out, xor_1_out, cin);
  and and_2 (and_2_out, a, b);
  xor xor_2 (sum, xor_1_out, cin);
  or or_1 (cout, and_1_out, and_2_out);
endmodule

module Add4 (
  input  a3,
  input  b3,
  input  a2,
  input  b2,
  input  a1,
  input  b1,
  input  a0,
  input  b0,
  input  cin,
  output cout,
  output sum_3,
  output sum_2,
  output sum_1,
  output sum_0
);

  wire fulladder_2_cout, fulladder_3_cout, fulladder_4_cout;

  FullAdder fulladder_1 (.a(a3), .b(b3), .cin(fulladder_2_cout), .sum(sum_3), .cout(cout));
  FullAdder fulladder_2 (.a(a2), .b(b2), .cin(fulladder_3_cout), .sum(sum_2), .cout(fulladder_2_cout));
  FullAdder fulladder_3 (.a(a1), .b(b1), .cin(fulladder_4_cout), .sum(sum_1), .cout(fulladder_3_cout));
  FullAdder fulladder_4 (.a(a0), .b(b0), .cin(cin), .sum(sum_0), .cout(fulladder_4_cout));
endmodule

module Inc4 (
  input  cin,
  input  in0,
  input  in1,
  input  in2,
  input  in3,
  output out0,
  output out1,
  output out2,
  output cout,
  output out3
);

  wire and_1_out, and_2_out, and_3_out;

  and and_1 (and_1_out, in0, cin);
  xor xor_1 (out0, in0, cin);
  and and_2 (and_2_out, in1, and_1_out);
  xor xor_2 (out1, in1, and_1_out);
  and and_3 (and_3_out, in2, and_2_out);
  xor xor_3 (out2, in2, and_2_out);
  and and_4 (cout, in3, and_3_out);
  xor xor_4 (out3, in3, and_3_out);
endmodule

module Inverter4 (
  input  in_3,
  input  in_2,
  input  in_1,
  input  in_0,
  input  inv,
  output out_3,
  output out_2,
  output out_1,
  output out_0
);

  xor xor_1 (out_3, inv, in_3);
  xor xor_2 (out_2, inv, in_2);
  xor xor_3 (out_1, inv, in_1);
  xor xor_4 (out_0, inv, in_0);
endmodule

module Zero4 (
  input  _3,
  input  _2,
  input  _1,
  input  _0,
  output zero
);

  wire or_1_out, or_2_out;

  or or_1 (or_1_out, _3, _2);
  or or_2 (or_2_out, _1, _0);
  nor nor_1 (zero, or_2_out, or_1_out);
endmodule

module ALU_2 (
  input  a_0,
  input  b_0,
  input  a_1,
  input  b_1,
  input  a_2,
  input  b_2,
  input  a_3,
  input  b_3,
  input  op,
  input  cin,
  output LEDop,
  output LEDcin,
  output sum_0,
  output sum_1,
  output sum_2,
  output sum_3
);

  wire inverter4_1_out_0, inverter4_1_out_1, inverter4_1_out_2, inverter4_1_out_3, xor_1_out;

  Add4 add4_1 (
    .cin(xor_1_out), .a3(a_3), .b3(inverter4_1_out_3), .a2(a_2), .b2(inverter4_1_out_2), .a1(a_1),
    .b1(inverter4_1_out_1), .a0(a_0), .b0(inverter4_1_out_0), .sum_3(sum_3), .sum_2(sum_2), .sum_1(sum_1),
    .sum_0(sum_0));  // open: cout
  Inverter4 inverter4_1 (
    .inv(op), .in_3(b_3), .in_2(b_2), .in_1(b_1), .in_0(b_0), .out_3(inverter4_1_out_3),
    .out_2(inverter4_1_out_2), .out_1(inverter4_1_out_1), .out_0(inverter4_1_out_0));
  xor xor_1 (xor_1_out, op, cin);

  assign LEDcin = cin;
  assign LEDop = op;
endmodule

module SR_Latch (
  input  set,
  input  reset,
  output Q,
  output nQ
);

  wire or_1_out, or_2_out;

  or or_1 (or_1_out, set, Q);
  not not_1 (Q, or_2_out);
  not not_2 (nQ, or_1_out);
  or or_2 (or_2_out, nQ, reset);
endmodule

module D_Latch (
  input  D,
  input  write,
  input  nrst,
  output Q,
  output nQ
);

  wire and_1_out, and_2_out, not_1_out, not_2_out, or_1_out;

  not not_1 (not_1_out, D);
  not not_2 (not_2_out, nrst);
  and and_1 (and_1_out, D, write);
  and and_2 (and_2_out, write, not_1_out);
  SR_Latch sr_latch_1 (.set(and_1_out), .Q(Q), .nQ(nQ), .reset(or_1_out));
  or or_1 (or_1_out, and_2_out, not_2_out);
endmodule

module D_FlipFlop (
  input  clk,
  input  D,
  input  nrst,
  output Q,
  output nQ
);

  wire d_latch_1_q, not_1_out, not_2_out;

  not not_1 (not_1_out, clk);
  D_Latch d_latch_1 (.D(D), .write(not_1_out), .nrst(nrst), .Q(d_latch_1_q));  // open: nQ
  not not_2 (not_2_out, not_1_out);
  D_Latch d_latch_2 (.D(d_latch_1_q), .write(not_2_out), .nrst(nrst), .Q(Q), .nQ(nQ));
endmodule

module Reg4LA (
  input  IN_3,
  input  IN_2,
  input  IN_1,
  input  IN_0,
  input  read,
  input  write,
  input  nrst,
  output LED_3,
  output LED_2,
  output LED_1,
  output LED_0,
  output OUT_3,
  output OUT_2,
  output OUT_1,
  output OUT_0,
  output LEDr,
  output LEDw,
  output LEDrst
);

  D_Latch d_latch_1 (.D(IN_3), .write(write), .nrst(nrst), .Q(LED_3));  // open: nQ
  assign OUT_3 = read ? LED_3 : 1'bz;  // Controlled_Buffer controlled_buffer_1
  D_Latch d_latch_2 (.D(IN_2), .write(write), .nrst(nrst), .Q(LED_2));  // open: nQ
  assign OUT_2 = read ? LED_2 : 1'bz;  // Controlled_Buffer controlled_buffer_2
  D_Latch d_latch_3 (.D(IN_1), .write(write), .nrst(nrst), .Q(LED_1));  // open: nQ
  assign OUT_1 = read ? LED_1 : 1'bz;  // Controlled_Buffer controlled_buffer_3
  D_Latch d_latch_4 (.D(IN_0), .write(write), .nrst(nrst), .Q(LED_0));  // open: nQ
  assign OUT_0 = read ? LED_0 : 1'bz;  // Controlled_Buffer controlled_buffer_4

  assign LEDr = read;
  assign LEDrst = nrst;
  assign LEDw = write;
endmodule

module Reg4FF (
  input  IN_3,
  input  IN_2,
  input  IN_1,
  input  IN_0,
  input  read,
  input  write,
  input  nrst,
  output LED_3,
  output LED_2,
  output LED_1,
  output LED_0,
  output OUT_3,
  output OUT_2,
  output OUT_1,
  output OUT_0,
  output LEDr,
  output LEDw,
  output LEDrst
);

  D_FlipFlop d_flipflop_1 (.clk(write), .D(IN_3), .nrst(nrst), .Q(LED_3));  // open: nQ
  assign OUT_3 = read ? LED_3 : 1'bz;  // Controlled_Buffer controlled_buffer_1
  D_FlipFlop d_flipflop_2 (.clk(write), .D(IN_2), .nrst(nrst), .Q(LED_2));  // open: nQ
  assign OUT_2 = read ? LED_2 : 1'bz;  // Controlled_Buffer controlled_buffer_2
  D_FlipFlop d_flipflop_3 (.clk(write), .D(IN_1), .nrst(nrst), .Q(LED_1));  // open: nQ
  assign OUT_1 = read ? LED_1 : 1'bz;  // Controlled_Buffer controlled_buffer_3
  D_FlipFlop d_flipflop_4 (.clk(write), .D(IN_0), .nrst(nrst), .Q(LED_0));  // open: nQ
  assign OUT_0 = read ? LED_0 : 1'bz;  // Controlled_Buffer controlled_buffer_4

  assign LEDr = read;
  assign LEDrst = nrst;
  assign LEDw = write;
endmodule

module Counter4 (
  input  clk,
  input  inc,
  input  IN_3,
  input  IN_2,
  input  IN_1,
  input  IN_0,
  input  read,
  input  write,
  input  nrst,
  output LEDclk,
  output LEDinc,
  output LED_3,
  output LED_2,
  output LED_1,
  output LED_0,
  output OUT_3,
  output OUT_2,
  output OUT_1,
  output OUT_0,
  output LEDr,
  output LEDw,
  output LEDrst
);

  wire and_1_out, and_2_out, and_3_out, and_4_out, multiplexer_1_out, multiplexer_2_out, multiplexer_3_out,
       multiplexer_4_out, xor_1_out, xor_2_out, xor_3_out, xor_4_out;

  and and_1 (and_1_out, and_2_out, LED_2);
  xor xor_1 (xor_1_out, and_1_out, LED_3);
  Multiplexer #(.enable("false")) multiplexer_1 (.in0(xor_1_out), .in1(IN_3), .out(multiplexer_1_out), .sel(write));
  D_FlipFlop d_flipflop_1 (.clk(clk), .D(multiplexer_1_out), .nrst(nrst), .Q(LED_3));  // open: nQ
  assign OUT_3 = read ? LED_3 : 1'bz;  // Controlled_Buffer controlled_buffer_1
  and and_2 (and_2_out, and_3_out, LED_1);
  xor xor_2 (xor_2_out, and_2_out, LED_2);
  Multiplexer #(.enable("false")) multiplexer_2 (.in0(xor_2_out), .in1(IN_2), .out(multiplexer_2_out), .sel(write));
  D_FlipFlop d_flipflop_2 (.clk(clk), .D(multiplexer_2_out), .nrst(nrst), .Q(LED_2));  // open: nQ
  assign OUT_2 = read ? LED_2 : 1'bz;  // Controlled_Buffer controlled_buffer_2
  and and_3 (and_3_out, and_4_out, LED_0);
  xor xor_3 (xor_3_out, and_3_out, LED_1);
  D_FlipFlop d_flipflop_3 (.clk(clk), .D(multiplexer_3_out), .nrst(nrst), .Q(LED_1));  // open: nQ
  Multiplexer #(.enable("false")) multiplexer_3 (.in0(xor_3_out), .in1(IN_1), .out(multiplexer_3_out), .sel(write));
  assign OUT_1 = read ? LED_1 : 1'bz;  // Controlled_Buffer controlled_buffer_3
  and and_4 (and_4_out, inc, ~write);  // AND_Gate
  xor xor_4 (xor_4_out, and_4_out, LED_0);
  D_FlipFlop d_flipflop_4 (.clk(clk), .D(multiplexer_4_out), .nrst(nrst), .Q(LED_0));  // open: nQ
  Multiplexer #(.enable("false")) multiplexer_4 (.in0(xor_4_out), .in1(IN_0), .out(multiplexer_4_out), .sel(write));
  assign OUT_0 = read ? LED_0 : 1'bz;  // Controlled_Buffer controlled_buffer_4

  assign LEDclk = clk;
  assign LEDinc = inc;
  assign LEDr = read;
  assign LEDrst = nrst;
  assign LEDw = write;
endmodule

module ZeroPass4 (
  input  IN_3,
  input  IN_2,
  input  IN_1,
  input  IN_0,
  input  enable,
  output LEDen,
  output OUT_3,
  output OUT_2,
  output OUT_1,
  output OUT_0
);

  and and_1 (OUT_3, enable, IN_3);
  and and_2 (OUT_2, enable, IN_2);
  and and_3 (OUT_1, enable, IN_1);
  and and_4 (OUT_0, enable, IN_0);

  assign LEDen = enable;
endmodule

module SRAM_Cell (
  input  IN,
  input  select,
  input  read,
  input  write,
  input  nrst,
  output LED,
  output OUT,
  output LEDsel,
  output LEDr,
  output LEDw,
  output LEDrst
);

  wire and_1_out, and_2_out;

  and and_1 (and_1_out, select, write);
  D_Latch d_latch_1 (.D(IN), .write(and_1_out), .nrst(nrst), .Q(LED));  // open: nQ
  assign OUT = and_2_out ? LED : 1'bz;  // Controlled_Buffer controlled_buffer_1
  and and_2 (and_2_out, select, read);

  assign LEDr = read;
  assign LEDrst = nrst;
  assign LEDsel = select;
  assign LEDw = write;
endmodule

module SRAM_4x4bit (
  input  ADDR_1,
  input  ADDR_0,
  input  select,
  input  IN_3,
  input  IN_2,
  input  IN_1,
  input  IN_0,
  input  read,
  input  write,
  input  nrst,
  output LEDsel_0,
  output LED_0__0,
  output LED_0__1,
  output LED_0__2,
  output LED_0__3,
  output LEDsel_1,
  output LED_1__0,
  output LED_1__1,
  output LED_1__2,
  output LED_1__3,
  output LEDsel_2,
  output LED_2__0,
  output LED_2__1,
  output LED_2__2,
  output LED_2__3,
  output LEDsel_3,
  output LED_3__0,
  output LED_3__1,
  output LED_3__2,
  output LED_3__3,
  output LEDsel,
  output LEDaddr_0,
  output LEDaddr_1,
  output LEDr,
  output LEDw,
  output LEDrst,
  output OUT_3,
  output OUT_2,
  output OUT_1,
  output OUT_0
);

  wire not_1_out, not_2_out;

  not not_1 (not_1_out, ADDR_1);
  not not_2 (not_2_out, ADDR_0);
  and and_1 (LEDsel_0, not_2_out, not_1_out, select);
  and and_2 (LEDsel_1, ADDR_0, not_1_out, select);
  and and_3 (LEDsel_2, not_2_out, ADDR_1, select);
  and and_4 (LEDsel_3, ADDR_0, ADDR_1, select);
  SRAM_Cell sram_cell_1 (
    .IN(IN_3), .select(LEDsel_0), .read(read), .write(write), .nrst(nrst), .LED(LED_0__3), .OUT(OUT_3));  // open: LEDsel, LEDr, LEDw, LEDrst
  SRAM_Cell sram_cell_2 (
    .IN(IN_3), .select(LEDsel_1), .read(read), .write(write), .nrst(nrst), .LED(LED_1__3), .OUT(OUT_3));  // open: LEDsel, LEDr, LEDw, LEDrst
  SRAM_Cell sram_cell_3 (
    .IN(IN_3), .select(LEDsel_2), .read(read), .write(write), .nrst(nrst), .LED(LED_2__3), .OUT(OUT_3));  // open: LEDsel, LEDr, LEDw, LEDrst
  SRAM_Cell sram_cell_4 (
    .IN(IN_3), .select(LEDsel_3), .read(read), .write(write), .nrst(nrst), .LED(LED_3__3), .OUT(OUT_3));  // open: LEDsel, LEDr, LEDw, LEDrst
  SRAM_Cell sram_cell_5 (
    .IN(IN_2), .select(LEDsel_0), .read(read), .write(write), .nrst(nrst), .LED(LED_0__2), .OUT(OUT_2));  // open: LEDsel, LEDr, LEDw, LEDrst
  SRAM_Cell sram_cell_6 (
    .IN(IN_2), .select(LEDsel_1), .read(read), .write(write), .nrst(nrst), .LED(LED_1__2), .OUT(OUT_2));  // open: LEDsel, LEDr, LEDw, LEDrst
  SRAM_Cell sram_cell_7 (
    .IN(IN_2), .select(LEDsel_2), .read(read), .write(write), .nrst(nrst), .LED(LED_2__2), .OUT(OUT_2));  // open: LEDsel, LEDr, LEDw, LEDrst
  SRAM_Cell sram_cell_8 (
    .IN(IN_2), .select(LEDsel_3), .read(read), .write(write), .nrst(nrst), .LED(LED_3__2), .OUT(OUT_2));  // open: LEDsel, LEDr, LEDw, LEDrst
  SRAM_Cell sram_cell_9 (
    .IN(IN_1), .select(LEDsel_0), .read(read), .write(write), .nrst(nrst), .LED(LED_0__1), .OUT(OUT_1));  // open: LEDsel, LEDr, LEDw, LEDrst
  SRAM_Cell sram_cell_10 (
    .IN(IN_1), .select(LEDsel_1), .read(read), .write(write), .nrst(nrst), .LED(LED_1__1), .OUT(OUT_1));  // open: LEDsel, LEDr, LEDw, LEDrst
  SRAM_Cell sram_cell_11 (
    .IN(IN_1), .select(LEDsel_2), .read(read), .write(write), .nrst(nrst), .LED(LED_2__1), .OUT(OUT_1));  // open: LEDsel, LEDr, LEDw, LEDrst
  SRAM_Cell sram_cell_12 (
    .IN(IN_1), .select(LEDsel_3), .read(read), .write(write), .nrst(nrst), .LED(LED_3__1), .OUT(OUT_1));  // open: LEDsel, LEDr, LEDw, LEDrst
  SRAM_Cell sram_cell_13 (
    .IN(IN_0), .select(LEDsel_0), .read(read), .write(write), .nrst(nrst), .LED(LED_0__0), .OUT(OUT_0));  // open: LEDsel, LEDr, LEDw, LEDrst
  SRAM_Cell sram_cell_14 (
    .IN(IN_0), .select(LEDsel_1), .read(read), .write(write), .nrst(nrst), .LED(LED_1__0), .OUT(OUT_0));  // open: LEDsel, LEDr, LEDw, LEDrst
  SRAM_Cell sram_cell_15 (
    .IN(IN_0), .select(LEDsel_2), .read(read), .write(write), .nrst(nrst), .LED(LED_2__0), .OUT(OUT_0));  // open: LEDsel, LEDr, LEDw, LEDrst
  SRAM_Cell sram_cell_16 (
    .IN(IN_0), .select(LEDsel_3), .read(read), .write(write), .nrst(nrst), .LED(LED_3__0), .OUT(OUT_0));  // open: LEDsel, LEDr, LEDw, LEDrst

  assign LEDaddr_0 = ADDR_0;
  assign LEDaddr_1 = ADDR_1;
  assign LEDr = read;
  assign LEDrst = nrst;
  assign LEDsel = select;
  assign LEDw = write;

  // Other names for the same wires on the sheet: _00 = LED_0__0; _01 = LED_0__1; _02 = LED_0__2; _03 = LED_0__3;
  //   _10 = LED_1__0; _11 = LED_1__1; _12 = LED_1__2; _13 = LED_1__3; _20 = LED_2__0; _21 = LED_2__1; _22 = LED_2__2;
  //   _23 = LED_2__3; _30 = LED_3__0; _31 = LED_3__1; _32 = LED_3__2; _33 = LED_3__3
endmodule

module SRAM_16x4bit (
  input  ADDR_3,
  input  ADDR_2,
  input  ADDR_1,
  input  ADDR_0,
  input  select,
  input  IN_3,
  input  IN_2,
  input  IN_1,
  input  IN_0,
  input  read,
  input  write,
  input  nrst,
  output LEDsel_0,
  output LED_0__0,
  output LED_0__1,
  output LED_0__2,
  output LED_0__3,
  output LEDsel_1,
  output LED_1__0,
  output LED_1__1,
  output LED_1__2,
  output LED_1__3,
  output LEDsel_2,
  output LED_2__0,
  output LED_2__1,
  output LED_2__2,
  output LED_2__3,
  output LEDsel_3,
  output LED_3__0,
  output LED_3__1,
  output LED_3__2,
  output LED_3__3,
  output LEDsel_4,
  output LED_4__0,
  output LED_4__1,
  output LED_4__2,
  output LED_4__3,
  output LEDsel_5,
  output LED_5__0,
  output LED_5__1,
  output LED_5__2,
  output LED_5__3,
  output LEDsel_6,
  output LED_6__0,
  output LED_6__1,
  output LED_6__2,
  output LED_6__3,
  output LEDsel_7,
  output LED_7__0,
  output LED_7__1,
  output LED_7__2,
  output LED_7__3,
  output LEDsel_8,
  output LED_8__0,
  output LED_8__1,
  output LED_8__2,
  output LED_8__3,
  output LEDsel_9,
  output LED_9__0,
  output LED_9__1,
  output LED_9__2,
  output LED_9__3,
  output LEDsel_A,
  output LED_A__0,
  output LED_A__1,
  output LED_A__2,
  output LED_A__3,
  output LEDsel_B,
  output LED_B__0,
  output LED_B__1,
  output LED_B__2,
  output LED_B__3,
  output LEDsel_C,
  output LED_C__0,
  output LED_C__1,
  output LED_C__2,
  output LED_C__3,
  output LEDsel_D,
  output LED_D__0,
  output LED_D__1,
  output LED_D__2,
  output LED_D__3,
  output LEDsel_E,
  output LED_E__0,
  output LED_E__1,
  output LED_E__2,
  output LED_E__3,
  output LEDsel_F,
  output LED_F__0,
  output LED_F__1,
  output LED_F__2,
  output LEDsel,
  output LED_F__3,
  output LEDaddr_0,
  output LEDaddr_1,
  output LEDaddr_0_2,
  output LEDaddr_1_2,
  output LEDr,
  output LEDw,
  output LEDrst,
  output OUT_3,
  output OUT_2,
  output OUT_1,
  output OUT_0
);

  wire not_1_out, not_2_out, not_3_out, not_4_out;

  not not_1 (not_1_out, ADDR_2);
  not not_2 (not_2_out, ADDR_3);
  not not_3 (not_3_out, ADDR_1);
  not not_4 (not_4_out, ADDR_0);
  and and_1 (LEDsel_0, select, not_4_out, not_3_out, not_1_out, not_2_out);
  and and_2 (LEDsel_1, select, ADDR_0, not_3_out, not_1_out, not_2_out);
  and and_3 (LEDsel_2, select, not_4_out, ADDR_1, not_1_out, not_2_out);
  and and_4 (LEDsel_3, select, ADDR_0, ADDR_1, not_1_out, not_2_out);
  and and_5 (LEDsel_4, select, not_4_out, not_3_out, ADDR_2, not_2_out);
  and and_6 (LEDsel_5, select, ADDR_0, not_3_out, ADDR_2, not_2_out);
  and and_7 (LEDsel_6, select, not_4_out, ADDR_1, ADDR_2, not_2_out);
  and and_8 (LEDsel_7, select, ADDR_0, ADDR_1, ADDR_2, not_2_out);
  and and_9 (LEDsel_8, select, not_4_out, not_3_out, not_1_out, ADDR_3);
  and and_10 (LEDsel_9, select, ADDR_0, not_3_out, not_1_out, ADDR_3);
  and and_11 (LEDsel_A, select, not_4_out, ADDR_1, not_1_out, ADDR_3);
  and and_12 (LEDsel_B, select, ADDR_0, ADDR_1, not_1_out, ADDR_3);
  and and_13 (LEDsel_C, select, not_4_out, not_3_out, ADDR_2, ADDR_3);
  and and_14 (LEDsel_D, select, ADDR_0, not_3_out, ADDR_2, ADDR_3);
  and and_15 (LEDsel_E, select, not_4_out, ADDR_1, ADDR_2, ADDR_3);
  and and_16 (LEDsel_F, select, ADDR_0, ADDR_1, ADDR_2, ADDR_3);
  SRAM_Cell sram_cell_1 (
    .IN(IN_3), .select(LEDsel_0), .read(read), .write(write), .nrst(nrst), .LED(LED_0__3), .OUT(OUT_3));  // open: LEDsel, LEDr, LEDw, LEDrst
  SRAM_Cell sram_cell_2 (
    .IN(IN_3), .select(LEDsel_1), .read(read), .write(write), .nrst(nrst), .LED(LED_1__3), .OUT(OUT_3));  // open: LEDsel, LEDr, LEDw, LEDrst
  SRAM_Cell sram_cell_3 (
    .IN(IN_3), .select(LEDsel_2), .read(read), .write(write), .nrst(nrst), .LED(LED_2__3), .OUT(OUT_3));  // open: LEDsel, LEDr, LEDw, LEDrst
  SRAM_Cell sram_cell_4 (
    .IN(IN_3), .select(LEDsel_3), .read(read), .write(write), .nrst(nrst), .LED(LED_3__3), .OUT(OUT_3));  // open: LEDsel, LEDr, LEDw, LEDrst
  SRAM_Cell sram_cell_5 (
    .IN(IN_3), .select(LEDsel_4), .read(read), .write(write), .nrst(nrst), .LED(LED_4__3), .OUT(OUT_3));  // open: LEDsel, LEDr, LEDw, LEDrst
  SRAM_Cell sram_cell_6 (
    .IN(IN_3), .select(LEDsel_5), .read(read), .write(write), .nrst(nrst), .LED(LED_5__3), .OUT(OUT_3));  // open: LEDsel, LEDr, LEDw, LEDrst
  SRAM_Cell sram_cell_7 (
    .IN(IN_3), .select(LEDsel_6), .read(read), .write(write), .nrst(nrst), .LED(LED_6__3), .OUT(OUT_3));  // open: LEDsel, LEDr, LEDw, LEDrst
  SRAM_Cell sram_cell_8 (
    .IN(IN_3), .select(LEDsel_7), .read(read), .write(write), .nrst(nrst), .LED(LED_7__3), .OUT(OUT_3));  // open: LEDsel, LEDr, LEDw, LEDrst
  SRAM_Cell sram_cell_9 (
    .IN(IN_3), .select(LEDsel_8), .read(read), .write(write), .nrst(nrst), .LED(LED_8__3), .OUT(OUT_3));  // open: LEDsel, LEDr, LEDw, LEDrst
  SRAM_Cell sram_cell_10 (
    .IN(IN_3), .select(LEDsel_9), .read(read), .write(write), .nrst(nrst), .LED(LED_9__3), .OUT(OUT_3));  // open: LEDsel, LEDr, LEDw, LEDrst
  SRAM_Cell sram_cell_11 (
    .IN(IN_3), .select(LEDsel_A), .read(read), .write(write), .nrst(nrst), .LED(LED_A__3), .OUT(OUT_3));  // open: LEDsel, LEDr, LEDw, LEDrst
  SRAM_Cell sram_cell_12 (
    .IN(IN_3), .select(LEDsel_B), .read(read), .write(write), .nrst(nrst), .LED(LED_B__3), .OUT(OUT_3));  // open: LEDsel, LEDr, LEDw, LEDrst
  SRAM_Cell sram_cell_13 (
    .IN(IN_3), .select(LEDsel_C), .read(read), .write(write), .nrst(nrst), .LED(LED_C__3), .OUT(OUT_3));  // open: LEDsel, LEDr, LEDw, LEDrst
  SRAM_Cell sram_cell_14 (
    .IN(IN_3), .select(LEDsel_D), .read(read), .write(write), .nrst(nrst), .LED(LED_D__3), .OUT(OUT_3));  // open: LEDsel, LEDr, LEDw, LEDrst
  SRAM_Cell sram_cell_15 (
    .IN(IN_3), .select(LEDsel_E), .read(read), .write(write), .nrst(nrst), .LED(LED_E__3), .OUT(OUT_3));  // open: LEDsel, LEDr, LEDw, LEDrst
  SRAM_Cell sram_cell_16 (
    .IN(IN_3), .select(LEDsel_F), .read(read), .write(write), .nrst(nrst), .LED(LED_F__3), .OUT(OUT_3));  // open: LEDsel, LEDr, LEDw, LEDrst
  SRAM_Cell sram_cell_17 (
    .IN(IN_2), .select(LEDsel_0), .read(read), .write(write), .nrst(nrst), .LED(LED_0__2), .OUT(OUT_2));  // open: LEDsel, LEDr, LEDw, LEDrst
  SRAM_Cell sram_cell_18 (
    .IN(IN_2), .select(LEDsel_1), .read(read), .write(write), .nrst(nrst), .LED(LED_1__2), .OUT(OUT_2));  // open: LEDsel, LEDr, LEDw, LEDrst
  SRAM_Cell sram_cell_19 (
    .IN(IN_2), .select(LEDsel_2), .read(read), .write(write), .nrst(nrst), .LED(LED_2__2), .OUT(OUT_2));  // open: LEDsel, LEDr, LEDw, LEDrst
  SRAM_Cell sram_cell_20 (
    .IN(IN_2), .select(LEDsel_3), .read(read), .write(write), .nrst(nrst), .LED(LED_3__2), .OUT(OUT_2));  // open: LEDsel, LEDr, LEDw, LEDrst
  SRAM_Cell sram_cell_21 (
    .IN(IN_2), .select(LEDsel_4), .read(read), .write(write), .nrst(nrst), .LED(LED_4__2), .OUT(OUT_2));  // open: LEDsel, LEDr, LEDw, LEDrst
  SRAM_Cell sram_cell_22 (
    .IN(IN_2), .select(LEDsel_5), .read(read), .write(write), .nrst(nrst), .LED(LED_5__2), .OUT(OUT_2));  // open: LEDsel, LEDr, LEDw, LEDrst
  SRAM_Cell sram_cell_23 (
    .IN(IN_2), .select(LEDsel_6), .read(read), .write(write), .nrst(nrst), .LED(LED_6__2), .OUT(OUT_2));  // open: LEDsel, LEDr, LEDw, LEDrst
  SRAM_Cell sram_cell_24 (
    .IN(IN_2), .select(LEDsel_7), .read(read), .write(write), .nrst(nrst), .LED(LED_7__2), .OUT(OUT_2));  // open: LEDsel, LEDr, LEDw, LEDrst
  SRAM_Cell sram_cell_25 (
    .IN(IN_2), .select(LEDsel_8), .read(read), .write(write), .nrst(nrst), .LED(LED_8__2), .OUT(OUT_2));  // open: LEDsel, LEDr, LEDw, LEDrst
  SRAM_Cell sram_cell_26 (
    .IN(IN_2), .select(LEDsel_9), .read(read), .write(write), .nrst(nrst), .LED(LED_9__2), .OUT(OUT_2));  // open: LEDsel, LEDr, LEDw, LEDrst
  SRAM_Cell sram_cell_27 (
    .IN(IN_2), .select(LEDsel_A), .read(read), .write(write), .nrst(nrst), .LED(LED_A__2), .OUT(OUT_2));  // open: LEDsel, LEDr, LEDw, LEDrst
  SRAM_Cell sram_cell_28 (
    .IN(IN_2), .select(LEDsel_B), .read(read), .write(write), .nrst(nrst), .LED(LED_B__2), .OUT(OUT_2));  // open: LEDsel, LEDr, LEDw, LEDrst
  SRAM_Cell sram_cell_29 (
    .IN(IN_2), .select(LEDsel_C), .read(read), .write(write), .nrst(nrst), .LED(LED_C__2), .OUT(OUT_2));  // open: LEDsel, LEDr, LEDw, LEDrst
  SRAM_Cell sram_cell_30 (
    .IN(IN_2), .select(LEDsel_D), .read(read), .write(write), .nrst(nrst), .LED(LED_D__2), .OUT(OUT_2));  // open: LEDsel, LEDr, LEDw, LEDrst
  SRAM_Cell sram_cell_31 (
    .IN(IN_2), .select(LEDsel_E), .read(read), .write(write), .nrst(nrst), .LED(LED_E__2), .OUT(OUT_2));  // open: LEDsel, LEDr, LEDw, LEDrst
  SRAM_Cell sram_cell_32 (
    .IN(IN_2), .select(LEDsel_F), .read(read), .write(write), .nrst(nrst), .LED(LED_F__2), .OUT(OUT_2));  // open: LEDsel, LEDr, LEDw, LEDrst
  SRAM_Cell sram_cell_33 (
    .IN(IN_1), .select(LEDsel_0), .read(read), .write(write), .nrst(nrst), .LED(LED_0__1), .OUT(OUT_1));  // open: LEDsel, LEDr, LEDw, LEDrst
  SRAM_Cell sram_cell_34 (
    .IN(IN_1), .select(LEDsel_1), .read(read), .write(write), .nrst(nrst), .LED(LED_1__1), .OUT(OUT_1));  // open: LEDsel, LEDr, LEDw, LEDrst
  SRAM_Cell sram_cell_35 (
    .IN(IN_1), .select(LEDsel_2), .read(read), .write(write), .nrst(nrst), .LED(LED_2__1), .OUT(OUT_1));  // open: LEDsel, LEDr, LEDw, LEDrst
  SRAM_Cell sram_cell_36 (
    .IN(IN_1), .select(LEDsel_3), .read(read), .write(write), .nrst(nrst), .LED(LED_3__1), .OUT(OUT_1));  // open: LEDsel, LEDr, LEDw, LEDrst
  SRAM_Cell sram_cell_37 (
    .IN(IN_1), .select(LEDsel_4), .read(read), .write(write), .nrst(nrst), .LED(LED_4__1), .OUT(OUT_1));  // open: LEDsel, LEDr, LEDw, LEDrst
  SRAM_Cell sram_cell_38 (
    .IN(IN_1), .select(LEDsel_5), .read(read), .write(write), .nrst(nrst), .LED(LED_5__1), .OUT(OUT_1));  // open: LEDsel, LEDr, LEDw, LEDrst
  SRAM_Cell sram_cell_39 (
    .IN(IN_1), .select(LEDsel_6), .read(read), .write(write), .nrst(nrst), .LED(LED_6__1), .OUT(OUT_1));  // open: LEDsel, LEDr, LEDw, LEDrst
  SRAM_Cell sram_cell_40 (
    .IN(IN_1), .select(LEDsel_7), .read(read), .write(write), .nrst(nrst), .LED(LED_7__1), .OUT(OUT_1));  // open: LEDsel, LEDr, LEDw, LEDrst
  SRAM_Cell sram_cell_41 (
    .IN(IN_1), .select(LEDsel_8), .read(read), .write(write), .nrst(nrst), .LED(LED_8__1), .OUT(OUT_1));  // open: LEDsel, LEDr, LEDw, LEDrst
  SRAM_Cell sram_cell_42 (
    .IN(IN_1), .select(LEDsel_9), .read(read), .write(write), .nrst(nrst), .LED(LED_9__1), .OUT(OUT_1));  // open: LEDsel, LEDr, LEDw, LEDrst
  SRAM_Cell sram_cell_43 (
    .IN(IN_1), .select(LEDsel_A), .read(read), .write(write), .nrst(nrst), .LED(LED_A__1), .OUT(OUT_1));  // open: LEDsel, LEDr, LEDw, LEDrst
  SRAM_Cell sram_cell_44 (
    .IN(IN_1), .select(LEDsel_B), .read(read), .write(write), .nrst(nrst), .LED(LED_B__1), .OUT(OUT_1));  // open: LEDsel, LEDr, LEDw, LEDrst
  SRAM_Cell sram_cell_45 (
    .IN(IN_1), .select(LEDsel_C), .read(read), .write(write), .nrst(nrst), .LED(LED_C__1), .OUT(OUT_1));  // open: LEDsel, LEDr, LEDw, LEDrst
  SRAM_Cell sram_cell_46 (
    .IN(IN_1), .select(LEDsel_D), .read(read), .write(write), .nrst(nrst), .LED(LED_D__1), .OUT(OUT_1));  // open: LEDsel, LEDr, LEDw, LEDrst
  SRAM_Cell sram_cell_47 (
    .IN(IN_1), .select(LEDsel_E), .read(read), .write(write), .nrst(nrst), .LED(LED_E__1), .OUT(OUT_1));  // open: LEDsel, LEDr, LEDw, LEDrst
  SRAM_Cell sram_cell_48 (
    .IN(IN_1), .select(LEDsel_F), .read(read), .write(write), .nrst(nrst), .LED(LED_F__1), .OUT(OUT_1));  // open: LEDsel, LEDr, LEDw, LEDrst
  SRAM_Cell sram_cell_49 (
    .IN(IN_0), .select(LEDsel_0), .read(read), .write(write), .nrst(nrst), .LED(LED_0__0), .OUT(OUT_0));  // open: LEDsel, LEDr, LEDw, LEDrst
  SRAM_Cell sram_cell_50 (
    .IN(IN_0), .select(LEDsel_1), .read(read), .write(write), .nrst(nrst), .LED(LED_1__0), .OUT(OUT_0));  // open: LEDsel, LEDr, LEDw, LEDrst
  SRAM_Cell sram_cell_51 (
    .IN(IN_0), .select(LEDsel_2), .read(read), .write(write), .nrst(nrst), .LED(LED_2__0), .OUT(OUT_0));  // open: LEDsel, LEDr, LEDw, LEDrst
  SRAM_Cell sram_cell_52 (
    .IN(IN_0), .select(LEDsel_3), .read(read), .write(write), .nrst(nrst), .LED(LED_3__0), .OUT(OUT_0));  // open: LEDsel, LEDr, LEDw, LEDrst
  SRAM_Cell sram_cell_53 (
    .IN(IN_0), .select(LEDsel_4), .read(read), .write(write), .nrst(nrst), .LED(LED_4__0), .OUT(OUT_0));  // open: LEDsel, LEDr, LEDw, LEDrst
  SRAM_Cell sram_cell_54 (
    .IN(IN_0), .select(LEDsel_5), .read(read), .write(write), .nrst(nrst), .LED(LED_5__0), .OUT(OUT_0));  // open: LEDsel, LEDr, LEDw, LEDrst
  SRAM_Cell sram_cell_55 (
    .IN(IN_0), .select(LEDsel_6), .read(read), .write(write), .nrst(nrst), .LED(LED_6__0), .OUT(OUT_0));  // open: LEDsel, LEDr, LEDw, LEDrst
  SRAM_Cell sram_cell_56 (
    .IN(IN_0), .select(LEDsel_7), .read(read), .write(write), .nrst(nrst), .LED(LED_7__0), .OUT(OUT_0));  // open: LEDsel, LEDr, LEDw, LEDrst
  SRAM_Cell sram_cell_57 (
    .IN(IN_0), .select(LEDsel_8), .read(read), .write(write), .nrst(nrst), .LED(LED_8__0), .OUT(OUT_0));  // open: LEDsel, LEDr, LEDw, LEDrst
  SRAM_Cell sram_cell_58 (
    .IN(IN_0), .select(LEDsel_9), .read(read), .write(write), .nrst(nrst), .LED(LED_9__0), .OUT(OUT_0));  // open: LEDsel, LEDr, LEDw, LEDrst
  SRAM_Cell sram_cell_59 (
    .IN(IN_0), .select(LEDsel_A), .read(read), .write(write), .nrst(nrst), .LED(LED_A__0), .OUT(OUT_0));  // open: LEDsel, LEDr, LEDw, LEDrst
  SRAM_Cell sram_cell_60 (
    .IN(IN_0), .select(LEDsel_B), .read(read), .write(write), .nrst(nrst), .LED(LED_B__0), .OUT(OUT_0));  // open: LEDsel, LEDr, LEDw, LEDrst
  SRAM_Cell sram_cell_61 (
    .IN(IN_0), .select(LEDsel_C), .read(read), .write(write), .nrst(nrst), .LED(LED_C__0), .OUT(OUT_0));  // open: LEDsel, LEDr, LEDw, LEDrst
  SRAM_Cell sram_cell_62 (
    .IN(IN_0), .select(LEDsel_D), .read(read), .write(write), .nrst(nrst), .LED(LED_D__0), .OUT(OUT_0));  // open: LEDsel, LEDr, LEDw, LEDrst
  SRAM_Cell sram_cell_63 (
    .IN(IN_0), .select(LEDsel_E), .read(read), .write(write), .nrst(nrst), .LED(LED_E__0), .OUT(OUT_0));  // open: LEDsel, LEDr, LEDw, LEDrst
  SRAM_Cell sram_cell_64 (
    .IN(IN_0), .select(LEDsel_F), .read(read), .write(write), .nrst(nrst), .LED(LED_F__0), .OUT(OUT_0));  // open: LEDsel, LEDr, LEDw, LEDrst

  assign LEDaddr_0 = ADDR_0;
  assign LEDaddr_0_2 = ADDR_2;
  assign LEDaddr_1 = ADDR_1;
  assign LEDaddr_1_2 = ADDR_3;
  assign LEDr = read;
  assign LEDrst = nrst;
  assign LEDsel = select;
  assign LEDw = write;

  // Other names for the same wires on the sheet: _00 = LED_0__0; _01 = LED_0__1; _02 = LED_0__2; _03 = LED_0__3;
  //   _10 = LED_1__0; _11 = LED_1__1; _12 = LED_1__2; _13 = LED_1__3; _20 = LED_2__0; _21 = LED_2__1; _22 = LED_2__2;
  //   _23 = LED_2__3; _30 = LED_3__0; _31 = LED_3__1; _32 = LED_3__2; _33 = LED_3__3; _40 = LED_4__0; _41 = LED_4__1;
  //   _42 = LED_4__2; _43 = LED_4__3; _50 = LED_5__0; _51 = LED_5__1; _52 = LED_5__2; _53 = LED_5__3; _60 = LED_6__0;
  //   _61 = LED_6__1; _62 = LED_6__2; _63 = LED_6__3; _70 = LED_7__0; _71 = LED_7__1; _72 = LED_7__2; _73 = LED_7__3;
  //   _80 = LED_8__0; _81 = LED_8__1; _82 = LED_8__2; _83 = LED_8__3; _90 = LED_9__0; _91 = LED_9__1; _92 = LED_9__2;
  //   _93 = LED_9__3; A0 = LED_A__0; A1 = LED_A__1; A2 = LED_A__2; A3 = LED_A__3; B0 = LED_B__0; B1 = LED_B__1;
  //   B2 = LED_B__2; B3 = LED_B__3; C0 = LED_C__0; C1 = LED_C__1; C2 = LED_C__2; C3 = LED_C__3; D0 = LED_D__0;
  //   D1 = LED_D__1; D2 = LED_D__2; D3 = LED_D__3; E0 = LED_E__0; E1 = LED_E__1; E2 = LED_E__2; E3 = LED_E__3;
  //   F0 = LED_F__0; F1 = LED_F__1; F2 = LED_F__2; F3 = LED_F__3
endmodule

module ClockLogic (
  input  clk,
  input  halt,
  input  resume,
  input  nrst,
  output clk_out,
  output halt_out
);

  wire and_1_out, and_2_out, and_3_out, and_4_out, d_flipflop_1_nq, d_flipflop_2_nq, d_flipflop_3_nq,
       d_flipflop_3_q;

  D_FlipFlop d_flipflop_1 (.clk(resume), .D(1'b1), .nrst(and_1_out), .nQ(d_flipflop_1_nq));  // open: Q
  and and_1 (and_1_out, nrst, d_flipflop_1_nq);
  D_FlipFlop d_flipflop_2 (.clk(halt), .D(1'b1), .nrst(and_2_out), .Q(halt_out), .nQ(d_flipflop_2_nq));
  and and_2 (and_2_out, d_flipflop_1_nq, nrst);
  and and_3 (and_3_out, d_flipflop_3_nq, ~clk);  // AND_Gate
  D_FlipFlop d_flipflop_3 (.clk(and_3_out), .D(1'b1), .nrst(and_4_out), .Q(d_flipflop_3_q), .nQ(d_flipflop_3_nq));
  and and_4 (and_4_out, d_flipflop_1_nq, nrst);
  and and_5 (clk_out, clk, d_flipflop_2_nq, d_flipflop_3_q);
endmodule

module Delayer (
  input  in,
  output out
);

  wire not_1_out, not_2_out, not_3_out, not_4_out, not_5_out, not_6_out, not_7_out, not_8_out, not_9_out,
       not_10_out, not_11_out, not_12_out, not_13_out, not_14_out, not_15_out;

  not not_1 (not_1_out, in);
  not not_2 (not_2_out, not_1_out);
  not not_3 (not_3_out, not_5_out);
  not not_4 (not_4_out, not_2_out);
  not not_5 (not_5_out, not_4_out);
  not not_6 (not_6_out, not_3_out);
  not not_7 (not_7_out, not_6_out);
  not not_8 (not_8_out, not_9_out);
  not not_9 (not_9_out, not_10_out);
  not not_10 (not_10_out, not_7_out);
  not not_11 (not_11_out, not_8_out);
  not not_12 (not_12_out, not_11_out);
  not not_13 (not_13_out, not_12_out);
  not not_14 (not_14_out, not_13_out);
  not not_15 (not_15_out, not_14_out);
  not not_16 (out, not_15_out);
endmodule

module Decoder2x4 (
  input  sel0,
  input  sel1,
  output _00,
  output _01,
  output _10,
  output _11
);

  wire not_1_out, not_2_out;

  not not_1 (not_1_out, sel0);
  not not_2 (not_2_out, sel1);
  and and_1 (_00, not_2_out, not_1_out);
  and and_2 (_01, not_2_out, sel0);
  and and_3 (_10, sel1, not_1_out);
  and and_4 (_11, sel1, sel0);
endmodule

module Mux2x4 (
  input  a3,
  input  b3,
  input  a2,
  input  b2,
  input  a1,
  input  b1,
  input  a0,
  input  b0,
  input  sel,
  output LEDsel,
  output out3,
  output out2,
  output out1,
  output out0
);

  Multiplexer #(.enable("false")) multiplexer_1 (.in0(a3), .in1(b3), .out(out3), .sel(sel));
  Multiplexer #(.enable("false")) multiplexer_2 (.in0(a2), .in1(b2), .out(out2), .sel(sel));
  Multiplexer #(.enable("false")) multiplexer_3 (.in0(a1), .in1(b1), .out(out1), .sel(sel));
  Multiplexer #(.enable("false")) multiplexer_4 (.in0(a0), .in1(b0), .out(out0), .sel(sel));

  assign LEDsel = sel;
endmodule

module BinToBCD___Add3 (
  input  IN_0,
  input  IN_1,
  input  IN_2,
  input  IN_3,
  output OUT_3,
  output OUT_2,
  output OUT_1,
  output OUT_0
);

  wire and_1_out, and_2_out, and_3_out, and_4_out, and_5_out, and_6_out, and_7_out, and_8_out, and_9_out,
       and_10_out, not_1_out, not_2_out, not_3_out, not_4_out;

  not not_1 (not_1_out, IN_0);
  not not_2 (not_2_out, IN_1);
  not not_3 (not_3_out, IN_2);
  not not_4 (not_4_out, IN_3);
  and and_1 (and_1_out, IN_2, IN_1);
  and and_2 (and_2_out, IN_2, IN_0);
  or or_1 (OUT_3, IN_3, and_1_out, and_2_out);
  and and_3 (and_3_out, IN_3, IN_0);
  or or_2 (OUT_2, and_3_out, and_5_out);
  and and_4 (and_4_out, IN_3, not_1_out);
  and and_5 (and_5_out, IN_2, not_2_out, not_1_out);
  and and_6 (and_6_out, not_3_out, IN_1);
  and and_7 (and_7_out, IN_1, IN_0);
  or or_3 (OUT_1, and_4_out, and_6_out, and_7_out);
  and and_8 (and_8_out, IN_3, not_1_out);
  and and_9 (and_9_out, not_4_out, not_3_out, IN_0);
  and and_10 (and_10_out, IN_2, IN_1, not_1_out);
  or or_4 (OUT_0, and_8_out, and_10_out, and_9_out);
endmodule

module BinToBCD4 (
  input  BIN_0,
  input  BIN_1,
  input  BIN_2,
  input  BIN_3,
  output BCD1_0,
  output BCD1_1,
  output BCD1_2,
  output BCD1_3,
  output BCD10_0,
  output BCD10_1,
  output BCD10_2,
  output BCD10_3
);

  BinToBCD___Add3 bintobcd_add3_1 (
    .IN_3(1'b0), .IN_2(BIN_3), .IN_1(BIN_2), .IN_0(BIN_1), .OUT_3(BCD10_0), .OUT_2(BCD1_3), .OUT_1(BCD1_2),
    .OUT_0(BCD1_1));

  assign BCD1_0 = BIN_0;
  assign BCD10_1 = 1'b0;
  assign BCD10_2 = 1'b0;
  assign BCD10_3 = 1'b0;
endmodule

module _7SegDisplay_BCD_Adapter (
  input  BCD_0,
  input  BCD_1,
  input  BCD_2,
  input  BCD_3,
  output a,
  output b,
  output c,
  output d,
  output e,
  output f,
  output g,
  output dp
);

  wire decoder_1_out0, decoder_1_out1, decoder_1_out2, decoder_1_out3, decoder_1_out4, decoder_1_out5,
       decoder_1_out6, decoder_1_out7, decoder_1_out8, decoder_1_out9;

  Decoder #(.select(4), .enable("false")) decoder_1 (
    .out0(decoder_1_out0), .out1(decoder_1_out1), .out2(decoder_1_out2), .out3(decoder_1_out3),
    .out4(decoder_1_out4), .out5(decoder_1_out5), .out6(decoder_1_out6), .out7(decoder_1_out7),
    .out8(decoder_1_out8), .out9(decoder_1_out9), .sel({BCD_3, BCD_2, BCD_1, BCD_0}));  // open: out10, out11, out12, out13, out14, out15
  or or_1 (a, decoder_1_out9, decoder_1_out8, decoder_1_out7, decoder_1_out6, decoder_1_out5, 1'b0, decoder_1_out3, decoder_1_out2, 1'b0, decoder_1_out0);
  or or_2 (b, decoder_1_out9, decoder_1_out8, decoder_1_out7, 1'b0, 1'b0, decoder_1_out4, decoder_1_out3, decoder_1_out2, decoder_1_out1, decoder_1_out0);
  or or_3 (c, decoder_1_out9, decoder_1_out8, decoder_1_out7, decoder_1_out6, decoder_1_out5, decoder_1_out4, decoder_1_out3, 1'b0, decoder_1_out1, decoder_1_out0);
  or or_4 (d, decoder_1_out9, decoder_1_out8, 1'b0, decoder_1_out6, decoder_1_out5, 1'b0, decoder_1_out3, decoder_1_out2, 1'b0, decoder_1_out0);
  or or_5 (e, 1'b0, decoder_1_out8, 1'b0, decoder_1_out6, 1'b0, 1'b0, 1'b0, decoder_1_out2, 1'b0, decoder_1_out0);
  or or_6 (f, decoder_1_out9, decoder_1_out8, 1'b0, decoder_1_out6, decoder_1_out5, decoder_1_out4, 1'b0, 1'b0, 1'b0, decoder_1_out0);
  or or_7 (g, decoder_1_out9, decoder_1_out8, 1'b0, decoder_1_out6, decoder_1_out5, decoder_1_out4, decoder_1_out3, decoder_1_out2, 1'b0, 1'b0);
  or or_8 (dp, 1'b0, 1'b0, 1'b0, 1'b0, 1'b0, 1'b0, 1'b0, 1'b0, 1'b0, 1'b0);
endmodule

module _7SegDisplay_HEX_Adapter (
  input  IN_0,
  input  IN_1,
  input  IN_2,
  input  IN_3,
  output a,
  output b,
  output c,
  output d,
  output e,
  output f,
  output g,
  output dp
);

  wire decoder_1_out0, decoder_1_out1, decoder_1_out2, decoder_1_out3, decoder_1_out4, decoder_1_out5,
       decoder_1_out6, decoder_1_out7, decoder_1_out8, decoder_1_out9, decoder_1_out10, decoder_1_out11,
       decoder_1_out12, decoder_1_out13, decoder_1_out14, decoder_1_out15;

  Decoder #(.select(4), .enable("false")) decoder_1 (
    .out0(decoder_1_out0), .out1(decoder_1_out1), .out2(decoder_1_out2), .out3(decoder_1_out3),
    .out4(decoder_1_out4), .out5(decoder_1_out5), .out6(decoder_1_out6), .out7(decoder_1_out7),
    .out8(decoder_1_out8), .out9(decoder_1_out9), .out10(decoder_1_out10), .out11(decoder_1_out11),
    .out12(decoder_1_out12), .out13(decoder_1_out13), .out14(decoder_1_out14), .out15(decoder_1_out15),
    .sel({IN_3, IN_2, IN_1, IN_0}));
  or or_1 (a, decoder_1_out15, decoder_1_out14, 1'b0, decoder_1_out12, 1'b0, decoder_1_out10, decoder_1_out9, decoder_1_out8, decoder_1_out7, decoder_1_out6, decoder_1_out5, 1'b0, decoder_1_out3, decoder_1_out2, 1'b0, decoder_1_out0);
  or or_2 (b, 1'b0, 1'b0, decoder_1_out13, 1'b0, 1'b0, decoder_1_out10, decoder_1_out9, decoder_1_out8, decoder_1_out7, 1'b0, 1'b0, decoder_1_out4, decoder_1_out3, decoder_1_out2, decoder_1_out1, decoder_1_out0);
  or or_3 (c, 1'b0, 1'b0, decoder_1_out13, 1'b0, decoder_1_out11, decoder_1_out10, decoder_1_out9, decoder_1_out8, decoder_1_out7, decoder_1_out6, decoder_1_out5, decoder_1_out4, decoder_1_out3, 1'b0, decoder_1_out1, decoder_1_out0);
  or or_4 (d, 1'b0, decoder_1_out14, decoder_1_out13, decoder_1_out12, decoder_1_out11, 1'b0, decoder_1_out9, decoder_1_out8, 1'b0, decoder_1_out6, decoder_1_out5, 1'b0, decoder_1_out3, decoder_1_out2, 1'b0, decoder_1_out0);
  or or_5 (e, decoder_1_out15, decoder_1_out14, decoder_1_out13, decoder_1_out12, decoder_1_out11, decoder_1_out10, 1'b0, decoder_1_out8, 1'b0, decoder_1_out6, 1'b0, 1'b0, 1'b0, decoder_1_out2, 1'b0, decoder_1_out0);
  or or_6 (f, decoder_1_out15, decoder_1_out14, 1'b0, decoder_1_out12, decoder_1_out11, decoder_1_out10, decoder_1_out9, decoder_1_out8, 1'b0, decoder_1_out6, decoder_1_out5, decoder_1_out4, 1'b0, 1'b0, 1'b0, decoder_1_out0);
  or or_7 (g, decoder_1_out15, decoder_1_out14, decoder_1_out13, 1'b0, decoder_1_out11, decoder_1_out10, decoder_1_out9, decoder_1_out8, 1'b0, decoder_1_out6, decoder_1_out5, decoder_1_out4, decoder_1_out3, decoder_1_out2, 1'b0, 1'b0);
  or or_8 (dp, 1'b0, 1'b0, 1'b0, 1'b0, 1'b0, 1'b0, 1'b0, 1'b0, 1'b0, 1'b0, 1'b0, 1'b0, 1'b0, 1'b0, 1'b0, 1'b0);
endmodule

module DEC_Diplay (
  input  BIN_0,
  input  BIN_1,
  input  BIN_2,
  input  BIN_3,
  output LED0,
  output LED1,
  output LED2,
  output LED3,
  output BCD1_0,
  output BCD1_1,
  output BCD1_2,
  output BCD1_3,
  output BCD10_0,
  output BCD10_1,
  output BCD10_2,
  output BCD10_3
);

  BinToBCD4 bintobcd4_1 (
    .BIN_0(BIN_0), .BIN_1(BIN_1), .BIN_2(BIN_2), .BIN_3(BIN_3), .BCD1_0(BCD1_0), .BCD1_1(BCD1_1),
    .BCD1_2(BCD1_2), .BCD1_3(BCD1_3), .BCD10_0(BCD10_0), .BCD10_1(BCD10_1), .BCD10_2(BCD10_2),
    .BCD10_3(BCD10_3));

  assign LED0 = BIN_0;
  assign LED1 = BIN_1;
  assign LED2 = BIN_2;
  assign LED3 = BIN_3;
endmodule

module BIN_Display (
  input  IN_0,
  input  IN_1,
  input  IN_2,
  input  IN_3,
  output LED0,
  output LED1,
  output LED2,
  output LED3
);


  assign LED0 = IN_0;
  assign LED1 = IN_1;
  assign LED2 = IN_2;
  assign LED3 = IN_3;
endmodule

module HEX_Display (
  input  BIN_0,
  input  BIN_1,
  input  BIN_2,
  input  BIN_3,
  output LED0,
  output LED1,
  output LED2,
  output LED3,
  output HEX3,
  output HEX2,
  output HEX1,
  output HEX0
);


  assign HEX0 = BIN_0;
  assign HEX1 = BIN_1;
  assign HEX2 = BIN_2;
  assign HEX3 = BIN_3;
  assign LED0 = BIN_0;
  assign LED1 = BIN_1;
  assign LED2 = BIN_2;
  assign LED3 = BIN_3;
endmodule

module Input4 (
  input  IN_0,
  input  IN_1,
  input  IN_2,
  input  IN_3,
  output [3:0] OUT
);


  assign OUT = {IN_3, IN_2, IN_1, IN_0};
endmodule
