// Logisim project cpu.circ as structural Verilog
module BranchChecker (
  input  zero,
  input  sign,
  input  carry,
  input  overflow,
  input  op2,
  input  op1,
  input  op0,
  output result
);

  wire and_1_out, and_2_out, and_3_out, and_4_out, and_5_out, and_6_out, and_7_out, decoder_1_out0,
       decoder_1_out1, decoder_1_out2, decoder_1_out3, decoder_1_out4, decoder_1_out5, decoder_1_out6,
       decoder_1_out7, or_1_out, or_2_out, xor_1_out;

  Decoder #(.select(3), .enable("false")) decoder_1 (
    .out0(decoder_1_out0), .out1(decoder_1_out1), .out2(decoder_1_out2), .out3(decoder_1_out3),
    .out4(decoder_1_out4), .out5(decoder_1_out5), .out6(decoder_1_out6), .out7(decoder_1_out7),
    .sel({op2, op1, op0}));
  or or_1 (or_1_out, zero, xor_1_out);
  or or_2 (or_2_out, carry, zero);
  xor xor_1 (xor_1_out, overflow, sign);
  and and_1 (and_1_out, decoder_1_out1, zero);
  and and_2 (and_2_out, decoder_1_out2, sign);
  and and_3 (and_3_out, decoder_1_out3, overflow);
  and and_4 (and_4_out, decoder_1_out4, carry);
  and and_5 (and_5_out, decoder_1_out5, or_2_out);
  and and_6 (and_6_out, decoder_1_out6, xor_1_out);
  and and_7 (and_7_out, decoder_1_out7, or_1_out);
  or or_3 (result, and_7_out, and_6_out, and_5_out, and_4_out, and_3_out, and_2_out, and_1_out, decoder_1_out0);
endmodule

module Control (
  input  rst,
  input  zero,
  input  sign,
  input  carry,
  input  overflow,
  input  clk,
  input  ir7,
  input  ir6,
  input  ir5,
  input  ir4,
  input  ir3,
  input  ir2,
  input  ir1,
  input  ir0,
  output rd_r,
  output ra_w,
  output rb_w,
  output bus_0,
  output io,
  output io_in_out,
  output io_data_addr,
  output rx_r,
  output rx_w,
  output fr_w,
  output rx1,
  output pc_w,
  output rx0,
  output pc_r,
  output ir_w,
  output cin,
  output mar_w,
  output op2,
  output ram_w,
  output op1,
  output op0,
  output ram_r,
  output halt,
  output new_cycle,
  output new_instr
);

  wire and_10_out, and_13_out, and_14_out, and_15_out, branchchecker_1_result, clock_1_p2, clock_1_p3,
       clock_1_p4, delayer_1_out, instr_state_qn, or_2_out, or_3_out;
  wire [1:0] multiplexer_2_out, multiplexer_3_out;
  wire [6:0] adder_1_out, mPC_q, multiplexer_1_out, rom_1_data;
  wire [6:6] instr_state_q;
  wire [31:4] rom_1_data_2;

  and and_1 (fr_w, rom_1_data_2[12], clock_1_p3);
  and and_2 (pc_w, rom_1_data_2[13], clock_1_p3);
  and and_3 (pc_r, rom_1_data_2[14], clock_1_p2);
  and and_4 (ir_w, rom_1_data_2[15], clock_1_p3);
  and and_5 (mar_w, rom_1_data_2[16], clock_1_p3);
  and and_6 (ram_w, rom_1_data_2[17], clock_1_p3);
  and and_7 (ram_r, rom_1_data_2[18], clock_1_p2);
  // Clock clock_1: pin names not known; wires that end beside it: clk, clock_1_p2, clock_1_p3, clock_1_p4
  nor nor_1 (new_cycle, clock_1_p2, clock_1_p3);
  or or_1 (clock_1_p4, rst, halt);
  and and_8 (ra_w, clock_1_p3, rom_1_data_2[10]);
  and and_9 (rd_r, clock_1_p2, rom_1_data_2[11]);
  Register #(.width(7)) mPC (.D(multiplexer_1_out), .en(1'b1), .Q(mPC_q), .clk(new_cycle), .clr(clock_1_p4));
  Multiplexer #(.select(2), .width(7), .enable("false")) multiplexer_1 (
    .in0(adder_1_out), .in1(adder_1_out), .in2(rom_1_data),
    .in3({instr_state_q[6], ir7, ir6, ir5, ir4, 2'b00}), .out(multiplexer_1_out), .sel(multiplexer_2_out));
  and and_10 (and_10_out, clock_1_p3, rom_1_data_2[31]);
  and and_11 (rb_w, clock_1_p3, rom_1_data_2[9]);
  Delayer delayer_1 (.in(new_cycle), .out(delayer_1_out));
  and and_12 (new_instr, delayer_1_out, and_13_out);
  and and_13 (and_13_out, ~mPC_q[6], ~mPC_q[5], ~mPC_q[4], ~mPC_q[3], ~mPC_q[2], ~mPC_q[1], mPC_q[0]);  // AND_Gate
  Adder #(.width(7)) adder_1 (.a(mPC_q), .b({7{1'b0}}), .out(adder_1_out), .cin(1'b1));  // open: cout
  D_Flip_Flop instr_state (
    .clk(and_10_out), .D(instr_state_qn), .Q(instr_state_q[6]), .Qn(instr_state_qn), .en(1'b1),
    .reset(clock_1_p4));  // open: preset
  ROM #(.addrWidth(7), .dataWidth(32)) rom_1 (
    .addr(mPC_q),
    .data({rom_1_data_2[31:27], rom_1_data, halt, rom_1_data_2[18:9], bus_0, io, rom_1_data_2[6:4], cin, op2, op1, op0}),
    .sel(1'b1));
  Multiplexer #(.select(2), .width(2), .enable("false")) multiplexer_2 (
    .in0(2'b00), .in1(multiplexer_3_out), .in2(2'b10), .in3(2'b11), .out(multiplexer_2_out),
    .sel(rom_1_data_2[29:28]));
  and and_14 (and_14_out, ir3, io);
  and and_15 (and_15_out, io, ~ir3);  // AND_Gate
  BranchChecker branchchecker_1 (
    .zero(zero), .sign(sign), .carry(carry), .overflow(overflow), .op0(ir0), .op1(ir1), .op2(ir2),
    .result(branchchecker_1_result));
  Multiplexer #(.width(2), .enable("false")) multiplexer_3 (
    .in0(2'b00), .in1(2'b10), .out(multiplexer_3_out), .sel(branchchecker_1_result));
  or or_2 (or_2_out, rom_1_data_2[6], and_15_out);
  or or_3 (or_3_out, rom_1_data_2[5], and_14_out);
  Multiplexer #(.width(2), .enable("false")) multiplexer_4 (
    .in0({ir3, ir2}), .in1({ir1, ir0}), .out({rx1, rx0}), .sel(rom_1_data_2[4]));
  and and_16 (rx_r, clock_1_p2, or_2_out);
  and and_17 (rx_w, clock_1_p3, or_3_out);

  assign io_data_addr = ir2;
  assign io_in_out = ir3;

  // Notes on the sheet:
  //   Map instructions to 1xxxx00 with xxxx=OPCODE
  //   to avoid collision with IFETCH.
  //   Instructions must complete in 4 steps.
  //   0x00 has no instruction since after reset it won't be executed.
  //   00xy -> jump to addr mPC+1
  //   01xy -> branch to either addr mPC+1 or ROM[mPC]
  //   10xy -> jump to addr ROM[mPC]
  //   11xy -> jump to instr in IR
  //   contents of rom_1 (hex, n*v repeats v):
  //   0 14700 280c b0048000 60*0 450 a0100820 0 0 14700 280c a0140030 0 10050 a0140020 0 0 10050 a0120040
  //   0 0 4400 2050 a0100830 0 15614400 a0102b0c 40200 a0102804 a0080000 0 0 0 a0100000 0 0 0 440 250
  //   a0101824 0 440 250 a0101825 0 450 a0101826 0 0 450 a0101827 0 0 440 250 a0101821 0 440 250 a0101822
  //   0 440 250 a0101823 0 440 a0101255
endmodule

module Computer (
  input  in_1,
  input  in_2,
  input  in_3,
  input  in_4,
  input  in_5,
  input  in_6,
  input  in_7,
  input  in_8,
  input  in_9,
  input  in_10,
  input  in_11,
  input  in_12,
  input  in_13,
  input  in_14,
  input  in_15,
  input  in_16,
  input  in_17,
  input  in_18,
  input  in_19,
  input  in_20,
  input  in_21,
  input  in_22,
  input  in_23
);

  wire alu_1_ledcin, alu_1_ledop, alu_1_ledz, alu_1_sum_0, alu_1_sum_1, alu_1_sum_2, alu_1_sum_3,
       alu_1_sum_4, alu_1_sum_5, alu_1_sum_6, alu_1_sum_7, alu_1_zero, B_p2, B_p4, B_p6, B_p8, B_p10, B_p12,
       B_p14, B_p16, B_p18, bcd_display_1_a, bcd_display_1_b, bcd_display_1_c, bcd_display_1_d,
       bcd_display_1_dp, bcd_display_1_e, bcd_display_1_f, bcd_display_1_g, bcd_display_2_a, bcd_display_2_b,
       bcd_display_2_c, bcd_display_2_d, bcd_display_2_dp, bcd_display_2_e, bcd_display_2_f, bcd_display_2_g,
       bcd_display_3_a, bcd_display_3_b, bcd_display_3_c, bcd_display_3_d, bcd_display_3_dp, bcd_display_3_e,
       bcd_display_3_f, bcd_display_3_g, bcd_display_4_a, bcd_display_4_b, bcd_display_4_c, bcd_display_4_d,
       bcd_display_4_dp, bcd_display_4_e, bcd_display_4_f, bcd_display_4_g, bcd_display_5_a, bcd_display_5_b,
       bcd_display_5_c, bcd_display_5_d, bcd_display_5_dp, bcd_display_5_e, bcd_display_5_f, bcd_display_5_g,
       bcd_display_6_a, bcd_display_6_b, bcd_display_6_c, bcd_display_6_d, bcd_display_6_dp, bcd_display_6_e,
       bcd_display_6_f, bcd_display_6_g, bcd_display_7_a, bcd_display_7_b, bcd_display_7_c, bcd_display_7_d,
       bcd_display_7_dp, bcd_display_7_e, bcd_display_7_f, bcd_display_7_g, bcd_display_8_a, bcd_display_8_b,
       bcd_display_8_c, bcd_display_8_d, bcd_display_8_dp, bcd_display_8_e, bcd_display_8_f, bcd_display_8_g,
       bcd_display_9_a, bcd_display_9_b, bcd_display_9_c, bcd_display_9_d, bcd_display_9_dp, bcd_display_9_e,
       bcd_display_9_f, bcd_display_9_g, bcd_display_10_a, bcd_display_10_b, bcd_display_10_c,
       bcd_display_10_d, bcd_display_10_dp, bcd_display_10_e, bcd_display_10_f, bcd_display_10_g,
       bcd_display_11_a, bcd_display_11_b, bcd_display_11_c, bcd_display_11_d, bcd_display_11_dp,
       bcd_display_11_e, bcd_display_11_f, bcd_display_11_g, bcd_display_12_a, bcd_display_12_b,
       bcd_display_12_c, bcd_display_12_d, bcd_display_12_dp, bcd_display_12_e, bcd_display_12_f,
       bcd_display_12_g, bcd_display_13_a, bcd_display_13_b, bcd_display_13_c, bcd_display_13_d,
       bcd_display_13_dp, bcd_display_13_e, bcd_display_13_f, bcd_display_13_g, bcd_display_14_a,
       bcd_display_14_b, bcd_display_14_c, bcd_display_14_d, bcd_display_14_dp, bcd_display_14_e,
       bcd_display_14_f, bcd_display_14_g, bcd_display_15_a, bcd_display_15_b, bcd_display_15_c,
       bcd_display_15_d, bcd_display_15_dp, bcd_display_15_e, bcd_display_15_f, bcd_display_15_g,
       bcd_display_16_a, bcd_display_16_b, bcd_display_16_c, bcd_display_16_d, bcd_display_16_dp,
       bcd_display_16_e, bcd_display_16_f, bcd_display_16_g, bcd_display_17_a, bcd_display_17_b,
       bcd_display_17_c, bcd_display_17_d, bcd_display_17_dp, bcd_display_17_e, bcd_display_17_f,
       bcd_display_17_g, bcd_display_18_a, bcd_display_18_b, bcd_display_18_c, bcd_display_18_d,
       bcd_display_18_dp, bcd_display_18_e, bcd_display_18_f, bcd_display_18_g, bcd_display_19_a,
       bcd_display_19_b, bcd_display_19_c, bcd_display_19_d, bcd_display_19_dp, bcd_display_19_e,
       bcd_display_19_f, bcd_display_19_g, bcd_display_20_a, bcd_display_20_b, bcd_display_20_c,
       bcd_display_20_d, bcd_display_20_dp, bcd_display_20_e, bcd_display_20_f, bcd_display_20_g,
       bcd_display_21_a, bcd_display_21_b, bcd_display_21_c, bcd_display_21_d, bcd_display_21_dp,
       bcd_display_21_e, bcd_display_21_f, bcd_display_21_g, bin_display_1_led0, bin_display_1_led1,
       bin_display_1_led2, bin_display_1_led3, bin_display_1_led4, bin_display_1_led5, bin_display_1_led6,
       bin_display_1_led7, clk, controlunit_1_p4, controlunit_1_p5, controlunit_1_p6, controlunit_1_p7,
       controlunit_1_p8, controlunit_1_p9, controlunit_1_p10, controlunit_1_p11, controlunit_1_p12,
       controlunit_1_p13, dec_diplay_1_bcd1_0, dec_diplay_1_bcd1_1, dec_diplay_1_bcd1_2, dec_diplay_1_bcd1_3,
       dec_diplay_1_bcd10_0, dec_diplay_1_bcd10_1, dec_diplay_1_bcd10_2, dec_diplay_1_bcd10_3,
       dec_diplay_1_bcd100_0, dec_diplay_1_bcd100_1, dec_diplay_1_bcd100_2, dec_diplay_1_bcd100_3,
       dec_diplay_1_led0, dec_diplay_1_led1, dec_diplay_1_led2, dec_diplay_1_led3, dec_diplay_1_led4,
       dec_diplay_1_led5, dec_diplay_1_led6, dec_diplay_1_led7, dec_diplay_2_bcd1_0, dec_diplay_2_bcd1_1,
       dec_diplay_2_bcd1_2, dec_diplay_2_bcd1_3, dec_diplay_2_bcd10_0, dec_diplay_2_bcd10_1,
       dec_diplay_2_bcd10_2, dec_diplay_2_bcd10_3, dec_diplay_2_bcd100_0, dec_diplay_2_bcd100_1,
       dec_diplay_2_bcd100_2, dec_diplay_2_bcd100_3, dec_diplay_2_led0, dec_diplay_2_led1, dec_diplay_2_led2,
       dec_diplay_2_led3, dec_diplay_2_led4, dec_diplay_2_led5, dec_diplay_2_led6, dec_diplay_2_led7,
       dec_diplay_3_bcd1_0, dec_diplay_3_bcd1_1, dec_diplay_3_bcd1_2, dec_diplay_3_bcd1_3,
       dec_diplay_3_bcd10_0, dec_diplay_3_bcd10_1, dec_diplay_3_bcd10_2, dec_diplay_3_bcd10_3,
       dec_diplay_3_bcd100_0, dec_diplay_3_bcd100_1, dec_diplay_3_bcd100_2, dec_diplay_3_bcd100_3,
       dec_diplay_3_led0, dec_diplay_3_led1, dec_diplay_3_led2, dec_diplay_3_led3, dec_diplay_3_led4,
       dec_diplay_3_led5, dec_diplay_3_led6, dec_diplay_3_led7, dec_diplay_4_bcd1_0, dec_diplay_4_bcd1_1,
       dec_diplay_4_bcd1_2, dec_diplay_4_bcd1_3, dec_diplay_4_bcd10_0, dec_diplay_4_bcd10_1,
       dec_diplay_4_bcd10_2, dec_diplay_4_bcd10_3, dec_diplay_4_bcd100_0, dec_diplay_4_bcd100_1,
       dec_diplay_4_bcd100_2, dec_diplay_4_bcd100_3, dec_diplay_4_led0, dec_diplay_4_led1, dec_diplay_4_led2,
       dec_diplay_4_led3, dec_diplay_4_led4, dec_diplay_4_led5, dec_diplay_4_led6, dec_diplay_4_led7,
       dec_diplay_5_bcd1_0, dec_diplay_5_bcd1_1, dec_diplay_5_bcd1_2, dec_diplay_5_bcd1_3,
       dec_diplay_5_bcd10_0, dec_diplay_5_bcd10_1, dec_diplay_5_bcd10_2, dec_diplay_5_bcd10_3,
       dec_diplay_5_bcd100_0, dec_diplay_5_bcd100_1, dec_diplay_5_bcd100_2, dec_diplay_5_bcd100_3,
       dec_diplay_5_led0, dec_diplay_5_led1, dec_diplay_5_led2, dec_diplay_5_led3, dec_diplay_5_led4,
       dec_diplay_5_led5, dec_diplay_5_led6, dec_diplay_5_led7, dec_diplay_6_bcd1_0, dec_diplay_6_bcd1_1,
       dec_diplay_6_bcd1_2, dec_diplay_6_bcd1_3, dec_diplay_6_bcd10_0, dec_diplay_6_bcd10_1,
       dec_diplay_6_bcd10_2, dec_diplay_6_bcd10_3, dec_diplay_6_bcd100_0, dec_diplay_6_bcd100_1,
       dec_diplay_6_bcd100_2, dec_diplay_6_bcd100_3, dec_diplay_6_led0, dec_diplay_6_led1, dec_diplay_6_led2,
       dec_diplay_6_led3, dec_diplay_6_led4, dec_diplay_6_led5, dec_diplay_6_led6, dec_diplay_6_led7,
       dec_diplay_7_bcd1_0, dec_diplay_7_bcd1_1, dec_diplay_7_bcd1_2, dec_diplay_7_bcd1_3,
       dec_diplay_7_bcd10_0, dec_diplay_7_bcd10_1, dec_diplay_7_bcd10_2, dec_diplay_7_bcd10_3,
       dec_diplay_7_bcd100_0, dec_diplay_7_bcd100_1, dec_diplay_7_bcd100_2, dec_diplay_7_bcd100_3,
       dec_diplay_7_led0, dec_diplay_7_led1, dec_diplay_7_led2, dec_diplay_7_led3, dec_diplay_7_led4,
       dec_diplay_7_led5, dec_diplay_7_led6, dec_diplay_7_led7, hex_display_1_led0, hex_display_1_led1,
       hex_display_1_led2, hex_display_1_led3, hex_display_1_led4, hex_display_1_led5, hex_display_1_led6,
       hex_display_1_led7, hex_display_2_led0, hex_display_2_led1, hex_display_2_led2, hex_display_2_led3,
       hex_display_2_led4, hex_display_2_led5, hex_display_2_led6, hex_display_2_led7, IR_led0, IR_led1,
       IR_led2, IR_led3, IR_led4, IR_led5, IR_led6, IR_led7, IR_ledr, IR_ledrst, IR_ledw, MAR_led0, MAR_led1,
       MAR_led2, MAR_led3, MAR_led4, MAR_led5, MAR_led6, MAR_led7, MAR_ledr, MAR_ledrst, MAR_ledw, MAR_out_0,
       MAR_out_1, MAR_out_2, MAR_out_3, MAR_out_4, MAR_out_5, MAR_out_6, MAR_out_7, memory_1_clk_out,
       memory_1_en_out, memory_1_ld_out, memory_1_leden, memory_1_ledrst, memory_1_ledrw, memory_1_rst_out,
       memory_1_str_out, micro, PC_led0, PC_led1, PC_led2, PC_led3, PC_led4, PC_led5, PC_led6, PC_led7,
       PC_ledr, PC_ledrst, PC_ledw, R0_led0, R0_led1, R0_led2, R0_led3, R0_led4, R0_led5, R0_led6, R0_led7,
       R0_ledr, R0_ledrst, R0_ledw, R0_out_0, R0_out_1, R0_out_2, R0_out_3, R0_out_4, R0_out_5, R0_out_6,
       R0_out_7, R1_led0, R1_led1, R1_led2, R1_led3, R1_led4, R1_led5, R1_led6, R1_led7, R1_ledr, R1_ledrst,
       R1_ledw, R2_led0, R2_led1, R2_led2, R2_led3, R2_led4, R2_led5, R2_led6, R2_led7, R2_ledr, R2_ledrst,
       R2_ledw, R3_led0, R3_led1, R3_led2, R3_led3, R3_led4, R3_led5, R3_led6, R3_led7, R3_ledr, R3_ledrst,
       R3_ledw, RA_2_led0, RA_2_led1, RA_2_led2, RA_2_led3, RA_2_led4, RA_2_led5, RA_2_led6, RA_2_led7,
       RA_2_ledr, RA_2_ledrst, RA_2_ledw, RA_led0, RA_led1, RA_led2, RA_led3, RA_led4, RA_led5, RA_led6,
       RA_led7, RA_ledr, RA_ledrst, RA_ledw, RA_out_0, RA_out_1, RA_out_2, RA_out_3, RA_out_4, RA_out_5,
       RA_out_6, RA_out_7, Z_led, Z_ledr, Z_ledrst, Z_ledw, Z_out;
  wire [3:0] hex_display_1_lsn, hex_display_1_msn, hex_display_2_lsn, hex_display_2_msn;
  wire [7:0] memory_1_addr_out, memory_1_data_out, undriven;

  DEC_Diplay dec_diplay_1 (
    .BIN_0(R0_led0), .BIN_1(R0_led1), .BIN_2(R0_led2), .BIN_3(R0_led3), .BIN_4(R0_led4), .BIN_5(R0_led5),
    .BIN_6(R0_led6), .BIN_7(R0_led7), .BCD1_0(dec_diplay_1_bcd1_0), .BCD1_1(dec_diplay_1_bcd1_1),
    .BCD1_2(dec_diplay_1_bcd1_2), .BCD1_3(dec_diplay_1_bcd1_3), .BCD10_0(dec_diplay_1_bcd10_0),
    .BCD10_1(dec_diplay_1_bcd10_1), .BCD10_2(dec_diplay_1_bcd10_2), .BCD10_3(dec_diplay_1_bcd10_3),
    .BCD100_0(dec_diplay_1_bcd100_0), .BCD100_1(dec_diplay_1_bcd100_1), .BCD100_2(dec_diplay_1_bcd100_2),
    .BCD100_3(dec_diplay_1_bcd100_3), .LED0(dec_diplay_1_led0), .LED1(dec_diplay_1_led1),
    .LED2(dec_diplay_1_led2), .LED3(dec_diplay_1_led3), .LED4(dec_diplay_1_led4), .LED5(dec_diplay_1_led5),
    .LED6(dec_diplay_1_led6), .LED7(dec_diplay_1_led7));
  LED led_1 (.in(dec_diplay_1_led7));
  LED led_2 (.in(R0_ledw));
  BCD_Display bcd_display_1 (
    .BCD_0(dec_diplay_1_bcd100_0), .BCD_1(dec_diplay_1_bcd100_1), .BCD_2(dec_diplay_1_bcd100_2),
    .BCD_3(dec_diplay_1_bcd100_3), .a(bcd_display_1_a), .b(bcd_display_1_b), .c(bcd_display_1_c),
    .d(bcd_display_1_d), .e(bcd_display_1_e), .f(bcd_display_1_f), .g(bcd_display_1_g), .dp(bcd_display_1_dp));
  _7_Segment_Display u_7_segment_display_1 (
    .g(bcd_display_1_g), .f(bcd_display_1_f), .a(bcd_display_1_a), .b(bcd_display_1_b), .e(bcd_display_1_e),
    .d(bcd_display_1_d), .c(bcd_display_1_c), .dp(bcd_display_1_dp));
  LED led_3 (.in(R0_ledrst));
  LED led_4 (.in(R0_ledr));
  DEC_Diplay dec_diplay_2 (
    .BIN_0(RA_led0), .BIN_1(RA_led1), .BIN_2(RA_led2), .BIN_3(RA_led3), .BIN_4(RA_led4), .BIN_5(RA_led5),
    .BIN_6(RA_led6), .BIN_7(RA_led7), .BCD1_0(dec_diplay_2_bcd1_0), .BCD1_1(dec_diplay_2_bcd1_1),
    .BCD1_2(dec_diplay_2_bcd1_2), .BCD1_3(dec_diplay_2_bcd1_3), .BCD10_0(dec_diplay_2_bcd10_0),
    .BCD10_1(dec_diplay_2_bcd10_1), .BCD10_2(dec_diplay_2_bcd10_2), .BCD10_3(dec_diplay_2_bcd10_3),
    .BCD100_0(dec_diplay_2_bcd100_0), .BCD100_1(dec_diplay_2_bcd100_1), .BCD100_2(dec_diplay_2_bcd100_2),
    .BCD100_3(dec_diplay_2_bcd100_3), .LED0(dec_diplay_2_led0), .LED1(dec_diplay_2_led1),
    .LED2(dec_diplay_2_led2), .LED3(dec_diplay_2_led3), .LED4(dec_diplay_2_led4), .LED5(dec_diplay_2_led5),
    .LED6(dec_diplay_2_led6), .LED7(dec_diplay_2_led7));
  LED led_5 (.in(dec_diplay_2_led7));
  LED led_6 (.in(RA_ledw));
  BCD_Display bcd_display_2 (
    .BCD_0(dec_diplay_2_bcd100_0), .BCD_1(dec_diplay_2_bcd100_1), .BCD_2(dec_diplay_2_bcd100_2),
    .BCD_3(dec_diplay_2_bcd100_3), .a(bcd_display_2_a), .b(bcd_display_2_b), .c(bcd_display_2_c),
    .d(bcd_display_2_d), .e(bcd_display_2_e), .f(bcd_display_2_f), .g(bcd_display_2_g), .dp(bcd_display_2_dp));
  _7_Segment_Display u_7_segment_display_2 (
    .g(bcd_display_2_g), .f(bcd_display_2_f), .a(bcd_display_2_a), .b(bcd_display_2_b), .e(bcd_display_2_e),
    .d(bcd_display_2_d), .c(bcd_display_2_c), .dp(bcd_display_2_dp));
  LED led_7 (.in(RA_ledrst));
  LED led_8 (.in(RA_ledr));
  LED led_9 (.in(dec_diplay_1_led5));
  LED led_10 (.in(dec_diplay_1_led6));
  LED led_11 (.in(dec_diplay_1_led3));
  LED led_12 (.in(dec_diplay_1_led4));
  BCD_Display bcd_display_3 (
    .BCD_0(dec_diplay_1_bcd10_0), .BCD_1(dec_diplay_1_bcd10_1), .BCD_2(dec_diplay_1_bcd10_2),
    .BCD_3(dec_diplay_1_bcd10_3), .a(bcd_display_3_a), .b(bcd_display_3_b), .c(bcd_display_3_c),
    .d(bcd_display_3_d), .e(bcd_display_3_e), .f(bcd_display_3_f), .g(bcd_display_3_g), .dp(bcd_display_3_dp));
  _7_Segment_Display u_7_segment_display_3 (
    .g(bcd_display_3_g), .f(bcd_display_3_f), .a(bcd_display_3_a), .b(bcd_display_3_b), .e(bcd_display_3_e),
    .d(bcd_display_3_d), .c(bcd_display_3_c), .dp(bcd_display_3_dp));
  Reg8 R0 (
    .read(in_1), .write(in_5), .nrst(in_4), .IN_7(R0_out_7), .IN_6(R0_out_6), .IN_5(R0_out_5),
    .IN_4(R0_out_4), .IN_3(R0_out_3), .IN_2(R0_out_2), .IN_1(R0_out_1), .IN_0(R0_out_0), .OUT_7(R0_out_7),
    .OUT_6(R0_out_6), .OUT_5(R0_out_5), .OUT_4(R0_out_4), .OUT_3(R0_out_3), .OUT_2(R0_out_2),
    .OUT_1(R0_out_1), .OUT_0(R0_out_0), .LEDr(R0_ledr), .LEDw(R0_ledw), .LEDrst(R0_ledrst), .LED0(R0_led0),
    .LED1(R0_led1), .LED2(R0_led2), .LED3(R0_led3), .LED4(R0_led4), .LED5(R0_led5), .LED6(R0_led6),
    .LED7(R0_led7));
  LED led_13 (.in(dec_diplay_2_led4));
  LED led_14 (.in(dec_diplay_2_led3));
  LED led_15 (.in(dec_diplay_2_led5));
  LED led_16 (.in(dec_diplay_2_led6));
  BCD_Display bcd_display_4 (
    .BCD_0(dec_diplay_2_bcd10_0), .BCD_1(dec_diplay_2_bcd10_1), .BCD_2(dec_diplay_2_bcd10_2),
    .BCD_3(dec_diplay_2_bcd10_3), .a(bcd_display_4_a), .b(bcd_display_4_b), .c(bcd_display_4_c),
    .d(bcd_display_4_d), .e(bcd_display_4_e), .f(bcd_display_4_f), .g(bcd_display_4_g), .dp(bcd_display_4_dp));
  _7_Segment_Display u_7_segment_display_4 (
    .g(bcd_display_4_g), .f(bcd_display_4_f), .a(bcd_display_4_a), .b(bcd_display_4_b), .e(bcd_display_4_e),
    .d(bcd_display_4_d), .c(bcd_display_4_c), .dp(bcd_display_4_dp));
  Reg8 RA (
    .read(1'b1), .write(in_2), .nrst(in_4), .IN_7(R0_out_7), .IN_6(R0_out_6), .IN_5(R0_out_5),
    .IN_4(R0_out_4), .IN_3(R0_out_3), .IN_2(R0_out_2), .IN_1(R0_out_1), .IN_0(R0_out_0), .OUT_7(RA_out_7),
    .OUT_6(RA_out_6), .OUT_5(RA_out_5), .OUT_4(RA_out_4), .OUT_3(RA_out_3), .OUT_2(RA_out_2),
    .OUT_1(RA_out_1), .OUT_0(RA_out_0), .LEDr(RA_ledr), .LEDw(RA_ledw), .LEDrst(RA_ledrst), .LED0(RA_led0),
    .LED1(RA_led1), .LED2(RA_led2), .LED3(RA_led3), .LED4(RA_led4), .LED5(RA_led5), .LED6(RA_led6),
    .LED7(RA_led7));
  LED led_17 (.in(dec_diplay_1_led1));
  LED led_18 (.in(dec_diplay_1_led0));
  LED led_19 (.in(dec_diplay_1_led2));
  BCD_Display bcd_display_5 (
    .BCD_0(dec_diplay_1_bcd1_0), .BCD_1(dec_diplay_1_bcd1_1), .BCD_2(dec_diplay_1_bcd1_2),
    .BCD_3(dec_diplay_1_bcd1_3), .a(bcd_display_5_a), .b(bcd_display_5_b), .c(bcd_display_5_c),
    .d(bcd_display_5_d), .e(bcd_display_5_e), .f(bcd_display_5_f), .g(bcd_display_5_g), .dp(bcd_display_5_dp));
  _7_Segment_Display u_7_segment_display_5 (
    .g(bcd_display_5_g), .f(bcd_display_5_f), .a(bcd_display_5_a), .b(bcd_display_5_b), .e(bcd_display_5_e),
    .d(bcd_display_5_d), .c(bcd_display_5_c), .dp(bcd_display_5_dp));
  LED led_20 (.in(dec_diplay_2_led1));
  LED led_21 (.in(dec_diplay_2_led0));
  LED led_22 (.in(dec_diplay_2_led2));
  BCD_Display bcd_display_6 (
    .BCD_0(dec_diplay_2_bcd1_0), .BCD_1(dec_diplay_2_bcd1_1), .BCD_2(dec_diplay_2_bcd1_2),
    .BCD_3(dec_diplay_2_bcd1_3), .a(bcd_display_6_a), .b(bcd_display_6_b), .c(bcd_display_6_c),
    .d(bcd_display_6_d), .e(bcd_display_6_e), .f(bcd_display_6_f), .g(bcd_display_6_g), .dp(bcd_display_6_dp));
  _7_Segment_Display u_7_segment_display_6 (
    .g(bcd_display_6_g), .f(bcd_display_6_f), .a(bcd_display_6_a), .b(bcd_display_6_b), .e(bcd_display_6_e),
    .d(bcd_display_6_d), .c(bcd_display_6_c), .dp(bcd_display_6_dp));
  DEC_Diplay dec_diplay_3 (
    .BIN_0(RA_2_led0), .BIN_1(RA_2_led1), .BIN_2(RA_2_led2), .BIN_3(RA_2_led3), .BIN_4(RA_2_led4),
    .BIN_5(RA_2_led5), .BIN_6(RA_2_led6), .BIN_7(RA_2_led7), .BCD1_0(dec_diplay_3_bcd1_0),
    .BCD1_1(dec_diplay_3_bcd1_1), .BCD1_2(dec_diplay_3_bcd1_2), .BCD1_3(dec_diplay_3_bcd1_3),
    .BCD10_0(dec_diplay_3_bcd10_0), .BCD10_1(dec_diplay_3_bcd10_1), .BCD10_2(dec_diplay_3_bcd10_2),
    .BCD10_3(dec_diplay_3_bcd10_3), .BCD100_0(dec_diplay_3_bcd100_0), .BCD100_1(dec_diplay_3_bcd100_1),
    .BCD100_2(dec_diplay_3_bcd100_2), .BCD100_3(dec_diplay_3_bcd100_3), .LED0(dec_diplay_3_led0),
    .LED1(dec_diplay_3_led1), .LED2(dec_diplay_3_led2), .LED3(dec_diplay_3_led3), .LED4(dec_diplay_3_led4),
    .LED5(dec_diplay_3_led5), .LED6(dec_diplay_3_led6), .LED7(dec_diplay_3_led7));
  LED led_23 (.in(dec_diplay_3_led7));
  LED led_24 (.in(RA_2_ledw));
  BCD_Display bcd_display_7 (
    .BCD_0(dec_diplay_3_bcd100_0), .BCD_1(dec_diplay_3_bcd100_1), .BCD_2(dec_diplay_3_bcd100_2),
    .BCD_3(dec_diplay_3_bcd100_3), .a(bcd_display_7_a), .b(bcd_display_7_b), .c(bcd_display_7_c),
    .d(bcd_display_7_d), .e(bcd_display_7_e), .f(bcd_display_7_f), .g(bcd_display_7_g), .dp(bcd_display_7_dp));
  LED led_25 (.in(RA_2_ledrst));
  LED led_26 (.in(RA_2_ledr));
  ALU_2 alu_1 (
    .a_0(RA_out_0), .a_1(RA_out_1), .a_2(RA_out_2), .a_3(RA_out_3), .a_4(RA_out_4), .a_5(RA_out_5),
    .a_6(RA_out_6), .a_7(RA_out_7), .zero(alu_1_zero), .b_0(B_p18), .b_1(B_p16), .b_2(B_p14), .b_3(B_p12),
    .b_4(B_p10), .b_5(B_p8), .b_6(B_p6), .b_7(B_p4), .op(in_13), .cin(in_10), .sum_0(alu_1_sum_0),
    .sum_1(alu_1_sum_1), .sum_2(alu_1_sum_2), .sum_3(alu_1_sum_3), .sum_4(alu_1_sum_4), .sum_5(alu_1_sum_5),
    .sum_6(alu_1_sum_6), .sum_7(alu_1_sum_7), .LEDcin(alu_1_ledcin), .LEDop(alu_1_ledop), .LEDz(alu_1_ledz));
  LED led_27 (.in(alu_1_ledop));
  LED led_28 (.in(dec_diplay_3_led4));
  LED led_29 (.in(dec_diplay_3_led5));
  LED led_30 (.in(dec_diplay_3_led6));
  BCD_Display bcd_display_8 (
    .BCD_0(dec_diplay_3_bcd10_0), .BCD_1(dec_diplay_3_bcd10_1), .BCD_2(dec_diplay_3_bcd10_2),
    .BCD_3(dec_diplay_3_bcd10_3), .a(bcd_display_8_a), .b(bcd_display_8_b), .c(bcd_display_8_c),
    .d(bcd_display_8_d), .e(bcd_display_8_e), .f(bcd_display_8_f), .g(bcd_display_8_g), .dp(bcd_display_8_dp));
  _7_Segment_Display u_7_segment_display_7 (
    .g(bcd_display_7_g), .f(bcd_display_7_f), .a(bcd_display_7_a), .b(bcd_display_7_b), .e(bcd_display_7_e),
    .d(bcd_display_7_d), .c(bcd_display_7_c), .dp(bcd_display_7_dp));
  _7_Segment_Display u_7_segment_display_8 (
    .g(bcd_display_8_g), .f(bcd_display_8_f), .a(bcd_display_8_a), .b(bcd_display_8_b), .e(bcd_display_8_e),
    .d(bcd_display_8_d), .c(bcd_display_8_c), .dp(bcd_display_8_dp));
  Reg8 RA_2 (
    .read(in_15), .write(in_18), .nrst(in_4), .IN_7(alu_1_sum_7), .IN_6(alu_1_sum_6), .IN_5(alu_1_sum_5),
    .IN_4(alu_1_sum_4), .IN_3(alu_1_sum_3), .IN_2(alu_1_sum_2), .IN_1(alu_1_sum_1), .IN_0(alu_1_sum_0),
    .OUT_7(R0_out_7), .OUT_6(R0_out_6), .OUT_5(R0_out_5), .OUT_4(R0_out_4), .OUT_3(R0_out_3),
    .OUT_2(R0_out_2), .OUT_1(R0_out_1), .OUT_0(R0_out_0), .LEDr(RA_2_ledr), .LEDw(RA_2_ledw),
    .LEDrst(RA_2_ledrst), .LED0(RA_2_led0), .LED1(RA_2_led1), .LED2(RA_2_led2), .LED3(RA_2_led3),
    .LED4(RA_2_led4), .LED5(RA_2_led5), .LED6(RA_2_led6), .LED7(RA_2_led7));
  DEC_Diplay dec_diplay_4 (
    .BIN_0(R1_led0), .BIN_1(R1_led1), .BIN_2(R1_led2), .BIN_3(R1_led3), .BIN_4(R1_led4), .BIN_5(R1_led5),
    .BIN_6(R1_led6), .BIN_7(R1_led7), .BCD1_0(dec_diplay_4_bcd1_0), .BCD1_1(dec_diplay_4_bcd1_1),
    .BCD1_2(dec_diplay_4_bcd1_2), .BCD1_3(dec_diplay_4_bcd1_3), .BCD10_0(dec_diplay_4_bcd10_0),
    .BCD10_1(dec_diplay_4_bcd10_1), .BCD10_2(dec_diplay_4_bcd10_2), .BCD10_3(dec_diplay_4_bcd10_3),
    .BCD100_0(dec_diplay_4_bcd100_0), .BCD100_1(dec_diplay_4_bcd100_1), .BCD100_2(dec_diplay_4_bcd100_2),
    .BCD100_3(dec_diplay_4_bcd100_3), .LED0(dec_diplay_4_led0), .LED1(dec_diplay_4_led1),
    .LED2(dec_diplay_4_led2), .LED3(dec_diplay_4_led3), .LED4(dec_diplay_4_led4), .LED5(dec_diplay_4_led5),
    .LED6(dec_diplay_4_led6), .LED7(dec_diplay_4_led7));
  LED led_31 (.in(R1_ledw));
  LED led_32 (.in(R1_ledrst));
  LED led_33 (.in(R1_ledr));
  DEC_Diplay dec_diplay_5 (
    .BIN_0(R0_out_0), .BIN_1(R0_out_1), .BIN_2(R0_out_2), .BIN_3(R0_out_3), .BIN_4(R0_out_4),
    .BIN_5(R0_out_5), .BIN_6(R0_out_6), .BIN_7(R0_out_7), .BCD1_0(dec_diplay_5_bcd1_0),
    .BCD1_1(dec_diplay_5_bcd1_1), .BCD1_2(dec_diplay_5_bcd1_2), .BCD1_3(dec_diplay_5_bcd1_3),
    .BCD10_0(dec_diplay_5_bcd10_0), .BCD10_1(dec_diplay_5_bcd10_1), .BCD10_2(dec_diplay_5_bcd10_2),
    .BCD10_3(dec_diplay_5_bcd10_3), .BCD100_0(dec_diplay_5_bcd100_0), .BCD100_1(dec_diplay_5_bcd100_1),
    .BCD100_2(dec_diplay_5_bcd100_2), .BCD100_3(dec_diplay_5_bcd100_3), .LED0(dec_diplay_5_led0),
    .LED1(dec_diplay_5_led1), .LED2(dec_diplay_5_led2), .LED3(dec_diplay_5_led3), .LED4(dec_diplay_5_led4),
    .LED5(dec_diplay_5_led5), .LED6(dec_diplay_5_led6), .LED7(dec_diplay_5_led7));
  LED led_34 (.in(B_p2));
  LED led_35 (.in(alu_1_ledcin));
  LED led_36 (.in(dec_diplay_3_led3));
  LED led_37 (.in(dec_diplay_3_led1));
  LED led_38 (.in(dec_diplay_3_led0));
  LED led_39 (.in(dec_diplay_3_led2));
  BCD_Display bcd_display_9 (
    .BCD_0(dec_diplay_3_bcd1_0), .BCD_1(dec_diplay_3_bcd1_1), .BCD_2(dec_diplay_3_bcd1_2),
    .BCD_3(dec_diplay_3_bcd1_3), .a(bcd_display_9_a), .b(bcd_display_9_b), .c(bcd_display_9_c),
    .d(bcd_display_9_d), .e(bcd_display_9_e), .f(bcd_display_9_f), .g(bcd_display_9_g), .dp(bcd_display_9_dp));
  _7_Segment_Display u_7_segment_display_9 (
    .g(bcd_display_9_g), .f(bcd_display_9_f), .a(bcd_display_9_a), .b(bcd_display_9_b), .e(bcd_display_9_e),
    .d(bcd_display_9_d), .c(bcd_display_9_c), .dp(bcd_display_9_dp));
  LED led_40 (.in(dec_diplay_4_led6));
  LED led_41 (.in(dec_diplay_4_led7));
  LED led_42 (.in(dec_diplay_4_led4));
  LED led_43 (.in(dec_diplay_4_led5));
  BCD_Display bcd_display_10 (
    .BCD_0(dec_diplay_4_bcd100_0), .BCD_1(dec_diplay_4_bcd100_1), .BCD_2(dec_diplay_4_bcd100_2),
    .BCD_3(dec_diplay_4_bcd100_3), .a(bcd_display_10_a), .b(bcd_display_10_b), .c(bcd_display_10_c),
    .d(bcd_display_10_d), .e(bcd_display_10_e), .f(bcd_display_10_f), .g(bcd_display_10_g),
    .dp(bcd_display_10_dp));
  BCD_Display bcd_display_11 (
    .BCD_0(dec_diplay_4_bcd10_0), .BCD_1(dec_diplay_4_bcd10_1), .BCD_2(dec_diplay_4_bcd10_2),
    .BCD_3(dec_diplay_4_bcd10_3), .a(bcd_display_11_a), .b(bcd_display_11_b), .c(bcd_display_11_c),
    .d(bcd_display_11_d), .e(bcd_display_11_e), .f(bcd_display_11_f), .g(bcd_display_11_g),
    .dp(bcd_display_11_dp));
  _7_Segment_Display u_7_segment_display_10 (
    .g(bcd_display_10_g), .f(bcd_display_10_f), .a(bcd_display_10_a), .b(bcd_display_10_b),
    .e(bcd_display_10_e), .d(bcd_display_10_d), .c(bcd_display_10_c), .dp(bcd_display_10_dp));
  _7_Segment_Display u_7_segment_display_11 (
    .g(bcd_display_11_g), .f(bcd_display_11_f), .a(bcd_display_11_a), .b(bcd_display_11_b),
    .e(bcd_display_11_e), .d(bcd_display_11_d), .c(bcd_display_11_c), .dp(bcd_display_11_dp));
  Reg8 R1 (
    .read(in_9), .write(in_12), .nrst(in_4), .IN_7(R0_out_7), .IN_6(R0_out_6), .IN_5(R0_out_5),
    .IN_4(R0_out_4), .IN_3(R0_out_3), .IN_2(R0_out_2), .IN_1(R0_out_1), .IN_0(R0_out_0), .OUT_7(R0_out_7),
    .OUT_6(R0_out_6), .OUT_5(R0_out_5), .OUT_4(R0_out_4), .OUT_3(R0_out_3), .OUT_2(R0_out_2),
    .OUT_1(R0_out_1), .OUT_0(R0_out_0), .LEDr(R1_ledr), .LEDw(R1_ledw), .LEDrst(R1_ledrst), .LED0(R1_led0),
    .LED1(R1_led1), .LED2(R1_led2), .LED3(R1_led3), .LED4(R1_led4), .LED5(R1_led5), .LED6(R1_led6),
    .LED7(R1_led7));
  LED led_44 (.in(dec_diplay_5_led7));
  LED led_45 (.in(dec_diplay_5_led5));
  LED led_46 (.in(dec_diplay_5_led6));
  LED led_47 (.in(dec_diplay_5_led4));
  BCD_Display bcd_display_12 (
    .BCD_0(dec_diplay_5_bcd10_0), .BCD_1(dec_diplay_5_bcd10_1), .BCD_2(dec_diplay_5_bcd10_2),
    .BCD_3(dec_diplay_5_bcd10_3), .a(bcd_display_12_a), .b(bcd_display_12_b), .c(bcd_display_12_c),
    .d(bcd_display_12_d), .e(bcd_display_12_e), .f(bcd_display_12_f), .g(bcd_display_12_g),
    .dp(bcd_display_12_dp));
  BCD_Display bcd_display_13 (
    .BCD_0(dec_diplay_5_bcd100_0), .BCD_1(dec_diplay_5_bcd100_1), .BCD_2(dec_diplay_5_bcd100_2),
    .BCD_3(dec_diplay_5_bcd100_3), .a(bcd_display_13_a), .b(bcd_display_13_b), .c(bcd_display_13_c),
    .d(bcd_display_13_d), .e(bcd_display_13_e), .f(bcd_display_13_f), .g(bcd_display_13_g),
    .dp(bcd_display_13_dp));
  _7_Segment_Display u_7_segment_display_12 (
    .g(bcd_display_12_g), .f(bcd_display_12_f), .a(bcd_display_12_a), .b(bcd_display_12_b),
    .e(bcd_display_12_e), .d(bcd_display_12_d), .c(bcd_display_12_c), .dp(bcd_display_12_dp));
  _7_Segment_Display u_7_segment_display_13 (
    .g(bcd_display_13_g), .f(bcd_display_13_f), .a(bcd_display_13_a), .b(bcd_display_13_b),
    .e(bcd_display_13_e), .d(bcd_display_13_d), .c(bcd_display_13_c), .dp(bcd_display_13_dp));
  // ZeroPass8 B: pin names not known; wires that end beside it: in_6, B_p2, R0_out_7, B_p4, R0_out_6, B_p6, R0_out_5, B_p8, R0_out_4, B_p10, R0_out_3, B_p12, R0_out_2, B_p14, R0_out_1, B_p16, R0_out_0, B_p18
  LED led_48 (.in(alu_1_ledz));
  LED led_49 (.in(dec_diplay_4_led3));
  LED led_50 (.in(dec_diplay_4_led2));
  LED led_51 (.in(dec_diplay_4_led1));
  LED led_52 (.in(dec_diplay_4_led0));
  BCD_Display bcd_display_14 (
    .BCD_0(dec_diplay_4_bcd1_0), .BCD_1(dec_diplay_4_bcd1_1), .BCD_2(dec_diplay_4_bcd1_2),
    .BCD_3(dec_diplay_4_bcd1_3), .a(bcd_display_14_a), .b(bcd_display_14_b), .c(bcd_display_14_c),
    .d(bcd_display_14_d), .e(bcd_display_14_e), .f(bcd_display_14_f), .g(bcd_display_14_g),
    .dp(bcd_display_14_dp));
  _7_Segment_Display u_7_segment_display_14 (
    .g(bcd_display_14_g), .f(bcd_display_14_f), .a(bcd_display_14_a), .b(bcd_display_14_b),
    .e(bcd_display_14_e), .d(bcd_display_14_d), .c(bcd_display_14_c), .dp(bcd_display_14_dp));
  LED led_53 (.in(dec_diplay_5_led1));
  LED led_54 (.in(dec_diplay_5_led2));
  LED led_55 (.in(dec_diplay_5_led3));
  LED led_56 (.in(dec_diplay_5_led0));
  BCD_Display bcd_display_15 (
    .BCD_0(dec_diplay_5_bcd1_0), .BCD_1(dec_diplay_5_bcd1_1), .BCD_2(dec_diplay_5_bcd1_2),
    .BCD_3(dec_diplay_5_bcd1_3), .a(bcd_display_15_a), .b(bcd_display_15_b), .c(bcd_display_15_c),
    .d(bcd_display_15_d), .e(bcd_display_15_e), .f(bcd_display_15_f), .g(bcd_display_15_g),
    .dp(bcd_display_15_dp));
  _7_Segment_Display u_7_segment_display_15 (
    .g(bcd_display_15_g), .f(bcd_display_15_f), .a(bcd_display_15_a), .b(bcd_display_15_b),
    .e(bcd_display_15_e), .d(bcd_display_15_d), .c(bcd_display_15_c), .dp(bcd_display_15_dp));
  LED led_57 (.in(Z_ledw));
  Reg1 Z (
    .IN(alu_1_zero), .read(1'b1), .write(in_20), .nrst(in_4), .LED(Z_led), .OUT(Z_out), .LEDr(Z_ledr),
    .LEDw(Z_ledw), .LEDrst(Z_ledrst));
  LED led_58 (.in(Z_ledrst));
  LED led_59 (.in(Z_led));
  LED led_60 (.in(Z_ledr));
  LED led_61 (.in(R2_ledw));
  LED led_62 (.in(R2_ledrst));
  LED led_63 (.in(R2_ledr));
  LED led_64 (.in(IR_ledw));
  LED led_65 (.in(IR_ledrst));
  LED led_66 (.in(IR_ledr));
  // ControlUnit controlunit_1: pin names not known; wires that end beside it: clk, in_4, Z_out, controlunit_1_p4, controlunit_1_p5, controlunit_1_p6, controlunit_1_p7, controlunit_1_p8, controlunit_1_p9, controlunit_1_p10, controlunit_1_p11, controlunit_1_p12, controlunit_1_p13, micro
  LED led_67 (.in(controlunit_1_p4));
  LED led_68 (.in(controlunit_1_p5));
  Clock_part clock_1 (.out(clk));
  DEC_Diplay dec_diplay_6 (
    .BIN_0(R2_led0), .BIN_1(R2_led1), .BIN_2(R2_led2), .BIN_3(R2_led3), .BIN_4(R2_led4), .BIN_5(R2_led5),
    .BIN_6(R2_led6), .BIN_7(R2_led7), .BCD1_0(dec_diplay_6_bcd1_0), .BCD1_1(dec_diplay_6_bcd1_1),
    .BCD1_2(dec_diplay_6_bcd1_2), .BCD1_3(dec_diplay_6_bcd1_3), .BCD10_0(dec_diplay_6_bcd10_0),
    .BCD10_1(dec_diplay_6_bcd10_1), .BCD10_2(dec_diplay_6_bcd10_2), .BCD10_3(dec_diplay_6_bcd10_3),
    .BCD100_0(dec_diplay_6_bcd100_0), .BCD100_1(dec_diplay_6_bcd100_1), .BCD100_2(dec_diplay_6_bcd100_2),
    .BCD100_3(dec_diplay_6_bcd100_3), .LED0(dec_diplay_6_led0), .LED1(dec_diplay_6_led1),
    .LED2(dec_diplay_6_led2), .LED3(dec_diplay_6_led3), .LED4(dec_diplay_6_led4), .LED5(dec_diplay_6_led5),
    .LED6(dec_diplay_6_led6), .LED7(dec_diplay_6_led7));
  LED led_69 (.in(dec_diplay_6_led6));
  LED led_70 (.in(dec_diplay_6_led7));
  LED led_71 (.in(dec_diplay_6_led5));
  BCD_Display bcd_display_16 (
    .BCD_0(dec_diplay_6_bcd10_0), .BCD_1(dec_diplay_6_bcd10_1), .BCD_2(dec_diplay_6_bcd10_2),
    .BCD_3(dec_diplay_6_bcd10_3), .a(bcd_display_16_a), .b(bcd_display_16_b), .c(bcd_display_16_c),
    .d(bcd_display_16_d), .e(bcd_display_16_e), .f(bcd_display_16_f), .g(bcd_display_16_g),
    .dp(bcd_display_16_dp));
  BCD_Display bcd_display_17 (
    .BCD_0(dec_diplay_6_bcd100_0), .BCD_1(dec_diplay_6_bcd100_1), .BCD_2(dec_diplay_6_bcd100_2),
    .BCD_3(dec_diplay_6_bcd100_3), .a(bcd_display_17_a), .b(bcd_display_17_b), .c(bcd_display_17_c),
    .d(bcd_display_17_d), .e(bcd_display_17_e), .f(bcd_display_17_f), .g(bcd_display_17_g),
    .dp(bcd_display_17_dp));
  _7_Segment_Display u_7_segment_display_16 (
    .g(bcd_display_17_g), .f(bcd_display_17_f), .a(bcd_display_17_a), .b(bcd_display_17_b),
    .e(bcd_display_17_e), .d(bcd_display_17_d), .c(bcd_display_17_c), .dp(bcd_display_17_dp));
  BIN_Display bin_display_1 (
    .IN_0(IR_led0), .IN_1(IR_led1), .IN_2(IR_led2), .IN_3(IR_led3), .IN_4(IR_led4), .IN_5(IR_led5),
    .IN_6(IR_led6), .IN_7(IR_led7), .LED0(bin_display_1_led0), .LED1(bin_display_1_led1),
    .LED2(bin_display_1_led2), .LED3(bin_display_1_led3), .LED4(bin_display_1_led4),
    .LED5(bin_display_1_led5), .LED6(bin_display_1_led6), .LED7(bin_display_1_led7));
  LED led_72 (.in(bin_display_1_led5));
  LED led_73 (.in(bin_display_1_led6));
  LED led_74 (.in(bin_display_1_led7));
  LED led_75 (.in(dec_diplay_6_led1));
  LED led_76 (.in(dec_diplay_6_led2));
  LED led_77 (.in(dec_diplay_6_led4));
  LED led_78 (.in(dec_diplay_6_led3));
  BCD_Display bcd_display_18 (
    .BCD_0(dec_diplay_6_bcd1_0), .BCD_1(dec_diplay_6_bcd1_1), .BCD_2(dec_diplay_6_bcd1_2),
    .BCD_3(dec_diplay_6_bcd1_3), .a(bcd_display_18_a), .b(bcd_display_18_b), .c(bcd_display_18_c),
    .d(bcd_display_18_d), .e(bcd_display_18_e), .f(bcd_display_18_f), .g(bcd_display_18_g),
    .dp(bcd_display_18_dp));
  _7_Segment_Display u_7_segment_display_17 (
    .g(bcd_display_16_g), .f(bcd_display_16_f), .a(bcd_display_16_a), .b(bcd_display_16_b),
    .e(bcd_display_16_e), .d(bcd_display_16_d), .c(bcd_display_16_c), .dp(bcd_display_16_dp));
  _7_Segment_Display u_7_segment_display_18 (
    .g(bcd_display_18_g), .f(bcd_display_18_f), .a(bcd_display_18_a), .b(bcd_display_18_b),
    .e(bcd_display_18_e), .d(bcd_display_18_d), .c(bcd_display_18_c), .dp(bcd_display_18_dp));
  Reg8 R2 (
    .read(in_14), .write(in_17), .nrst(in_4), .IN_7(R0_out_7), .IN_6(R0_out_6), .IN_5(R0_out_5),
    .IN_4(R0_out_4), .IN_3(R0_out_3), .IN_2(R0_out_2), .IN_1(R0_out_1), .IN_0(R0_out_0), .OUT_7(R0_out_7),
    .OUT_6(R0_out_6), .OUT_5(R0_out_5), .OUT_4(R0_out_4), .OUT_3(R0_out_3), .OUT_2(R0_out_2),
    .OUT_1(R0_out_1), .OUT_0(R0_out_0), .LEDr(R2_ledr), .LEDw(R2_ledw), .LEDrst(R2_ledrst), .LED0(R2_led0),
    .LED1(R2_led1), .LED2(R2_led2), .LED3(R2_led3), .LED4(R2_led4), .LED5(R2_led5), .LED6(R2_led6),
    .LED7(R2_led7));
  LED led_79 (.in(bin_display_1_led1));
  LED led_80 (.in(bin_display_1_led3));
  LED led_81 (.in(bin_display_1_led4));
  LED led_82 (.in(bin_display_1_led2));
  Reg8 IR (
    .read(1'b1), .write(in_11), .nrst(in_4), .IN_7(R0_out_7), .IN_6(R0_out_6), .IN_5(R0_out_5),
    .IN_4(R0_out_4), .IN_3(R0_out_3), .IN_2(R0_out_2), .IN_1(R0_out_1), .IN_0(R0_out_0),
    .OUT_7(controlunit_1_p6), .OUT_6(controlunit_1_p7), .OUT_5(controlunit_1_p8), .OUT_4(controlunit_1_p9),
    .OUT_3(controlunit_1_p10), .OUT_2(controlunit_1_p11), .OUT_1(controlunit_1_p12),
    .OUT_0(controlunit_1_p13), .LEDr(IR_ledr), .LEDw(IR_ledw), .LEDrst(IR_ledrst), .LED0(IR_led0),
    .LED1(IR_led1), .LED2(IR_led2), .LED3(IR_led3), .LED4(IR_led4), .LED5(IR_led5), .LED6(IR_led6),
    .LED7(IR_led7));
  LED led_83 (.in(dec_diplay_6_led0));
  LED led_84 (.in(bin_display_1_led0));
  LED led_85 (.in(R3_ledw));
  LED led_86 (.in(R3_ledrst));
  LED led_87 (.in(R3_ledr));
  LED led_88 (.in(PC_ledw));
  LED led_89 (.in(PC_ledrst));
  LED led_90 (.in(PC_ledr));
  DEC_Diplay dec_diplay_7 (
    .BIN_0(R3_led0), .BIN_1(R3_led1), .BIN_2(R3_led2), .BIN_3(R3_led3), .BIN_4(R3_led4), .BIN_5(R3_led5),
    .BIN_6(R3_led6), .BIN_7(R3_led7), .BCD1_0(dec_diplay_7_bcd1_0), .BCD1_1(dec_diplay_7_bcd1_1),
    .BCD1_2(dec_diplay_7_bcd1_2), .BCD1_3(dec_diplay_7_bcd1_3), .BCD10_0(dec_diplay_7_bcd10_0),
    .BCD10_1(dec_diplay_7_bcd10_1), .BCD10_2(dec_diplay_7_bcd10_2), .BCD10_3(dec_diplay_7_bcd10_3),
    .BCD100_0(dec_diplay_7_bcd100_0), .BCD100_1(dec_diplay_7_bcd100_1), .BCD100_2(dec_diplay_7_bcd100_2),
    .BCD100_3(dec_diplay_7_bcd100_3), .LED0(dec_diplay_7_led0), .LED1(dec_diplay_7_led1),
    .LED2(dec_diplay_7_led2), .LED3(dec_diplay_7_led3), .LED4(dec_diplay_7_led4), .LED5(dec_diplay_7_led5),
    .LED6(dec_diplay_7_led6), .LED7(dec_diplay_7_led7));
  LED led_91 (.in(dec_diplay_7_led6));
  LED led_92 (.in(dec_diplay_7_led7));
  BCD_Display bcd_display_19 (
    .BCD_0(dec_diplay_7_bcd100_0), .BCD_1(dec_diplay_7_bcd100_1), .BCD_2(dec_diplay_7_bcd100_2),
    .BCD_3(dec_diplay_7_bcd100_3), .a(bcd_display_19_a), .b(bcd_display_19_b), .c(bcd_display_19_c),
    .d(bcd_display_19_d), .e(bcd_display_19_e), .f(bcd_display_19_f), .g(bcd_display_19_g),
    .dp(bcd_display_19_dp));
  _7_Segment_Display u_7_segment_display_19 (
    .g(bcd_display_19_g), .f(bcd_display_19_f), .a(bcd_display_19_a), .b(bcd_display_19_b),
    .e(bcd_display_19_e), .d(bcd_display_19_d), .c(bcd_display_19_c), .dp(bcd_display_19_dp));
  HEX_Display hex_display_1 (
    .BIN_0(PC_led0), .LED0(hex_display_1_led0), .BIN_1(PC_led1), .LED1(hex_display_1_led1), .BIN_2(PC_led2),
    .LED2(hex_display_1_led2), .BIN_3(PC_led3), .LED3(hex_display_1_led3), .BIN_4(PC_led4),
    .LED4(hex_display_1_led4), .BIN_5(PC_led5), .LED5(hex_display_1_led5), .BIN_6(PC_led6),
    .LED6(hex_display_1_led6), .BIN_7(PC_led7), .LED7(hex_display_1_led7), .MSN(hex_display_1_msn),
    .LSN(hex_display_1_lsn));
  LED led_93 (.in(hex_display_1_led6));
  LED led_94 (.in(hex_display_1_led7));
  LED led_95 (.in(dec_diplay_7_led2));
  LED led_96 (.in(dec_diplay_7_led3));
  LED led_97 (.in(dec_diplay_7_led4));
  LED led_98 (.in(dec_diplay_7_led5));
  BCD_Display bcd_display_20 (
    .BCD_0(dec_diplay_7_bcd1_0), .BCD_1(dec_diplay_7_bcd1_1), .BCD_2(dec_diplay_7_bcd1_2),
    .BCD_3(dec_diplay_7_bcd1_3), .a(bcd_display_20_a), .b(bcd_display_20_b), .c(bcd_display_20_c),
    .d(bcd_display_20_d), .e(bcd_display_20_e), .f(bcd_display_20_f), .g(bcd_display_20_g),
    .dp(bcd_display_20_dp));
  BCD_Display bcd_display_21 (
    .BCD_0(dec_diplay_7_bcd10_0), .BCD_1(dec_diplay_7_bcd10_1), .BCD_2(dec_diplay_7_bcd10_2),
    .BCD_3(dec_diplay_7_bcd10_3), .a(bcd_display_21_a), .b(bcd_display_21_b), .c(bcd_display_21_c),
    .d(bcd_display_21_d), .e(bcd_display_21_e), .f(bcd_display_21_f), .g(bcd_display_21_g),
    .dp(bcd_display_21_dp));
  _7_Segment_Display u_7_segment_display_20 (
    .g(bcd_display_20_g), .f(bcd_display_20_f), .a(bcd_display_20_a), .b(bcd_display_20_b),
    .e(bcd_display_20_e), .d(bcd_display_20_d), .c(bcd_display_20_c), .dp(bcd_display_20_dp));
  _7_Segment_Display u_7_segment_display_21 (
    .g(bcd_display_21_g), .f(bcd_display_21_f), .a(bcd_display_21_a), .b(bcd_display_21_b),
    .e(bcd_display_21_e), .d(bcd_display_21_d), .c(bcd_display_21_c), .dp(bcd_display_21_dp));
  Reg8 R3 (
    .read(in_22), .write(in_23), .nrst(in_4), .IN_7(R0_out_7), .IN_6(R0_out_6), .IN_5(R0_out_5),
    .IN_4(R0_out_4), .IN_3(R0_out_3), .IN_2(R0_out_2), .IN_1(R0_out_1), .IN_0(R0_out_0), .OUT_7(R0_out_7),
    .OUT_6(R0_out_6), .OUT_5(R0_out_5), .OUT_4(R0_out_4), .OUT_3(R0_out_3), .OUT_2(R0_out_2),
    .OUT_1(R0_out_1), .OUT_0(R0_out_0), .LEDr(R3_ledr), .LEDw(R3_ledw), .LEDrst(R3_ledrst), .LED0(R3_led0),
    .LED1(R3_led1), .LED2(R3_led2), .LED3(R3_led3), .LED4(R3_led4), .LED5(R3_led5), .LED6(R3_led6),
    .LED7(R3_led7));
  LED led_99 (.in(hex_display_1_led3));
  LED led_100 (.in(hex_display_1_led2));
  LED led_101 (.in(hex_display_1_led5));
  LED led_102 (.in(hex_display_1_led4));
  Reg8 PC (
    .read(in_3), .write(in_7), .nrst(in_4), .IN_7(R0_out_7), .IN_6(R0_out_6), .IN_5(R0_out_5),
    .IN_4(R0_out_4), .IN_3(R0_out_3), .IN_2(R0_out_2), .IN_1(R0_out_1), .IN_0(R0_out_0), .OUT_7(R0_out_7),
    .OUT_6(R0_out_6), .OUT_5(R0_out_5), .OUT_4(R0_out_4), .OUT_3(R0_out_3), .OUT_2(R0_out_2),
    .OUT_1(R0_out_1), .OUT_0(R0_out_0), .LEDr(PC_ledr), .LEDw(PC_ledw), .LEDrst(PC_ledrst), .LED0(PC_led0),
    .LED1(PC_led1), .LED2(PC_led2), .LED3(PC_led3), .LED4(PC_led4), .LED5(PC_led5), .LED6(PC_led6),
    .LED7(PC_led7));
  Hex_Digit_Display hex_digit_display_1 (.value(hex_display_1_lsn));  // open: dp
  Hex_Digit_Display hex_digit_display_2 (.value(hex_display_1_msn));  // open: dp
  LED led_103 (.in(dec_diplay_7_led1));
  LED led_104 (.in(dec_diplay_7_led0));
  LED led_105 (.in(hex_display_1_led1));
  LED led_106 (.in(hex_display_1_led0));
  HEX_Display hex_display_2 (
    .BIN_0(MAR_led0), .LED0(hex_display_2_led0), .BIN_1(MAR_led1), .LED1(hex_display_2_led1),
    .BIN_2(MAR_led2), .LED2(hex_display_2_led2), .BIN_3(MAR_led3), .LED3(hex_display_2_led3),
    .BIN_4(MAR_led4), .LED4(hex_display_2_led4), .BIN_5(MAR_led5), .LED5(hex_display_2_led5),
    .BIN_6(MAR_led6), .LED6(hex_display_2_led6), .BIN_7(MAR_led7), .LED7(hex_display_2_led7),
    .MSN(hex_display_2_msn), .LSN(hex_display_2_lsn));
  LED led_107 (.in(MAR_ledw));
  LED led_108 (.in(MAR_ledrst));
  LED led_109 (.in(MAR_ledr));
  Memory_2 memory_1 (
    .ADDR_0(MAR_out_0), .ADDR_1(MAR_out_1), .ADDR_2(MAR_out_2), .ADDR_3(MAR_out_3), .ADDR_4(MAR_out_4),
    .ADDR_5(MAR_out_5), .ADDR_6(MAR_out_6), .ADDR_7(MAR_out_7), .IN_0(R0_out_0), .IN_1(R0_out_1),
    .IN_2(R0_out_2), .IN_3(R0_out_3), .IN_4(R0_out_4), .IN_5(R0_out_5), .IN_6(R0_out_6), .IN_7(R0_out_7),
    .OUT_0(R0_out_0), .OUT_1(R0_out_1), .OUT_2(R0_out_2), .OUT_3(R0_out_3), .OUT_4(R0_out_4),
    .OUT_5(R0_out_5), .OUT_6(R0_out_6), .OUT_7(R0_out_7), .rst(in_8), .load_store(in_21), .enable(in_19),
    .LEDen(memory_1_leden), .LEDrw(memory_1_ledrw), .LEDrst(memory_1_ledrst), .ADDR_OUT(memory_1_addr_out),
    .str_out(memory_1_str_out), .ld_out(memory_1_ld_out), .clk_out(memory_1_clk_out),
    .rst_out(memory_1_rst_out), .en_out(memory_1_en_out), .DATA_OUT(memory_1_data_out), .DATA_IN(undriven));
  LED led_110 (.in(memory_1_leden));
  LED led_111 (.in(memory_1_ledrw));
  LED led_112 (.in(memory_1_ledrst));
  LED led_113 (.in(hex_display_2_led4));
  LED led_114 (.in(hex_display_2_led5));
  LED led_115 (.in(hex_display_2_led6));
  LED led_116 (.in(hex_display_2_led7));
  Reg8 MAR (
    .read(1'b1), .write(in_16), .nrst(in_4), .IN_7(R0_out_7), .IN_6(R0_out_6), .IN_5(R0_out_5),
    .IN_4(R0_out_4), .IN_3(R0_out_3), .IN_2(R0_out_2), .IN_1(R0_out_1), .IN_0(R0_out_0), .OUT_7(MAR_out_7),
    .OUT_6(MAR_out_6), .OUT_5(MAR_out_5), .OUT_4(MAR_out_4), .OUT_3(MAR_out_3), .OUT_2(MAR_out_2),
    .OUT_1(MAR_out_1), .OUT_0(MAR_out_0), .LEDr(MAR_ledr), .LEDw(MAR_ledw), .LEDrst(MAR_ledrst),
    .LED0(MAR_led0), .LED1(MAR_led1), .LED2(MAR_led2), .LED3(MAR_led3), .LED4(MAR_led4), .LED5(MAR_led5),
    .LED6(MAR_led6), .LED7(MAR_led7));
  Hex_Digit_Display hex_digit_display_3 (.value(hex_display_2_msn));  // open: dp
  LED led_117 (.in(hex_display_2_led1));
  LED led_118 (.in(hex_display_2_led3));
  LED led_119 (.in(hex_display_2_led2));
  LED led_120 (.in(hex_display_2_led0));
  Hex_Digit_Display hex_digit_display_4 (.value(hex_display_2_lsn));  // open: dp
  RAM #(.bus("separate")) ram_1 (
    .addr(memory_1_addr_out), .din(undriven), .data(memory_1_data_out), .str(memory_1_str_out),
    .sel(memory_1_en_out), .clk(memory_1_clk_out), .ld(memory_1_ld_out), .clr(memory_1_rst_out));

  // Other names for the same wires on the sheet: b_en = in_6; cin = in_10; fr_w = in_20; ir_w = in_11; mar_w = in_16;
  //   mem_en = in_19; mem_rst = in_8; mem_rw = in_21; nrst = in_4; op = in_13; pc_r = in_3; pc_w = in_7; r0_r = in_1;
  //   r0_w = in_5; r1_r = in_9; r1_w = in_12; r2_r = in_14; r2_w = in_17; r3_r = in_22; r3_w = in_23; ra_w = in_2;
  //   rd_r = in_15; rd_w = in_18

  // Notes on the sheet:
  //   0000 ra rb  |  mov  ra, rb    |  ra = rb
  //   0001 ra xx  |  data ra, imm8  |  ra = ram[pc++]
  //   0010 ra rb  |  ldr  ra, [rb]  |  ra = ram[rb]
  //   0011 ra rb  |  str  ra, [rb]  |  ram[rb] = ra
  //   0101 00 00  |  br   imm8      |  if true: pc = ram[pc+1]
  //   0101 00 01  |  bz   imm8      |  if z==1: pc = ram[pc+1]
  //   0101 00 10  |  bnz  imm8      |  if z==0: pc = ram[pc+1]
  //   0110 xx xx  |  halt           |  stop computer
  //   1000 ra rb  |  add  ra, rb    |  ra = ra + rb;  (z)
  //   1001 ra rb  |  sub  ra, rb    |  ra = ra - rb;  (z)
  //   1111 ra rb  |  cmp  ra, rb    |       ra - rb;  (z)
endmodule

module ControlUnit (
  input  FLAG_z,
  input  INSTR_0,
  input  INSTR_1,
  input  INSTR_2,
  input  INSTR_3,
  input  INSTR_4,
  input  INSTR_5,
  input  INSTR_6,
  input  INSTR_7,
  input  clk,
  input  nrst,
  output br,
  output r0_r,
  output [15:0] mINSTR,
  output LEDclkr,
  output LEDclkw,
  output LEDclk,
  output LEDrst
);

  wire and_1_out, and_2_out, and_3_out, and_4_out, decoder_1_out0, decoder_1_out1, decoder_1_out2,
       decoder_1_out3, decoder_2_out0, decoder_2_out1, decoder_2_out2, decoder_2_out3, or_1_out, or_2_out,
       undriven;

  Decoder #(.select(2), .enable("false")) decoder_1 (
    .out0(decoder_1_out0), .out1(decoder_1_out1), .out2(decoder_1_out2), .out3(decoder_1_out3),
    .sel({INSTR_1, INSTR_0}));
  Decoder #(.select(2), .enable("false")) decoder_2 (
    .out0(decoder_2_out0), .out1(decoder_2_out1), .out2(decoder_2_out2), .out3(decoder_2_out3),
    .sel({INSTR_3, INSTR_2}));
  Decoder #(.select(4), .enable("false")) decoder_3 (.sel({INSTR_7, INSTR_6, INSTR_5, INSTR_4}));  // open: out0, out1, out2, out3, out4, out5, out6, out7, out8, out9, out10, out11, out12, out13, out14, out15
  buf and_1 (and_1_out, decoder_1_out0);  // AND_Gate
  buf and_2 (and_2_out, decoder_2_out0);  // AND_Gate
  or or_1 (or_1_out, and_1_out, and_2_out);
  Clock clock_1 (.clk_r(LEDclkr), .clk(clk), .clk_w(LEDclkw), .nrst(nrst));  // open: clk_out
  D_Latch d_latch_1 ();  // open: D, write, nrst, Q, nQ
  and and_3 (and_3_out, decoder_1_out2, ~FLAG_z);  // AND_Gate
  and and_4 (and_4_out, decoder_1_out1, FLAG_z);
  or or_2 (or_2_out, and_3_out, and_4_out, decoder_1_out0);
  and and_5 (br, or_2_out, undriven);
  buf and_6 (r0_r, or_1_out);  // AND_Gate

  assign LEDclk = clk;
  assign LEDrst = nrst;
endmodule

module Clock (
  input  clk,
  input  nrst,
  output clk_r,
  output clk_w,
  output clk_out
);

  wire and_1_out, and_2_out, or_1_out, or_2_out, reset_logic_nq, reset_logic_q, state_nq;

  and and_1 (and_1_out, clk, reset_logic_nq);
  D_FlipFlop reset_logic (.clk(and_1_out), .D(1'b1), .nrst(nrst), .Q(reset_logic_q), .nQ(reset_logic_nq));
  and and_2 (and_2_out, clk, reset_logic_q);
  D_FlipFlop state (.clk(and_2_out), .D(state_nq), .nrst(nrst), .Q(clk_out), .nQ(state_nq));
  or or_1 (or_1_out, and_2_out, clk_out);
  buf buffer_1 (clk_r, or_1_out);
  not not_1 (clk_w, or_2_out);
  or or_2 (or_2_out, state_nq, and_2_out);
endmodule

module Stepper8 (
  input  clk,
  input  nrst,
  output LEDclk,
  output LEDrst,
  output LED1,
  output LED2,
  output LED3,
  output LED4,
  output LED5,
  output LED6,
  output LED7,
  output LED8,
  output step1,
  output step2,
  output step3,
  output step4,
  output step5,
  output step6,
  output step7,
  output step8
);

  wire d_latch_1_q, d_latch_2_q, d_latch_3_nq, d_latch_3_q, d_latch_4_q, d_latch_5_nq, d_latch_5_q,
       d_latch_6_q, d_latch_7_nq, d_latch_7_q, d_latch_8_q, d_latch_9_nq, d_latch_9_q, d_latch_10_q,
       d_latch_11_nq, d_latch_11_q, d_latch_12_q, d_latch_13_nq, d_latch_13_q, d_latch_14_q, d_latch_15_nq,
       d_latch_15_q, d_latch_16_nq, d_latch_16_q, d_latch_17_q, not_1_out, not_2_out, or_1_out, or_2_out;

  not not_1 (not_1_out, clk);
  or or_1 (or_1_out, d_latch_16_q, not_1_out);
  or or_2 (or_2_out, clk, d_latch_16_q);
  D_Latch d_latch_1 (.D(not_2_out), .write(or_2_out), .nrst(nrst), .Q(d_latch_1_q));  // open: nQ
  not not_2 (not_2_out, d_latch_16_q);
  D_Latch d_latch_2 (.D(d_latch_1_q), .write(or_1_out), .nrst(nrst), .Q(d_latch_2_q));  // open: nQ
  D_Latch d_latch_3 (.D(d_latch_2_q), .write(or_2_out), .nrst(nrst), .Q(d_latch_3_q), .nQ(d_latch_3_nq));
  and and_1 (LED1, d_latch_1_q, d_latch_3_nq);
  D_Latch d_latch_4 (.D(d_latch_3_q), .write(or_1_out), .nrst(nrst), .Q(d_latch_4_q));  // open: nQ
  D_Latch d_latch_5 (.D(d_latch_4_q), .write(or_2_out), .nrst(nrst), .Q(d_latch_5_q), .nQ(d_latch_5_nq));
  and and_2 (LED2, d_latch_3_q, d_latch_5_nq);
  D_Latch d_latch_6 (.D(d_latch_5_q), .write(or_1_out), .nrst(nrst), .Q(d_latch_6_q));  // open: nQ
  D_Latch d_latch_7 (.D(d_latch_6_q), .write(or_2_out), .nrst(nrst), .Q(d_latch_7_q), .nQ(d_latch_7_nq));
  and and_3 (LED3, d_latch_5_q, d_latch_7_nq);
  D_Latch d_latch_8 (.D(d_latch_7_q), .write(or_1_out), .nrst(nrst), .Q(d_latch_8_q));  // open: nQ
  and and_4 (LED4, d_latch_7_q, d_latch_9_nq);
  D_Latch d_latch_9 (.D(d_latch_8_q), .write(or_2_out), .nrst(nrst), .Q(d_latch_9_q), .nQ(d_latch_9_nq));
  D_Latch d_latch_10 (.D(d_latch_9_q), .write(or_1_out), .nrst(nrst), .Q(d_latch_10_q));  // open: nQ
  and and_5 (LED5, d_latch_9_q, d_latch_11_nq);
  D_Latch d_latch_11 (.D(d_latch_10_q), .write(or_2_out), .nrst(nrst), .Q(d_latch_11_q), .nQ(d_latch_11_nq));
  D_Latch d_latch_12 (.D(d_latch_11_q), .write(or_1_out), .nrst(nrst), .Q(d_latch_12_q));  // open: nQ
  and and_6 (LED6, d_latch_11_q, d_latch_13_nq);
  D_Latch d_latch_13 (.D(d_latch_12_q), .write(or_2_out), .nrst(nrst), .Q(d_latch_13_q), .nQ(d_latch_13_nq));
  D_Latch d_latch_14 (.D(d_latch_13_q), .write(or_1_out), .nrst(nrst), .Q(d_latch_14_q));  // open: nQ
  D_Latch d_latch_15 (.D(d_latch_14_q), .write(or_2_out), .nrst(nrst), .Q(d_latch_15_q), .nQ(d_latch_15_nq));
  and and_7 (LED7, d_latch_13_q, d_latch_15_nq);
  D_Latch d_latch_16 (.D(d_latch_17_q), .write(or_2_out), .nrst(nrst), .Q(d_latch_16_q), .nQ(d_latch_16_nq));
  D_Latch d_latch_17 (.D(d_latch_15_q), .write(or_1_out), .nrst(nrst), .Q(d_latch_17_q));  // open: nQ
  and and_8 (LED8, d_latch_15_q, d_latch_16_nq);

  assign LEDclk = clk;
  assign LEDrst = nrst;
  assign step1 = LED1;
  assign step2 = LED2;
  assign step3 = LED3;
  assign step4 = LED4;
  assign step5 = LED5;
  assign step6 = LED6;
  assign step7 = LED7;
  assign step8 = LED8;
endmodule

module FullAdder (
  input  a,
  input  b,
  input  cin,
  output sum,
  output cout
);

  wire and_1_out, and_2_out, xor_1_out;

  xor xor_1 (xor_1_out, a, b);
  and and_1 (and_1_out, xor_1_out, cin);
  and and_2 (and_2_out, a, b);
  xor xor_2 (sum, xor_1_out, cin);
  or or_1 (cout, and_1_out, and_2_out);
endmodule

module Add8 (
  input  a7,
  input  b7,
  input  a6,
  input  b6,
  input  a5,
  input  b5,
  input  a4,
  input  b4,
  input  a3,
  input  b3,
  input  a2,
  input  b2,
  input  a1,
  input  b1,
  input  a0,
  input  b0,
  input  cin,
  output cout,
  output sum_7,
  output sum_6,
  output sum_5,
  output sum_4,
  output sum_3,
  output sum_2,
  output sum_1,
  output sum_0
);

  wire fulladder_2_cout, fulladder_3_cout, fulladder_4_cout, fulladder_5_cout, fulladder_6_cout,
       fulladder_7_cout, fulladder_8_cout;

  FullAdder fulladder_1 (.a(a7), .b(b7), .cin(fulladder_3_cout), .sum(sum_7), .cout(cout));
  FullAdder fulladder_2 (.a(a5), .b(b5), .cin(fulladder_4_cout), .sum(sum_5), .cout(fulladder_2_cout));
  FullAdder fulladder_3 (.a(a6), .b(b6), .cin(fulladder_2_cout), .sum(sum_6), .cout(fulladder_3_cout));
  FullAdder fulladder_4 (.a(a4), .b(b4), .cin(fulladder_5_cout), .sum(sum_4), .cout(fulladder_4_cout));
  FullAdder fulladder_5 (.a(a3), .b(b3), .cin(fulladder_6_cout), .sum(sum_3), .cout(fulladder_5_cout));
  FullAdder fulladder_6 (.a(a2), .b(b2), .cin(fulladder_7_cout), .sum(sum_2), .cout(fulladder_6_cout));
  FullAdder fulladder_7 (.a(a1), .b(b1), .cin(fulladder_8_cout), .sum(sum_1), .cout(fulladder_7_cout));
  FullAdder fulladder_8 (.a(a0), .b(b0), .cin(cin), .sum(sum_0), .cout(fulladder_8_cout));
endmodule

module Inverter8 (
  input  in_7,
  input  in_6,
  input  in_5,
  input  in_4,
  input  in_3,
  input  in_2,
  input  in_1,
  input  in_0,
  input  inv,
  output out_7,
  output out_6,
  output out_5,
  output out_4,
  output out_3,
  output out_2,
  output out_1,
  output out_0
);

  xor xor_1 (out_7, inv, in_7);
  xor xor_2 (out_5, inv, in_5);
  xor xor_3 (out_6, inv, in_6);
  xor xor_4 (out_4, inv, in_4);
  xor xor_5 (out_2, inv, in_2);
  xor xor_6 (out_3, inv, in_3);
  xor xor_7 (out_1, inv, in_1);
  xor xor_8 (out_0, inv, in_0);
endmodule

module Zero8 (
  input  _7,
  input  _6,
  input  _5,
  input  _4,
  input  _3,
  input  _2,
  input  _1,
  input  _0,
  output zero
);

  wire or_1_out, or_2_out, or_3_out, or_4_out;

  nor nor_1 (zero, or_1_out, or_2_out, or_4_out, or_3_out);
  or or_1 (or_1_out, _7, _6);
  or or_2 (or_2_out, _5, _4);
  or or_3 (or_3_out, _1, _0);
  or or_4 (or_4_out, _3, _2);
endmodule

module ALU_2 (
  input  a_0,
  input  b_0,
  input  a_1,
  input  b_1,
  input  a_2,
  input  b_2,
  input  a_3,
  input  b_3,
  input  a_4,
  input  b_4,
  input  a_5,
  input  b_5,
  input  a_6,
  input  b_6,
  input  a_7,
  input  b_7,
  input  op,
  input  cin,
  output LEDop,
  output LEDcin,
  output sum_0,
  output sum_1,
  output sum_2,
  output sum_3,
  output sum_4,
  output sum_5,
  output sum_6,
  output sum_7,
  output LEDz,
  output zero
);

  wire inverter8_1_out_0, inverter8_1_out_1, inverter8_1_out_2, inverter8_1_out_3, inverter8_1_out_4,
       inverter8_1_out_5, inverter8_1_out_6, inverter8_1_out_7, xor_1_out;

  Inverter8 inverter8_1 (
    .inv(op), .in_7(b_7), .in_6(b_6), .in_5(b_5), .in_4(b_4), .in_3(b_3), .in_2(b_2), .in_1(b_1), .in_0(b_0),
    .out_7(inverter8_1_out_7), .out_6(inverter8_1_out_6), .out_5(inverter8_1_out_5),
    .out_4(inverter8_1_out_4), .out_3(inverter8_1_out_3), .out_2(inverter8_1_out_2),
    .out_1(inverter8_1_out_1), .out_0(inverter8_1_out_0));
  Add8 add8_1 (
    .cin(xor_1_out), .a7(a_7), .b7(inverter8_1_out_7), .a6(a_6), .b6(inverter8_1_out_6), .a5(a_5),
    .b5(inverter8_1_out_5), .a4(a_4), .b4(inverter8_1_out_4), .a3(a_3), .b3(inverter8_1_out_3), .a2(a_2),
    .b2(inverter8_1_out_2), .a1(a_1), .b1(inverter8_1_out_1), .a0(a_0), .b0(inverter8_1_out_0),
    .sum_7(sum_7), .sum_6(sum_6), .sum_5(sum_5), .sum_4(sum_4), .sum_3(sum_3), .sum_2(sum_2), .sum_1(sum_1),
    .sum_0(sum_0));  // open: cout
  Zero8 zero8_1 (
    .zero(LEDz), ._7(sum_7), ._6(sum_6), ._5(sum_5), ._4(sum_4), ._3(sum_3), ._2(sum_2), ._1(sum_1),
    ._0(sum_0));
  xor xor_1 (xor_1_out, op, cin);

  assign LEDcin = cin;
  assign LEDop = op;
  assign zero = LEDz;
endmodule

module SR_Latch (
  input  set,
  input  reset,
  output Q,
  output nQ
);

  wire or_1_out, or_2_out;

  or or_1 (or_1_out, set, Q);
  not not_1 (Q, or_2_out);
  not not_2 (nQ, or_1_out);
  or or_2 (or_2_out, nQ, reset);
endmodule

module D_Latch (
  input  D,
  input  write,
  input  nrst,
  output Q,
  output nQ
);

  wire and_1_out, and_2_out, not_1_out, not_2_out, or_1_out;

  not not_1 (not_1_out, D);
  not not_2 (not_2_out, nrst);
  and and_1 (and_1_out, D, write);
  and and_2 (and_2_out, write, not_1_out);
  SR_Latch sr_latch_1 (.set(and_1_out), .Q(Q), .nQ(nQ), .reset(or_1_out));
  or or_1 (or_1_out, and_2_out, not_2_out);
endmodule

module D_FlipFlop (
  input  clk,
  input  D,
  input  nrst,
  output Q,
  output nQ
);

  wire d_latch_1_q, not_1_out, not_2_out;

  not not_1 (not_1_out, clk);
  D_Latch d_latch_1 (.D(D), .write(not_1_out), .nrst(nrst), .Q(d_latch_1_q));  // open: nQ
  not not_2 (not_2_out, not_1_out);
  D_Latch d_latch_2 (.D(d_latch_1_q), .write(not_2_out), .nrst(nrst), .Q(Q), .nQ(nQ));
endmodule

module Reg1 (
  input  IN,
  input  read,
  input  write,
  input  nrst,
  output LED,
  output OUT,
  output LEDr,
  output LEDw,
  output LEDrst
);

  D_Latch d_latch_1 (.D(IN), .write(write), .nrst(nrst), .Q(LED));  // open: nQ
  assign OUT = read ? LED : 1'bz;  // Controlled_Buffer controlled_buffer_1

  assign LEDr = read;
  assign LEDrst = nrst;
  assign LEDw = write;
endmodule

module Reg8 (
  input  IN_7,
  input  IN_6,
  input  IN_5,
  input  IN_4,
  input  IN_3,
  input  IN_2,
  input  IN_1,
  input  IN_0,
  input  read,
  input  write,
  input  nrst,
  output OUT_7,
  output OUT_6,
  output OUT_5,
  output OUT_4,
  output OUT_3,
  output OUT_2,
  output OUT_1,
  output OUT_0,
  output LEDr,
  output LEDw,
  output LEDrst,
  output LED7,
  output LED6,
  output LED5,
  output LED4,
  output LED3,
  output LED2,
  output LED1,
  output LED0
);

  Reg1 reg1_1 (
    .IN(IN_7), .read(read), .write(write), .nrst(nrst), .LED(LED7), .OUT(OUT_7));  // open: LEDr, LEDw, LEDrst
  Reg1 reg1_2 (
    .IN(IN_6), .read(read), .write(write), .nrst(nrst), .LED(LED6), .OUT(OUT_6));  // open: LEDr, LEDw, LEDrst
  Reg1 reg1_3 (
    .IN(IN_5), .read(read), .write(write), .nrst(nrst), .LED(LED5), .OUT(OUT_5));  // open: LEDr, LEDw, LEDrst
  Reg1 reg1_4 (
    .IN(IN_4), .read(read), .write(write), .nrst(nrst), .LED(LED4), .OUT(OUT_4));  // open: LEDr, LEDw, LEDrst
  Reg1 reg1_5 (
    .IN(IN_3), .read(read), .write(write), .nrst(nrst), .LED(LED3), .OUT(OUT_3));  // open: LEDr, LEDw, LEDrst
  Reg1 reg1_6 (
    .IN(IN_2), .read(read), .write(write), .nrst(nrst), .LED(LED2), .OUT(OUT_2));  // open: LEDr, LEDw, LEDrst
  Reg1 reg1_7 (
    .IN(IN_1), .read(read), .write(write), .nrst(nrst), .LED(LED1), .OUT(OUT_1));  // open: LEDr, LEDw, LEDrst
  Reg1 reg1_8 (
    .IN(IN_0), .read(read), .write(write), .nrst(nrst), .LED(LED0), .OUT(OUT_0));  // open: LEDr, LEDw, LEDrst

  assign LEDr = read;
  assign LEDrst = nrst;
  assign LEDw = write;

  // Other names for the same wires on the sheet: _0 = LED0; _1 = LED1; _2 = LED2; _3 = LED3; _4 = LED4; _5 = LED5;
  //   _6 = LED6; _7 = LED7
endmodule

module SRAM_Cell (
  input  IN,
  input  select,
  input  read,
  input  write,
  input  nrst,
  output LED,
  output OUT,
  output LEDsel,
  output LEDr,
  output LEDw,
  output LEDrst
);

  wire and_1_out, and_2_out;

  and and_1 (and_1_out, select, write);
  D_Latch d_latch_1 (.D(IN), .write(and_1_out), .nrst(nrst), .Q(LED));  // open: nQ
  assign OUT = and_2_out ? LED : 1'bz;  // Controlled_Buffer controlled_buffer_1
  and and_2 (and_2_out, select, read);

  assign LEDr = read;
  assign LEDrst = nrst;
  assign LEDsel = select;
  assign LEDw = write;
endmodule

module SRAM_4B (
  input  ADDR_1,
  input  ADDR_0,
  input  select,
  input  IN_7,
  input  IN_6,
  input  IN_5,
  input  IN_4,
  input  IN_3,
  input  IN_2,
  input  IN_1,
  input  IN_0,
  input  read,
  input  write,
  input  nrst,
  output LEDsel_0,
  output LED_0__0,
  output LED_0__1,
  output LED_0__2,
  output LED_0__3,
  output LED_0__4,
  output LED_0__5,
  output LED_0__6,
  output LED_0__7,
  output LEDsel_1,
  output LED_1__0,
  output LED_1__1,
  output LED_1__2,
  output LED_1__3,
  output LED_1__4,
  output LED_1__5,
  output LED_1__6,
  output LED_1__7,
  output LEDsel_2,
  output LED_2__0,
  output LED_2__1,
  output LED_2__2,
  output LED_2__3,
  output LED_2__4,
  output LED_2__5,
  output LED_2__6,
  output LED_2__7,
  output LEDsel_3,
  output LED_3__0,
  output LED_3__1,
  output LED_3__2,
  output LED_3__3,
  output LEDsel,
  output LED_3__4,
  output LEDaddr_0,
  output LED_3__5,
  output LEDaddr_1,
  output LED_3__6,
  output LED_3__7,
  output LEDr,
  output LEDw,
  output LEDrst,
  output OUT_7,
  output OUT_6,
  output OUT_5,
  output OUT_4,
  output OUT_3,
  output OUT_2,
  output OUT_1,
  output OUT_0
);

  wire not_1_out, not_2_out;

  not not_1 (not_1_out, ADDR_1);
  not not_2 (not_2_out, ADDR_0);
  and and_1 (LEDsel_0, not_2_out, not_1_out, select);
  and and_2 (LEDsel_1, ADDR_0, not_1_out, select);
  and and_3 (LEDsel_2, not_2_out, ADDR_1, select);
  and and_4 (LEDsel_3, ADDR_0, ADDR_1, select);
  SRAM_Cell sram_cell_1 (
    .IN(IN_7), .select(LEDsel_0), .read(read), .write(write), .nrst(nrst), .LED(LED_0__7), .OUT(OUT_7));  // open: LEDsel, LEDr, LEDw, LEDrst
  SRAM_Cell sram_cell_2 (
    .IN(IN_7), .select(LEDsel_1), .read(read), .write(write), .nrst(nrst), .LED(LED_1__7), .OUT(OUT_7));  // open: LEDsel, LEDr, LEDw, LEDrst
  SRAM_Cell sram_cell_3 (
    .IN(IN_7), .select(LEDsel_2), .read(read), .write(write), .nrst(nrst), .LED(LED_2__7), .OUT(OUT_7));  // open: LEDsel, LEDr, LEDw, LEDrst
  SRAM_Cell sram_cell_4 (
    .IN(IN_7), .select(LEDsel_3), .read(read), .write(write), .nrst(nrst), .LED(LED_3__7), .OUT(OUT_7));  // open: LEDsel, LEDr, LEDw, LEDrst
  SRAM_Cell sram_cell_5 (
    .IN(IN_6), .select(LEDsel_0), .read(read), .write(write), .nrst(nrst), .LED(LED_0__6), .OUT(OUT_6));  // open: LEDsel, LEDr, LEDw, LEDrst
  SRAM_Cell sram_cell_6 (
    .IN(IN_6), .select(LEDsel_1), .read(read), .write(write), .nrst(nrst), .LED(LED_1__6), .OUT(OUT_6));  // open: LEDsel, LEDr, LEDw, LEDrst
  SRAM_Cell sram_cell_7 (
    .IN(IN_6), .select(LEDsel_2), .read(read), .write(write), .nrst(nrst), .LED(LED_2__6), .OUT(OUT_6));  // open: LEDsel, LEDr, LEDw, LEDrst
  SRAM_Cell sram_cell_8 (
    .IN(IN_6), .select(LEDsel_3), .read(read), .write(write), .nrst(nrst), .LED(LED_3__6), .OUT(OUT_6));  // open: LEDsel, LEDr, LEDw, LEDrst
  SRAM_Cell sram_cell_9 (
    .IN(IN_5), .select(LEDsel_0), .read(read), .write(write), .nrst(nrst), .LED(LED_0__5), .OUT(OUT_5));  // open: LEDsel, LEDr, LEDw, LEDrst
  SRAM_Cell sram_cell_10 (
    .IN(IN_5), .select(LEDsel_1), .read(read), .write(write), .nrst(nrst), .LED(LED_1__5), .OUT(OUT_5));  // open: LEDsel, LEDr, LEDw, LEDrst
  SRAM_Cell sram_cell_11 (
    .IN(IN_5), .select(LEDsel_2), .read(read), .write(write), .nrst(nrst), .LED(LED_2__5), .OUT(OUT_5));  // open: LEDsel, LEDr, LEDw, LEDrst
  SRAM_Cell sram_cell_12 (
    .IN(IN_5), .select(LEDsel_3), .read(read), .write(write), .nrst(nrst), .LED(LED_3__5), .OUT(OUT_5));  // open: LEDsel, LEDr, LEDw, LEDrst
  SRAM_Cell sram_cell_13 (
    .IN(IN_4), .select(LEDsel_0), .read(read), .write(write), .nrst(nrst), .LED(LED_0__4), .OUT(OUT_4));  // open: LEDsel, LEDr, LEDw, LEDrst
  SRAM_Cell sram_cell_14 (
    .IN(IN_4), .select(LEDsel_1), .read(read), .write(write), .nrst(nrst), .LED(LED_1__4), .OUT(OUT_4));  // open: LEDsel, LEDr, LEDw, LEDrst
  SRAM_Cell sram_cell_15 (
    .IN(IN_4), .select(LEDsel_2), .read(read), .write(write), .nrst(nrst), .LED(LED_2__4), .OUT(OUT_4));  // open: LEDsel, LEDr, LEDw, LEDrst
  SRAM_Cell sram_cell_16 (
    .IN(IN_4), .select(LEDsel_3), .read(read), .write(write), .nrst(nrst), .LED(LED_3__4), .OUT(OUT_4));  // open: LEDsel, LEDr, LEDw, LEDrst
  SRAM_Cell sram_cell_17 (
    .IN(IN_3), .select(LEDsel_0), .read(read), .write(write), .nrst(nrst), .LED(LED_0__3), .OUT(OUT_3));  // open: LEDsel, LEDr, LEDw, LEDrst
  SRAM_Cell sram_cell_18 (
    .IN(IN_3), .select(LEDsel_1), .read(read), .write(write), .nrst(nrst), .LED(LED_1__3), .OUT(OUT_3));  // open: LEDsel, LEDr, LEDw, LEDrst
  SRAM_Cell sram_cell_19 (
    .IN(IN_3), .select(LEDsel_2), .read(read), .write(write), .nrst(nrst), .LED(LED_2__3), .OUT(OUT_3));  // open: LEDsel, LEDr, LEDw, LEDrst
  SRAM_Cell sram_cell_20 (
    .IN(IN_3), .select(LEDsel_3), .read(read), .write(write), .nrst(nrst), .LED(LED_3__3), .OUT(OUT_3));  // open: LEDsel, LEDr, LEDw, LEDrst
  SRAM_Cell sram_cell_21 (
    .IN(IN_2), .select(LEDsel_0), .read(read), .write(write), .nrst(nrst), .LED(LED_0__2), .OUT(OUT_2));  // open: LEDsel, LEDr, LEDw, LEDrst
  SRAM_Cell sram_cell_22 (
    .IN(IN_2), .select(LEDsel_1), .read(read), .write(write), .nrst(nrst), .LED(LED_1__2), .OUT(OUT_2));  // open: LEDsel, LEDr, LEDw, LEDrst
  SRAM_Cell sram_cell_23 (
    .IN(IN_2), .select(LEDsel_2), .read(read), .write(write), .nrst(nrst), .LED(LED_2__2), .OUT(OUT_2));  // open: LEDsel, LEDr, LEDw, LEDrst
  SRAM_Cell sram_cell_24 (
    .IN(IN_2), .select(LEDsel_3), .read(read), .write(write), .nrst(nrst), .LED(LED_3__2), .OUT(OUT_2));  // open: LEDsel, LEDr, LEDw, LEDrst
  SRAM_Cell sram_cell_25 (
    .IN(IN_1), .select(LEDsel_0), .read(read), .write(write), .nrst(nrst), .LED(LED_0__1), .OUT(OUT_1));  // open: LEDsel, LEDr, LEDw, LEDrst
  SRAM_Cell sram_cell_26 (
    .IN(IN_1), .select(LEDsel_1), .read(read), .write(write), .nrst(nrst), .LED(LED_1__1), .OUT(OUT_1));  // open: LEDsel, LEDr, LEDw, LEDrst
  SRAM_Cell sram_cell_27 (
    .IN(IN_1), .select(LEDsel_2), .read(read), .write(write), .nrst(nrst), .LED(LED_2__1), .OUT(OUT_1));  // open: LEDsel, LEDr, LEDw, LEDrst
  SRAM_Cell sram_cell_28 (
    .IN(IN_1), .select(LEDsel_3), .read(read), .write(write), .nrst(nrst), .LED(LED_3__1), .OUT(OUT_1));  // open: LEDsel, LEDr, LEDw, LEDrst
  SRAM_Cell sram_cell_29 (
    .IN(IN_0), .select(LEDsel_0), .read(read), .write(write), .nrst(nrst), .LED(LED_0__0), .OUT(OUT_0));  // open: LEDsel, LEDr, LEDw, LEDrst
  SRAM_Cell sram_cell_30 (
    .IN(IN_0), .select(LEDsel_1), .read(read), .write(write), .nrst(nrst), .LED(LED_1__0), .OUT(OUT_0));  // open: LEDsel, LEDr, LEDw, LEDrst
  SRAM_Cell sram_cell_31 (
    .IN(IN_0), .select(LEDsel_2), .read(read), .write(write), .nrst(nrst), .LED(LED_2__0), .OUT(OUT_0));  // open: LEDsel, LEDr, LEDw, LEDrst
  SRAM_Cell sram_cell_32 (
    .IN(IN_0), .select(LEDsel_3), .read(read), .write(write), .nrst(nrst), .LED(LED_3__0), .OUT(OUT_0));  // open: LEDsel, LEDr, LEDw, LEDrst

  assign LEDaddr_0 = ADDR_0;
  assign LEDaddr_1 = ADDR_1;
  assign LEDr = read;
  assign LEDrst = nrst;
  assign LEDsel = select;
  assign LEDw = write;

  // Other names for the same wires on the sheet: _00 = LED_0__0; _01 = LED_0__1; _02 = LED_0__2; _03 = LED_0__3;
  //   _04 = LED_0__4; _05 = LED_0__5; _06 = LED_0__6; _07 = LED_0__7; _10 = LED_1__0; _11 = LED_1__1; _12 = LED_1__2;
  //   _13 = LED_1__3; _14 = LED_1__4; _15 = LED_1__5; _16 = LED_1__6; _17 = LED_1__7; _20 = LED_2__0; _21 = LED_2__1;
  //   _22 = LED_2__2; _23 = LED_2__3; _24 = LED_2__4; _25 = LED_2__5; _26 = LED_2__6; _27 = LED_2__7; _30 = LED_3__0;
  //   _31 = LED_3__1; _32 = LED_3__2; _33 = LED_3__3; _34 = LED_3__4; _35 = LED_3__5; _36 = LED_3__6; _37 = LED_3__7
endmodule

module SRAM_16B (
);

  SRAM_4B sram_4b_1 ();  // open: read, write, nrst, LEDsel_0, LED_0__0, LED_0__1, LED_0__2, LED_0__3, LEDsel_1, LED_1__0, LED_1__1, LED_1__2, LED_1__3, LEDsel_2, LED_2__0, LED_2__1, LED_2__2, LED_2__3, LEDsel_3, LED_3__0, LED_3__1, LED_3__2, LED_3__3, LEDr, LEDw, LEDrst, ADDR_1, ADDR_0, select, IN_3, IN_2, IN_1, IN_0, OUT_3, OUT_2, OUT_1, OUT_0, LEDsel, LEDaddr_0, LEDaddr_1, IN_7, IN_6, IN_5, IN_4, OUT_7, OUT_6, OUT_5, OUT_4, LED_0__4, LED_0__5, LED_0__6, LED_0__7, LED_1__4, LED_1__5, LED_1__6, LED_1__7, LED_2__4, LED_2__5, LED_2__6, LED_2__7, LED_3__4, LED_3__5, LED_3__6, LED_3__7
  SRAM_4B sram_4b_2 ();  // open: read, write, nrst, LEDsel_0, LED_0__0, LED_0__1, LED_0__2, LED_0__3, LEDsel_1, LED_1__0, LED_1__1, LED_1__2, LED_1__3, LEDsel_2, LED_2__0, LED_2__1, LED_2__2, LED_2__3, LEDsel_3, LED_3__0, LED_3__1, LED_3__2, LED_3__3, LEDr, LEDw, LEDrst, ADDR_1, ADDR_0, select, IN_3, IN_2, IN_1, IN_0, OUT_3, OUT_2, OUT_1, OUT_0, LEDsel, LEDaddr_0, LEDaddr_1, IN_7, IN_6, IN_5, IN_4, OUT_7, OUT_6, OUT_5, OUT_4, LED_0__4, LED_0__5, LED_0__6, LED_0__7, LED_1__4, LED_1__5, LED_1__6, LED_1__7, LED_2__4, LED_2__5, LED_2__6, LED_2__7, LED_3__4, LED_3__5, LED_3__6, LED_3__7
endmodule

module Memory_2 (
  input  ADDR_0,
  input  IN_0,
  input  ADDR_1,
  input  IN_1,
  input  ADDR_2,
  input  IN_2,
  input  ADDR_3,
  input  IN_3,
  input  ADDR_4,
  input  IN_4,
  input  ADDR_5,
  input  IN_5,
  input  ADDR_6,
  input  IN_6,
  input  ADDR_7,
  input  IN_7,
  input  [7:0] DATA_IN,
  input  enable,
  input  load_store,
  input  rst,
  output [7:0] ADDR_OUT,
  output [7:0] DATA_OUT,
  output en_out,
  output ld_out,
  output str_out,
  output OUT_0,
  output clk_out,
  output OUT_1,
  output rst_out,
  output OUT_2,
  output OUT_3,
  output OUT_4,
  output LEDen,
  output OUT_5,
  output LEDrw,
  output OUT_6,
  output LEDrst,
  output OUT_7
);

  and and_1 (ld_out, enable, ~load_store);  // AND_Gate
  and and_2 (str_out, enable, load_store);
  Delayer delayer_1 (.in(load_store), .out(clk_out));
  RAM #(.bus("separate")) ram_1 ();  // open: addr, din, data, str, sel, clk, ld, clr

  assign ADDR_OUT = {ADDR_7, ADDR_6, ADDR_5, ADDR_4, ADDR_3, ADDR_2, ADDR_1, ADDR_0};
  assign DATA_OUT = {IN_7, IN_6, IN_5, IN_4, IN_3, IN_2, IN_1, IN_0};
  assign en_out = enable;
  assign LEDen = enable;
  assign LEDrst = rst;
  assign LEDrw = load_store;
  assign OUT_0 = DATA_IN[0];
  assign OUT_1 = DATA_IN[1];
  assign OUT_2 = DATA_IN[2];
  assign OUT_3 = DATA_IN[3];
  assign OUT_4 = DATA_IN[4];
  assign OUT_5 = DATA_IN[5];
  assign OUT_6 = DATA_IN[6];
  assign OUT_7 = DATA_IN[7];
  assign rst_out = rst;
endmodule

module ZeroPass8 (
  input  IN_7,
  input  IN_6,
  input  IN_5,
  input  IN_4,
  input  IN_3,
  input  IN_2,
  input  IN_1,
  input  IN_0,
  input  enable,
  output LEDen,
  output LED7,
  output LED6,
  output LED5,
  output LED4,
  output LED3,
  output LED2,
  output LED1,
  output LED0,
  output OUT_7,
  output OUT_6,
  output OUT_5,
  output OUT_4,
  output OUT_3,
  output OUT_2,
  output OUT_1,
  output OUT_0
);

  and and_1 (LED7, enable, IN_7);
  and and_2 (LED6, enable, IN_6);
  and and_3 (LED5, enable, IN_5);
  and and_4 (LED4, enable, IN_4);
  and and_5 (LED3, enable, IN_3);
  and and_6 (LED2, enable, IN_2);
  and and_7 (LED1, enable, IN_1);
  and and_8 (LED0, enable, IN_0);

  assign LEDen = enable;
  assign OUT_0 = LED0;
  assign OUT_1 = LED1;
  assign OUT_2 = LED2;
  assign OUT_3 = LED3;
  assign OUT_4 = LED4;
  assign OUT_5 = LED5;
  assign OUT_6 = LED6;
  assign OUT_7 = LED7;
endmodule

module Delayer (
  input  in,
  output out
);

  wire not_1_out, not_2_out, not_3_out, not_4_out, not_5_out, not_6_out, not_7_out;

  not not_1 (not_1_out, in);
  not not_2 (not_2_out, not_1_out);
  not not_3 (not_3_out, not_2_out);
  not not_4 (not_4_out, not_5_out);
  not not_5 (not_5_out, not_3_out);
  not not_6 (not_6_out, not_4_out);
  not not_7 (not_7_out, not_6_out);
  not not_8 (out, not_7_out);
endmodule

module BinToBCD___Add3 (
  input  IN_0,
  input  IN_1,
  input  IN_2,
  input  IN_3,
  output OUT_3,
  output OUT_2,
  output OUT_1,
  output OUT_0
);

  wire and_1_out, and_2_out, and_3_out, and_4_out, and_5_out, and_6_out, and_7_out, and_8_out, and_9_out,
       and_10_out, not_1_out, not_2_out, not_3_out, not_4_out;

  not not_1 (not_1_out, IN_0);
  not not_2 (not_2_out, IN_1);
  not not_3 (not_3_out, IN_2);
  not not_4 (not_4_out, IN_3);
  and and_1 (and_1_out, IN_2, IN_1);
  and and_2 (and_2_out, IN_2, IN_0);
  or or_1 (OUT_3, IN_3, and_1_out, and_2_out);
  and and_3 (and_3_out, IN_3, IN_0);
  or or_2 (OUT_2, and_3_out, and_5_out);
  and and_4 (and_4_out, IN_3, not_1_out);
  and and_5 (and_5_out, IN_2, not_2_out, not_1_out);
  and and_6 (and_6_out, IN_1, IN_0);
  and and_7 (and_7_out, not_3_out, IN_1);
  or or_3 (OUT_1, and_4_out, and_7_out, and_6_out);
  and and_8 (and_8_out, IN_3, not_1_out);
  and and_9 (and_9_out, not_4_out, not_3_out, IN_0);
  and and_10 (and_10_out, IN_2, IN_1, not_1_out);
  or or_4 (OUT_0, and_8_out, and_10_out, and_9_out);
endmodule

module BinToBCD8 (
  input  BIN_0,
  input  BIN_1,
  input  BIN_2,
  input  BIN_3,
  input  BIN_4,
  input  BIN_5,
  input  BIN_6,
  input  BIN_7,
  output BCD1_0,
  output BCD1_1,
  output BCD1_2,
  output BCD1_3,
  output BCD10_0,
  output BCD10_1,
  output BCD10_2,
  output BCD10_3,
  output BCD100_0,
  output BCD100_1,
  output BCD100_2,
  output BCD100_3
);

  wire bintobcd_add3_1_out_0, bintobcd_add3_1_out_1, bintobcd_add3_1_out_2, bintobcd_add3_1_out_3,
       bintobcd_add3_2_out_0, bintobcd_add3_2_out_1, bintobcd_add3_2_out_2, bintobcd_add3_2_out_3,
       bintobcd_add3_3_out_0, bintobcd_add3_3_out_1, bintobcd_add3_3_out_2, bintobcd_add3_3_out_3,
       bintobcd_add3_4_out_0, bintobcd_add3_4_out_1, bintobcd_add3_4_out_2, bintobcd_add3_6_out_0,
       bintobcd_add3_6_out_1, bintobcd_add3_6_out_2, bintobcd_add3_6_out_3;

  BinToBCD___Add3 bintobcd_add3_1 (
    .IN_3(1'b0), .IN_2(BIN_7), .IN_1(BIN_6), .IN_0(BIN_5), .OUT_3(bintobcd_add3_1_out_3),
    .OUT_2(bintobcd_add3_1_out_2), .OUT_1(bintobcd_add3_1_out_1), .OUT_0(bintobcd_add3_1_out_0));
  BinToBCD___Add3 bintobcd_add3_2 (
    .IN_3(bintobcd_add3_1_out_2), .IN_2(bintobcd_add3_1_out_1), .IN_1(bintobcd_add3_1_out_0), .IN_0(BIN_4),
    .OUT_3(bintobcd_add3_2_out_3), .OUT_2(bintobcd_add3_2_out_2), .OUT_1(bintobcd_add3_2_out_1),
    .OUT_0(bintobcd_add3_2_out_0));
  BinToBCD___Add3 bintobcd_add3_3 (
    .IN_3(bintobcd_add3_2_out_2), .IN_2(bintobcd_add3_2_out_1), .IN_1(bintobcd_add3_2_out_0), .IN_0(BIN_3),
    .OUT_3(bintobcd_add3_3_out_3), .OUT_2(bintobcd_add3_3_out_2), .OUT_1(bintobcd_add3_3_out_1),
    .OUT_0(bintobcd_add3_3_out_0));
  BinToBCD___Add3 bintobcd_add3_4 (
    .IN_3(1'b0), .IN_2(bintobcd_add3_1_out_3), .IN_1(bintobcd_add3_2_out_3), .IN_0(bintobcd_add3_3_out_3),
    .OUT_3(BCD100_1), .OUT_2(bintobcd_add3_4_out_2), .OUT_1(bintobcd_add3_4_out_1),
    .OUT_0(bintobcd_add3_4_out_0));
  BinToBCD___Add3 bintobcd_add3_5 (
    .IN_3(bintobcd_add3_4_out_2), .IN_2(bintobcd_add3_4_out_1), .IN_1(bintobcd_add3_4_out_0),
    .IN_0(bintobcd_add3_6_out_3), .OUT_3(BCD100_0), .OUT_2(BCD10_3), .OUT_1(BCD10_2), .OUT_0(BCD10_1));
  BinToBCD___Add3 bintobcd_add3_6 (
    .IN_3(bintobcd_add3_3_out_2), .IN_2(bintobcd_add3_3_out_1), .IN_1(bintobcd_add3_3_out_0), .IN_0(BIN_2),
    .OUT_3(bintobcd_add3_6_out_3), .OUT_2(bintobcd_add3_6_out_2), .OUT_1(bintobcd_add3_6_out_1),
    .OUT_0(bintobcd_add3_6_out_0));
  BinToBCD___Add3 bintobcd_add3_7 (
    .IN_3(bintobcd_add3_6_out_2), .IN_2(bintobcd_add3_6_out_1), .IN_1(bintobcd_add3_6_out_0), .IN_0(BIN_1),
    .OUT_3(BCD10_0), .OUT_2(BCD1_3), .OUT_1(BCD1_2), .OUT_0(BCD1_1));

  assign BCD1_0 = BIN_0;
  assign BCD100_2 = 1'b0;
  assign BCD100_3 = 1'b0;
endmodule

module BCD_Display (
  input  BCD_0,
  input  BCD_1,
  input  BCD_2,
  input  BCD_3,
  output a,
  output b,
  output c,
  output d,
  output e,
  output f,
  output g,
  output dp
);

  wire decoder_1_out0, decoder_1_out1, decoder_1_out2, decoder_1_out3, decoder_1_out4, decoder_1_out5,
       decoder_1_out6, decoder_1_out7, decoder_1_out8, decoder_1_out9;

  Decoder #(.select(4), .enable("false")) decoder_1 (
    .out0(decoder_1_out0), .out1(decoder_1_out1), .out2(decoder_1_out2), .out3(decoder_1_out3),
    .out4(decoder_1_out4), .out5(decoder_1_out5), .out6(decoder_1_out6), .out7(decoder_1_out7),
    .out8(decoder_1_out8), .out9(decoder_1_out9), .sel({BCD_3, BCD_2, BCD_1, BCD_0}));  // open: out10, out11, out12, out13, out14, out15
  or or_1 (a, decoder_1_out9, decoder_1_out8, decoder_1_out7, decoder_1_out6, decoder_1_out5, 1'b0, decoder_1_out3, decoder_1_out2, 1'b0, decoder_1_out0);
  or or_2 (b, decoder_1_out9, decoder_1_out8, decoder_1_out7, 1'b0, 1'b0, decoder_1_out4, decoder_1_out3, decoder_1_out2, decoder_1_out1, decoder_1_out0);
  or or_3 (c, decoder_1_out9, decoder_1_out8, decoder_1_out7, decoder_1_out6, decoder_1_out5, decoder_1_out4, decoder_1_out3, 1'b0, decoder_1_out1, decoder_1_out0);
  or or_4 (d, decoder_1_out9, decoder_1_out8, 1'b0, decoder_1_out6, decoder_1_out5, 1'b0, decoder_1_out3, decoder_1_out2, 1'b0, decoder_1_out0);
  or or_5 (e, 1'b0, decoder_1_out8, 1'b0, decoder_1_out6, 1'b0, 1'b0, 1'b0, decoder_1_out2, 1'b0, decoder_1_out0);
  or or_6 (f, decoder_1_out9, decoder_1_out8, 1'b0, decoder_1_out6, decoder_1_out5, decoder_1_out4, 1'b0, 1'b0, 1'b0, decoder_1_out0);
  or or_7 (g, decoder_1_out9, decoder_1_out8, 1'b0, decoder_1_out6, decoder_1_out5, decoder_1_out4, decoder_1_out3, decoder_1_out2, 1'b0, 1'b0);
  or or_8 (dp, 1'b0, 1'b0, 1'b0, 1'b0, 1'b0, 1'b0, 1'b0, 1'b0, 1'b0, 1'b0);
endmodule

module DEC_Diplay (
  input  BIN_0,
  input  BIN_1,
  input  BIN_2,
  input  BIN_3,
  input  BIN_4,
  input  BIN_5,
  input  BIN_6,
  input  BIN_7,
  output LED0,
  output LED1,
  output LED2,
  output LED3,
  output LED4,
  output LED5,
  output LED6,
  output LED7,
  output BCD1_0,
  output BCD1_1,
  output BCD1_2,
  output BCD1_3,
  output BCD10_0,
  output BCD10_1,
  output BCD10_2,
  output BCD10_3,
  output BCD100_0,
  output BCD100_1,
  output BCD100_2,
  output BCD100_3
);

  BinToBCD8 bintobcd8_1 (
    .BIN_0(BIN_0), .BIN_1(BIN_1), .BIN_2(BIN_2), .BIN_3(BIN_3), .BIN_4(BIN_4), .BIN_5(BIN_5), .BIN_6(BIN_6),
    .BIN_7(BIN_7), .BCD1_0(BCD1_0), .BCD1_1(BCD1_1), .BCD1_2(BCD1_2), .BCD1_3(BCD1_3), .BCD10_0(BCD10_0),
    .BCD10_1(BCD10_1), .BCD10_2(BCD10_2), .BCD10_3(BCD10_3), .BCD100_0(BCD100_0), .BCD100_1(BCD100_1),
    .BCD100_2(BCD100_2), .BCD100_3(BCD100_3));

  assign LED0 = BIN_0;
  assign LED1 = BIN_1;
  assign LED2 = BIN_2;
  assign LED3 = BIN_3;
  assign LED4 = BIN_4;
  assign LED5 = BIN_5;
  assign LED6 = BIN_6;
  assign LED7 = BIN_7;
endmodule

module BIN_Display (
  input  IN_0,
  input  IN_1,
  input  IN_2,
  input  IN_3,
  input  IN_4,
  input  IN_5,
  input  IN_6,
  input  IN_7,
  output LED0,
  output LED1,
  output LED2,
  output LED3,
  output LED4,
  output LED5,
  output LED6,
  output LED7
);


  assign LED0 = IN_0;
  assign LED1 = IN_1;
  assign LED2 = IN_2;
  assign LED3 = IN_3;
  assign LED4 = IN_4;
  assign LED5 = IN_5;
  assign LED6 = IN_6;
  assign LED7 = IN_7;
endmodule

module HEX_Display (
  input  BIN_0,
  input  BIN_1,
  input  BIN_2,
  input  BIN_3,
  input  BIN_4,
  input  BIN_5,
  input  BIN_6,
  input  BIN_7,
  output LED0,
  output LED1,
  output LED2,
  output LED3,
  output LED4,
  output LED5,
  output LED6,
  output LED7,
  output [3:0] MSN,
  output [3:0] LSN
);


  assign LED0 = BIN_0;
  assign LED1 = BIN_1;
  assign LED2 = BIN_2;
  assign LED3 = BIN_3;
  assign LED4 = BIN_4;
  assign LED5 = BIN_5;
  assign LED6 = BIN_6;
  assign LED7 = BIN_7;
  assign LSN = {BIN_3, BIN_2, BIN_1, BIN_0};
  assign MSN = {BIN_7, BIN_6, BIN_5, BIN_4};
endmodule
