// Logisim project v0.circ as structural Verilog
module Computer (
  input  in_1,
  input  in_2,
  input  in_3,
  input  in_4,
  input  in_5,
  input  in_6,
  input  in_7,
  input  in_8,
  input  in_9,
  input  in_10,
  input  in_11,
  input  in_12,
  input  MANUAL,
  input  ON
);

  wire _0_leden, _0_out_0, _0_out_1, _0_out_2, _0_out_3, ACC_led_0, ACC_led_1, ACC_led_2, ACC_led_3,
       ACC_ledr, ACC_ledrst, ACC_ledw, ACC_out_0, ACC_out_1, ACC_out_2, ACC_out_3, acc_r, acc_w,
       alu_1_ledcin, alu_1_ledop, alu_1_sum_0, alu_1_sum_1, alu_1_sum_2, alu_1_sum_3, bin_display_1_led0,
       bin_display_1_led1, bin_display_1_led2, bin_display_1_led3, cin, clk, CLOCK_out, controlunit_1_led0,
       controlunit_1_led1, controlunit_1_led2, controlunit_1_led3, controlunit_1_led4, controlunit_1_led5,
       controlunit_1_led6, controlunit_1_led7, controlunit_1_led8, controlunit_1_led9, controlunit_1_led10,
       controlunit_1_led11, controlunit_1_led12, controlunit_1_led13, controlunit_1_led14,
       controlunit_1_led15, controlunit_1_led16, controlunit_1_ledclk, controlunit_1_ledclkr,
       controlunit_1_ledclkw, controlunit_1_ledhalt, controlunit_1_ledinstr0, controlunit_1_ledinstr1,
       controlunit_1_ledinstr2, controlunit_1_ledinstr3, controlunit_1_ledrst, controlunit_1_ledstep1,
       controlunit_1_ledstep2, controlunit_1_ledstep3, controlunit_1_ledstep4, controlunit_1_ledstep5,
       controlunit_1_ledstep6, controlunit_1_ledstep7, controlunit_1_ledzero, dec_diplay_1_bcd1_0,
       dec_diplay_1_bcd1_1, dec_diplay_1_bcd1_2, dec_diplay_1_bcd1_3, dec_diplay_1_bcd10_0,
       dec_diplay_1_bcd10_1, dec_diplay_1_bcd10_2, dec_diplay_1_bcd10_3, dec_diplay_1_led0,
       dec_diplay_1_led1, dec_diplay_1_led2, dec_diplay_1_led3, dec_diplay_2_bcd1_0, dec_diplay_2_bcd1_1,
       dec_diplay_2_bcd1_2, dec_diplay_2_bcd1_3, dec_diplay_2_bcd10_0, dec_diplay_2_bcd10_1,
       dec_diplay_2_bcd10_2, dec_diplay_2_bcd10_3, dec_diplay_2_led0, dec_diplay_2_led1, dec_diplay_2_led2,
       dec_diplay_2_led3, dec_diplay_3_bcd1_0, dec_diplay_3_bcd1_1, dec_diplay_3_bcd1_2, dec_diplay_3_bcd1_3,
       dec_diplay_3_bcd10_0, dec_diplay_3_bcd10_1, dec_diplay_3_bcd10_2, dec_diplay_3_bcd10_3,
       dec_diplay_3_led0, dec_diplay_3_led1, dec_diplay_3_led2, dec_diplay_3_led3, dec_diplay_4_bcd1_0,
       dec_diplay_4_bcd1_1, dec_diplay_4_bcd1_2, dec_diplay_4_bcd1_3, dec_diplay_4_bcd10_0,
       dec_diplay_4_bcd10_1, dec_diplay_4_bcd10_2, dec_diplay_4_bcd10_3, dec_diplay_4_led0,
       dec_diplay_4_led1, dec_diplay_4_led2, dec_diplay_4_led3, dec_diplay_5_bcd1_0, dec_diplay_5_bcd1_1,
       dec_diplay_5_bcd1_2, dec_diplay_5_bcd1_3, dec_diplay_5_bcd10_0, dec_diplay_5_bcd10_1,
       dec_diplay_5_bcd10_2, dec_diplay_5_bcd10_3, dec_diplay_5_led0, dec_diplay_5_led1, dec_diplay_5_led2,
       dec_diplay_5_led3, dec_diplay_6_bcd1_0, dec_diplay_6_bcd1_1, dec_diplay_6_bcd1_2, dec_diplay_6_bcd1_3,
       dec_diplay_6_bcd10_0, dec_diplay_6_bcd10_1, dec_diplay_6_bcd10_2, dec_diplay_6_bcd10_3,
       dec_diplay_6_led0, dec_diplay_6_led1, dec_diplay_6_led2, dec_diplay_6_led3, drom_r, IMM_led_0__0,
       IMM_led_0__1, IMM_led_0__2, IMM_led_0__3, IMM_led_1__0, IMM_led_1__1, IMM_led_1__2, IMM_led_1__3,
       IMM_led_2__0, IMM_led_2__1, IMM_led_2__2, IMM_led_2__3, IMM_led_3__0, IMM_led_3__1, IMM_led_3__2,
       IMM_led_3__3, IMM_led_4__0, IMM_led_4__1, IMM_led_4__2, IMM_led_4__3, IMM_led_5__0, IMM_led_5__1,
       IMM_led_5__2, IMM_led_5__3, IMM_led_6__0, IMM_led_6__1, IMM_led_6__2, IMM_led_6__3, IMM_led_7__0,
       IMM_led_7__1, IMM_led_7__2, IMM_led_7__3, IMM_led_8__0, IMM_led_8__1, IMM_led_8__2, IMM_led_8__3,
       IMM_led_9__0, IMM_led_9__1, IMM_led_9__2, IMM_led_9__3, IMM_led_a__0, IMM_led_a__1, IMM_led_a__2,
       IMM_led_a__3, IMM_led_b__0, IMM_led_b__1, IMM_led_b__2, IMM_led_b__3, IMM_led_c__0, IMM_led_c__1,
       IMM_led_c__2, IMM_led_c__3, IMM_led_d__0, IMM_led_d__1, IMM_led_d__2, IMM_led_d__3, IMM_led_e__0,
       IMM_led_e__1, IMM_led_e__2, IMM_led_e__3, IMM_led_f__0, IMM_led_f__1, IMM_led_f__2, IMM_led_f__3,
       IMM_ledaddr_0, IMM_ledaddr_0_2, IMM_ledaddr_1, IMM_ledaddr_1_2, IMM_ledr, IMM_ledrst, IMM_ledsel,
       IMM_ledsel_0, IMM_ledsel_1, IMM_ledsel_2, IMM_ledsel_3, IMM_ledsel_4, IMM_ledsel_5, IMM_ledsel_6,
       IMM_ledsel_7, IMM_ledsel_8, IMM_ledsel_9, IMM_ledsel_a, IMM_ledsel_b, IMM_ledsel_c, IMM_ledsel_d,
       IMM_ledsel_e, IMM_ledsel_f, IMM_ledw, IR_led_0, IR_led_1, IR_led_2, IR_led_3, IR_ledr, IR_ledrst,
       IR_ledw, IR_out_0, IR_out_1, IR_out_2, IR_out_3, ir_w, irom_r, mar_w, mux2x4_1_ledsel, mux2x4_1_out0,
       mux2x4_1_out1, mux2x4_1_out2, mux2x4_1_out3, muxB, n7segdisplay_bcd_adapter_1_a,
       n7segdisplay_bcd_adapter_1_b, n7segdisplay_bcd_adapter_1_c, n7segdisplay_bcd_adapter_1_d,
       n7segdisplay_bcd_adapter_1_dp, n7segdisplay_bcd_adapter_1_e, n7segdisplay_bcd_adapter_1_f,
       n7segdisplay_bcd_adapter_1_g, n7segdisplay_bcd_adapter_2_a, n7segdisplay_bcd_adapter_2_b,
       n7segdisplay_bcd_adapter_2_c, n7segdisplay_bcd_adapter_2_d, n7segdisplay_bcd_adapter_2_dp,
       n7segdisplay_bcd_adapter_2_e, n7segdisplay_bcd_adapter_2_f, n7segdisplay_bcd_adapter_2_g,
       n7segdisplay_bcd_adapter_3_a, n7segdisplay_bcd_adapter_3_b, n7segdisplay_bcd_adapter_3_c,
       n7segdisplay_bcd_adapter_3_d, n7segdisplay_bcd_adapter_3_dp, n7segdisplay_bcd_adapter_3_e,
       n7segdisplay_bcd_adapter_3_f, n7segdisplay_bcd_adapter_3_g, n7segdisplay_bcd_adapter_4_a,
       n7segdisplay_bcd_adapter_4_b, n7segdisplay_bcd_adapter_4_c, n7segdisplay_bcd_adapter_4_d,
       n7segdisplay_bcd_adapter_4_dp, n7segdisplay_bcd_adapter_4_e, n7segdisplay_bcd_adapter_4_f,
       n7segdisplay_bcd_adapter_4_g, n7segdisplay_bcd_adapter_5_a, n7segdisplay_bcd_adapter_5_b,
       n7segdisplay_bcd_adapter_5_c, n7segdisplay_bcd_adapter_5_d, n7segdisplay_bcd_adapter_5_dp,
       n7segdisplay_bcd_adapter_5_e, n7segdisplay_bcd_adapter_5_f, n7segdisplay_bcd_adapter_5_g,
       n7segdisplay_bcd_adapter_6_a, n7segdisplay_bcd_adapter_6_b, n7segdisplay_bcd_adapter_6_c,
       n7segdisplay_bcd_adapter_6_d, n7segdisplay_bcd_adapter_6_dp, n7segdisplay_bcd_adapter_6_e,
       n7segdisplay_bcd_adapter_6_f, n7segdisplay_bcd_adapter_6_g, n7segdisplay_bcd_adapter_7_a,
       n7segdisplay_bcd_adapter_7_b, n7segdisplay_bcd_adapter_7_c, n7segdisplay_bcd_adapter_7_d,
       n7segdisplay_bcd_adapter_7_dp, n7segdisplay_bcd_adapter_7_e, n7segdisplay_bcd_adapter_7_f,
       n7segdisplay_bcd_adapter_7_g, n7segdisplay_bcd_adapter_8_a, n7segdisplay_bcd_adapter_8_b,
       n7segdisplay_bcd_adapter_8_c, n7segdisplay_bcd_adapter_8_d, n7segdisplay_bcd_adapter_8_dp,
       n7segdisplay_bcd_adapter_8_e, n7segdisplay_bcd_adapter_8_f, n7segdisplay_bcd_adapter_8_g,
       n7segdisplay_bcd_adapter_9_a, n7segdisplay_bcd_adapter_9_b, n7segdisplay_bcd_adapter_9_c,
       n7segdisplay_bcd_adapter_9_d, n7segdisplay_bcd_adapter_9_dp, n7segdisplay_bcd_adapter_9_e,
       n7segdisplay_bcd_adapter_9_f, n7segdisplay_bcd_adapter_9_g, n7segdisplay_bcd_adapter_10_a,
       n7segdisplay_bcd_adapter_10_b, n7segdisplay_bcd_adapter_10_c, n7segdisplay_bcd_adapter_10_d,
       n7segdisplay_bcd_adapter_10_dp, n7segdisplay_bcd_adapter_10_e, n7segdisplay_bcd_adapter_10_f,
       n7segdisplay_bcd_adapter_10_g, n7segdisplay_bcd_adapter_11_a, n7segdisplay_bcd_adapter_11_b,
       n7segdisplay_bcd_adapter_11_c, n7segdisplay_bcd_adapter_11_d, n7segdisplay_bcd_adapter_11_dp,
       n7segdisplay_bcd_adapter_11_e, n7segdisplay_bcd_adapter_11_f, n7segdisplay_bcd_adapter_11_g,
       n7segdisplay_bcd_adapter_12_a, n7segdisplay_bcd_adapter_12_b, n7segdisplay_bcd_adapter_12_c,
       n7segdisplay_bcd_adapter_12_d, n7segdisplay_bcd_adapter_12_dp, n7segdisplay_bcd_adapter_12_e,
       n7segdisplay_bcd_adapter_12_f, n7segdisplay_bcd_adapter_12_g, nrom_rst, nrst, op, OP_led_0__0,
       OP_led_0__1, OP_led_0__2, OP_led_0__3, OP_led_1__0, OP_led_1__1, OP_led_1__2, OP_led_1__3,
       OP_led_2__0, OP_led_2__1, OP_led_2__2, OP_led_2__3, OP_led_3__0, OP_led_3__1, OP_led_3__2,
       OP_led_3__3, OP_led_4__0, OP_led_4__1, OP_led_4__2, OP_led_4__3, OP_led_5__0, OP_led_5__1,
       OP_led_5__2, OP_led_5__3, OP_led_6__0, OP_led_6__1, OP_led_6__2, OP_led_6__3, OP_led_7__0,
       OP_led_7__1, OP_led_7__2, OP_led_7__3, OP_led_8__0, OP_led_8__1, OP_led_8__2, OP_led_8__3,
       OP_led_9__0, OP_led_9__1, OP_led_9__2, OP_led_9__3, OP_led_a__0, OP_led_a__1, OP_led_a__2,
       OP_led_a__3, OP_led_b__0, OP_led_b__1, OP_led_b__2, OP_led_b__3, OP_led_c__0, OP_led_c__1,
       OP_led_c__2, OP_led_c__3, OP_led_d__0, OP_led_d__1, OP_led_d__2, OP_led_d__3, OP_led_e__0,
       OP_led_e__1, OP_led_e__2, OP_led_e__3, OP_led_f__0, OP_led_f__1, OP_led_f__2, OP_led_f__3,
       OP_ledaddr_0, OP_ledaddr_0_2, OP_ledaddr_1, OP_ledaddr_1_2, OP_ledr, OP_ledrst, OP_ledsel,
       OP_ledsel_0, OP_ledsel_1, OP_ledsel_2, OP_ledsel_3, OP_ledsel_4, OP_ledsel_5, OP_ledsel_6,
       OP_ledsel_7, OP_ledsel_8, OP_ledsel_9, OP_ledsel_a, OP_ledsel_b, OP_ledsel_c, OP_ledsel_d,
       OP_ledsel_e, OP_ledsel_f, OP_ledw, PC_led_0, PC_led_1, PC_led_2, PC_led_3, PC_ledr, PC_ledrst,
       PC_ledw, pc_r, pc_w, RAM_led_0__0, RAM_led_0__1, RAM_led_0__2, RAM_led_0__3, RAM_led_1__0,
       RAM_led_1__1, RAM_led_1__2, RAM_led_1__3, RAM_led_2__0, RAM_led_2__1, RAM_led_2__2, RAM_led_2__3,
       RAM_led_3__0, RAM_led_3__1, RAM_led_3__2, RAM_led_3__3, RAM_led_4__0, RAM_led_4__1, RAM_led_4__2,
       RAM_led_4__3, RAM_led_5__0, RAM_led_5__1, RAM_led_5__2, RAM_led_5__3, RAM_led_6__0, RAM_led_6__1,
       RAM_led_6__2, RAM_led_6__3, RAM_led_7__0, RAM_led_7__1, RAM_led_7__2, RAM_led_7__3, RAM_led_8__0,
       RAM_led_8__1, RAM_led_8__2, RAM_led_8__3, RAM_led_9__0, RAM_led_9__1, RAM_led_9__2, RAM_led_9__3,
       RAM_led_a__0, RAM_led_a__1, RAM_led_a__2, RAM_led_a__3, RAM_led_b__0, RAM_led_b__1, RAM_led_b__2,
       RAM_led_b__3, RAM_led_c__0, RAM_led_c__1, RAM_led_c__2, RAM_led_c__3, RAM_led_d__0, RAM_led_d__1,
       RAM_led_d__2, RAM_led_d__3, RAM_led_e__0, RAM_led_e__1, RAM_led_e__2, RAM_led_e__3, RAM_led_f__0,
       RAM_led_f__1, RAM_led_f__2, RAM_led_f__3, RAM_ledaddr_0, RAM_ledaddr_0_2, RAM_ledaddr_1,
       RAM_ledaddr_1_2, RAM_ledr, RAM_ledrst, RAM_ledsel, RAM_ledsel_0, RAM_ledsel_1, RAM_ledsel_2,
       RAM_ledsel_3, RAM_ledsel_4, RAM_ledsel_5, RAM_ledsel_6, RAM_ledsel_7, RAM_ledsel_8, RAM_ledsel_9,
       RAM_ledsel_a, RAM_ledsel_b, RAM_ledsel_c, RAM_ledsel_d, RAM_ledsel_e, RAM_ledsel_f, RAM_ledw,
       RAM_MAR_led_0, RAM_MAR_led_1, RAM_MAR_led_2, RAM_MAR_led_3, RAM_MAR_ledr, RAM_MAR_ledrst,
       RAM_MAR_ledw, RAM_MAR_out_0, RAM_MAR_out_1, RAM_MAR_out_2, RAM_MAR_out_3, RAM_out_0, RAM_out_1,
       RAM_out_2, RAM_out_3, ram_r, ram_w, RES_led_0, RES_led_1, RES_led_2, RES_led_3, RES_ledr, RES_ledrst,
       RES_ledw, res_r, res_w, RESET_out, RESET_ROM_out, resume, rmar_w, ROM_MAR_led_0, ROM_MAR_led_1,
       ROM_MAR_led_2, ROM_MAR_led_3, ROM_MAR_ledr, ROM_MAR_ledrst, ROM_MAR_ledw, ROM_MAR_out_0,
       ROM_MAR_out_1, ROM_MAR_out_2, ROM_MAR_out_3, rom_w, TMP_led_0, TMP_led_1, TMP_led_2, TMP_led_3,
       TMP_ledr, TMP_ledrst, TMP_ledw, TMP_out_0, TMP_out_1, TMP_out_2, TMP_out_3, tmp_w, WRITE_ROM_out,
       zero4_1_zero;
  wire [3:0] romADDR, romDATA, romINSTR;

  Reg4LA RAM_MAR (
    .LED_3(RAM_MAR_led_3), .OUT_3(RAM_MAR_out_3), .IN_3(RAM_out_3), .read(1'b1), .LEDr(RAM_MAR_ledr),
    .write(mar_w), .LEDw(RAM_MAR_ledw), .nrst(nrst), .LEDrst(RAM_MAR_ledrst), .LED_2(RAM_MAR_led_2),
    .OUT_2(RAM_MAR_out_2), .IN_2(RAM_out_2), .LED_1(RAM_MAR_led_1), .OUT_1(RAM_MAR_out_1), .IN_1(RAM_out_1),
    .LED_0(RAM_MAR_led_0), .OUT_0(RAM_MAR_out_0), .IN_0(RAM_out_0));
  Reg4LA TMP (
    .LED_3(TMP_led_3), .OUT_3(TMP_out_3), .IN_3(RAM_out_3), .read(1'b1), .LEDr(TMP_ledr), .write(tmp_w),
    .LEDw(TMP_ledw), .nrst(nrst), .LEDrst(TMP_ledrst), .LED_2(TMP_led_2), .OUT_2(TMP_out_2),
    .IN_2(RAM_out_2), .LED_1(TMP_led_1), .OUT_1(TMP_out_1), .IN_1(RAM_out_1), .LED_0(TMP_led_0),
    .OUT_0(TMP_out_0), .IN_0(RAM_out_0));
  LED led_1 (.in(TMP_ledw));
  LED led_2 (.in(TMP_ledrst));
  LED led_3 (.in(TMP_ledr));
  DEC_Diplay dec_diplay_1 (
    .BIN_0(RAM_MAR_led_0), .BIN_1(RAM_MAR_led_1), .BIN_2(RAM_MAR_led_2), .BIN_3(RAM_MAR_led_3),
    .LED0(dec_diplay_1_led0), .LED1(dec_diplay_1_led1), .LED2(dec_diplay_1_led2), .LED3(dec_diplay_1_led3),
    .BCD1_1(dec_diplay_1_bcd1_1), .BCD1_0(dec_diplay_1_bcd1_0), .BCD1_2(dec_diplay_1_bcd1_2),
    .BCD1_3(dec_diplay_1_bcd1_3), .BCD10_0(dec_diplay_1_bcd10_0), .BCD10_1(dec_diplay_1_bcd10_1),
    .BCD10_2(dec_diplay_1_bcd10_2), .BCD10_3(dec_diplay_1_bcd10_3));
  LED led_4 (.in(dec_diplay_1_led3));
  _7SegDisplay_BCD_Adapter u_7segdisplay_bcd_adapter_1 (
    .BCD_0(dec_diplay_1_bcd10_0), .BCD_1(dec_diplay_1_bcd10_1), .BCD_2(dec_diplay_1_bcd10_2),
    .BCD_3(dec_diplay_1_bcd10_3), .a(n7segdisplay_bcd_adapter_1_a), .b(n7segdisplay_bcd_adapter_1_b),
    .c(n7segdisplay_bcd_adapter_1_c), .d(n7segdisplay_bcd_adapter_1_d), .e(n7segdisplay_bcd_adapter_1_e),
    .f(n7segdisplay_bcd_adapter_1_f), .g(n7segdisplay_bcd_adapter_1_g), .dp(n7segdisplay_bcd_adapter_1_dp));
  LED led_5 (.in(RAM_MAR_ledw));
  _7_Segment_Display u_7_segment_display_1 (
    .g(n7segdisplay_bcd_adapter_1_g), .f(n7segdisplay_bcd_adapter_1_f), .a(n7segdisplay_bcd_adapter_1_a),
    .b(n7segdisplay_bcd_adapter_1_b), .e(n7segdisplay_bcd_adapter_1_e), .d(n7segdisplay_bcd_adapter_1_d),
    .c(n7segdisplay_bcd_adapter_1_c), .dp(n7segdisplay_bcd_adapter_1_dp));
  LED led_6 (.in(RAM_MAR_ledrst));
  LED led_7 (.in(RAM_MAR_ledr));
  SRAM_16x4bit RAM (
    .read(ram_r), .write(ram_w), .nrst(nrst), .LEDsel_0(RAM_ledsel_0), .LED_0__0(RAM_led_0__0),
    .LED_0__1(RAM_led_0__1), .LED_0__2(RAM_led_0__2), .LED_0__3(RAM_led_0__3), .LEDsel_1(RAM_ledsel_1),
    .LED_1__0(RAM_led_1__0), .LED_1__1(RAM_led_1__1), .LED_1__2(RAM_led_1__2), .LED_1__3(RAM_led_1__3),
    .LEDsel_2(RAM_ledsel_2), .LED_2__0(RAM_led_2__0), .LED_2__1(RAM_led_2__1), .LED_2__2(RAM_led_2__2),
    .LED_2__3(RAM_led_2__3), .LEDsel_3(RAM_ledsel_3), .LED_3__0(RAM_led_3__0), .LED_3__1(RAM_led_3__1),
    .LED_3__2(RAM_led_3__2), .LED_3__3(RAM_led_3__3), .LEDsel_4(RAM_ledsel_4), .LED_4__0(RAM_led_4__0),
    .LED_4__1(RAM_led_4__1), .LED_4__2(RAM_led_4__2), .LED_4__3(RAM_led_4__3), .LEDsel_5(RAM_ledsel_5),
    .LED_5__0(RAM_led_5__0), .LED_5__1(RAM_led_5__1), .LED_5__2(RAM_led_5__2), .LED_5__3(RAM_led_5__3),
    .LEDsel_6(RAM_ledsel_6), .LED_6__0(RAM_led_6__0), .LED_6__1(RAM_led_6__1), .LED_6__2(RAM_led_6__2),
    .LED_6__3(RAM_led_6__3), .LEDsel_7(RAM_ledsel_7), .LED_7__0(RAM_led_7__0), .LED_7__1(RAM_led_7__1),
    .LED_7__2(RAM_led_7__2), .LED_7__3(RAM_led_7__3), .LEDr(RAM_ledr), .LEDw(RAM_ledw), .LEDrst(RAM_ledrst),
    .ADDR_3(RAM_MAR_out_3), .ADDR_2(RAM_MAR_out_2), .ADDR_1(RAM_MAR_out_1), .ADDR_0(RAM_MAR_out_0),
    .select(1'b1), .IN_3(RAM_out_3), .IN_2(RAM_out_2), .IN_1(RAM_out_1), .IN_0(RAM_out_0),
    .LEDaddr_1_2(RAM_ledaddr_1_2), .LEDaddr_0_2(RAM_ledaddr_0_2), .LEDaddr_1(RAM_ledaddr_1),
    .LEDaddr_0(RAM_ledaddr_0), .LEDsel(RAM_ledsel), .OUT_3(RAM_out_3), .OUT_2(RAM_out_2), .OUT_1(RAM_out_1),
    .OUT_0(RAM_out_0), .LEDsel_8(RAM_ledsel_8), .LED_8__0(RAM_led_8__0), .LED_8__1(RAM_led_8__1),
    .LED_8__2(RAM_led_8__2), .LED_8__3(RAM_led_8__3), .LEDsel_9(RAM_ledsel_9), .LED_9__0(RAM_led_9__0),
    .LED_9__1(RAM_led_9__1), .LED_9__2(RAM_led_9__2), .LED_9__3(RAM_led_9__3), .LEDsel_A(RAM_ledsel_a),
    .LED_A__0(RAM_led_a__0), .LED_A__1(RAM_led_a__1), .LED_A__2(RAM_led_a__2), .LED_A__3(RAM_led_a__3),
    .LEDsel_B(RAM_ledsel_b), .LED_B__0(RAM_led_b__0), .LED_B__1(RAM_led_b__1), .LED_B__2(RAM_led_b__2),
    .LED_B__3(RAM_led_b__3), .LEDsel_C(RAM_ledsel_c), .LED_C__0(RAM_led_c__0), .LED_C__1(RAM_led_c__1),
    .LED_C__2(RAM_led_c__2), .LED_C__3(RAM_led_c__3), .LEDsel_D(RAM_ledsel_d), .LED_D__0(RAM_led_d__0),
    .LED_D__1(RAM_led_d__1), .LED_D__2(RAM_led_d__2), .LED_D__3(RAM_led_d__3), .LEDsel_E(RAM_ledsel_e),
    .LED_E__0(RAM_led_e__0), .LED_E__1(RAM_led_e__1), .LED_E__2(RAM_led_e__2), .LED_E__3(RAM_led_e__3),
    .LEDsel_F(RAM_ledsel_f), .LED_F__0(RAM_led_f__0), .LED_F__1(RAM_led_f__1), .LED_F__2(RAM_led_f__2),
    .LED_F__3(RAM_led_f__3));
  LED led_8 (.in(RAM_ledaddr_1_2));
  LED led_9 (.in(RAM_ledsel));
  LED led_10 (.in(RAM_ledw));
  LED led_11 (.in(RAM_ledrst));
  LED led_12 (.in(RAM_ledr));
  DEC_Diplay dec_diplay_2 (
    .BIN_0(TMP_led_0), .BIN_1(TMP_led_1), .BIN_2(TMP_led_2), .BIN_3(TMP_led_3), .LED0(dec_diplay_2_led0),
    .LED1(dec_diplay_2_led1), .LED2(dec_diplay_2_led2), .LED3(dec_diplay_2_led3),
    .BCD1_1(dec_diplay_2_bcd1_1), .BCD1_0(dec_diplay_2_bcd1_0), .BCD1_2(dec_diplay_2_bcd1_2),
    .BCD1_3(dec_diplay_2_bcd1_3), .BCD10_0(dec_diplay_2_bcd10_0), .BCD10_1(dec_diplay_2_bcd10_1),
    .BCD10_2(dec_diplay_2_bcd10_2), .BCD10_3(dec_diplay_2_bcd10_3));
  LED led_13 (.in(dec_diplay_2_led3));
  _7SegDisplay_BCD_Adapter u_7segdisplay_bcd_adapter_2 (
    .BCD_0(dec_diplay_2_bcd10_0), .BCD_1(dec_diplay_2_bcd10_1), .BCD_2(dec_diplay_2_bcd10_2),
    .BCD_3(dec_diplay_2_bcd10_3), .a(n7segdisplay_bcd_adapter_2_a), .b(n7segdisplay_bcd_adapter_2_b),
    .c(n7segdisplay_bcd_adapter_2_c), .d(n7segdisplay_bcd_adapter_2_d), .e(n7segdisplay_bcd_adapter_2_e),
    .f(n7segdisplay_bcd_adapter_2_f), .g(n7segdisplay_bcd_adapter_2_g), .dp(n7segdisplay_bcd_adapter_2_dp));
  _7_Segment_Display u_7_segment_display_2 (
    .g(n7segdisplay_bcd_adapter_2_g), .f(n7segdisplay_bcd_adapter_2_f), .a(n7segdisplay_bcd_adapter_2_a),
    .b(n7segdisplay_bcd_adapter_2_b), .e(n7segdisplay_bcd_adapter_2_e), .d(n7segdisplay_bcd_adapter_2_d),
    .c(n7segdisplay_bcd_adapter_2_c), .dp(n7segdisplay_bcd_adapter_2_dp));
  LED led_14 (.in(dec_diplay_1_led0));
  LED led_15 (.in(dec_diplay_1_led1));
  LED led_16 (.in(dec_diplay_1_led2));
  _7SegDisplay_BCD_Adapter u_7segdisplay_bcd_adapter_3 (
    .BCD_0(dec_diplay_1_bcd1_0), .BCD_1(dec_diplay_1_bcd1_1), .BCD_2(dec_diplay_1_bcd1_2),
    .BCD_3(dec_diplay_1_bcd1_3), .a(n7segdisplay_bcd_adapter_3_a), .b(n7segdisplay_bcd_adapter_3_b),
    .c(n7segdisplay_bcd_adapter_3_c), .d(n7segdisplay_bcd_adapter_3_d), .e(n7segdisplay_bcd_adapter_3_e),
    .f(n7segdisplay_bcd_adapter_3_f), .g(n7segdisplay_bcd_adapter_3_g), .dp(n7segdisplay_bcd_adapter_3_dp));
  _7_Segment_Display u_7_segment_display_3 (
    .g(n7segdisplay_bcd_adapter_3_g), .f(n7segdisplay_bcd_adapter_3_f), .a(n7segdisplay_bcd_adapter_3_a),
    .b(n7segdisplay_bcd_adapter_3_b), .e(n7segdisplay_bcd_adapter_3_e), .d(n7segdisplay_bcd_adapter_3_d),
    .c(n7segdisplay_bcd_adapter_3_c), .dp(n7segdisplay_bcd_adapter_3_dp));
  LED led_17 (.in(RAM_ledaddr_1));
  LED led_18 (.in(RAM_ledaddr_0_2));
  LED led_19 (.in(RAM_ledaddr_0));
  LED led_20 (.in(RAM_ledsel_0));
  LED led_21 (.in(RAM_ledsel_1));
  LED led_22 (.in(RAM_ledsel_2));
  LED led_23 (.in(RAM_ledsel_3));
  LED led_24 (.in(RAM_ledsel_4));
  LED led_25 (.in(RAM_ledsel_5));
  LED led_26 (.in(RAM_ledsel_6));
  LED led_27 (.in(RAM_ledsel_7));
  LED led_28 (.in(RAM_ledsel_8));
  LED led_29 (.in(RAM_ledsel_9));
  LED led_30 (.in(RAM_ledsel_a));
  LED led_31 (.in(RAM_ledsel_b));
  LED led_32 (.in(RAM_ledsel_c));
  LED led_33 (.in(RAM_ledsel_d));
  LED led_34 (.in(RAM_ledsel_e));
  LED led_35 (.in(RAM_ledsel_f));
  LED led_36 (.in(dec_diplay_2_led2));
  LED led_37 (.in(dec_diplay_2_led1));
  LED led_38 (.in(dec_diplay_2_led0));
  _7SegDisplay_BCD_Adapter u_7segdisplay_bcd_adapter_4 (
    .BCD_0(dec_diplay_2_bcd1_0), .BCD_1(dec_diplay_2_bcd1_1), .BCD_2(dec_diplay_2_bcd1_2),
    .BCD_3(dec_diplay_2_bcd1_3), .a(n7segdisplay_bcd_adapter_4_a), .b(n7segdisplay_bcd_adapter_4_b),
    .c(n7segdisplay_bcd_adapter_4_c), .d(n7segdisplay_bcd_adapter_4_d), .e(n7segdisplay_bcd_adapter_4_e),
    .f(n7segdisplay_bcd_adapter_4_f), .g(n7segdisplay_bcd_adapter_4_g), .dp(n7segdisplay_bcd_adapter_4_dp));
  _7_Segment_Display u_7_segment_display_4 (
    .g(n7segdisplay_bcd_adapter_4_g), .f(n7segdisplay_bcd_adapter_4_f), .a(n7segdisplay_bcd_adapter_4_a),
    .b(n7segdisplay_bcd_adapter_4_b), .e(n7segdisplay_bcd_adapter_4_e), .d(n7segdisplay_bcd_adapter_4_d),
    .c(n7segdisplay_bcd_adapter_4_c), .dp(n7segdisplay_bcd_adapter_4_dp));
  Reg4LA RES (
    .LED_3(RES_led_3), .OUT_3(RAM_out_3), .IN_3(alu_1_sum_3), .read(res_r), .LEDr(RES_ledr), .write(res_w),
    .LEDw(RES_ledw), .nrst(nrst), .LEDrst(RES_ledrst), .LED_2(RES_led_2), .OUT_2(RAM_out_2),
    .IN_2(alu_1_sum_2), .LED_1(RES_led_1), .OUT_1(RAM_out_1), .IN_1(alu_1_sum_1), .LED_0(RES_led_0),
    .OUT_0(RAM_out_0), .IN_0(alu_1_sum_0));
  DEC_Diplay dec_diplay_3 (
    .BIN_0(RES_led_0), .BIN_1(RES_led_1), .BIN_2(RES_led_2), .BIN_3(RES_led_3), .LED0(dec_diplay_3_led0),
    .LED1(dec_diplay_3_led1), .LED2(dec_diplay_3_led2), .LED3(dec_diplay_3_led3),
    .BCD1_1(dec_diplay_3_bcd1_1), .BCD1_0(dec_diplay_3_bcd1_0), .BCD1_2(dec_diplay_3_bcd1_2),
    .BCD1_3(dec_diplay_3_bcd1_3), .BCD10_0(dec_diplay_3_bcd10_0), .BCD10_1(dec_diplay_3_bcd10_1),
    .BCD10_2(dec_diplay_3_bcd10_2), .BCD10_3(dec_diplay_3_bcd10_3));
  LED led_39 (.in(RES_ledw));
  LED led_40 (.in(RES_ledrst));
  LED led_41 (.in(RES_ledr));
  LED led_42 (.in(RAM_led_0__1));
  LED led_43 (.in(RAM_led_0__3));
  LED led_44 (.in(RAM_led_0__2));
  LED led_45 (.in(RAM_led_1__2));
  LED led_46 (.in(RAM_led_1__1));
  LED led_47 (.in(RAM_led_1__3));
  LED led_48 (.in(RAM_led_2__2));
  LED led_49 (.in(RAM_led_2__1));
  LED led_50 (.in(RAM_led_2__3));
  LED led_51 (.in(RAM_led_3__2));
  LED led_52 (.in(RAM_led_3__1));
  LED led_53 (.in(RAM_led_3__3));
  LED led_54 (.in(RAM_led_4__2));
  LED led_55 (.in(RAM_led_4__1));
  LED led_56 (.in(RAM_led_4__3));
  LED led_57 (.in(RAM_led_5__2));
  LED led_58 (.in(RAM_led_5__3));
  LED led_59 (.in(RAM_led_5__1));
  LED led_60 (.in(RAM_led_6__3));
  LED led_61 (.in(RAM_led_6__2));
  LED led_62 (.in(RAM_led_6__1));
  LED led_63 (.in(RAM_led_7__2));
  LED led_64 (.in(RAM_led_7__3));
  LED led_65 (.in(RAM_led_7__1));
  LED led_66 (.in(RAM_led_8__3));
  LED led_67 (.in(RAM_led_8__2));
  LED led_68 (.in(RAM_led_8__1));
  LED led_69 (.in(RAM_led_9__2));
  LED led_70 (.in(RAM_led_9__1));
  LED led_71 (.in(RAM_led_9__3));
  LED led_72 (.in(RAM_led_a__1));
  LED led_73 (.in(RAM_led_a__3));
  LED led_74 (.in(RAM_led_a__2));
  LED led_75 (.in(RAM_led_b__3));
  LED led_76 (.in(RAM_led_b__1));
  LED led_77 (.in(RAM_led_b__2));
  LED led_78 (.in(RAM_led_c__3));
  LED led_79 (.in(RAM_led_c__2));
  LED led_80 (.in(RAM_led_c__1));
  LED led_81 (.in(RAM_led_d__1));
  LED led_82 (.in(RAM_led_d__2));
  LED led_83 (.in(RAM_led_d__3));
  LED led_84 (.in(RAM_led_e__3));
  LED led_85 (.in(RAM_led_e__2));
  LED led_86 (.in(RAM_led_e__1));
  LED led_87 (.in(RAM_led_f__3));
  LED led_88 (.in(RAM_led_f__1));
  LED led_89 (.in(RAM_led_f__2));
  ALU alu_1 (
    .a_0(TMP_out_0), .a_1(TMP_out_1), .a_2(TMP_out_2), .a_3(TMP_out_3), .b_0(_0_out_0), .b_1(_0_out_1),
    .b_2(_0_out_2), .b_3(_0_out_3), .op(op), .cin(cin), .sum_0(alu_1_sum_0), .sum_1(alu_1_sum_1),
    .sum_2(alu_1_sum_2), .sum_3(alu_1_sum_3), .LEDcin(alu_1_ledcin), .LEDop(alu_1_ledop));
  LED led_90 (.in(alu_1_ledcin));
  LED led_91 (.in(alu_1_ledop));
  LED led_92 (.in(dec_diplay_3_led1));
  LED led_93 (.in(dec_diplay_3_led3));
  LED led_94 (.in(dec_diplay_3_led2));
  _7SegDisplay_BCD_Adapter u_7segdisplay_bcd_adapter_5 (
    .BCD_0(dec_diplay_3_bcd1_0), .BCD_1(dec_diplay_3_bcd1_1), .BCD_2(dec_diplay_3_bcd1_2),
    .BCD_3(dec_diplay_3_bcd1_3), .a(n7segdisplay_bcd_adapter_5_a), .b(n7segdisplay_bcd_adapter_5_b),
    .c(n7segdisplay_bcd_adapter_5_c), .d(n7segdisplay_bcd_adapter_5_d), .e(n7segdisplay_bcd_adapter_5_e),
    .f(n7segdisplay_bcd_adapter_5_f), .g(n7segdisplay_bcd_adapter_5_g), .dp(n7segdisplay_bcd_adapter_5_dp));
  _7SegDisplay_BCD_Adapter u_7segdisplay_bcd_adapter_6 (
    .BCD_0(dec_diplay_3_bcd10_0), .BCD_1(dec_diplay_3_bcd10_1), .BCD_2(dec_diplay_3_bcd10_2),
    .BCD_3(dec_diplay_3_bcd10_3), .a(n7segdisplay_bcd_adapter_6_a), .b(n7segdisplay_bcd_adapter_6_b),
    .c(n7segdisplay_bcd_adapter_6_c), .d(n7segdisplay_bcd_adapter_6_d), .e(n7segdisplay_bcd_adapter_6_e),
    .f(n7segdisplay_bcd_adapter_6_f), .g(n7segdisplay_bcd_adapter_6_g), .dp(n7segdisplay_bcd_adapter_6_dp));
  _7_Segment_Display u_7_segment_display_5 (
    .g(n7segdisplay_bcd_adapter_6_g), .f(n7segdisplay_bcd_adapter_6_f), .a(n7segdisplay_bcd_adapter_6_a),
    .b(n7segdisplay_bcd_adapter_6_b), .e(n7segdisplay_bcd_adapter_6_e), .d(n7segdisplay_bcd_adapter_6_d),
    .c(n7segdisplay_bcd_adapter_6_c), .dp(n7segdisplay_bcd_adapter_6_dp));
  _7_Segment_Display u_7_segment_display_6 (
    .g(n7segdisplay_bcd_adapter_5_g), .f(n7segdisplay_bcd_adapter_5_f), .a(n7segdisplay_bcd_adapter_5_a),
    .b(n7segdisplay_bcd_adapter_5_b), .e(n7segdisplay_bcd_adapter_5_e), .d(n7segdisplay_bcd_adapter_5_d),
    .c(n7segdisplay_bcd_adapter_5_c), .dp(n7segdisplay_bcd_adapter_5_dp));
  LED led_95 (.in(RAM_led_0__0));
  LED led_96 (.in(RAM_led_1__0));
  LED led_97 (.in(RAM_led_2__0));
  LED led_98 (.in(RAM_led_3__0));
  LED led_99 (.in(RAM_led_4__0));
  LED led_100 (.in(RAM_led_5__0));
  LED led_101 (.in(RAM_led_6__0));
  LED led_102 (.in(RAM_led_7__0));
  LED led_103 (.in(RAM_led_8__0));
  LED led_104 (.in(RAM_led_9__0));
  LED led_105 (.in(RAM_led_a__0));
  LED led_106 (.in(RAM_led_b__0));
  LED led_107 (.in(RAM_led_c__0));
  LED led_108 (.in(RAM_led_d__0));
  LED led_109 (.in(RAM_led_e__0));
  LED led_110 (.in(RAM_led_f__0));
  ZeroPass4 _0 (
    .enable(muxB), .LEDen(_0_leden), .IN_3(RAM_out_3), .IN_2(RAM_out_2), .IN_1(RAM_out_1), .IN_0(RAM_out_0),
    .OUT_3(_0_out_3), .OUT_2(_0_out_2), .OUT_1(_0_out_1), .OUT_0(_0_out_0));
  LED led_111 (.in(_0_leden));
  LED led_112 (.in(dec_diplay_3_led0));
  SRAM_16x4bit u_OP (
    .read(irom_r), .write(rom_w), .nrst(nrom_rst), .LEDsel_0(OP_ledsel_0), .LED_0__0(OP_led_0__0),
    .LED_0__1(OP_led_0__1), .LED_0__2(OP_led_0__2), .LED_0__3(OP_led_0__3), .LEDsel_1(OP_ledsel_1),
    .LED_1__0(OP_led_1__0), .LED_1__1(OP_led_1__1), .LED_1__2(OP_led_1__2), .LED_1__3(OP_led_1__3),
    .LEDsel_2(OP_ledsel_2), .LED_2__0(OP_led_2__0), .LED_2__1(OP_led_2__1), .LED_2__2(OP_led_2__2),
    .LED_2__3(OP_led_2__3), .LEDsel_3(OP_ledsel_3), .LED_3__0(OP_led_3__0), .LED_3__1(OP_led_3__1),
    .LED_3__2(OP_led_3__2), .LED_3__3(OP_led_3__3), .LEDsel_4(OP_ledsel_4), .LED_4__0(OP_led_4__0),
    .LED_4__1(OP_led_4__1), .LED_4__2(OP_led_4__2), .LED_4__3(OP_led_4__3), .LEDsel_5(OP_ledsel_5),
    .LED_5__0(OP_led_5__0), .LED_5__1(OP_led_5__1), .LED_5__2(OP_led_5__2), .LED_5__3(OP_led_5__3),
    .LEDsel_6(OP_ledsel_6), .LED_6__0(OP_led_6__0), .LED_6__1(OP_led_6__1), .LED_6__2(OP_led_6__2),
    .LED_6__3(OP_led_6__3), .LEDsel_7(OP_ledsel_7), .LED_7__0(OP_led_7__0), .LED_7__1(OP_led_7__1),
    .LED_7__2(OP_led_7__2), .LED_7__3(OP_led_7__3), .LEDr(OP_ledr), .LEDw(OP_ledw), .LEDrst(OP_ledrst),
    .ADDR_3(mux2x4_1_out3), .ADDR_2(mux2x4_1_out2), .ADDR_1(mux2x4_1_out1), .ADDR_0(mux2x4_1_out0),
    .select(1'b1), .IN_3(romINSTR[3]), .IN_2(romINSTR[2]), .IN_1(romINSTR[1]), .IN_0(romINSTR[0]),
    .LEDaddr_1_2(OP_ledaddr_1_2), .LEDaddr_0_2(OP_ledaddr_0_2), .LEDaddr_1(OP_ledaddr_1),
    .LEDaddr_0(OP_ledaddr_0), .LEDsel(OP_ledsel), .OUT_3(RAM_out_3), .OUT_2(RAM_out_2), .OUT_1(RAM_out_1),
    .OUT_0(RAM_out_0), .LEDsel_8(OP_ledsel_8), .LED_8__0(OP_led_8__0), .LED_8__1(OP_led_8__1),
    .LED_8__2(OP_led_8__2), .LED_8__3(OP_led_8__3), .LEDsel_9(OP_ledsel_9), .LED_9__0(OP_led_9__0),
    .LED_9__1(OP_led_9__1), .LED_9__2(OP_led_9__2), .LED_9__3(OP_led_9__3), .LEDsel_A(OP_ledsel_a),
    .LED_A__0(OP_led_a__0), .LED_A__1(OP_led_a__1), .LED_A__2(OP_led_a__2), .LED_A__3(OP_led_a__3),
    .LEDsel_B(OP_ledsel_b), .LED_B__0(OP_led_b__0), .LED_B__1(OP_led_b__1), .LED_B__2(OP_led_b__2),
    .LED_B__3(OP_led_b__3), .LEDsel_C(OP_ledsel_c), .LED_C__0(OP_led_c__0), .LED_C__1(OP_led_c__1),
    .LED_C__2(OP_led_c__2), .LED_C__3(OP_led_c__3), .LEDsel_D(OP_ledsel_d), .LED_D__0(OP_led_d__0),
    .LED_D__1(OP_led_d__1), .LED_D__2(OP_led_d__2), .LED_D__3(OP_led_d__3), .LEDsel_E(OP_ledsel_e),
    .LED_E__0(OP_led_e__0), .LED_E__1(OP_led_e__1), .LED_E__2(OP_led_e__2), .LED_E__3(OP_led_e__3),
    .LEDsel_F(OP_ledsel_f), .LED_F__0(OP_led_f__0), .LED_F__1(OP_led_f__1), .LED_F__2(OP_led_f__2),
    .LED_F__3(OP_led_f__3));
  LED led_113 (.in(OP_ledaddr_1_2));
  LED led_114 (.in(OP_ledsel));
  LED led_115 (.in(OP_ledw));
  LED led_116 (.in(OP_ledrst));
  LED led_117 (.in(OP_ledr));
  Reg4LA ACC (
    .LED_3(ACC_led_3), .OUT_3(ACC_out_3), .IN_3(RAM_out_3), .read(1'b1), .LEDr(ACC_ledr), .write(acc_w),
    .LEDw(ACC_ledw), .nrst(nrst), .LEDrst(ACC_ledrst), .LED_2(ACC_led_2), .OUT_2(ACC_out_2),
    .IN_2(RAM_out_2), .LED_1(ACC_led_1), .OUT_1(ACC_out_1), .IN_1(RAM_out_1), .LED_0(ACC_led_0),
    .OUT_0(ACC_out_0), .IN_0(RAM_out_0));
  LED led_118 (.in(ACC_ledw));
  LED led_119 (.in(ACC_ledrst));
  LED led_120 (.in(ACC_ledr));
  assign RAM_out_0 = acc_r ? ACC_out_0 : 1'bz;  // Controlled_Buffer controlled_buffer_1
  assign RAM_out_1 = acc_r ? ACC_out_1 : 1'bz;  // Controlled_Buffer controlled_buffer_2
  assign RAM_out_2 = acc_r ? ACC_out_2 : 1'bz;  // Controlled_Buffer controlled_buffer_3
  assign RAM_out_3 = acc_r ? ACC_out_3 : 1'bz;  // Controlled_Buffer controlled_buffer_4
  ControlUnit controlunit_1 (
    .zero(zero4_1_zero), .LEDzero(controlunit_1_ledzero), .LEDinstr0(controlunit_1_ledinstr0),
    .LEDinstr1(controlunit_1_ledinstr1), .LEDinstr2(controlunit_1_ledinstr2),
    .LEDinstr3(controlunit_1_ledinstr3), .clk(clk), .nrst(nrst), .LEDrst(controlunit_1_ledrst),
    .LEDhalt(controlunit_1_ledhalt), .resume(resume), .INSTR_0(IR_out_0), .INSTR_1(IR_out_1),
    .INSTR_2(IR_out_2), .INSTR_3(IR_out_3), .LEDclkr(controlunit_1_ledclkr), .LEDclkw(controlunit_1_ledclkw),
    .LED16(controlunit_1_led16), .LED15(controlunit_1_led15), .LED14(controlunit_1_led14),
    .LED13(controlunit_1_led13), .LED12(controlunit_1_led12), .LED11(controlunit_1_led11),
    .LED10(controlunit_1_led10), .LED9(controlunit_1_led9), .LED8(controlunit_1_led8),
    .LED7(controlunit_1_led7), .LED6(controlunit_1_led6), .LED5(controlunit_1_led5),
    .LED4(controlunit_1_led4), .LED3(controlunit_1_led3), .LED2(controlunit_1_led2),
    .LED1(controlunit_1_led1), .LED0(controlunit_1_led0), .rom_mar_w(rmar_w), .irom_r(irom_r),
    .drom_r(drom_r), .pc_r(pc_r), .pc_w(pc_w), .ir_w(ir_w), .ram_mar_w(mar_w), .ram_r(ram_r), .ram_w(ram_w),
    .acc_r(acc_r), .acc_w(acc_w), .temp_w(tmp_w), .muxB(muxB), .aluop(op), .cin(cin), .res_r(res_r),
    .res_w(res_w), .LEDstep1(controlunit_1_ledstep1), .LEDstep2(controlunit_1_ledstep2),
    .LEDstep3(controlunit_1_ledstep3), .LEDstep4(controlunit_1_ledstep4), .LEDstep5(controlunit_1_ledstep5),
    .LEDstep6(controlunit_1_ledstep6), .LEDstep7(controlunit_1_ledstep7), .LEDclk(controlunit_1_ledclk));
  LED led_121 (.in(controlunit_1_ledhalt));
  LED led_122 (.in(controlunit_1_ledclk));
  LED led_123 (.in(controlunit_1_ledrst));
  LED led_124 (.in(controlunit_1_led16));
  Reg4LA ROM_MAR (
    .LED_3(ROM_MAR_led_3), .OUT_3(ROM_MAR_out_3), .IN_3(RAM_out_3), .read(1'b1), .LEDr(ROM_MAR_ledr),
    .write(rmar_w), .LEDw(ROM_MAR_ledw), .nrst(nrst), .LEDrst(ROM_MAR_ledrst), .LED_2(ROM_MAR_led_2),
    .OUT_2(ROM_MAR_out_2), .IN_2(RAM_out_2), .LED_1(ROM_MAR_led_1), .OUT_1(ROM_MAR_out_1), .IN_1(RAM_out_1),
    .LED_0(ROM_MAR_led_0), .OUT_0(ROM_MAR_out_0), .IN_0(RAM_out_0));
  LED led_125 (.in(OP_ledaddr_0_2));
  LED led_126 (.in(OP_ledaddr_0));
  LED led_127 (.in(OP_ledaddr_1));
  LED led_128 (.in(OP_ledsel_0));
  LED led_129 (.in(OP_ledsel_1));
  LED led_130 (.in(OP_ledsel_2));
  LED led_131 (.in(OP_ledsel_3));
  LED led_132 (.in(OP_ledsel_4));
  LED led_133 (.in(OP_ledsel_5));
  LED led_134 (.in(OP_ledsel_6));
  LED led_135 (.in(OP_ledsel_7));
  LED led_136 (.in(OP_ledsel_8));
  LED led_137 (.in(OP_ledsel_9));
  LED led_138 (.in(OP_ledsel_a));
  LED led_139 (.in(OP_ledsel_b));
  LED led_140 (.in(OP_ledsel_c));
  LED led_141 (.in(OP_ledsel_d));
  LED led_142 (.in(OP_ledsel_e));
  LED led_143 (.in(OP_ledsel_f));
  DEC_Diplay dec_diplay_4 (
    .BIN_0(ACC_led_0), .BIN_1(ACC_led_1), .BIN_2(ACC_led_2), .BIN_3(ACC_led_3), .LED0(dec_diplay_4_led0),
    .LED1(dec_diplay_4_led1), .LED2(dec_diplay_4_led2), .LED3(dec_diplay_4_led3),
    .BCD1_1(dec_diplay_4_bcd1_1), .BCD1_0(dec_diplay_4_bcd1_0), .BCD1_2(dec_diplay_4_bcd1_2),
    .BCD1_3(dec_diplay_4_bcd1_3), .BCD10_0(dec_diplay_4_bcd10_0), .BCD10_1(dec_diplay_4_bcd10_1),
    .BCD10_2(dec_diplay_4_bcd10_2), .BCD10_3(dec_diplay_4_bcd10_3));
  LED led_144 (.in(dec_diplay_4_led3));
  LED led_145 (.in(dec_diplay_4_led2));
  _7SegDisplay_BCD_Adapter u_7segdisplay_bcd_adapter_7 (
    .BCD_0(dec_diplay_4_bcd10_0), .BCD_1(dec_diplay_4_bcd10_1), .BCD_2(dec_diplay_4_bcd10_2),
    .BCD_3(dec_diplay_4_bcd10_3), .a(n7segdisplay_bcd_adapter_7_a), .b(n7segdisplay_bcd_adapter_7_b),
    .c(n7segdisplay_bcd_adapter_7_c), .d(n7segdisplay_bcd_adapter_7_d), .e(n7segdisplay_bcd_adapter_7_e),
    .f(n7segdisplay_bcd_adapter_7_f), .g(n7segdisplay_bcd_adapter_7_g), .dp(n7segdisplay_bcd_adapter_7_dp));
  _7_Segment_Display u_7_segment_display_7 (
    .g(n7segdisplay_bcd_adapter_7_g), .f(n7segdisplay_bcd_adapter_7_f), .a(n7segdisplay_bcd_adapter_7_a),
    .b(n7segdisplay_bcd_adapter_7_b), .e(n7segdisplay_bcd_adapter_7_e), .d(n7segdisplay_bcd_adapter_7_d),
    .c(n7segdisplay_bcd_adapter_7_c), .dp(n7segdisplay_bcd_adapter_7_dp));
  Zero4 zero4_1 (._3(ACC_out_3), ._2(ACC_out_2), ._1(ACC_out_1), ._0(ACC_out_0), .zero(zero4_1_zero));
  LED led_146 (.in(controlunit_1_ledclkr));
  LED led_147 (.in(controlunit_1_ledclkw));
  LED led_148 (.in(controlunit_1_led15));
  DEC_Diplay dec_diplay_5 (
    .BIN_0(ROM_MAR_led_0), .BIN_1(ROM_MAR_led_1), .BIN_2(ROM_MAR_led_2), .BIN_3(ROM_MAR_led_3),
    .LED0(dec_diplay_5_led0), .LED1(dec_diplay_5_led1), .LED2(dec_diplay_5_led2), .LED3(dec_diplay_5_led3),
    .BCD1_1(dec_diplay_5_bcd1_1), .BCD1_0(dec_diplay_5_bcd1_0), .BCD1_2(dec_diplay_5_bcd1_2),
    .BCD1_3(dec_diplay_5_bcd1_3), .BCD10_0(dec_diplay_5_bcd10_0), .BCD10_1(dec_diplay_5_bcd10_1),
    .BCD10_2(dec_diplay_5_bcd10_2), .BCD10_3(dec_diplay_5_bcd10_3));
  _7SegDisplay_BCD_Adapter u_7segdisplay_bcd_adapter_8 (
    .BCD_0(dec_diplay_5_bcd10_0), .BCD_1(dec_diplay_5_bcd10_1), .BCD_2(dec_diplay_5_bcd10_2),
    .BCD_3(dec_diplay_5_bcd10_3), .a(n7segdisplay_bcd_adapter_8_a), .b(n7segdisplay_bcd_adapter_8_b),
    .c(n7segdisplay_bcd_adapter_8_c), .d(n7segdisplay_bcd_adapter_8_d), .e(n7segdisplay_bcd_adapter_8_e),
    .f(n7segdisplay_bcd_adapter_8_f), .g(n7segdisplay_bcd_adapter_8_g), .dp(n7segdisplay_bcd_adapter_8_dp));
  _7_Segment_Display u_7_segment_display_8 (
    .g(n7segdisplay_bcd_adapter_8_g), .f(n7segdisplay_bcd_adapter_8_f), .a(n7segdisplay_bcd_adapter_8_a),
    .b(n7segdisplay_bcd_adapter_8_b), .e(n7segdisplay_bcd_adapter_8_e), .d(n7segdisplay_bcd_adapter_8_d),
    .c(n7segdisplay_bcd_adapter_8_c), .dp(n7segdisplay_bcd_adapter_8_dp));
  LED led_149 (.in(ROM_MAR_ledw));
  LED led_150 (.in(ROM_MAR_ledrst));
  LED led_151 (.in(ROM_MAR_ledr));
  Mux2x4 mux2x4_1 (
    .sel(MANUAL), .a3(ROM_MAR_out_3), .b3(romADDR[3]), .out3(mux2x4_1_out3), .a2(ROM_MAR_out_2),
    .b2(romADDR[2]), .out2(mux2x4_1_out2), .a1(ROM_MAR_out_1), .b1(romADDR[1]), .a0(ROM_MAR_out_0),
    .b0(romADDR[0]), .out1(mux2x4_1_out1), .out0(mux2x4_1_out0), .LEDsel(mux2x4_1_ledsel));
  LED led_152 (.in(OP_led_0__1));
  LED led_153 (.in(OP_led_0__2));
  LED led_154 (.in(OP_led_0__3));
  LED led_155 (.in(OP_led_1__1));
  LED led_156 (.in(OP_led_1__3));
  LED led_157 (.in(OP_led_1__2));
  LED led_158 (.in(OP_led_2__1));
  LED led_159 (.in(OP_led_2__3));
  LED led_160 (.in(OP_led_2__2));
  LED led_161 (.in(OP_led_3__3));
  LED led_162 (.in(OP_led_3__1));
  LED led_163 (.in(OP_led_3__2));
  LED led_164 (.in(OP_led_4__1));
  LED led_165 (.in(OP_led_4__3));
  LED led_166 (.in(OP_led_4__2));
  LED led_167 (.in(OP_led_5__2));
  LED led_168 (.in(OP_led_5__1));
  LED led_169 (.in(OP_led_5__3));
  LED led_170 (.in(OP_led_6__2));
  LED led_171 (.in(OP_led_6__1));
  LED led_172 (.in(OP_led_6__3));
  LED led_173 (.in(OP_led_7__1));
  LED led_174 (.in(OP_led_7__3));
  LED led_175 (.in(OP_led_7__2));
  LED led_176 (.in(OP_led_8__1));
  LED led_177 (.in(OP_led_8__2));
  LED led_178 (.in(OP_led_8__3));
  LED led_179 (.in(OP_led_9__1));
  LED led_180 (.in(OP_led_9__2));
  LED led_181 (.in(OP_led_9__3));
  LED led_182 (.in(OP_led_a__3));
  LED led_183 (.in(OP_led_a__2));
  LED led_184 (.in(OP_led_a__1));
  LED led_185 (.in(OP_led_b__3));
  LED led_186 (.in(OP_led_b__2));
  LED led_187 (.in(OP_led_b__1));
  LED led_188 (.in(OP_led_c__2));
  LED led_189 (.in(OP_led_c__1));
  LED led_190 (.in(OP_led_c__3));
  LED led_191 (.in(OP_led_d__2));
  LED led_192 (.in(OP_led_d__3));
  LED led_193 (.in(OP_led_d__1));
  LED led_194 (.in(OP_led_e__2));
  LED led_195 (.in(OP_led_e__1));
  LED led_196 (.in(OP_led_e__3));
  LED led_197 (.in(OP_led_f__3));
  LED led_198 (.in(OP_led_f__2));
  LED led_199 (.in(OP_led_f__1));
  LED led_200 (.in(dec_diplay_4_led0));
  LED led_201 (.in(dec_diplay_4_led1));
  _7SegDisplay_BCD_Adapter u_7segdisplay_bcd_adapter_9 (
    .BCD_0(dec_diplay_4_bcd1_0), .BCD_1(dec_diplay_4_bcd1_1), .BCD_2(dec_diplay_4_bcd1_2),
    .BCD_3(dec_diplay_4_bcd1_3), .a(n7segdisplay_bcd_adapter_9_a), .b(n7segdisplay_bcd_adapter_9_b),
    .c(n7segdisplay_bcd_adapter_9_c), .d(n7segdisplay_bcd_adapter_9_d), .e(n7segdisplay_bcd_adapter_9_e),
    .f(n7segdisplay_bcd_adapter_9_f), .g(n7segdisplay_bcd_adapter_9_g), .dp(n7segdisplay_bcd_adapter_9_dp));
  _7_Segment_Display u_7_segment_display_9 (
    .g(n7segdisplay_bcd_adapter_9_g), .f(n7segdisplay_bcd_adapter_9_f), .a(n7segdisplay_bcd_adapter_9_a),
    .b(n7segdisplay_bcd_adapter_9_b), .e(n7segdisplay_bcd_adapter_9_e), .d(n7segdisplay_bcd_adapter_9_d),
    .c(n7segdisplay_bcd_adapter_9_c), .dp(n7segdisplay_bcd_adapter_9_dp));
  LED led_202 (.in(controlunit_1_led13));
  LED led_203 (.in(controlunit_1_led14));
  LED led_204 (.in(dec_diplay_5_led0));
  LED led_205 (.in(dec_diplay_5_led2));
  LED led_206 (.in(dec_diplay_5_led1));
  LED led_207 (.in(dec_diplay_5_led3));
  _7SegDisplay_BCD_Adapter u_7segdisplay_bcd_adapter_10 (
    .BCD_0(dec_diplay_5_bcd1_0), .BCD_1(dec_diplay_5_bcd1_1), .BCD_2(dec_diplay_5_bcd1_2),
    .BCD_3(dec_diplay_5_bcd1_3), .a(n7segdisplay_bcd_adapter_10_a), .b(n7segdisplay_bcd_adapter_10_b),
    .c(n7segdisplay_bcd_adapter_10_c), .d(n7segdisplay_bcd_adapter_10_d), .e(n7segdisplay_bcd_adapter_10_e),
    .f(n7segdisplay_bcd_adapter_10_f), .g(n7segdisplay_bcd_adapter_10_g), .dp(n7segdisplay_bcd_adapter_10_dp));
  _7_Segment_Display u_7_segment_display_10 (
    .g(n7segdisplay_bcd_adapter_10_g), .f(n7segdisplay_bcd_adapter_10_f), .a(n7segdisplay_bcd_adapter_10_a),
    .b(n7segdisplay_bcd_adapter_10_b), .e(n7segdisplay_bcd_adapter_10_e), .d(n7segdisplay_bcd_adapter_10_d),
    .c(n7segdisplay_bcd_adapter_10_c), .dp(n7segdisplay_bcd_adapter_10_dp));
  LED led_208 (.in(mux2x4_1_ledsel));
  LED led_209 (.in(OP_led_0__0));
  LED led_210 (.in(OP_led_1__0));
  LED led_211 (.in(OP_led_2__0));
  LED led_212 (.in(OP_led_3__0));
  LED led_213 (.in(OP_led_4__0));
  LED led_214 (.in(OP_led_5__0));
  LED led_215 (.in(OP_led_6__0));
  LED led_216 (.in(OP_led_7__0));
  LED led_217 (.in(OP_led_8__0));
  LED led_218 (.in(OP_led_9__0));
  LED led_219 (.in(OP_led_a__0));
  LED led_220 (.in(OP_led_b__0));
  LED led_221 (.in(OP_led_c__0));
  LED led_222 (.in(OP_led_d__0));
  LED led_223 (.in(OP_led_e__0));
  LED led_224 (.in(OP_led_f__0));
  LED led_225 (.in(controlunit_1_led12));
  SRAM_16x4bit IMM (
    .read(drom_r), .write(rom_w), .nrst(nrom_rst), .LEDsel_0(IMM_ledsel_0), .LED_0__0(IMM_led_0__0),
    .LED_0__1(IMM_led_0__1), .LED_0__2(IMM_led_0__2), .LED_0__3(IMM_led_0__3), .LEDsel_1(IMM_ledsel_1),
    .LED_1__0(IMM_led_1__0), .LED_1__1(IMM_led_1__1), .LED_1__2(IMM_led_1__2), .LED_1__3(IMM_led_1__3),
    .LEDsel_2(IMM_ledsel_2), .LED_2__0(IMM_led_2__0), .LED_2__1(IMM_led_2__1), .LED_2__2(IMM_led_2__2),
    .LED_2__3(IMM_led_2__3), .LEDsel_3(IMM_ledsel_3), .LED_3__0(IMM_led_3__0), .LED_3__1(IMM_led_3__1),
    .LED_3__2(IMM_led_3__2), .LED_3__3(IMM_led_3__3), .LEDsel_4(IMM_ledsel_4), .LED_4__0(IMM_led_4__0),
    .LED_4__1(IMM_led_4__1), .LED_4__2(IMM_led_4__2), .LED_4__3(IMM_led_4__3), .LEDsel_5(IMM_ledsel_5),
    .LED_5__0(IMM_led_5__0), .LED_5__1(IMM_led_5__1), .LED_5__2(IMM_led_5__2), .LED_5__3(IMM_led_5__3),
    .LEDsel_6(IMM_ledsel_6), .LED_6__0(IMM_led_6__0), .LED_6__1(IMM_led_6__1), .LED_6__2(IMM_led_6__2),
    .LED_6__3(IMM_led_6__3), .LEDsel_7(IMM_ledsel_7), .LED_7__0(IMM_led_7__0), .LED_7__1(IMM_led_7__1),
    .LED_7__2(IMM_led_7__2), .LED_7__3(IMM_led_7__3), .LEDr(IMM_ledr), .LEDw(IMM_ledw), .LEDrst(IMM_ledrst),
    .ADDR_3(mux2x4_1_out3), .ADDR_2(mux2x4_1_out2), .ADDR_1(mux2x4_1_out1), .ADDR_0(mux2x4_1_out0),
    .select(1'b1), .IN_3(romDATA[3]), .IN_2(romDATA[2]), .IN_1(romDATA[1]), .IN_0(romDATA[0]),
    .LEDaddr_1_2(IMM_ledaddr_1_2), .LEDaddr_0_2(IMM_ledaddr_0_2), .LEDaddr_1(IMM_ledaddr_1),
    .LEDaddr_0(IMM_ledaddr_0), .LEDsel(IMM_ledsel), .OUT_3(RAM_out_3), .OUT_2(RAM_out_2), .OUT_1(RAM_out_1),
    .OUT_0(RAM_out_0), .LEDsel_8(IMM_ledsel_8), .LED_8__0(IMM_led_8__0), .LED_8__1(IMM_led_8__1),
    .LED_8__2(IMM_led_8__2), .LED_8__3(IMM_led_8__3), .LEDsel_9(IMM_ledsel_9), .LED_9__0(IMM_led_9__0),
    .LED_9__1(IMM_led_9__1), .LED_9__2(IMM_led_9__2), .LED_9__3(IMM_led_9__3), .LEDsel_A(IMM_ledsel_a),
    .LED_A__0(IMM_led_a__0), .LED_A__1(IMM_led_a__1), .LED_A__2(IMM_led_a__2), .LED_A__3(IMM_led_a__3),
    .LEDsel_B(IMM_ledsel_b), .LED_B__0(IMM_led_b__0), .LED_B__1(IMM_led_b__1), .LED_B__2(IMM_led_b__2),
    .LED_B__3(IMM_led_b__3), .LEDsel_C(IMM_ledsel_c), .LED_C__0(IMM_led_c__0), .LED_C__1(IMM_led_c__1),
    .LED_C__2(IMM_led_c__2), .LED_C__3(IMM_led_c__3), .LEDsel_D(IMM_ledsel_d), .LED_D__0(IMM_led_d__0),
    .LED_D__1(IMM_led_d__1), .LED_D__2(IMM_led_d__2), .LED_D__3(IMM_led_d__3), .LEDsel_E(IMM_ledsel_e),
    .LED_E__0(IMM_led_e__0), .LED_E__1(IMM_led_e__1), .LED_E__2(IMM_led_e__2), .LED_E__3(IMM_led_e__3),
    .LEDsel_F(IMM_ledsel_f), .LED_F__0(IMM_led_f__0), .LED_F__1(IMM_led_f__1), .LED_F__2(IMM_led_f__2),
    .LED_F__3(IMM_led_f__3));
  Reg4LA IR (
    .LED_3(IR_led_3), .OUT_3(IR_out_3), .IN_3(RAM_out_3), .read(1'b1), .LEDr(IR_ledr), .write(ir_w),
    .LEDw(IR_ledw), .nrst(nrst), .LEDrst(IR_ledrst), .LED_2(IR_led_2), .OUT_2(IR_out_2), .IN_2(RAM_out_2),
    .LED_1(IR_led_1), .OUT_1(IR_out_1), .IN_1(RAM_out_1), .LED_0(IR_led_0), .OUT_0(IR_out_0), .IN_0(RAM_out_0));
  LED led_226 (.in(controlunit_1_led10));
  LED led_227 (.in(controlunit_1_led11));
  LED led_228 (.in(IMM_ledaddr_1));
  LED led_229 (.in(IMM_ledaddr_0_2));
  LED led_230 (.in(IMM_ledaddr_1_2));
  LED led_231 (.in(IMM_ledsel_0));
  LED led_232 (.in(IMM_ledsel));
  LED led_233 (.in(IMM_ledsel_1));
  LED led_234 (.in(IMM_ledw));
  LED led_235 (.in(IMM_ledrst));
  LED led_236 (.in(IMM_ledsel_2));
  LED led_237 (.in(IMM_ledsel_3));
  LED led_238 (.in(IMM_ledr));
  LED led_239 (.in(IMM_ledsel_4));
  LED led_240 (.in(IMM_ledsel_5));
  LED led_241 (.in(IMM_ledsel_6));
  LED led_242 (.in(IMM_ledsel_7));
  LED led_243 (.in(IMM_ledsel_8));
  LED led_244 (.in(IMM_ledsel_9));
  LED led_245 (.in(IMM_ledsel_a));
  LED led_246 (.in(IMM_ledsel_b));
  LED led_247 (.in(IMM_ledsel_c));
  LED led_248 (.in(IMM_ledsel_d));
  LED led_249 (.in(IMM_ledsel_e));
  LED led_250 (.in(IMM_ledsel_f));
  BIN_Display bin_display_1 (
    .IN_0(IR_led_0), .IN_1(IR_led_1), .IN_2(IR_led_2), .IN_3(IR_led_3), .LED0(bin_display_1_led0),
    .LED1(bin_display_1_led1), .LED2(bin_display_1_led2), .LED3(bin_display_1_led3));
  LED led_251 (.in(IR_ledw));
  LED led_252 (.in(IR_ledrst));
  LED led_253 (.in(IR_ledr));
  LED led_254 (.in(controlunit_1_ledzero));
  LED led_255 (.in(controlunit_1_ledstep3));
  LED led_256 (.in(controlunit_1_ledstep2));
  LED led_257 (.in(controlunit_1_ledstep1));
  LED led_258 (.in(controlunit_1_led9));
  LED led_259 (.in(controlunit_1_led8));
  LED led_260 (.in(IMM_ledaddr_0));
  LED led_261 (.in(IMM_led_0__3));
  LED led_262 (.in(IMM_led_1__3));
  LED led_263 (.in(IMM_led_2__3));
  LED led_264 (.in(IMM_led_3__3));
  LED led_265 (.in(IMM_led_4__3));
  LED led_266 (.in(IMM_led_5__3));
  LED led_267 (.in(IMM_led_6__3));
  LED led_268 (.in(IMM_led_7__3));
  LED led_269 (.in(IMM_led_8__3));
  LED led_270 (.in(IMM_led_9__3));
  LED led_271 (.in(IMM_led_a__3));
  LED led_272 (.in(IMM_led_b__3));
  LED led_273 (.in(IMM_led_c__3));
  LED led_274 (.in(IMM_led_d__3));
  LED led_275 (.in(IMM_led_e__3));
  LED led_276 (.in(IMM_led_f__3));
  LED led_277 (.in(bin_display_1_led3));
  LED led_278 (.in(bin_display_1_led0));
  LED led_279 (.in(bin_display_1_led2));
  LED led_280 (.in(bin_display_1_led1));
  LED led_281 (.in(controlunit_1_ledinstr2));
  LED led_282 (.in(controlunit_1_ledinstr1));
  LED led_283 (.in(controlunit_1_ledinstr3));
  LED led_284 (.in(controlunit_1_ledinstr0));
  LED led_285 (.in(controlunit_1_ledstep5));
  LED led_286 (.in(controlunit_1_ledstep7));
  LED led_287 (.in(controlunit_1_ledstep6));
  LED led_288 (.in(controlunit_1_ledstep4));
  LED led_289 (.in(controlunit_1_led7));
  LED led_290 (.in(IMM_led_0__1));
  LED led_291 (.in(IMM_led_0__2));
  LED led_292 (.in(IMM_led_0__0));
  LED led_293 (.in(IMM_led_1__0));
  LED led_294 (.in(IMM_led_1__1));
  LED led_295 (.in(IMM_led_1__2));
  LED led_296 (.in(IMM_led_2__2));
  LED led_297 (.in(IMM_led_2__0));
  LED led_298 (.in(IMM_led_2__1));
  LED led_299 (.in(IMM_led_3__0));
  LED led_300 (.in(IMM_led_3__2));
  LED led_301 (.in(IMM_led_3__1));
  LED led_302 (.in(IMM_led_4__0));
  LED led_303 (.in(IMM_led_4__1));
  LED led_304 (.in(IMM_led_4__2));
  LED led_305 (.in(IMM_led_5__2));
  LED led_306 (.in(IMM_led_5__0));
  LED led_307 (.in(IMM_led_5__1));
  LED led_308 (.in(IMM_led_6__2));
  LED led_309 (.in(IMM_led_6__0));
  LED led_310 (.in(IMM_led_6__1));
  LED led_311 (.in(IMM_led_7__1));
  LED led_312 (.in(IMM_led_7__2));
  LED led_313 (.in(IMM_led_7__0));
  LED led_314 (.in(IMM_led_8__2));
  LED led_315 (.in(IMM_led_8__1));
  LED led_316 (.in(IMM_led_8__0));
  LED led_317 (.in(IMM_led_9__2));
  LED led_318 (.in(IMM_led_9__1));
  LED led_319 (.in(IMM_led_9__0));
  LED led_320 (.in(IMM_led_a__2));
  LED led_321 (.in(IMM_led_a__0));
  LED led_322 (.in(IMM_led_a__1));
  LED led_323 (.in(IMM_led_b__2));
  LED led_324 (.in(IMM_led_b__0));
  LED led_325 (.in(IMM_led_b__1));
  LED led_326 (.in(IMM_led_c__1));
  LED led_327 (.in(IMM_led_c__2));
  LED led_328 (.in(IMM_led_c__0));
  LED led_329 (.in(IMM_led_d__2));
  LED led_330 (.in(IMM_led_d__0));
  LED led_331 (.in(IMM_led_d__1));
  LED led_332 (.in(IMM_led_e__0));
  LED led_333 (.in(IMM_led_e__2));
  LED led_334 (.in(IMM_led_e__1));
  LED led_335 (.in(IMM_led_f__0));
  LED led_336 (.in(IMM_led_f__1));
  LED led_337 (.in(IMM_led_f__2));
  LED led_338 (.in(controlunit_1_led5));
  LED led_339 (.in(controlunit_1_led6));
  LED led_340 (.in(controlunit_1_led4));
  Reg4LA PC (
    .LED_3(PC_led_3), .OUT_3(RAM_out_3), .IN_3(RAM_out_3), .read(pc_r), .LEDr(PC_ledr), .write(pc_w),
    .LEDw(PC_ledw), .nrst(nrst), .LEDrst(PC_ledrst), .LED_2(PC_led_2), .OUT_2(RAM_out_2), .IN_2(RAM_out_2),
    .LED_1(PC_led_1), .OUT_1(RAM_out_1), .IN_1(RAM_out_1), .LED_0(PC_led_0), .OUT_0(RAM_out_0),
    .IN_0(RAM_out_0));
  LED led_341 (.in(PC_ledw));
  LED led_342 (.in(PC_ledrst));
  LED led_343 (.in(PC_ledr));
  LED led_344 (.in(controlunit_1_led3));
  LED led_345 (.in(controlunit_1_led2));
  DEC_Diplay dec_diplay_6 (
    .BIN_0(PC_led_0), .BIN_1(PC_led_1), .BIN_2(PC_led_2), .BIN_3(PC_led_3), .LED0(dec_diplay_6_led0),
    .LED1(dec_diplay_6_led1), .LED2(dec_diplay_6_led2), .LED3(dec_diplay_6_led3),
    .BCD1_1(dec_diplay_6_bcd1_1), .BCD1_0(dec_diplay_6_bcd1_0), .BCD1_2(dec_diplay_6_bcd1_2),
    .BCD1_3(dec_diplay_6_bcd1_3), .BCD10_0(dec_diplay_6_bcd10_0), .BCD10_1(dec_diplay_6_bcd10_1),
    .BCD10_2(dec_diplay_6_bcd10_2), .BCD10_3(dec_diplay_6_bcd10_3));
  LED led_346 (.in(dec_diplay_6_led2));
  LED led_347 (.in(dec_diplay_6_led3));
  LED led_348 (.in(dec_diplay_6_led1));
  _7SegDisplay_BCD_Adapter u_7segdisplay_bcd_adapter_11 (
    .BCD_0(dec_diplay_6_bcd10_0), .BCD_1(dec_diplay_6_bcd10_1), .BCD_2(dec_diplay_6_bcd10_2),
    .BCD_3(dec_diplay_6_bcd10_3), .a(n7segdisplay_bcd_adapter_11_a), .b(n7segdisplay_bcd_adapter_11_b),
    .c(n7segdisplay_bcd_adapter_11_c), .d(n7segdisplay_bcd_adapter_11_d), .e(n7segdisplay_bcd_adapter_11_e),
    .f(n7segdisplay_bcd_adapter_11_f), .g(n7segdisplay_bcd_adapter_11_g), .dp(n7segdisplay_bcd_adapter_11_dp));
  _7SegDisplay_BCD_Adapter u_7segdisplay_bcd_adapter_12 (
    .BCD_0(dec_diplay_6_bcd1_0), .BCD_1(dec_diplay_6_bcd1_1), .BCD_2(dec_diplay_6_bcd1_2),
    .BCD_3(dec_diplay_6_bcd1_3), .a(n7segdisplay_bcd_adapter_12_a), .b(n7segdisplay_bcd_adapter_12_b),
    .c(n7segdisplay_bcd_adapter_12_c), .d(n7segdisplay_bcd_adapter_12_d), .e(n7segdisplay_bcd_adapter_12_e),
    .f(n7segdisplay_bcd_adapter_12_f), .g(n7segdisplay_bcd_adapter_12_g), .dp(n7segdisplay_bcd_adapter_12_dp));
  _7_Segment_Display u_7_segment_display_11 (
    .g(n7segdisplay_bcd_adapter_11_g), .f(n7segdisplay_bcd_adapter_11_f), .a(n7segdisplay_bcd_adapter_11_a),
    .b(n7segdisplay_bcd_adapter_11_b), .e(n7segdisplay_bcd_adapter_11_e), .d(n7segdisplay_bcd_adapter_11_d),
    .c(n7segdisplay_bcd_adapter_11_c), .dp(n7segdisplay_bcd_adapter_11_dp));
  _7_Segment_Display u_7_segment_display_12 (
    .g(n7segdisplay_bcd_adapter_12_g), .f(n7segdisplay_bcd_adapter_12_f), .a(n7segdisplay_bcd_adapter_12_a),
    .b(n7segdisplay_bcd_adapter_12_b), .e(n7segdisplay_bcd_adapter_12_e), .d(n7segdisplay_bcd_adapter_12_d),
    .c(n7segdisplay_bcd_adapter_12_c), .dp(n7segdisplay_bcd_adapter_12_dp));
  LED led_349 (.in(controlunit_1_led1));
  LED led_350 (.in(controlunit_1_led0));
  LED led_351 (.in(dec_diplay_6_led0));
  Input4 input4_1 (.IN_0(in_4), .IN_1(in_3), .IN_2(in_2), .IN_3(in_1), .OUT(romADDR));
  Input4 input4_2 (.IN_0(in_8), .IN_1(in_7), .IN_2(in_6), .IN_3(in_5), .OUT(romINSTR));
  Button WRITE_ROM (.out(WRITE_ROM_out));
  Clock_part CLOCK (.out(CLOCK_out));
  Button RESET_ROM (.out(RESET_ROM_out));
  Button RESET (.out(RESET_out));
  Button u_RESUME (.out(resume));
  Input4 input4_3 (.IN_0(in_12), .IN_1(in_11), .IN_2(in_10), .IN_3(in_9), .OUT(romDATA));
  and and_1 (rom_w, WRITE_ROM_out, MANUAL);
  and and_2 (clk, ~MANUAL, CLOCK_out);  // AND_Gate
  and and_3 (nrom_rst, ~RESET_ROM_out, ON);  // AND_Gate
  and and_4 (nrst, ~RESET_out, ON);  // AND_Gate

  // Other names for the same wires on the sheet: muxROM = MANUAL

  // Notes on the sheet:
  //   0000 imm  -  add  imm   -  ACC = ACC +  imm
  //   0001 imm  -  add [imm]  -  ACC = ACC + [imm]
  //   0010 imm  -  sub  imm   -  ACC = ACC -  imm
  //   0011 imm  -  sub [imm]  -  ACC = ACC - [imm]
  //   0100 imm  -  mov  imm   -  ACC =  imm
  //   0101 imm  -  ld  [imm]  -  ACC = [imm]
  //   011x imm  -  str [imm]  -  [imm] = ACC
  //   1000 imm  -  bz   imm   -  if ACC == 0: PC =  imm
  //   1001 imm  -  bz  [imm]  -  if ACC == 0: PC = [imm]
  //   1100 imm  -  bnz  imm   -  if ACC != 0: PC =  imm
  //   1101 imm  -  bnz [imm]  -  if ACC != 0: PC = [imm]
  //   1100 imm  -  jmp  imm   -  PC =  imm
  //   1101 imm  -  jmp [imm]  -  PC = [imm]
  //   111x imm  -  halt       -  ignore clock
endmodule

module ControlUnit (
  input  INSTR_0,
  input  INSTR_1,
  input  INSTR_2,
  input  INSTR_3,
  input  zero,
  input  resume,
  input  clk,
  input  nrst,
  output LEDinstr0,
  output LEDinstr1,
  output LEDinstr2,
  output LEDinstr3,
  output LEDzero,
  output LEDstep1,
  output LEDstep2,
  output LEDstep3,
  output LEDstep4,
  output LEDstep5,
  output LEDstep6,
  output LEDstep7,
  output LEDhalt,
  output LEDclkr,
  output LEDclk,
  output LEDclkw,
  output LEDrst,
  output LED16,
  output LED15,
  output LED14,
  output LED13,
  output LED12,
  output LED11,
  output LED10,
  output LED9,
  output LED8,
  output LED7,
  output LED6,
  output LED5,
  output LED4,
  output LED3,
  output LED2,
  output LED1,
  output LED0,
  output rom_mar_w,
  output irom_r,
  output drom_r,
  output pc_r,
  output pc_w,
  output ir_w,
  output ram_mar_w,
  output ram_r,
  output ram_w,
  output acc_r,
  output acc_w,
  output temp_w,
  output muxB,
  output aluop,
  output cin,
  output res_r,
  output res_w
);

  wire and_1_out, and_2_out, and_3_out, and_6_out, and_8_out, and_10_out, and_11_out, and_13_out, and_16_out,
       and_19_out, and_20_out, and_21_out, and_23_out, and_24_out, and_25_out, and_26_out, and_28_out,
       and_29_out, and_31_out, and_32_out, and_36_out, and_37_out, and_39_out, and_40_out, nor_1_out,
       or_1_out, or_2_out, or_3_out, or_4_out, or_5_out, or_6_out, or_7_out;

  ClockLogic clocklogic_1 (
    .clk(clk), .halt(and_1_out), .resume(resume), .nrst(nrst), .clk_out(LEDclk), .halt_out(LEDhalt));
  Stepper7 stepper7_1 (
    .clk(LEDclkr), .nrst(nrst), .step1(LEDstep1), .step2(cin), .step3(LEDstep3), .step4(LEDstep4),
    .step5(LEDstep5), .step6(LEDstep6), .step7(LEDstep7));
  Clock clock_1 (.clk(LEDclk), .nrst(nrst), .clk_r(LEDclkr), .clk_w(LEDclkw));
  and and_1 (and_1_out, and_3_out, nor_1_out);
  and and_2 (and_2_out, INSTR_3, INSTR_2, INSTR_1);
  and and_3 (and_3_out, LEDstep7, and_2_out);
  nor nor_1 (nor_1_out, LEDclkw, LEDclkr);
  and and_4 (LED16, LEDclkw, LEDstep1);
  and and_5 (irom_r, LEDclkr, cin);
  and and_6 (and_6_out, LEDstep6, ~INSTR_0);  // AND_Gate
  or or_1 (or_1_out, LEDstep4, and_6_out);
  and and_7 (drom_r, LEDclkr, or_1_out);
  and and_8 (and_8_out, INSTR_3, ~INSTR_2, ~INSTR_1, zero);  // AND_Gate
  and and_9 (LED13, LEDclkr, LEDstep1);
  and and_10 (and_10_out, INSTR_3, ~INSTR_2, INSTR_1, ~zero);  // AND_Gate
  or or_2 (or_2_out, and_8_out, and_10_out, and_13_out);
  and and_11 (and_11_out, LEDstep6, or_2_out);
  or or_3 (or_3_out, LEDstep3, and_11_out);
  and and_12 (LED12, LEDclkw, or_3_out);
  and and_13 (and_13_out, INSTR_3, INSTR_2, ~INSTR_1);  // AND_Gate
  and and_14 (ir_w, LEDclkw, cin);
  and and_15 (LED10, LEDclkw, LEDstep4);
  and and_16 (and_16_out, LEDstep6, INSTR_0);
  and and_17 (LED9, LEDclkr, and_16_out);
  and and_18 (LED8, LEDclkw, and_20_out);
  and and_19 (and_19_out, ~INSTR_3, INSTR_2, INSTR_1);  // AND_Gate
  and and_20 (and_20_out, LEDstep5, and_19_out);
  and and_21 (and_21_out, LEDstep5, ~INSTR_3);  // AND_Gate
  and and_22 (acc_r, LEDclkr, and_21_out);
  and and_23 (and_23_out, ~INSTR_3, ~INSTR_2);  // AND_Gate
  and and_24 (and_24_out, ~INSTR_3, INSTR_2, ~INSTR_1);  // AND_Gate
  and and_25 (and_25_out, LEDstep7, and_23_out);
  and and_26 (and_26_out, LEDstep6, and_24_out);
  or or_4 (or_4_out, and_25_out, and_26_out);
  and and_27 (acc_w, LEDclkw, or_4_out);
  and and_28 (and_28_out, ~INSTR_3, ~INSTR_2);  // AND_Gate
  and and_29 (and_29_out, LEDstep5, and_28_out);
  or or_5 (or_5_out, LEDstep1, and_29_out);
  and and_30 (LED5, LEDclkw, or_5_out);
  and and_31 (and_31_out, ~INSTR_3, ~INSTR_2);  // AND_Gate
  and and_32 (and_32_out, LEDstep6, and_31_out);
  and and_33 (LED4, LEDclkr, and_32_out);
  and and_34 (aluop, LEDstep6, INSTR_1);
  or or_6 (or_6_out, LEDstep3, and_37_out);
  and and_35 (LED1, LEDclkr, or_6_out);
  and and_36 (and_36_out, ~INSTR_3, ~INSTR_2);  // AND_Gate
  and and_37 (and_37_out, LEDstep7, and_36_out);
  and and_38 (LED0, LEDclkw, or_7_out);
  and and_39 (and_39_out, ~INSTR_3, ~INSTR_2);  // AND_Gate
  and and_40 (and_40_out, LEDstep6, and_39_out);
  or or_7 (or_7_out, cin, and_40_out);

  assign LED2 = cin;
  assign LED3 = aluop;
  assign LED6 = acc_w;
  assign LED7 = acc_r;
  assign LED11 = ir_w;
  assign LED14 = drom_r;
  assign LED15 = irom_r;
  assign LEDinstr0 = INSTR_0;
  assign LEDinstr1 = INSTR_1;
  assign LEDinstr2 = INSTR_2;
  assign LEDinstr3 = INSTR_3;
  assign LEDrst = nrst;
  assign LEDstep2 = cin;
  assign LEDzero = zero;
  assign muxB = LED4;
  assign pc_r = LED13;
  assign pc_w = LED12;
  assign ram_mar_w = LED10;
  assign ram_r = LED9;
  assign ram_w = LED8;
  assign res_r = LED1;
  assign res_w = LED0;
  assign rom_mar_w = LED16;
  assign temp_w = LED5;
endmodule

module Clock (
  input  clk,
  input  nrst,
  output clk_r,
  output clk_w
);

  wire and_1_out, and_2_out, d_flipflop_1_nq, d_flipflop_1_q, d_flipflop_2_nq, d_flipflop_2_q, or_1_out,
       or_2_out;

  and and_1 (and_1_out, clk, d_flipflop_1_nq);
  D_FlipFlop d_flipflop_1 (.clk(and_1_out), .D(1'b1), .nrst(nrst), .Q(d_flipflop_1_q), .nQ(d_flipflop_1_nq));
  and and_2 (and_2_out, clk, d_flipflop_1_q);
  D_FlipFlop d_flipflop_2 (.clk(and_2_out), .D(d_flipflop_2_nq), .nrst(nrst), .Q(d_flipflop_2_q), .nQ(d_flipflop_2_nq));
  or or_1 (or_1_out, and_2_out, d_flipflop_2_q);
  or or_2 (or_2_out, d_flipflop_2_nq, and_2_out);
  buf buffer_1 (clk_r, or_1_out);
  not not_1 (clk_w, or_2_out);
endmodule

module Stepper7 (
  input  clk,
  input  nrst,
  output step1,
  output step2,
  output step3,
  output step4,
  output step5,
  output step6,
  output step7
);

  wire d_latch_1_q, d_latch_2_q, d_latch_3_nq, d_latch_3_q, d_latch_4_q, d_latch_5_nq, d_latch_5_q,
       d_latch_6_q, d_latch_7_nq, d_latch_7_q, d_latch_8_q, d_latch_9_nq, d_latch_9_q, d_latch_10_q,
       d_latch_11_nq, d_latch_11_q, d_latch_12_q, d_latch_13_nq, d_latch_13_q, d_latch_14_q, d_latch_15_nq,
       d_latch_15_q, not_1_out, not_2_out, or_1_out, or_2_out;

  not not_1 (not_1_out, clk);
  or or_1 (or_1_out, d_latch_15_q, not_1_out);
  or or_2 (or_2_out, clk, d_latch_15_q);
  not not_2 (not_2_out, d_latch_15_q);
  D_Latch d_latch_1 (.D(not_2_out), .write(or_2_out), .nrst(nrst), .Q(d_latch_1_q));  // open: nQ
  D_Latch d_latch_2 (.D(d_latch_1_q), .write(or_1_out), .nrst(nrst), .Q(d_latch_2_q));  // open: nQ
  D_Latch d_latch_3 (.D(d_latch_2_q), .write(or_2_out), .nrst(nrst), .Q(d_latch_3_q), .nQ(d_latch_3_nq));
  and and_1 (step1, d_latch_1_q, d_latch_3_nq);
  D_Latch d_latch_4 (.D(d_latch_3_q), .write(or_1_out), .nrst(nrst), .Q(d_latch_4_q));  // open: nQ
  D_Latch d_latch_5 (.D(d_latch_4_q), .write(or_2_out), .nrst(nrst), .Q(d_latch_5_q), .nQ(d_latch_5_nq));
  and and_2 (step2, d_latch_3_q, d_latch_5_nq);
  D_Latch d_latch_6 (.D(d_latch_5_q), .write(or_1_out), .nrst(nrst), .Q(d_latch_6_q));  // open: nQ
  and and_3 (step3, d_latch_5_q, d_latch_7_nq);
  D_Latch d_latch_7 (.D(d_latch_6_q), .write(or_2_out), .nrst(nrst), .Q(d_latch_7_q), .nQ(d_latch_7_nq));
  D_Latch d_latch_8 (.D(d_latch_7_q), .write(or_1_out), .nrst(nrst), .Q(d_latch_8_q));  // open: nQ
  and and_4 (step4, d_latch_7_q, d_latch_9_nq);
  D_Latch d_latch_9 (.D(d_latch_8_q), .write(or_2_out), .nrst(nrst), .Q(d_latch_9_q), .nQ(d_latch_9_nq));
  D_Latch d_latch_10 (.D(d_latch_9_q), .write(or_1_out), .nrst(nrst), .Q(d_latch_10_q));  // open: nQ
  and and_5 (step5, d_latch_9_q, d_latch_11_nq);
  D_Latch d_latch_11 (.D(d_latch_10_q), .write(or_2_out), .nrst(nrst), .Q(d_latch_11_q), .nQ(d_latch_11_nq));
  D_Latch d_latch_12 (.D(d_latch_11_q), .write(or_1_out), .nrst(nrst), .Q(d_latch_12_q));  // open: nQ
  D_Latch d_latch_13 (.D(d_latch_12_q), .write(or_2_out), .nrst(nrst), .Q(d_latch_13_q), .nQ(d_latch_13_nq));
  and and_6 (step6, d_latch_11_q, d_latch_13_nq);
  D_Latch d_latch_14 (.D(d_latch_13_q), .write(or_1_out), .nrst(nrst), .Q(d_latch_14_q));  // open: nQ
  D_Latch d_latch_15 (.D(d_latch_14_q), .write(or_2_out), .nrst(nrst), .Q(d_latch_15_q), .nQ(d_latch_15_nq));
  and and_7 (step7, d_latch_13_q, d_latch_15_nq);
endmodule
