// Logisim project v1.circ as structural Verilog
module Computer (
  input  in_1,
  input  in_2,
  input  in_3,
  input  in_4,
  input  in_5,
  input  in_6,
  input  in_7,
  input  in_8,
  input  in_9,
  input  in_10,
  input  in_11,
  input  in_12,
  input  MANUAL,
  input  ON,
  input  RESUME
);

  wire _0_leden, _0_out_0, _0_out_1, _0_out_2, _0_out_3, ACC_led_0, ACC_led_1, ACC_led_2, ACC_led_3,
       ACC_ledr, ACC_ledrst, ACC_ledw, ACC_out_0, ACC_out_1, ACC_out_2, ACC_out_3, acc_w, alu_1_ledcin,
       alu_1_ledop, alu_1_sum_0, alu_1_sum_1, alu_1_sum_2, alu_1_sum_3, bin_display_1_led0,
       bin_display_1_led1, bin_display_1_led2, bin_display_1_led3, clk, CLOCK_out, controlunit_1_led0,
       controlunit_1_led1, controlunit_1_led2, controlunit_1_led3, controlunit_1_led4, controlunit_1_led5,
       controlunit_1_led6, controlunit_1_led7, controlunit_1_ledclk, controlunit_1_ledexec,
       controlunit_1_ledhalt, controlunit_1_ledifetch, controlunit_1_ledinstr0, controlunit_1_ledinstr1,
       controlunit_1_ledinstr2, controlunit_1_ledinstr3, controlunit_1_ledrst, controlunit_1_ledzero,
       dec_diplay_1_bcd1_0, dec_diplay_1_bcd1_1, dec_diplay_1_bcd1_2, dec_diplay_1_bcd1_3,
       dec_diplay_1_bcd10_0, dec_diplay_1_bcd10_1, dec_diplay_1_bcd10_2, dec_diplay_1_bcd10_3,
       dec_diplay_1_led0, dec_diplay_1_led1, dec_diplay_1_led2, dec_diplay_1_led3, dec_diplay_2_bcd1_0,
       dec_diplay_2_bcd1_1, dec_diplay_2_bcd1_2, dec_diplay_2_bcd1_3, dec_diplay_2_bcd10_0,
       dec_diplay_2_bcd10_1, dec_diplay_2_bcd10_2, dec_diplay_2_bcd10_3, dec_diplay_2_led0,
       dec_diplay_2_led1, dec_diplay_2_led2, dec_diplay_2_led3, dec_diplay_3_bcd1_0, dec_diplay_3_bcd1_1,
       dec_diplay_3_bcd1_2, dec_diplay_3_bcd1_3, dec_diplay_3_bcd10_0, dec_diplay_3_bcd10_1,
       dec_diplay_3_bcd10_2, dec_diplay_3_bcd10_3, dec_diplay_3_led0, dec_diplay_3_led1, dec_diplay_3_led2,
       dec_diplay_3_led3, inc4_1_out0, inc4_1_out1, inc4_1_out2, inc4_1_out3, IR_led_0, IR_led_1, IR_led_2,
       IR_led_3, IR_ledr, IR_ledrst, IR_ledw, IR_out_0, IR_out_1, IR_out_2, IR_out_3, ir_w, mux2x4_1_ledsel,
       mux2x4_1_out0, mux2x4_1_out1, mux2x4_1_out2, mux2x4_1_out3, mux2x4_2_ledsel, mux2x4_2_out0,
       mux2x4_2_out1, mux2x4_2_out2, mux2x4_2_out3, mux2x4_3_ledsel, mux2x4_3_out0, mux2x4_3_out1,
       mux2x4_3_out2, mux2x4_3_out3, mux2x4_4_ledsel, mux2x4_4_out0, mux2x4_4_out1, mux2x4_4_out2,
       mux2x4_4_out3, muxA, muxB, muxPC, n7segdisplay_bcd_adapter_1_a, n7segdisplay_bcd_adapter_1_b,
       n7segdisplay_bcd_adapter_1_c, n7segdisplay_bcd_adapter_1_d, n7segdisplay_bcd_adapter_1_dp,
       n7segdisplay_bcd_adapter_1_e, n7segdisplay_bcd_adapter_1_f, n7segdisplay_bcd_adapter_1_g,
       n7segdisplay_bcd_adapter_2_a, n7segdisplay_bcd_adapter_2_b, n7segdisplay_bcd_adapter_2_c,
       n7segdisplay_bcd_adapter_2_d, n7segdisplay_bcd_adapter_2_dp, n7segdisplay_bcd_adapter_2_e,
       n7segdisplay_bcd_adapter_2_f, n7segdisplay_bcd_adapter_2_g, n7segdisplay_bcd_adapter_3_a,
       n7segdisplay_bcd_adapter_3_b, n7segdisplay_bcd_adapter_3_c, n7segdisplay_bcd_adapter_3_d,
       n7segdisplay_bcd_adapter_3_dp, n7segdisplay_bcd_adapter_3_e, n7segdisplay_bcd_adapter_3_f,
       n7segdisplay_bcd_adapter_3_g, n7segdisplay_bcd_adapter_4_a, n7segdisplay_bcd_adapter_4_b,
       n7segdisplay_bcd_adapter_4_c, n7segdisplay_bcd_adapter_4_d, n7segdisplay_bcd_adapter_4_dp,
       n7segdisplay_bcd_adapter_4_e, n7segdisplay_bcd_adapter_4_f, n7segdisplay_bcd_adapter_4_g,
       n7segdisplay_bcd_adapter_5_a, n7segdisplay_bcd_adapter_5_b, n7segdisplay_bcd_adapter_5_c,
       n7segdisplay_bcd_adapter_5_d, n7segdisplay_bcd_adapter_5_dp, n7segdisplay_bcd_adapter_5_e,
       n7segdisplay_bcd_adapter_5_f, n7segdisplay_bcd_adapter_5_g, n7segdisplay_bcd_adapter_6_a,
       n7segdisplay_bcd_adapter_6_b, n7segdisplay_bcd_adapter_6_c, n7segdisplay_bcd_adapter_6_d,
       n7segdisplay_bcd_adapter_6_dp, n7segdisplay_bcd_adapter_6_e, n7segdisplay_bcd_adapter_6_f,
       n7segdisplay_bcd_adapter_6_g, nrom_rst, nrst, op, pc_w, RAM_led_0__0, RAM_led_0__1, RAM_led_0__2,
       RAM_led_0__3, RAM_led_1__0, RAM_led_1__1, RAM_led_1__2, RAM_led_1__3, RAM_led_2__0, RAM_led_2__1,
       RAM_led_2__2, RAM_led_2__3, RAM_led_3__0, RAM_led_3__1, RAM_led_3__2, RAM_led_3__3, RAM_led_4__0,
       RAM_led_4__1, RAM_led_4__2, RAM_led_4__3, RAM_led_5__0, RAM_led_5__1, RAM_led_5__2, RAM_led_5__3,
       RAM_led_6__0, RAM_led_6__1, RAM_led_6__2, RAM_led_6__3, RAM_led_7__0, RAM_led_7__1, RAM_led_7__2,
       RAM_led_7__3, RAM_led_8__0, RAM_led_8__1, RAM_led_8__2, RAM_led_8__3, RAM_led_9__0, RAM_led_9__1,
       RAM_led_9__2, RAM_led_9__3, RAM_led_a__0, RAM_led_a__1, RAM_led_a__2, RAM_led_a__3, RAM_led_b__0,
       RAM_led_b__1, RAM_led_b__2, RAM_led_b__3, RAM_led_c__0, RAM_led_c__1, RAM_led_c__2, RAM_led_c__3,
       RAM_led_d__0, RAM_led_d__1, RAM_led_d__2, RAM_led_d__3, RAM_led_e__0, RAM_led_e__1, RAM_led_e__2,
       RAM_led_e__3, RAM_led_f__0, RAM_led_f__1, RAM_led_f__2, RAM_led_f__3, RAM_ledaddr_0, RAM_ledaddr_0_2,
       RAM_ledaddr_1, RAM_ledaddr_1_2, RAM_ledr, RAM_ledrst, RAM_ledsel, RAM_ledsel_0, RAM_ledsel_1,
       RAM_ledsel_2, RAM_ledsel_3, RAM_ledsel_4, RAM_ledsel_5, RAM_ledsel_6, RAM_ledsel_7, RAM_ledsel_8,
       RAM_ledsel_9, RAM_ledsel_a, RAM_ledsel_b, RAM_ledsel_c, RAM_ledsel_d, RAM_ledsel_e, RAM_ledsel_f,
       RAM_ledw, RAM_out_0, RAM_out_1, RAM_out_2, RAM_out_3, ram_w, reg4ff_1_led_0, reg4ff_1_led_1,
       reg4ff_1_led_2, reg4ff_1_led_3, reg4ff_1_ledr, reg4ff_1_ledrst, reg4ff_1_ledw, reg4ff_1_out_0,
       reg4ff_1_out_1, reg4ff_1_out_2, reg4ff_1_out_3, reg4ff_2_led_0, reg4ff_2_led_1, reg4ff_2_led_2,
       reg4ff_2_led_3, reg4ff_2_ledr, reg4ff_2_ledrst, reg4ff_2_ledw, reg4ff_2_out_0, reg4ff_2_out_1,
       reg4ff_2_out_2, reg4ff_2_out_3, RESET_out, RESET_ROM_out, rom_w, sram_16x4bit_1_led_0__0,
       sram_16x4bit_1_led_0__1, sram_16x4bit_1_led_0__2, sram_16x4bit_1_led_0__3, sram_16x4bit_1_led_1__0,
       sram_16x4bit_1_led_1__1, sram_16x4bit_1_led_1__2, sram_16x4bit_1_led_1__3, sram_16x4bit_1_led_2__0,
       sram_16x4bit_1_led_2__1, sram_16x4bit_1_led_2__2, sram_16x4bit_1_led_2__3, sram_16x4bit_1_led_3__0,
       sram_16x4bit_1_led_3__1, sram_16x4bit_1_led_3__2, sram_16x4bit_1_led_3__3, sram_16x4bit_1_led_4__0,
       sram_16x4bit_1_led_4__1, sram_16x4bit_1_led_4__2, sram_16x4bit_1_led_4__3, sram_16x4bit_1_led_5__0,
       sram_16x4bit_1_led_5__1, sram_16x4bit_1_led_5__2, sram_16x4bit_1_led_5__3, sram_16x4bit_1_led_6__0,
       sram_16x4bit_1_led_6__1, sram_16x4bit_1_led_6__2, sram_16x4bit_1_led_6__3, sram_16x4bit_1_led_7__0,
       sram_16x4bit_1_led_7__1, sram_16x4bit_1_led_7__2, sram_16x4bit_1_led_7__3, sram_16x4bit_1_led_8__0,
       sram_16x4bit_1_led_8__1, sram_16x4bit_1_led_8__2, sram_16x4bit_1_led_8__3, sram_16x4bit_1_led_9__0,
       sram_16x4bit_1_led_9__1, sram_16x4bit_1_led_9__2, sram_16x4bit_1_led_9__3, sram_16x4bit_1_led_a__0,
       sram_16x4bit_1_led_a__1, sram_16x4bit_1_led_a__2, sram_16x4bit_1_led_a__3, sram_16x4bit_1_led_b__0,
       sram_16x4bit_1_led_b__1, sram_16x4bit_1_led_b__2, sram_16x4bit_1_led_b__3, sram_16x4bit_1_led_c__0,
       sram_16x4bit_1_led_c__1, sram_16x4bit_1_led_c__2, sram_16x4bit_1_led_c__3, sram_16x4bit_1_led_d__0,
       sram_16x4bit_1_led_d__1, sram_16x4bit_1_led_d__2, sram_16x4bit_1_led_d__3, sram_16x4bit_1_led_e__0,
       sram_16x4bit_1_led_e__1, sram_16x4bit_1_led_e__2, sram_16x4bit_1_led_e__3, sram_16x4bit_1_led_f__0,
       sram_16x4bit_1_led_f__1, sram_16x4bit_1_led_f__2, sram_16x4bit_1_led_f__3, sram_16x4bit_1_ledaddr_0,
       sram_16x4bit_1_ledaddr_0_2, sram_16x4bit_1_ledaddr_1, sram_16x4bit_1_ledaddr_1_2, sram_16x4bit_1_ledr,
       sram_16x4bit_1_ledrst, sram_16x4bit_1_ledsel, sram_16x4bit_1_ledsel_0, sram_16x4bit_1_ledsel_1,
       sram_16x4bit_1_ledsel_2, sram_16x4bit_1_ledsel_3, sram_16x4bit_1_ledsel_4, sram_16x4bit_1_ledsel_5,
       sram_16x4bit_1_ledsel_6, sram_16x4bit_1_ledsel_7, sram_16x4bit_1_ledsel_8, sram_16x4bit_1_ledsel_9,
       sram_16x4bit_1_ledsel_a, sram_16x4bit_1_ledsel_b, sram_16x4bit_1_ledsel_c, sram_16x4bit_1_ledsel_d,
       sram_16x4bit_1_ledsel_e, sram_16x4bit_1_ledsel_f, sram_16x4bit_1_ledw, sram_16x4bit_1_out_0,
       sram_16x4bit_1_out_1, sram_16x4bit_1_out_2, sram_16x4bit_1_out_3, sram_16x4bit_2_led_0__0,
       sram_16x4bit_2_led_0__1, sram_16x4bit_2_led_0__2, sram_16x4bit_2_led_0__3, sram_16x4bit_2_led_1__0,
       sram_16x4bit_2_led_1__1, sram_16x4bit_2_led_1__2, sram_16x4bit_2_led_1__3, sram_16x4bit_2_led_2__0,
       sram_16x4bit_2_led_2__1, sram_16x4bit_2_led_2__2, sram_16x4bit_2_led_2__3, sram_16x4bit_2_led_3__0,
       sram_16x4bit_2_led_3__1, sram_16x4bit_2_led_3__2, sram_16x4bit_2_led_3__3, sram_16x4bit_2_led_4__0,
       sram_16x4bit_2_led_4__1, sram_16x4bit_2_led_4__2, sram_16x4bit_2_led_4__3, sram_16x4bit_2_led_5__0,
       sram_16x4bit_2_led_5__1, sram_16x4bit_2_led_5__2, sram_16x4bit_2_led_5__3, sram_16x4bit_2_led_6__0,
       sram_16x4bit_2_led_6__1, sram_16x4bit_2_led_6__2, sram_16x4bit_2_led_6__3, sram_16x4bit_2_led_7__0,
       sram_16x4bit_2_led_7__1, sram_16x4bit_2_led_7__2, sram_16x4bit_2_led_7__3, sram_16x4bit_2_led_8__0,
       sram_16x4bit_2_led_8__1, sram_16x4bit_2_led_8__2, sram_16x4bit_2_led_8__3, sram_16x4bit_2_led_9__0,
       sram_16x4bit_2_led_9__1, sram_16x4bit_2_led_9__2, sram_16x4bit_2_led_9__3, sram_16x4bit_2_led_a__0,
       sram_16x4bit_2_led_a__1, sram_16x4bit_2_led_a__2, sram_16x4bit_2_led_a__3, sram_16x4bit_2_led_b__0,
       sram_16x4bit_2_led_b__1, sram_16x4bit_2_led_b__2, sram_16x4bit_2_led_b__3, sram_16x4bit_2_led_c__0,
       sram_16x4bit_2_led_c__1, sram_16x4bit_2_led_c__2, sram_16x4bit_2_led_c__3, sram_16x4bit_2_led_d__0,
       sram_16x4bit_2_led_d__1, sram_16x4bit_2_led_d__2, sram_16x4bit_2_led_d__3, sram_16x4bit_2_led_e__0,
       sram_16x4bit_2_led_e__1, sram_16x4bit_2_led_e__2, sram_16x4bit_2_led_e__3, sram_16x4bit_2_led_f__0,
       sram_16x4bit_2_led_f__1, sram_16x4bit_2_led_f__2, sram_16x4bit_2_led_f__3, sram_16x4bit_2_ledaddr_0,
       sram_16x4bit_2_ledaddr_0_2, sram_16x4bit_2_ledaddr_1, sram_16x4bit_2_ledaddr_1_2, sram_16x4bit_2_ledr,
       sram_16x4bit_2_ledrst, sram_16x4bit_2_ledsel, sram_16x4bit_2_ledsel_0, sram_16x4bit_2_ledsel_1,
       sram_16x4bit_2_ledsel_2, sram_16x4bit_2_ledsel_3, sram_16x4bit_2_ledsel_4, sram_16x4bit_2_ledsel_5,
       sram_16x4bit_2_ledsel_6, sram_16x4bit_2_ledsel_7, sram_16x4bit_2_ledsel_8, sram_16x4bit_2_ledsel_9,
       sram_16x4bit_2_ledsel_a, sram_16x4bit_2_ledsel_b, sram_16x4bit_2_ledsel_c, sram_16x4bit_2_ledsel_d,
       sram_16x4bit_2_ledsel_e, sram_16x4bit_2_ledsel_f, sram_16x4bit_2_ledw, sram_16x4bit_2_out_0,
       sram_16x4bit_2_out_1, sram_16x4bit_2_out_2, sram_16x4bit_2_out_3, WRITE_ROM_out, zero4_1_zero;
  wire [3:0] romADDR, romIMM, romOPCODE;

  Mux2x4 mux2x4_1 (
    .sel(MANUAL), .a3(reg4ff_2_out_3), .b3(romADDR[3]), .out3(mux2x4_1_out3), .a2(reg4ff_2_out_2),
    .b2(romADDR[2]), .out2(mux2x4_1_out2), .a1(reg4ff_2_out_1), .b1(romADDR[1]), .a0(reg4ff_2_out_0),
    .b0(romADDR[0]), .out1(mux2x4_1_out1), .out0(mux2x4_1_out0), .LEDsel(mux2x4_1_ledsel));
  LED led_1 (.in(mux2x4_1_ledsel));
  SRAM_16x4bit sram_16x4bit_1 (
    .read(1'b1), .write(rom_w), .nrst(nrom_rst), .LEDsel_0(sram_16x4bit_1_ledsel_0),
    .LED_0__0(sram_16x4bit_1_led_0__0), .LED_0__1(sram_16x4bit_1_led_0__1),
    .LED_0__2(sram_16x4bit_1_led_0__2), .LED_0__3(sram_16x4bit_1_led_0__3),
    .LEDsel_1(sram_16x4bit_1_ledsel_1), .LED_1__0(sram_16x4bit_1_led_1__0),
    .LED_1__1(sram_16x4bit_1_led_1__1), .LED_1__2(sram_16x4bit_1_led_1__2),
    .LED_1__3(sram_16x4bit_1_led_1__3), .LEDsel_2(sram_16x4bit_1_ledsel_2),
    .LED_2__0(sram_16x4bit_1_led_2__0), .LED_2__1(sram_16x4bit_1_led_2__1),
    .LED_2__2(sram_16x4bit_1_led_2__2), .LED_2__3(sram_16x4bit_1_led_2__3),
    .LEDsel_3(sram_16x4bit_1_ledsel_3), .LED_3__0(sram_16x4bit_1_led_3__0),
    .LED_3__1(sram_16x4bit_1_led_3__1), .LED_3__2(sram_16x4bit_1_led_3__2),
    .LED_3__3(sram_16x4bit_1_led_3__3), .LEDsel_4(sram_16x4bit_1_ledsel_4),
    .LED_4__0(sram_16x4bit_1_led_4__0), .LED_4__1(sram_16x4bit_1_led_4__1),
    .LED_4__2(sram_16x4bit_1_led_4__2), .LED_4__3(sram_16x4bit_1_led_4__3),
    .LEDsel_5(sram_16x4bit_1_ledsel_5), .LED_5__0(sram_16x4bit_1_led_5__0),
    .LED_5__1(sram_16x4bit_1_led_5__1), .LED_5__2(sram_16x4bit_1_led_5__2),
    .LED_5__3(sram_16x4bit_1_led_5__3), .LEDsel_6(sram_16x4bit_1_ledsel_6),
    .LED_6__0(sram_16x4bit_1_led_6__0), .LED_6__1(sram_16x4bit_1_led_6__1),
    .LED_6__2(sram_16x4bit_1_led_6__2), .LED_6__3(sram_16x4bit_1_led_6__3),
    .LEDsel_7(sram_16x4bit_1_ledsel_7), .LED_7__0(sram_16x4bit_1_led_7__0),
    .LED_7__1(sram_16x4bit_1_led_7__1), .LED_7__2(sram_16x4bit_1_led_7__2),
    .LED_7__3(sram_16x4bit_1_led_7__3), .LEDr(sram_16x4bit_1_ledr), .LEDw(sram_16x4bit_1_ledw),
    .LEDrst(sram_16x4bit_1_ledrst), .ADDR_3(mux2x4_1_out3), .ADDR_2(mux2x4_1_out2), .ADDR_1(mux2x4_1_out1),
    .ADDR_0(mux2x4_1_out0), .select(1'b1), .IN_3(romOPCODE[3]), .IN_2(romOPCODE[2]), .IN_1(romOPCODE[1]),
    .IN_0(romOPCODE[0]), .LEDaddr_1_2(sram_16x4bit_1_ledaddr_1_2), .LEDaddr_0_2(sram_16x4bit_1_ledaddr_0_2),
    .LEDaddr_1(sram_16x4bit_1_ledaddr_1), .LEDaddr_0(sram_16x4bit_1_ledaddr_0),
    .LEDsel(sram_16x4bit_1_ledsel), .OUT_3(sram_16x4bit_1_out_3), .OUT_2(sram_16x4bit_1_out_2),
    .OUT_1(sram_16x4bit_1_out_1), .OUT_0(sram_16x4bit_1_out_0), .LEDsel_8(sram_16x4bit_1_ledsel_8),
    .LED_8__0(sram_16x4bit_1_led_8__0), .LED_8__1(sram_16x4bit_1_led_8__1),
    .LED_8__2(sram_16x4bit_1_led_8__2), .LED_8__3(sram_16x4bit_1_led_8__3),
    .LEDsel_9(sram_16x4bit_1_ledsel_9), .LED_9__0(sram_16x4bit_1_led_9__0),
    .LED_9__1(sram_16x4bit_1_led_9__1), .LED_9__2(sram_16x4bit_1_led_9__2),
    .LED_9__3(sram_16x4bit_1_led_9__3), .LEDsel_A(sram_16x4bit_1_ledsel_a),
    .LED_A__0(sram_16x4bit_1_led_a__0), .LED_A__1(sram_16x4bit_1_led_a__1),
    .LED_A__2(sram_16x4bit_1_led_a__2), .LED_A__3(sram_16x4bit_1_led_a__3),
    .LEDsel_B(sram_16x4bit_1_ledsel_b), .LED_B__0(sram_16x4bit_1_led_b__0),
    .LED_B__1(sram_16x4bit_1_led_b__1), .LED_B__2(sram_16x4bit_1_led_b__2),
    .LED_B__3(sram_16x4bit_1_led_b__3), .LEDsel_C(sram_16x4bit_1_ledsel_c),
    .LED_C__0(sram_16x4bit_1_led_c__0), .LED_C__1(sram_16x4bit_1_led_c__1),
    .LED_C__2(sram_16x4bit_1_led_c__2), .LED_C__3(sram_16x4bit_1_led_c__3),
    .LEDsel_D(sram_16x4bit_1_ledsel_d), .LED_D__0(sram_16x4bit_1_led_d__0),
    .LED_D__1(sram_16x4bit_1_led_d__1), .LED_D__2(sram_16x4bit_1_led_d__2),
    .LED_D__3(sram_16x4bit_1_led_d__3), .LEDsel_E(sram_16x4bit_1_ledsel_e),
    .LED_E__0(sram_16x4bit_1_led_e__0), .LED_E__1(sram_16x4bit_1_led_e__1),
    .LED_E__2(sram_16x4bit_1_led_e__2), .LED_E__3(sram_16x4bit_1_led_e__3),
    .LEDsel_F(sram_16x4bit_1_ledsel_f), .LED_F__0(sram_16x4bit_1_led_f__0),
    .LED_F__1(sram_16x4bit_1_led_f__1), .LED_F__2(sram_16x4bit_1_led_f__2), .LED_F__3(sram_16x4bit_1_led_f__3));
  LED led_2 (.in(sram_16x4bit_1_ledaddr_0_2));
  LED led_3 (.in(sram_16x4bit_1_ledaddr_1_2));
  LED led_4 (.in(sram_16x4bit_1_ledsel));
  LED led_5 (.in(sram_16x4bit_1_ledw));
  LED led_6 (.in(sram_16x4bit_1_ledrst));
  LED led_7 (.in(sram_16x4bit_1_ledr));
  ControlUnit controlunit_1 (
    .INSTR_0(IR_out_0), .LEDinstr0(controlunit_1_ledinstr0), .INSTR_1(IR_out_1),
    .LEDinstr1(controlunit_1_ledinstr1), .INSTR_2(IR_out_2), .LEDinstr2(controlunit_1_ledinstr2),
    .INSTR_3(IR_out_3), .LEDinstr3(controlunit_1_ledinstr3), .zero(zero4_1_zero),
    .LEDzero(controlunit_1_ledzero), .resume(RESUME), .LEDhalt(controlunit_1_ledhalt), .clk(clk),
    .LEDclk(controlunit_1_ledclk), .LEDifetch(controlunit_1_ledifetch), .nrst(nrst),
    .LEDrst(controlunit_1_ledrst), .LED7(controlunit_1_led7), .LED6(controlunit_1_led6),
    .LED5(controlunit_1_led5), .LED4(controlunit_1_led4), .LED3(controlunit_1_led3),
    .LED2(controlunit_1_led2), .LED1(controlunit_1_led1), .LED0(controlunit_1_led0), .ir_w(ir_w),
    .muxPC(muxPC), .pc_w(pc_w), .acc_w(acc_w), .ram_w(ram_w), .op(op), .muxA(muxA), .muxB(muxB),
    .LEDexec(controlunit_1_ledexec));
  LED led_8 (.in(controlunit_1_ledhalt));
  LED led_9 (.in(controlunit_1_ledclk));
  LED led_10 (.in(controlunit_1_ledrst));
  LED led_11 (.in(controlunit_1_led7));
  LED led_12 (.in(sram_16x4bit_1_ledaddr_0));
  LED led_13 (.in(sram_16x4bit_1_ledaddr_1));
  LED led_14 (.in(sram_16x4bit_1_ledsel_0));
  LED led_15 (.in(sram_16x4bit_1_ledsel_1));
  LED led_16 (.in(sram_16x4bit_1_ledsel_2));
  LED led_17 (.in(sram_16x4bit_1_ledsel_3));
  LED led_18 (.in(sram_16x4bit_1_ledsel_4));
  LED led_19 (.in(sram_16x4bit_1_ledsel_5));
  LED led_20 (.in(sram_16x4bit_1_ledsel_6));
  LED led_21 (.in(sram_16x4bit_1_ledsel_7));
  LED led_22 (.in(sram_16x4bit_1_ledsel_8));
  LED led_23 (.in(sram_16x4bit_1_ledsel_9));
  LED led_24 (.in(sram_16x4bit_1_ledsel_a));
  LED led_25 (.in(sram_16x4bit_1_ledsel_b));
  LED led_26 (.in(sram_16x4bit_1_ledsel_c));
  LED led_27 (.in(sram_16x4bit_1_ledsel_d));
  LED led_28 (.in(sram_16x4bit_1_ledsel_e));
  LED led_29 (.in(sram_16x4bit_1_ledsel_f));
  Reg4FF IR (
    .IN_3(sram_16x4bit_1_out_3), .IN_2(sram_16x4bit_1_out_2), .IN_1(sram_16x4bit_1_out_1),
    .IN_0(sram_16x4bit_1_out_0), .read(1'b1), .write(ir_w), .nrst(nrst), .LED_3(IR_led_3), .LED_2(IR_led_2),
    .LED_1(IR_led_1), .LED_0(IR_led_0), .OUT_3(IR_out_3), .OUT_2(IR_out_2), .OUT_1(IR_out_1),
    .OUT_0(IR_out_0), .LEDr(IR_ledr), .LEDw(IR_ledw), .LEDrst(IR_ledrst));
  BIN_Display bin_display_1 (
    .IN_0(IR_led_0), .IN_1(IR_led_1), .IN_2(IR_led_2), .IN_3(IR_led_3), .LED0(bin_display_1_led0),
    .LED1(bin_display_1_led1), .LED2(bin_display_1_led2), .LED3(bin_display_1_led3));
  LED led_30 (.in(IR_ledw));
  LED led_31 (.in(IR_ledrst));
  LED led_32 (.in(IR_ledr));
  LED led_33 (.in(controlunit_1_ledifetch));
  LED led_34 (.in(controlunit_1_ledexec));
  LED led_35 (.in(controlunit_1_led5));
  LED led_36 (.in(controlunit_1_led6));
  Clock CLOCK (.out(CLOCK_out));
  and and_1 (clk, CLOCK_out, ~MANUAL);  // AND_Gate
  LED led_37 (.in(sram_16x4bit_1_led_0__1));
  LED led_38 (.in(sram_16x4bit_1_led_0__3));
  LED led_39 (.in(sram_16x4bit_1_led_0__0));
  LED led_40 (.in(sram_16x4bit_1_led_0__2));
  LED led_41 (.in(sram_16x4bit_1_led_1__3));
  LED led_42 (.in(sram_16x4bit_1_led_1__1));
  LED led_43 (.in(sram_16x4bit_1_led_1__2));
  LED led_44 (.in(sram_16x4bit_1_led_1__0));
  LED led_45 (.in(sram_16x4bit_1_led_2__2));
  LED led_46 (.in(sram_16x4bit_1_led_2__0));
  LED led_47 (.in(sram_16x4bit_1_led_2__3));
  LED led_48 (.in(sram_16x4bit_1_led_2__1));
  LED led_49 (.in(sram_16x4bit_1_led_3__2));
  LED led_50 (.in(sram_16x4bit_1_led_3__0));
  LED led_51 (.in(sram_16x4bit_1_led_3__3));
  LED led_52 (.in(sram_16x4bit_1_led_3__1));
  LED led_53 (.in(sram_16x4bit_1_led_4__1));
  LED led_54 (.in(sram_16x4bit_1_led_4__2));
  LED led_55 (.in(sram_16x4bit_1_led_4__3));
  LED led_56 (.in(sram_16x4bit_1_led_4__0));
  LED led_57 (.in(sram_16x4bit_1_led_5__0));
  LED led_58 (.in(sram_16x4bit_1_led_5__2));
  LED led_59 (.in(sram_16x4bit_1_led_5__1));
  LED led_60 (.in(sram_16x4bit_1_led_5__3));
  LED led_61 (.in(sram_16x4bit_1_led_6__2));
  LED led_62 (.in(sram_16x4bit_1_led_6__1));
  LED led_63 (.in(sram_16x4bit_1_led_6__3));
  LED led_64 (.in(sram_16x4bit_1_led_6__0));
  LED led_65 (.in(sram_16x4bit_1_led_7__1));
  LED led_66 (.in(sram_16x4bit_1_led_7__3));
  LED led_67 (.in(sram_16x4bit_1_led_7__2));
  LED led_68 (.in(sram_16x4bit_1_led_7__0));
  LED led_69 (.in(sram_16x4bit_1_led_8__3));
  LED led_70 (.in(sram_16x4bit_1_led_8__2));
  LED led_71 (.in(sram_16x4bit_1_led_8__1));
  LED led_72 (.in(sram_16x4bit_1_led_8__0));
  LED led_73 (.in(sram_16x4bit_1_led_9__0));
  LED led_74 (.in(sram_16x4bit_1_led_9__3));
  LED led_75 (.in(sram_16x4bit_1_led_9__1));
  LED led_76 (.in(sram_16x4bit_1_led_9__2));
  LED led_77 (.in(sram_16x4bit_1_led_a__1));
  LED led_78 (.in(sram_16x4bit_1_led_a__0));
  LED led_79 (.in(sram_16x4bit_1_led_a__3));
  LED led_80 (.in(sram_16x4bit_1_led_a__2));
  LED led_81 (.in(sram_16x4bit_1_led_b__2));
  LED led_82 (.in(sram_16x4bit_1_led_b__3));
  LED led_83 (.in(sram_16x4bit_1_led_b__1));
  LED led_84 (.in(sram_16x4bit_1_led_b__0));
  LED led_85 (.in(sram_16x4bit_1_led_c__3));
  LED led_86 (.in(sram_16x4bit_1_led_c__0));
  LED led_87 (.in(sram_16x4bit_1_led_c__1));
  LED led_88 (.in(sram_16x4bit_1_led_c__2));
  LED led_89 (.in(sram_16x4bit_1_led_d__2));
  LED led_90 (.in(sram_16x4bit_1_led_d__1));
  LED led_91 (.in(sram_16x4bit_1_led_d__0));
  LED led_92 (.in(sram_16x4bit_1_led_d__3));
  LED led_93 (.in(sram_16x4bit_1_led_e__0));
  LED led_94 (.in(sram_16x4bit_1_led_e__3));
  LED led_95 (.in(sram_16x4bit_1_led_e__2));
  LED led_96 (.in(sram_16x4bit_1_led_e__1));
  LED led_97 (.in(sram_16x4bit_1_led_f__2));
  LED led_98 (.in(sram_16x4bit_1_led_f__3));
  LED led_99 (.in(sram_16x4bit_1_led_f__1));
  LED led_100 (.in(sram_16x4bit_1_led_f__0));
  LED led_101 (.in(bin_display_1_led2));
  LED led_102 (.in(bin_display_1_led1));
  LED led_103 (.in(bin_display_1_led3));
  LED led_104 (.in(bin_display_1_led0));
  LED led_105 (.in(controlunit_1_ledinstr1));
  LED led_106 (.in(controlunit_1_ledinstr0));
  LED led_107 (.in(controlunit_1_ledinstr3));
  LED led_108 (.in(controlunit_1_ledinstr2));
  LED led_109 (.in(controlunit_1_led4));
  Mux2x4 mux2x4_2 (
    .sel(MANUAL), .a3(reg4ff_2_out_3), .b3(romADDR[3]), .out3(mux2x4_2_out3), .a2(reg4ff_2_out_2),
    .b2(romADDR[2]), .out2(mux2x4_2_out2), .a1(reg4ff_2_out_1), .b1(romADDR[1]), .a0(reg4ff_2_out_0),
    .b0(romADDR[0]), .out1(mux2x4_2_out1), .out0(mux2x4_2_out0), .LEDsel(mux2x4_2_ledsel));
  LED led_110 (.in(controlunit_1_led3));
  LED led_111 (.in(controlunit_1_led2));
  LED led_112 (.in(mux2x4_2_ledsel));
  SRAM_16x4bit sram_16x4bit_2 (
    .read(1'b1), .write(rom_w), .nrst(nrom_rst), .LEDsel_0(sram_16x4bit_2_ledsel_0),
    .LED_0__0(sram_16x4bit_2_led_0__0), .LED_0__1(sram_16x4bit_2_led_0__1),
    .LED_0__2(sram_16x4bit_2_led_0__2), .LED_0__3(sram_16x4bit_2_led_0__3),
    .LEDsel_1(sram_16x4bit_2_ledsel_1), .LED_1__0(sram_16x4bit_2_led_1__0),
    .LED_1__1(sram_16x4bit_2_led_1__1), .LED_1__2(sram_16x4bit_2_led_1__2),
    .LED_1__3(sram_16x4bit_2_led_1__3), .LEDsel_2(sram_16x4bit_2_ledsel_2),
    .LED_2__0(sram_16x4bit_2_led_2__0), .LED_2__1(sram_16x4bit_2_led_2__1),
    .LED_2__2(sram_16x4bit_2_led_2__2), .LED_2__3(sram_16x4bit_2_led_2__3),
    .LEDsel_3(sram_16x4bit_2_ledsel_3), .LED_3__0(sram_16x4bit_2_led_3__0),
    .LED_3__1(sram_16x4bit_2_led_3__1), .LED_3__2(sram_16x4bit_2_led_3__2),
    .LED_3__3(sram_16x4bit_2_led_3__3), .LEDsel_4(sram_16x4bit_2_ledsel_4),
    .LED_4__0(sram_16x4bit_2_led_4__0), .LED_4__1(sram_16x4bit_2_led_4__1),
    .LED_4__2(sram_16x4bit_2_led_4__2), .LED_4__3(sram_16x4bit_2_led_4__3),
    .LEDsel_5(sram_16x4bit_2_ledsel_5), .LED_5__0(sram_16x4bit_2_led_5__0),
    .LED_5__1(sram_16x4bit_2_led_5__1), .LED_5__2(sram_16x4bit_2_led_5__2),
    .LED_5__3(sram_16x4bit_2_led_5__3), .LEDsel_6(sram_16x4bit_2_ledsel_6),
    .LED_6__0(sram_16x4bit_2_led_6__0), .LED_6__1(sram_16x4bit_2_led_6__1),
    .LED_6__2(sram_16x4bit_2_led_6__2), .LED_6__3(sram_16x4bit_2_led_6__3),
    .LEDsel_7(sram_16x4bit_2_ledsel_7), .LED_7__0(sram_16x4bit_2_led_7__0),
    .LED_7__1(sram_16x4bit_2_led_7__1), .LED_7__2(sram_16x4bit_2_led_7__2),
    .LED_7__3(sram_16x4bit_2_led_7__3), .LEDr(sram_16x4bit_2_ledr), .LEDw(sram_16x4bit_2_ledw),
    .LEDrst(sram_16x4bit_2_ledrst), .ADDR_3(mux2x4_2_out3), .ADDR_2(mux2x4_2_out2), .ADDR_1(mux2x4_2_out1),
    .ADDR_0(mux2x4_2_out0), .select(1'b1), .IN_3(romIMM[3]), .IN_2(romIMM[2]), .IN_1(romIMM[1]),
    .IN_0(romIMM[0]), .LEDaddr_1_2(sram_16x4bit_2_ledaddr_1_2), .LEDaddr_0_2(sram_16x4bit_2_ledaddr_0_2),
    .LEDaddr_1(sram_16x4bit_2_ledaddr_1), .LEDaddr_0(sram_16x4bit_2_ledaddr_0),
    .LEDsel(sram_16x4bit_2_ledsel), .OUT_3(sram_16x4bit_2_out_3), .OUT_2(sram_16x4bit_2_out_2),
    .OUT_1(sram_16x4bit_2_out_1), .OUT_0(sram_16x4bit_2_out_0), .LEDsel_8(sram_16x4bit_2_ledsel_8),
    .LED_8__0(sram_16x4bit_2_led_8__0), .LED_8__1(sram_16x4bit_2_led_8__1),
    .LED_8__2(sram_16x4bit_2_led_8__2), .LED_8__3(sram_16x4bit_2_led_8__3),
    .LEDsel_9(sram_16x4bit_2_ledsel_9), .LED_9__0(sram_16x4bit_2_led_9__0),
    .LED_9__1(sram_16x4bit_2_led_9__1), .LED_9__2(sram_16x4bit_2_led_9__2),
    .LED_9__3(sram_16x4bit_2_led_9__3), .LEDsel_A(sram_16x4bit_2_ledsel_a),
    .LED_A__0(sram_16x4bit_2_led_a__0), .LED_A__1(sram_16x4bit_2_led_a__1),
    .LED_A__2(sram_16x4bit_2_led_a__2), .LED_A__3(sram_16x4bit_2_led_a__3),
    .LEDsel_B(sram_16x4bit_2_ledsel_b), .LED_B__0(sram_16x4bit_2_led_b__0),
    .LED_B__1(sram_16x4bit_2_led_b__1), .LED_B__2(sram_16x4bit_2_led_b__2),
    .LED_B__3(sram_16x4bit_2_led_b__3), .LEDsel_C(sram_16x4bit_2_ledsel_c),
    .LED_C__0(sram_16x4bit_2_led_c__0), .LED_C__1(sram_16x4bit_2_led_c__1),
    .LED_C__2(sram_16x4bit_2_led_c__2), .LED_C__3(sram_16x4bit_2_led_c__3),
    .LEDsel_D(sram_16x4bit_2_ledsel_d), .LED_D__0(sram_16x4bit_2_led_d__0),
    .LED_D__1(sram_16x4bit_2_led_d__1), .LED_D__2(sram_16x4bit_2_led_d__2),
    .LED_D__3(sram_16x4bit_2_led_d__3), .LEDsel_E(sram_16x4bit_2_ledsel_e),
    .LED_E__0(sram_16x4bit_2_led_e__0), .LED_E__1(sram_16x4bit_2_led_e__1),
    .LED_E__2(sram_16x4bit_2_led_e__2), .LED_E__3(sram_16x4bit_2_led_e__3),
    .LEDsel_F(sram_16x4bit_2_ledsel_f), .LED_F__0(sram_16x4bit_2_led_f__0),
    .LED_F__1(sram_16x4bit_2_led_f__1), .LED_F__2(sram_16x4bit_2_led_f__2), .LED_F__3(sram_16x4bit_2_led_f__3));
  LED led_113 (.in(sram_16x4bit_2_ledaddr_1_2));
  LED led_114 (.in(sram_16x4bit_2_ledaddr_0_2));
  LED led_115 (.in(sram_16x4bit_2_ledsel));
  LED led_116 (.in(sram_16x4bit_2_ledw));
  LED led_117 (.in(sram_16x4bit_2_ledrst));
  LED led_118 (.in(sram_16x4bit_2_ledr));
  LED led_119 (.in(controlunit_1_led1));
  LED led_120 (.in(controlunit_1_led0));
  Button RESET (.out(RESET_out));
  LED led_121 (.in(sram_16x4bit_2_ledaddr_1));
  LED led_122 (.in(sram_16x4bit_2_ledaddr_0));
  LED led_123 (.in(sram_16x4bit_2_ledsel_0));
  LED led_124 (.in(sram_16x4bit_2_ledsel_1));
  LED led_125 (.in(sram_16x4bit_2_ledsel_2));
  LED led_126 (.in(sram_16x4bit_2_ledsel_3));
  LED led_127 (.in(sram_16x4bit_2_ledsel_4));
  LED led_128 (.in(sram_16x4bit_2_ledsel_5));
  LED led_129 (.in(sram_16x4bit_2_ledsel_6));
  LED led_130 (.in(sram_16x4bit_2_ledsel_7));
  LED led_131 (.in(sram_16x4bit_2_ledsel_8));
  LED led_132 (.in(sram_16x4bit_2_ledsel_9));
  LED led_133 (.in(sram_16x4bit_2_ledsel_a));
  LED led_134 (.in(sram_16x4bit_2_ledsel_b));
  LED led_135 (.in(sram_16x4bit_2_ledsel_c));
  LED led_136 (.in(sram_16x4bit_2_ledsel_d));
  LED led_137 (.in(sram_16x4bit_2_ledsel_e));
  LED led_138 (.in(sram_16x4bit_2_ledsel_f));
  Reg4FF reg4ff_1 (
    .IN_3(sram_16x4bit_2_out_3), .IN_2(sram_16x4bit_2_out_2), .IN_1(sram_16x4bit_2_out_1),
    .IN_0(sram_16x4bit_2_out_0), .read(1'b1), .write(ir_w), .nrst(nrst), .LED_3(reg4ff_1_led_3),
    .LED_2(reg4ff_1_led_2), .LED_1(reg4ff_1_led_1), .LED_0(reg4ff_1_led_0), .OUT_3(reg4ff_1_out_3),
    .OUT_2(reg4ff_1_out_2), .OUT_1(reg4ff_1_out_1), .OUT_0(reg4ff_1_out_0), .LEDr(reg4ff_1_ledr),
    .LEDw(reg4ff_1_ledw), .LEDrst(reg4ff_1_ledrst));
  DEC_Diplay dec_diplay_1 (
    .BIN_0(reg4ff_1_led_0), .BIN_1(reg4ff_1_led_1), .BIN_2(reg4ff_1_led_2), .BIN_3(reg4ff_1_led_3),
    .LED0(dec_diplay_1_led0), .LED1(dec_diplay_1_led1), .LED2(dec_diplay_1_led2), .LED3(dec_diplay_1_led3),
    .BCD1_1(dec_diplay_1_bcd1_1), .BCD1_0(dec_diplay_1_bcd1_0), .BCD1_2(dec_diplay_1_bcd1_2),
    .BCD1_3(dec_diplay_1_bcd1_3), .BCD10_0(dec_diplay_1_bcd10_0), .BCD10_1(dec_diplay_1_bcd10_1),
    .BCD10_2(dec_diplay_1_bcd10_2), .BCD10_3(dec_diplay_1_bcd10_3));
  _7SegDisplay_BCD_Adapter u_7segdisplay_bcd_adapter_1 (
    .BCD_0(dec_diplay_1_bcd10_0), .BCD_1(dec_diplay_1_bcd10_1), .BCD_2(dec_diplay_1_bcd10_2),
    .BCD_3(dec_diplay_1_bcd10_3), .a(n7segdisplay_bcd_adapter_1_a), .b(n7segdisplay_bcd_adapter_1_b),
    .c(n7segdisplay_bcd_adapter_1_c), .d(n7segdisplay_bcd_adapter_1_d), .e(n7segdisplay_bcd_adapter_1_e),
    .f(n7segdisplay_bcd_adapter_1_f), .g(n7segdisplay_bcd_adapter_1_g), .dp(n7segdisplay_bcd_adapter_1_dp));
  LED led_139 (.in(reg4ff_1_ledw));
  LED led_140 (.in(reg4ff_1_ledrst));
  LED led_141 (.in(reg4ff_1_ledr));
  LED led_142 (.in(controlunit_1_ledzero));
  and and_2 (nrst, ~RESET_out, ON);  // AND_Gate
  LED led_143 (.in(sram_16x4bit_2_led_0__3));
  LED led_144 (.in(sram_16x4bit_2_led_0__1));
  LED led_145 (.in(sram_16x4bit_2_led_0__2));
  LED led_146 (.in(sram_16x4bit_2_led_0__0));
  LED led_147 (.in(sram_16x4bit_2_led_1__1));
  LED led_148 (.in(sram_16x4bit_2_led_1__3));
  LED led_149 (.in(sram_16x4bit_2_led_1__2));
  LED led_150 (.in(sram_16x4bit_2_led_1__0));
  LED led_151 (.in(sram_16x4bit_2_led_2__3));
  LED led_152 (.in(sram_16x4bit_2_led_2__1));
  LED led_153 (.in(sram_16x4bit_2_led_2__0));
  LED led_154 (.in(sram_16x4bit_2_led_2__2));
  LED led_155 (.in(sram_16x4bit_2_led_3__0));
  LED led_156 (.in(sram_16x4bit_2_led_3__3));
  LED led_157 (.in(sram_16x4bit_2_led_3__1));
  LED led_158 (.in(sram_16x4bit_2_led_3__2));
  LED led_159 (.in(sram_16x4bit_2_led_4__1));
  LED led_160 (.in(sram_16x4bit_2_led_4__0));
  LED led_161 (.in(sram_16x4bit_2_led_4__2));
  LED led_162 (.in(sram_16x4bit_2_led_4__3));
  LED led_163 (.in(sram_16x4bit_2_led_5__2));
  LED led_164 (.in(sram_16x4bit_2_led_5__0));
  LED led_165 (.in(sram_16x4bit_2_led_5__1));
  LED led_166 (.in(sram_16x4bit_2_led_5__3));
  LED led_167 (.in(sram_16x4bit_2_led_6__1));
  LED led_168 (.in(sram_16x4bit_2_led_6__3));
  LED led_169 (.in(sram_16x4bit_2_led_6__0));
  LED led_170 (.in(sram_16x4bit_2_led_6__2));
  LED led_171 (.in(sram_16x4bit_2_led_7__0));
  LED led_172 (.in(sram_16x4bit_2_led_7__2));
  LED led_173 (.in(sram_16x4bit_2_led_7__3));
  LED led_174 (.in(sram_16x4bit_2_led_7__1));
  LED led_175 (.in(sram_16x4bit_2_led_8__2));
  LED led_176 (.in(sram_16x4bit_2_led_8__3));
  LED led_177 (.in(sram_16x4bit_2_led_8__0));
  LED led_178 (.in(sram_16x4bit_2_led_8__1));
  LED led_179 (.in(sram_16x4bit_2_led_9__2));
  LED led_180 (.in(sram_16x4bit_2_led_9__3));
  LED led_181 (.in(sram_16x4bit_2_led_9__1));
  LED led_182 (.in(sram_16x4bit_2_led_9__0));
  LED led_183 (.in(sram_16x4bit_2_led_a__3));
  LED led_184 (.in(sram_16x4bit_2_led_a__1));
  LED led_185 (.in(sram_16x4bit_2_led_a__2));
  LED led_186 (.in(sram_16x4bit_2_led_a__0));
  LED led_187 (.in(sram_16x4bit_2_led_b__3));
  LED led_188 (.in(sram_16x4bit_2_led_b__1));
  LED led_189 (.in(sram_16x4bit_2_led_b__2));
  LED led_190 (.in(sram_16x4bit_2_led_b__0));
  LED led_191 (.in(sram_16x4bit_2_led_c__0));
  LED led_192 (.in(sram_16x4bit_2_led_c__3));
  LED led_193 (.in(sram_16x4bit_2_led_c__2));
  LED led_194 (.in(sram_16x4bit_2_led_c__1));
  LED led_195 (.in(sram_16x4bit_2_led_d__0));
  LED led_196 (.in(sram_16x4bit_2_led_d__3));
  LED led_197 (.in(sram_16x4bit_2_led_d__2));
  LED led_198 (.in(sram_16x4bit_2_led_d__1));
  LED led_199 (.in(sram_16x4bit_2_led_e__1));
  LED led_200 (.in(sram_16x4bit_2_led_e__3));
  LED led_201 (.in(sram_16x4bit_2_led_e__2));
  LED led_202 (.in(sram_16x4bit_2_led_e__0));
  LED led_203 (.in(sram_16x4bit_2_led_f__3));
  LED led_204 (.in(sram_16x4bit_2_led_f__2));
  LED led_205 (.in(sram_16x4bit_2_led_f__0));
  LED led_206 (.in(sram_16x4bit_2_led_f__1));
  LED led_207 (.in(dec_diplay_1_led2));
  LED led_208 (.in(dec_diplay_1_led3));
  LED led_209 (.in(dec_diplay_1_led0));
  LED led_210 (.in(dec_diplay_1_led1));
  _7SegDisplay_BCD_Adapter u_7segdisplay_bcd_adapter_2 (
    .BCD_0(dec_diplay_1_bcd1_0), .BCD_1(dec_diplay_1_bcd1_1), .BCD_2(dec_diplay_1_bcd1_2),
    .BCD_3(dec_diplay_1_bcd1_3), .a(n7segdisplay_bcd_adapter_2_a), .b(n7segdisplay_bcd_adapter_2_b),
    .c(n7segdisplay_bcd_adapter_2_c), .d(n7segdisplay_bcd_adapter_2_d), .e(n7segdisplay_bcd_adapter_2_e),
    .f(n7segdisplay_bcd_adapter_2_f), .g(n7segdisplay_bcd_adapter_2_g), .dp(n7segdisplay_bcd_adapter_2_dp));
  _7_Segment_Display u_7_segment_display_1 (
    .g(n7segdisplay_bcd_adapter_1_g), .f(n7segdisplay_bcd_adapter_1_f), .a(n7segdisplay_bcd_adapter_1_a),
    .b(n7segdisplay_bcd_adapter_1_b), .e(n7segdisplay_bcd_adapter_1_e), .d(n7segdisplay_bcd_adapter_1_d),
    .c(n7segdisplay_bcd_adapter_1_c), .dp(n7segdisplay_bcd_adapter_1_dp));
  _7_Segment_Display u_7_segment_display_2 (
    .g(n7segdisplay_bcd_adapter_2_g), .f(n7segdisplay_bcd_adapter_2_f), .a(n7segdisplay_bcd_adapter_2_a),
    .b(n7segdisplay_bcd_adapter_2_b), .e(n7segdisplay_bcd_adapter_2_e), .d(n7segdisplay_bcd_adapter_2_d),
    .c(n7segdisplay_bcd_adapter_2_c), .dp(n7segdisplay_bcd_adapter_2_dp));
  Inc4 inc4_1 (
    .cin(1'b1), .in0(reg4ff_2_out_0), .in1(reg4ff_2_out_1), .in2(reg4ff_2_out_2), .in3(reg4ff_2_out_3),
    .out0(inc4_1_out0), .out1(inc4_1_out1), .out2(inc4_1_out2), .out3(inc4_1_out3));  // open: cout
  Mux2x4 mux2x4_3 (
    .sel(muxPC), .a3(inc4_1_out3), .b3(mux2x4_4_out3), .out3(mux2x4_3_out3), .a2(inc4_1_out2),
    .b2(mux2x4_4_out2), .out2(mux2x4_3_out2), .a1(inc4_1_out1), .b1(mux2x4_4_out1), .a0(inc4_1_out0),
    .b0(mux2x4_4_out0), .out1(mux2x4_3_out1), .out0(mux2x4_3_out0), .LEDsel(mux2x4_3_ledsel));
  LED led_211 (.in(mux2x4_3_ledsel));
  Reg4FF reg4ff_2 (
    .IN_3(mux2x4_3_out3), .IN_2(mux2x4_3_out2), .IN_1(mux2x4_3_out1), .IN_0(mux2x4_3_out0), .read(1'b1),
    .write(pc_w), .nrst(nrst), .LED_3(reg4ff_2_led_3), .LED_2(reg4ff_2_led_2), .LED_1(reg4ff_2_led_1),
    .LED_0(reg4ff_2_led_0), .OUT_3(reg4ff_2_out_3), .OUT_2(reg4ff_2_out_2), .OUT_1(reg4ff_2_out_1),
    .OUT_0(reg4ff_2_out_0), .LEDr(reg4ff_2_ledr), .LEDw(reg4ff_2_ledw), .LEDrst(reg4ff_2_ledrst));
  DEC_Diplay dec_diplay_2 (
    .BIN_0(reg4ff_2_led_0), .BIN_1(reg4ff_2_led_1), .BIN_2(reg4ff_2_led_2), .BIN_3(reg4ff_2_led_3),
    .LED0(dec_diplay_2_led0), .LED1(dec_diplay_2_led1), .LED2(dec_diplay_2_led2), .LED3(dec_diplay_2_led3),
    .BCD1_1(dec_diplay_2_bcd1_1), .BCD1_0(dec_diplay_2_bcd1_0), .BCD1_2(dec_diplay_2_bcd1_2),
    .BCD1_3(dec_diplay_2_bcd1_3), .BCD10_0(dec_diplay_2_bcd10_0), .BCD10_1(dec_diplay_2_bcd10_1),
    .BCD10_2(dec_diplay_2_bcd10_2), .BCD10_3(dec_diplay_2_bcd10_3));
  _7SegDisplay_BCD_Adapter u_7segdisplay_bcd_adapter_3 (
    .BCD_0(dec_diplay_2_bcd10_0), .BCD_1(dec_diplay_2_bcd10_1), .BCD_2(dec_diplay_2_bcd10_2),
    .BCD_3(dec_diplay_2_bcd10_3), .a(n7segdisplay_bcd_adapter_3_a), .b(n7segdisplay_bcd_adapter_3_b),
    .c(n7segdisplay_bcd_adapter_3_c), .d(n7segdisplay_bcd_adapter_3_d), .e(n7segdisplay_bcd_adapter_3_e),
    .f(n7segdisplay_bcd_adapter_3_f), .g(n7segdisplay_bcd_adapter_3_g), .dp(n7segdisplay_bcd_adapter_3_dp));
  LED led_212 (.in(reg4ff_2_ledw));
  LED led_213 (.in(reg4ff_2_ledrst));
  LED led_214 (.in(reg4ff_2_ledr));
  Input4 input4_1 (.IN_0(in_4), .IN_1(in_3), .IN_2(in_2), .IN_3(in_1), .OUT(romADDR));
  LED led_215 (.in(dec_diplay_2_led3));
  LED led_216 (.in(dec_diplay_2_led2));
  LED led_217 (.in(dec_diplay_2_led1));
  LED led_218 (.in(dec_diplay_2_led0));
  _7SegDisplay_BCD_Adapter u_7segdisplay_bcd_adapter_4 (
    .BCD_0(dec_diplay_2_bcd1_0), .BCD_1(dec_diplay_2_bcd1_1), .BCD_2(dec_diplay_2_bcd1_2),
    .BCD_3(dec_diplay_2_bcd1_3), .a(n7segdisplay_bcd_adapter_4_a), .b(n7segdisplay_bcd_adapter_4_b),
    .c(n7segdisplay_bcd_adapter_4_c), .d(n7segdisplay_bcd_adapter_4_d), .e(n7segdisplay_bcd_adapter_4_e),
    .f(n7segdisplay_bcd_adapter_4_f), .g(n7segdisplay_bcd_adapter_4_g), .dp(n7segdisplay_bcd_adapter_4_dp));
  _7_Segment_Display u_7_segment_display_3 (
    .g(n7segdisplay_bcd_adapter_4_g), .f(n7segdisplay_bcd_adapter_4_f), .a(n7segdisplay_bcd_adapter_4_a),
    .b(n7segdisplay_bcd_adapter_4_b), .e(n7segdisplay_bcd_adapter_4_e), .d(n7segdisplay_bcd_adapter_4_d),
    .c(n7segdisplay_bcd_adapter_4_c), .dp(n7segdisplay_bcd_adapter_4_dp));
  _7_Segment_Display u_7_segment_display_4 (
    .g(n7segdisplay_bcd_adapter_3_g), .f(n7segdisplay_bcd_adapter_3_f), .a(n7segdisplay_bcd_adapter_3_a),
    .b(n7segdisplay_bcd_adapter_3_b), .e(n7segdisplay_bcd_adapter_3_e), .d(n7segdisplay_bcd_adapter_3_d),
    .c(n7segdisplay_bcd_adapter_3_c), .dp(n7segdisplay_bcd_adapter_3_dp));
  Input4 input4_2 (.IN_0(in_8), .IN_1(in_7), .IN_2(in_6), .IN_3(in_5), .OUT(romOPCODE));
  Input4 input4_3 (.IN_0(in_12), .IN_1(in_11), .IN_2(in_10), .IN_3(in_9), .OUT(romIMM));
  Button WRITE_ROM (.out(WRITE_ROM_out));
  Button RESET_ROM (.out(RESET_ROM_out));
  and and_3 (rom_w, WRITE_ROM_out, MANUAL);
  and and_4 (nrom_rst, ~RESET_ROM_out, ON);  // AND_Gate
  ZeroPass4 _0 (
    .enable(muxA), .LEDen(_0_leden), .IN_3(ACC_out_3), .IN_2(ACC_out_2), .IN_1(ACC_out_1), .IN_0(ACC_out_0),
    .OUT_3(_0_out_3), .OUT_2(_0_out_2), .OUT_1(_0_out_1), .OUT_0(_0_out_0));
  LED led_219 (.in(_0_leden));
  Reg4FF ACC (
    .IN_3(alu_1_sum_3), .IN_2(alu_1_sum_2), .IN_1(alu_1_sum_1), .IN_0(alu_1_sum_0), .read(1'b1),
    .write(acc_w), .nrst(nrst), .LED_3(ACC_led_3), .LED_2(ACC_led_2), .LED_1(ACC_led_1), .LED_0(ACC_led_0),
    .OUT_3(ACC_out_3), .OUT_2(ACC_out_2), .OUT_1(ACC_out_1), .OUT_0(ACC_out_0), .LEDr(ACC_ledr),
    .LEDw(ACC_ledw), .LEDrst(ACC_ledrst));
  LED led_220 (.in(ACC_ledw));
  LED led_221 (.in(ACC_ledrst));
  LED led_222 (.in(ACC_ledr));
  SRAM_16x4bit RAM (
    .read(1'b1), .write(ram_w), .nrst(nrst), .LEDsel_0(RAM_ledsel_0), .LED_0__0(RAM_led_0__0),
    .LED_0__1(RAM_led_0__1), .LED_0__2(RAM_led_0__2), .LED_0__3(RAM_led_0__3), .LEDsel_1(RAM_ledsel_1),
    .LED_1__0(RAM_led_1__0), .LED_1__1(RAM_led_1__1), .LED_1__2(RAM_led_1__2), .LED_1__3(RAM_led_1__3),
    .LEDsel_2(RAM_ledsel_2), .LED_2__0(RAM_led_2__0), .LED_2__1(RAM_led_2__1), .LED_2__2(RAM_led_2__2),
    .LED_2__3(RAM_led_2__3), .LEDsel_3(RAM_ledsel_3), .LED_3__0(RAM_led_3__0), .LED_3__1(RAM_led_3__1),
    .LED_3__2(RAM_led_3__2), .LED_3__3(RAM_led_3__3), .LEDsel_4(RAM_ledsel_4), .LED_4__0(RAM_led_4__0),
    .LED_4__1(RAM_led_4__1), .LED_4__2(RAM_led_4__2), .LED_4__3(RAM_led_4__3), .LEDsel_5(RAM_ledsel_5),
    .LED_5__0(RAM_led_5__0), .LED_5__1(RAM_led_5__1), .LED_5__2(RAM_led_5__2), .LED_5__3(RAM_led_5__3),
    .LEDsel_6(RAM_ledsel_6), .LED_6__0(RAM_led_6__0), .LED_6__1(RAM_led_6__1), .LED_6__2(RAM_led_6__2),
    .LED_6__3(RAM_led_6__3), .LEDsel_7(RAM_ledsel_7), .LED_7__0(RAM_led_7__0), .LED_7__1(RAM_led_7__1),
    .LED_7__2(RAM_led_7__2), .LED_7__3(RAM_led_7__3), .LEDr(RAM_ledr), .LEDw(RAM_ledw), .LEDrst(RAM_ledrst),
    .ADDR_3(reg4ff_1_out_3), .ADDR_2(reg4ff_1_out_2), .ADDR_1(reg4ff_1_out_1), .ADDR_0(reg4ff_1_out_0),
    .select(1'b1), .IN_3(ACC_out_3), .IN_2(ACC_out_2), .IN_1(ACC_out_1), .IN_0(ACC_out_0),
    .LEDaddr_1_2(RAM_ledaddr_1_2), .LEDaddr_0_2(RAM_ledaddr_0_2), .LEDaddr_1(RAM_ledaddr_1),
    .LEDaddr_0(RAM_ledaddr_0), .LEDsel(RAM_ledsel), .OUT_3(RAM_out_3), .OUT_2(RAM_out_2), .OUT_1(RAM_out_1),
    .OUT_0(RAM_out_0), .LEDsel_8(RAM_ledsel_8), .LED_8__0(RAM_led_8__0), .LED_8__1(RAM_led_8__1),
    .LED_8__2(RAM_led_8__2), .LED_8__3(RAM_led_8__3), .LEDsel_9(RAM_ledsel_9), .LED_9__0(RAM_led_9__0),
    .LED_9__1(RAM_led_9__1), .LED_9__2(RAM_led_9__2), .LED_9__3(RAM_led_9__3), .LEDsel_A(RAM_ledsel_a),
    .LED_A__0(RAM_led_a__0), .LED_A__1(RAM_led_a__1), .LED_A__2(RAM_led_a__2), .LED_A__3(RAM_led_a__3),
    .LEDsel_B(RAM_ledsel_b), .LED_B__0(RAM_led_b__0), .LED_B__1(RAM_led_b__1), .LED_B__2(RAM_led_b__2),
    .LED_B__3(RAM_led_b__3), .LEDsel_C(RAM_ledsel_c), .LED_C__0(RAM_led_c__0), .LED_C__1(RAM_led_c__1),
    .LED_C__2(RAM_led_c__2), .LED_C__3(RAM_led_c__3), .LEDsel_D(RAM_ledsel_d), .LED_D__0(RAM_led_d__0),
    .LED_D__1(RAM_led_d__1), .LED_D__2(RAM_led_d__2), .LED_D__3(RAM_led_d__3), .LEDsel_E(RAM_ledsel_e),
    .LED_E__0(RAM_led_e__0), .LED_E__1(RAM_led_e__1), .LED_E__2(RAM_led_e__2), .LED_E__3(RAM_led_e__3),
    .LEDsel_F(RAM_ledsel_f), .LED_F__0(RAM_led_f__0), .LED_F__1(RAM_led_f__1), .LED_F__2(RAM_led_f__2),
    .LED_F__3(RAM_led_f__3));
  ALU alu_1 (
    .a_0(_0_out_0), .a_1(_0_out_1), .a_2(_0_out_2), .a_3(_0_out_3), .b_0(mux2x4_4_out0), .b_1(mux2x4_4_out1),
    .b_2(mux2x4_4_out2), .b_3(mux2x4_4_out3), .op(op), .cin(1'b0), .sum_0(alu_1_sum_0), .sum_1(alu_1_sum_1),
    .sum_2(alu_1_sum_2), .sum_3(alu_1_sum_3), .LEDcin(alu_1_ledcin), .LEDop(alu_1_ledop));
  LED led_223 (.in(alu_1_ledop));
  DEC_Diplay dec_diplay_3 (
    .BIN_0(ACC_led_0), .BIN_1(ACC_led_1), .BIN_2(ACC_led_2), .BIN_3(ACC_led_3), .LED0(dec_diplay_3_led0),
    .LED1(dec_diplay_3_led1), .LED2(dec_diplay_3_led2), .LED3(dec_diplay_3_led3),
    .BCD1_1(dec_diplay_3_bcd1_1), .BCD1_0(dec_diplay_3_bcd1_0), .BCD1_2(dec_diplay_3_bcd1_2),
    .BCD1_3(dec_diplay_3_bcd1_3), .BCD10_0(dec_diplay_3_bcd10_0), .BCD10_1(dec_diplay_3_bcd10_1),
    .BCD10_2(dec_diplay_3_bcd10_2), .BCD10_3(dec_diplay_3_bcd10_3));
  LED led_224 (.in(dec_diplay_3_led3));
  LED led_225 (.in(dec_diplay_3_led2));
  _7SegDisplay_BCD_Adapter u_7segdisplay_bcd_adapter_5 (
    .BCD_0(dec_diplay_3_bcd10_0), .BCD_1(dec_diplay_3_bcd10_1), .BCD_2(dec_diplay_3_bcd10_2),
    .BCD_3(dec_diplay_3_bcd10_3), .a(n7segdisplay_bcd_adapter_5_a), .b(n7segdisplay_bcd_adapter_5_b),
    .c(n7segdisplay_bcd_adapter_5_c), .d(n7segdisplay_bcd_adapter_5_d), .e(n7segdisplay_bcd_adapter_5_e),
    .f(n7segdisplay_bcd_adapter_5_f), .g(n7segdisplay_bcd_adapter_5_g), .dp(n7segdisplay_bcd_adapter_5_dp));
  _7_Segment_Display u_7_segment_display_5 (
    .g(n7segdisplay_bcd_adapter_5_g), .f(n7segdisplay_bcd_adapter_5_f), .a(n7segdisplay_bcd_adapter_5_a),
    .b(n7segdisplay_bcd_adapter_5_b), .e(n7segdisplay_bcd_adapter_5_e), .d(n7segdisplay_bcd_adapter_5_d),
    .c(n7segdisplay_bcd_adapter_5_c), .dp(n7segdisplay_bcd_adapter_5_dp));
  Zero4 zero4_1 (._3(ACC_out_3), ._2(ACC_out_2), ._1(ACC_out_1), ._0(ACC_out_0), .zero(zero4_1_zero));
  LED led_226 (.in(RAM_ledaddr_0));
  LED led_227 (.in(RAM_ledaddr_1));
  LED led_228 (.in(RAM_ledaddr_1_2));
  LED led_229 (.in(RAM_ledaddr_0_2));
  LED led_230 (.in(RAM_ledsel));
  LED led_231 (.in(RAM_ledsel_0));
  LED led_232 (.in(RAM_ledsel_1));
  LED led_233 (.in(RAM_ledw));
  LED led_234 (.in(RAM_ledrst));
  LED led_235 (.in(RAM_ledsel_2));
  LED led_236 (.in(RAM_ledsel_3));
  LED led_237 (.in(RAM_ledr));
  LED led_238 (.in(RAM_ledsel_4));
  LED led_239 (.in(RAM_ledsel_5));
  LED led_240 (.in(RAM_ledsel_6));
  LED led_241 (.in(RAM_ledsel_7));
  LED led_242 (.in(RAM_ledsel_8));
  LED led_243 (.in(RAM_ledsel_9));
  LED led_244 (.in(RAM_ledsel_a));
  LED led_245 (.in(RAM_ledsel_b));
  LED led_246 (.in(RAM_ledsel_c));
  LED led_247 (.in(RAM_ledsel_d));
  LED led_248 (.in(RAM_ledsel_e));
  LED led_249 (.in(RAM_ledsel_f));
  Mux2x4 mux2x4_4 (
    .sel(muxB), .a3(reg4ff_1_out_3), .b3(RAM_out_3), .out3(mux2x4_4_out3), .a2(reg4ff_1_out_2),
    .b2(RAM_out_2), .out2(mux2x4_4_out2), .a1(reg4ff_1_out_1), .b1(RAM_out_1), .a0(reg4ff_1_out_0),
    .b0(RAM_out_0), .out1(mux2x4_4_out1), .out0(mux2x4_4_out0), .LEDsel(mux2x4_4_ledsel));
  LED led_250 (.in(mux2x4_4_ledsel));
  LED led_251 (.in(alu_1_ledcin));
  LED led_252 (.in(dec_diplay_3_led1));
  LED led_253 (.in(dec_diplay_3_led0));
  _7SegDisplay_BCD_Adapter u_7segdisplay_bcd_adapter_6 (
    .BCD_0(dec_diplay_3_bcd1_0), .BCD_1(dec_diplay_3_bcd1_1), .BCD_2(dec_diplay_3_bcd1_2),
    .BCD_3(dec_diplay_3_bcd1_3), .a(n7segdisplay_bcd_adapter_6_a), .b(n7segdisplay_bcd_adapter_6_b),
    .c(n7segdisplay_bcd_adapter_6_c), .d(n7segdisplay_bcd_adapter_6_d), .e(n7segdisplay_bcd_adapter_6_e),
    .f(n7segdisplay_bcd_adapter_6_f), .g(n7segdisplay_bcd_adapter_6_g), .dp(n7segdisplay_bcd_adapter_6_dp));
  _7_Segment_Display u_7_segment_display_6 (
    .g(n7segdisplay_bcd_adapter_6_g), .f(n7segdisplay_bcd_adapter_6_f), .a(n7segdisplay_bcd_adapter_6_a),
    .b(n7segdisplay_bcd_adapter_6_b), .e(n7segdisplay_bcd_adapter_6_e), .d(n7segdisplay_bcd_adapter_6_d),
    .c(n7segdisplay_bcd_adapter_6_c), .dp(n7segdisplay_bcd_adapter_6_dp));
  LED led_254 (.in(RAM_led_0__3));
  LED led_255 (.in(RAM_led_0__2));
  LED led_256 (.in(RAM_led_1__2));
  LED led_257 (.in(RAM_led_1__3));
  LED led_258 (.in(RAM_led_2__3));
  LED led_259 (.in(RAM_led_2__2));
  LED led_260 (.in(RAM_led_3__3));
  LED led_261 (.in(RAM_led_3__2));
  LED led_262 (.in(RAM_led_4__3));
  LED led_263 (.in(RAM_led_4__2));
  LED led_264 (.in(RAM_led_5__3));
  LED led_265 (.in(RAM_led_5__2));
  LED led_266 (.in(RAM_led_6__2));
  LED led_267 (.in(RAM_led_6__3));
  LED led_268 (.in(RAM_led_7__3));
  LED led_269 (.in(RAM_led_7__2));
  LED led_270 (.in(RAM_led_8__2));
  LED led_271 (.in(RAM_led_8__3));
  LED led_272 (.in(RAM_led_9__3));
  LED led_273 (.in(RAM_led_9__2));
  LED led_274 (.in(RAM_led_a__3));
  LED led_275 (.in(RAM_led_a__2));
  LED led_276 (.in(RAM_led_b__3));
  LED led_277 (.in(RAM_led_b__2));
  LED led_278 (.in(RAM_led_c__3));
  LED led_279 (.in(RAM_led_c__2));
  LED led_280 (.in(RAM_led_d__3));
  LED led_281 (.in(RAM_led_d__2));
  LED led_282 (.in(RAM_led_e__2));
  LED led_283 (.in(RAM_led_e__3));
  LED led_284 (.in(RAM_led_f__2));
  LED led_285 (.in(RAM_led_f__3));
  LED led_286 (.in(RAM_led_0__1));
  LED led_287 (.in(RAM_led_0__0));
  LED led_288 (.in(RAM_led_1__0));
  LED led_289 (.in(RAM_led_1__1));
  LED led_290 (.in(RAM_led_2__1));
  LED led_291 (.in(RAM_led_2__0));
  LED led_292 (.in(RAM_led_3__0));
  LED led_293 (.in(RAM_led_3__1));
  LED led_294 (.in(RAM_led_4__0));
  LED led_295 (.in(RAM_led_4__1));
  LED led_296 (.in(RAM_led_5__0));
  LED led_297 (.in(RAM_led_5__1));
  LED led_298 (.in(RAM_led_6__1));
  LED led_299 (.in(RAM_led_6__0));
  LED led_300 (.in(RAM_led_7__1));
  LED led_301 (.in(RAM_led_7__0));
  LED led_302 (.in(RAM_led_8__1));
  LED led_303 (.in(RAM_led_8__0));
  LED led_304 (.in(RAM_led_9__0));
  LED led_305 (.in(RAM_led_9__1));
  LED led_306 (.in(RAM_led_a__0));
  LED led_307 (.in(RAM_led_a__1));
  LED led_308 (.in(RAM_led_b__1));
  LED led_309 (.in(RAM_led_b__0));
  LED led_310 (.in(RAM_led_c__0));
  LED led_311 (.in(RAM_led_c__1));
  LED led_312 (.in(RAM_led_d__1));
  LED led_313 (.in(RAM_led_d__0));
  LED led_314 (.in(RAM_led_e__1));
  LED led_315 (.in(RAM_led_e__0));
  LED led_316 (.in(RAM_led_f__1));
  LED led_317 (.in(RAM_led_f__0));

  // Notes on the sheet:
  //   0000 imm  -  add  imm   -  ACC = ACC +  imm
  //   0001 imm  -  add [imm]  -  ACC = ACC + [imm]
  //   0010 imm  -  sub  imm   -  ACC = ACC -  imm
  //   0011 imm  -  sub [imm]  -  ACC = ACC - [imm]
  //   0100 imm  -  mov  imm   -  ACC =  imm
  //   0101 imm  -  ld  [imm]  -  ACC = [imm]
  //   011x imm  -  str [imm]  -  [imm] = ACC
  //   1000 imm  -  bz   imm   -  if ACC == 0: PC =  imm
  //   1001 imm  -  bz  [imm]  -  if ACC == 0: PC = [imm]
  //   1100 imm  -  bnz  imm   -  if ACC != 0: PC =  imm
  //   1101 imm  -  bnz [imm]  -  if ACC != 0: PC = [imm]
  //   1100 imm  -  jmp  imm   -  PC =  imm
  //   1101 imm  -  jmp [imm]  -  PC = [imm]
  //   111x imm  -  halt       -  ignore clock
endmodule

module ControlUnit (
  input  INSTR_0,
  input  INSTR_1,
  input  INSTR_2,
  input  INSTR_3,
  input  zero,
  input  resume,
  input  clk,
  input  nrst,
  output LEDinstr0,
  output LEDinstr1,
  output LEDinstr2,
  output LEDinstr3,
  output LEDzero,
  output LEDhalt,
  output LEDclk,
  output LEDifetch,
  output LEDexec,
  output LEDrst,
  output LED7,
  output LED6,
  output LED5,
  output LED4,
  output LED3,
  output LED2,
  output LED1,
  output LED0,
  output ir_w,
  output muxPC,
  output pc_w,
  output acc_w,
  output ram_w,
  output op,
  output muxA,
  output muxB
);

  wire and_1_out, and_2_out, and_3_out, and_4_out, and_5_out, and_6_out, and_8_out, and_9_out, and_11_out,
       clocklogic_1_clk_out, or_2_out;

  ClockLogic clocklogic_1 (
    .clk(clk), .halt(and_2_out), .resume(resume), .nrst(nrst), .clk_out(clocklogic_1_clk_out),
    .halt_out(LEDhalt));
  and and_1 (and_1_out, INSTR_3, INSTR_2, INSTR_1);
  and and_2 (and_2_out, and_1_out, and_3_out);
  D_FlipFlop d_flipflop_1 (.clk(clocklogic_1_clk_out), .D(LEDexec), .nrst(nrst), .Q(ir_w), .nQ(LEDexec));
  and and_3 (and_3_out, ~LEDclk, LEDexec);  // AND_Gate
  Delayer delayer_1 (.in(clocklogic_1_clk_out), .out(LEDclk));
  and and_4 (and_4_out, INSTR_3, ~INSTR_2, ~INSTR_1, zero);  // AND_Gate
  and and_5 (and_5_out, INSTR_3, ~INSTR_2, INSTR_1, ~zero);  // AND_Gate
  or or_1 (LED6, and_4_out, and_5_out, and_6_out);
  and and_6 (and_6_out, INSTR_3, INSTR_2, ~INSTR_1);  // AND_Gate
  and and_7 (LED5, LEDexec, LEDclk);
  and and_8 (and_8_out, ~INSTR_3, ~INSTR_1);  // AND_Gate
  and and_9 (and_9_out, ~INSTR_3, ~INSTR_2);  // AND_Gate
  or or_2 (or_2_out, and_9_out, and_8_out);
  and and_10 (acc_w, LEDexec, LEDclk, or_2_out);
  and and_11 (and_11_out, ~INSTR_3, INSTR_2, INSTR_1);  // AND_Gate
  and and_12 (LED3, LEDexec, LEDclk, and_11_out);
  and and_13 (LED1, ~INSTR_3, ~INSTR_2);  // AND_Gate
  and and_14 (LED2, ~INSTR_3, ~INSTR_2, INSTR_1);  // AND_Gate

  assign LED0 = INSTR_0;
  assign LED4 = acc_w;
  assign LED7 = ir_w;
  assign LEDifetch = ir_w;
  assign LEDinstr0 = INSTR_0;
  assign LEDinstr1 = INSTR_1;
  assign LEDinstr2 = INSTR_2;
  assign LEDinstr3 = INSTR_3;
  assign LEDrst = nrst;
  assign LEDzero = zero;
  assign muxA = LED1;
  assign muxB = INSTR_0;
  assign muxPC = LED6;
  assign op = LED2;
  assign pc_w = LED5;
  assign ram_w = LED3;
endmodule
